// Logisim project jdh8.circ as structural Verilog: 29 circuits, main circuit main
module main (
);

  wire addr_1_eaux, addr_1_eramout, addr_1_erom, addr_1_lramout, aimm, and_1_out, and_2_out, asp, cc, clk,
       clock_1_out, ealu, edev, eop1, eop2, eram, ereg, err, ex, fall, hlt, jnz, ldev, ldf, ldh, ldl, ldx,
       ldy, lop, lprt, lram, lreg, not_1_out, not_2_out, not_3_out, not_4_out, not_5_out, not_6_out,
       not_7_out, pow, rise, sel, spdec, spinc;
  wire [2:0] addr_1_selaux, exc, sel0, sel1;
  wire [3:0] op;
  wire [7:0] dbus, f, op0, op1, op2, ram_1_dout, regs_1_hout, regs_1_lout, rom_1_data;
  wire [15:0] addr_1_addrout, auxregs_1_pcout, auxregs_1_spout;

  and and_1 (and_1_out, eram, addr_1_eaux);
  and and_2 (and_2_out, lram, addr_1_eaux);
  regs regs_1 (
    .lout(regs_1_lout), .fout(f), .dout(dbus), .hout(regs_1_hout), .ereg(ereg), .sel(sel), .ldh(ldh),
    .ldl(ldl), .ldf(ldf), .sel0(sel0), .sel1(sel1), .din(dbus), .clk(clk), .lreg(lreg));
  auxregs auxregs_1 (
    .pcout(auxregs_1_pcout), .spout(auxregs_1_spout), .dbusout(dbus), .clk(clk), .sel(addr_1_selaux),
    .h(regs_1_hout), .l(regs_1_lout), .dbus(dbus), .lop(lop), .jnz(jnz), .en(and_1_out), .ld(and_2_out),
    .spinc(spinc), .spdec(spdec));
  alu alu_1 (.dout(dbus), .op(op[2:0]), .clk(clk), .ldx(ldx), .ldy(ldy), .ealu(ealu), .ldf(ldf), .fin(f), .din(dbus));
  Clock clock_1 (.out(clock_1_out));
  and and_3 (clk, clock_1_out, not_1_out);
  not not_1 (not_1_out, hlt);
  not not_2 (not_2_out, clk);
  not not_3 (not_3_out, clk);
  not not_4 (not_4_out, not_3_out);
  not not_5 (not_5_out, clk);
  not not_6 (not_6_out, not_5_out);
  not not_7 (not_7_out, not_6_out);
  and and_4 (fall, not_2_out, not_4_out);
  and and_5 (rise, clk, not_7_out);
  addr addr_1 (
    .eramout(addr_1_eramout), .lramout(addr_1_lramout), .eaux(addr_1_eaux), .selaux(addr_1_selaux),
    .addrout(addr_1_addrout), .erom(addr_1_erom), .eram(eram), .apc(lop), .asp(asp), .aimm(aimm),
    .hl({regs_1_hout, regs_1_lout}), .pc(auxregs_1_pcout), .sp(auxregs_1_spout), .imm({op2, op1}), .lram(lram));
  dev dev_1 (
    .dbusout(dbus), .powout(pow), .hltout(hlt), .errout(err), .clk(clk), .edev(edev), .ldev(ldev),
    .lprt(lprt), .dbusin(dbus));
  ROM #(.addrWidth(15)) rom_1 (.addr(addr_1_addrout[14:0]), .data(rom_1_data));
  RAM #(.addrWidth(15), .clearpin("true"), .enables("line")) ram_1 (
    .addr(addr_1_addrout[14:0]), .we(addr_1_lramout), .clk(clk), .din(dbus), .dout(ram_1_dout), .clr(1'b0));
  opc opc_1 (
    .sel0(sel0), .sel1(sel1), .lop(lop), .ex(ex), .excout(exc), .op1out(op1), .op2out(op2), .dbusout(dbus),
    .op0out(op0), .op(op), .dbus(dbus), .fall(fall), .cc(cc), .eop1(eop1), .eop2(eop2), .clk(clk));
  assign dbus = addr_1_erom ? rom_1_data : 8'bz;  // Controlled_Buffer controlled_buffer_1
  assign dbus = addr_1_eramout ? ram_1_dout : 8'bz;  // Controlled_Buffer controlled_buffer_2
  control control_1 (
    .ldy(ldy), .ldf(ldf), .ealu(ealu), .ldh(ldh), .ldl(ldl), .lprt(lprt), .ldev(ldev), .ldx(ldx), .cc(cc),
    .ereg(ereg), .lreg(lreg), .sel(sel), .asp(asp), .aimm(aimm), .lram(lram), .spinc(spinc), .spdec(spdec),
    .jnz(jnz), .eram(eram), .eop1(eop1), .eop2(eop2), .edev(edev), .op0(op0), .ex(ex), .exc(exc));

  // Notes on the sheet:
  //   contents of rom_1 (hex, n*v repeats v):
  //   0 0 1 1 2 7 b 0 9b 1 8 1 9 3 b7 f7 f2 1 50 6 0 6a 77 0 c7 8 87
endmodule

module opc (
  input  clk,
  input  [7:0] dbus,
  input  fall,
  input  cc,
  input  eop1,
  input  eop2,
  output [7:0] op0out,
  output [3:0] op,
  output [2:0] sel0,
  output [2:0] sel1,
  output lop,
  output ex,
  output [2:0] excout,
  output [7:0] op1out,
  output [7:0] op2out,
  output [7:0] dbusout
);

  wire a000_out, a001_out, a010_out, a101_out, and_1_out, and_2_out, and_3_out, and_4_out, and_7_out,
       and_8_out, and_9_out, comparator_1_lt, decoder_1_out0, decoder_1_out1, decoder_1_out2, decoder_1_out3,
       ld1, ld2, ld3, not_1_out, not_2_out, not_3_out, not_4_out, not_5_out, not_6_out, or_1_out;
  wire [7:0] opc_q;
  wire [7:3] exc_q;

  and and_1 (and_1_out, cc, fall);
  Comparator #(.mode("unsigned"), .width(4)) comparator_1 (.a(op), .b(4'b0111), .lt(comparator_1_lt));  // open: gt, eq
  not not_1 (not_1_out, op[0]);
  not not_2 (not_2_out, op[1]);
  not not_3 (not_3_out, op[2]);
  and a001 (a001_out, op[0], not_3_out, not_2_out);
  not not_4 (not_4_out, op0out[3]);
  and and_2 (and_2_out, lop, decoder_1_out0);
  and and_3 (and_3_out, lop, decoder_1_out1);
  and and_4 (and_4_out, lop, decoder_1_out2);
  and a010 (a010_out, not_1_out, op[1], not_1_out);
  and a101 (a101_out, op[0], not_2_out, op[2]);
  or or_1 (or_1_out, a001_out, a010_out, a101_out);
  and and_5 (ld3, not_4_out, comparator_1_lt, or_1_out);
  Register op0 (.D(dbus), .en(and_2_out), .clk(clk), .Q({op, op0out[3:0]}), .clr(1'b0));
  Register op1 (.D(dbus), .en(and_3_out), .clk(clk), .Q(op1out), .clr(1'b0));
  Register op2 (.D(dbus), .en(and_4_out), .clk(clk), .Q(op2out), .clr(1'b0));
  Counter #(.trigger("falling")) opc (
    .count(lop), .Q(opc_q), .up(1'b1), .clk(clk), .clr(and_1_out));  // open: load, D, carry
  Counter #(.trigger("falling")) exc (
    .count(ex), .Q({exc_q, excout}), .up(1'b1), .clk(clk), .clr(and_1_out));  // open: load, D, carry
  and a000 (a000_out, op[2], op[1], op[0]);
  not not_5 (not_5_out, a101_out);
  not not_6 (not_6_out, a000_out);
  and and_6 (ld1, comparator_1_lt, not_5_out, not_6_out, op0out[3]);
  nor nor_1 (ld2, ld3, ld1);
  Decoder #(.select(2)) decoder_1 (
    .out0(decoder_1_out0), .out1(decoder_1_out1), .out2(decoder_1_out2), .out3(decoder_1_out3),
    .sel(opc_q[1:0]), .en(1'b1));
  assign dbusout = eop1 ? op1out : 8'bz;  // Controlled_Buffer controlled_buffer_1
  assign dbusout = eop2 ? op2out : 8'bz;  // Controlled_Buffer controlled_buffer_2
  and and_7 (and_7_out, decoder_1_out1, ld1);
  and and_8 (and_8_out, decoder_1_out2, ld2);
  and and_9 (and_9_out, decoder_1_out3, ld3);
  or or_2 (ex, and_7_out, and_8_out, and_9_out);
  not not_7 (lop, ex);

  assign op0out[7:4] = op;
  assign sel0 = op0out[2:0];
  assign sel1 = op1out[2:0];

  // Other names for the same wires on the sheet: exc[2:0] = excout; y = op0out[3]

  // Notes on the sheet:
  //   ld3 instructions are: (1) LW IMM16, (2) SW IMM16, (5) LDA IMM16
  //   ld1 instructions are: (3) PUSH REG, (4) POP REG, (6) JNZ REG
  //   and (1) LW REG, [HL] (2) SW [HL], REG
endmodule

module auxregs (
  input  clk,
  input  [2:0] sel,
  input  [7:0] h,
  input  [7:0] l,
  input  [7:0] dbus,
  input  lop,
  input  jnz,
  input  en,
  input  ld,
  input  spinc,
  input  spdec,
  output [15:0] pcout,
  output [15:0] spout,
  output [7:0] dbusout
);

  wire and_1_out, and_2_out, and_3_out, and_4_out, and_5_out, and_6_out, and_7_out, and_8_out, and_9_out,
       and_10_out, and_11_out, and_12_out, and_13_out, comparator_1_gt, comparator_1_lt, decoder_1_out2,
       decoder_1_out3, decoder_1_out4, decoder_1_out5, decoder_1_out6, decoder_1_out7, not_1_out, not_2_out,
       or_1_out, or_2_out, or_3_out, or_4_out, or_5_out, or_6_out, or_7_out;
  wire [7:0] controlled_buffer_1_out, controlled_buffer_2_out, controlled_buffer_3_out,
       controlled_buffer_4_out, mbl_q;
  wire [15:0] adder_1_out, multiplexer_1_out, multiplexer_2_out;

  Multiplexer #(.enable("false"), .width(16)) multiplexer_1 (
    .in0(pcout), .in1(spout), .out(multiplexer_1_out), .sel(or_1_out));
  or or_1 (or_1_out, spinc, spdec);
  Multiplexer #(.enable("false"), .width(16)) multiplexer_2 (
    .in0(16'h1), .in1({16{1'b1}}), .out(multiplexer_2_out), .sel(spdec));
  Adder #(.width(16)) adder_1 (
    .a(multiplexer_1_out), .b(multiplexer_2_out), .out(adder_1_out), .cin(1'b0));  // open: cout
  or or_2 (or_2_out, lop, and_1_out);
  not not_1 (not_1_out, or_2_out);
  not not_2 (not_2_out, or_1_out);
  or or_3 (or_3_out, comparator_1_gt, comparator_1_lt);
  Comparator comparator_1 (.a({8{1'b0}}), .b(dbus), .gt(comparator_1_gt), .lt(comparator_1_lt));  // open: eq
  assign controlled_buffer_1_out = not_1_out ? dbus : 8'bz;  // Controlled_Buffer controlled_buffer_1
  assign controlled_buffer_2_out = not_1_out ? dbus : 8'bz;  // Controlled_Buffer controlled_buffer_2
  assign controlled_buffer_3_out = not_2_out ? dbus : 8'bz;  // Controlled_Buffer controlled_buffer_3
  assign controlled_buffer_4_out = not_2_out ? dbus : 8'bz;  // Controlled_Buffer controlled_buffer_4
  and and_1 (and_1_out, jnz, or_3_out);
  assign controlled_buffer_1_out = lop ? adder_1_out[7:0] : 8'bz;  // Controlled_Buffer controlled_buffer_5
  assign controlled_buffer_1_out = and_1_out ? l : 8'bz;  // Controlled_Buffer controlled_buffer_6
  assign controlled_buffer_2_out = lop ? adder_1_out[15:8] : 8'bz;  // Controlled_Buffer controlled_buffer_7
  assign controlled_buffer_2_out = and_1_out ? h : 8'bz;  // Controlled_Buffer controlled_buffer_8
  assign controlled_buffer_3_out = or_1_out ? adder_1_out[7:0] : 8'bz;  // Controlled_Buffer controlled_buffer_9
  assign controlled_buffer_4_out = or_1_out ? adder_1_out[15:8] : 8'bz;  // Controlled_Buffer controlled_buffer_10
  Register pcl (.D(controlled_buffer_1_out), .en(or_4_out), .clk(clk), .Q(pcout[7:0]));  // open: clr
  or or_4 (or_4_out, or_2_out, and_2_out);
  Register pch (.D(controlled_buffer_2_out), .en(or_5_out), .clk(clk), .Q(pcout[15:8]));  // open: clr
  or or_5 (or_5_out, or_2_out, and_3_out);
  Register spl (.D(controlled_buffer_3_out), .en(or_6_out), .clk(clk), .Q(spout[7:0]));  // open: clr
  or or_6 (or_6_out, or_1_out, and_4_out);
  Register sph (.D(controlled_buffer_4_out), .en(or_7_out), .clk(clk), .Q(spout[15:8]));  // open: clr
  or or_7 (or_7_out, or_1_out, and_5_out);
  Register mbl (.D(dbus), .en(and_6_out), .clk(clk), .Q(mbl_q));  // open: clr
  Register mbh (.D(dbus), .en(and_7_out), .clk(clk), .Q(mbl_q));  // open: clr
  and and_2 (and_2_out, ld, decoder_1_out6);
  and and_3 (and_3_out, ld, decoder_1_out7);
  and and_4 (and_4_out, ld, decoder_1_out4);
  and and_5 (and_5_out, ld, decoder_1_out5);
  and and_6 (and_6_out, ld, decoder_1_out2);
  and and_7 (and_7_out, ld, decoder_1_out3);
  Decoder #(.select(3)) decoder_1 (
    .out2(decoder_1_out2), .out3(decoder_1_out3), .out4(decoder_1_out4), .out5(decoder_1_out5),
    .out6(decoder_1_out6), .out7(decoder_1_out7), .sel(sel), .en(1'b1));  // open: out0, out1
  assign dbusout = and_8_out ? pcout[7:0] : 8'bz;  // Controlled_Buffer controlled_buffer_11
  and and_8 (and_8_out, decoder_1_out6, en);
  assign dbusout = and_9_out ? pcout[15:8] : 8'bz;  // Controlled_Buffer controlled_buffer_12
  and and_9 (and_9_out, decoder_1_out7, en);
  assign dbusout = and_10_out ? spout[7:0] : 8'bz;  // Controlled_Buffer controlled_buffer_13
  and and_10 (and_10_out, decoder_1_out4, en);
  assign dbusout = and_11_out ? spout[15:8] : 8'bz;  // Controlled_Buffer controlled_buffer_14
  and and_11 (and_11_out, decoder_1_out5, en);
  assign dbusout = and_12_out ? mbl_q : 8'bz;  // Controlled_Buffer controlled_buffer_15
  and and_12 (and_12_out, decoder_1_out2, en);
  assign dbusout = and_13_out ? mbl_q : 8'bz;  // Controlled_Buffer controlled_buffer_16
  and and_13 (and_13_out, decoder_1_out3, en);

  // Other names for the same wires on the sheet: pc[15:0] = pcout; sp[15:0] = spout
endmodule

module addr (
  input  lram,
  input  eram,
  input  apc,
  input  asp,
  input  aimm,
  input  [15:0] hl,
  input  [15:0] pc,
  input  [15:0] sp,
  input  [15:0] imm,
  output erom,
  output eramout,
  output lramout,
  output eaux,
  output [2:0] selaux,
  output [15:0] addrout
);

  wire and_2_out, and_3_out, nor_1_out, not_1_out, not_2_out, or_1_out, or_2_out;

  or or_1 (or_1_out, eram, apc);
  nor nor_1 (nor_1_out, apc, asp, aimm);
  assign addrout = nor_1_out ? hl : 16'bz;  // Controlled_Buffer controlled_buffer_1
  assign addrout = apc ? pc : 16'bz;  // Controlled_Buffer controlled_buffer_2
  assign addrout = asp ? sp : 16'bz;  // Controlled_Buffer controlled_buffer_3
  assign addrout = aimm ? imm : 16'bz;  // Controlled_Buffer controlled_buffer_4
  or or_2 (or_2_out, addrout[1], addrout[2]);
  and and_1 (eaux, or_2_out, and_2_out);
  and and_2 (and_2_out, addrout[3], addrout[4], addrout[5], addrout[6], addrout[7], addrout[8], addrout[9], addrout[10], addrout[11], addrout[12], addrout[13], addrout[14], addrout[15]);
  and and_3 (and_3_out, addrout[15], not_1_out);
  not not_1 (not_1_out, eaux);
  Hex_Digit_Display hex_digit_display_1 (.value(addrout[15:12]));  // open: dp
  and and_4 (erom, or_1_out, not_2_out);
  not not_2 (not_2_out, addrout[15]);
  and and_5 (eramout, or_1_out, and_3_out);
  and and_6 (lramout, and_3_out, lram);
  Hex_Digit_Display hex_digit_display_2 (.value(addrout[11:8]));  // open: dp
  Hex_Digit_Display hex_digit_display_3 (.value(addrout[7:4]));  // open: dp
  Hex_Digit_Display hex_digit_display_4 (.value(addrout[3:0]));  // open: dp

  assign selaux = addrout[2:0];
endmodule

module dev (
  input  clk,
  input  edev,
  input  ldev,
  input  lprt,
  input  [7:0] dbusin,
  output errout,
  output powout,
  output hltout,
  output [7:0] dbusout
);

  wire and_1_out, and_2_out, nand_1_out;
  wire [7:0] prt_q, sta_q;

  nand nand_1 (nand_1_out, prt_q[7], prt_q[6], prt_q[5], prt_q[4], prt_q[3], prt_q[2], prt_q[1], prt_q[0]);
  and and_1 (and_1_out, edev, nand_1_out);
  and and_2 (and_2_out, ldev, nand_1_out);
  Register sta (
    .D(dbusin), .en(and_2_out), .clk(clk), .Q({sta_q[7:4], hltout, powout, errout, sta_q[0]}));  // open: clr
  Register prt (.D(dbusin), .en(lprt), .clk(clk), .Q(prt_q));  // open: clr
  LED err (.in(errout));
  LED pow (.in(powout));
  assign dbusout = and_1_out ? {sta_q[7:4], hltout, powout, errout, sta_q[0]} : 8'bz;  // Controlled_Buffer controlled_buffer_1
  LED hlt (.in(hltout));
endmodule

module regs (
  input  lreg,
  input  ereg,
  input  sel,
  input  ldh,
  input  ldl,
  input  ldf,
  input  [2:0] sel0,
  input  [2:0] sel1,
  input  [7:0] din,
  input  clk,
  output [7:0] dout,
  output [7:0] lout,
  output [7:0] hout,
  output [7:0] fout
);

  wire and_1_out, and_2_out, decoder_1_out0, decoder_1_out1, decoder_1_out2, decoder_1_out3, decoder_1_out4,
       decoder_1_out5, decoder_1_out6, decoder_1_out7, decoder_2_out0, decoder_2_out1, decoder_2_out2,
       decoder_2_out3, decoder_2_out4, decoder_2_out5, decoder_2_out6, decoder_2_out7, not_1_out, not_2_out,
       or_1_out, or_2_out, or_3_out;
  wire [2:0] controlled_buffer_1_out;
  wire [7:0] A_q, B_q, C_q, D_q, Z_q;

  not not_1 (not_1_out, or_1_out);
  not not_2 (not_2_out, sel);
  or or_1 (or_1_out, ldf, or_2_out);
  and and_1 (and_1_out, not_1_out, not_2_out);
  and and_2 (and_2_out, sel, not_1_out);
  or or_2 (or_2_out, ldl, ldh);
  assign controlled_buffer_1_out = and_1_out ? sel0 : 3'bz;  // Controlled_Buffer controlled_buffer_1
  assign controlled_buffer_1_out = and_2_out ? sel1 : 3'bz;  // Controlled_Buffer controlled_buffer_2
  assign controlled_buffer_1_out = ldh ? 3'b101 : 3'bz;  // Controlled_Buffer controlled_buffer_3
  assign controlled_buffer_1_out = ldl ? 3'b100 : 3'bz;  // Controlled_Buffer controlled_buffer_4
  assign controlled_buffer_1_out = ldf ? 3'b111 : 3'bz;  // Controlled_Buffer controlled_buffer_5
  or or_3 (or_3_out, lreg, or_1_out);
  Decoder #(.select(3)) decoder_1 (
    .out0(decoder_1_out0), .out1(decoder_1_out1), .out2(decoder_1_out2), .out3(decoder_1_out3),
    .out4(decoder_1_out4), .out5(decoder_1_out5), .out6(decoder_1_out6), .out7(decoder_1_out7),
    .sel(controlled_buffer_1_out), .en(or_3_out));
  Register A (.D(din), .en(decoder_1_out0), .clk(clk), .Q(A_q), .clr(1'b0));
  Register B (.D(din), .en(decoder_1_out1), .clk(clk), .Q(B_q), .clr(1'b0));
  Register C (.D(din), .en(decoder_1_out2), .clk(clk), .Q(C_q), .clr(1'b0));
  Register D (.D(din), .en(decoder_1_out3), .clk(clk), .Q(D_q), .clr(1'b0));
  Register L (.D(din), .en(decoder_1_out4), .clk(clk), .Q(lout), .clr(1'b0));
  Register H (.D(din), .en(decoder_1_out5), .clk(clk), .Q(hout), .clr(1'b0));
  Register Z (.D(din), .en(decoder_1_out6), .clk(clk), .Q(Z_q), .clr(1'b0));
  Register F (.D(din), .en(decoder_1_out7), .clk(clk), .Q(fout), .clr(1'b0));
  Decoder #(.select(3)) decoder_2 (
    .out0(decoder_2_out0), .out1(decoder_2_out1), .out2(decoder_2_out2), .out3(decoder_2_out3),
    .out4(decoder_2_out4), .out5(decoder_2_out5), .out6(decoder_2_out6), .out7(decoder_2_out7),
    .sel(controlled_buffer_1_out), .en(ereg));
  assign dout = decoder_2_out0 ? A_q : 8'bz;  // Controlled_Buffer controlled_buffer_6
  assign dout = decoder_2_out1 ? B_q : 8'bz;  // Controlled_Buffer controlled_buffer_7
  assign dout = decoder_2_out2 ? C_q : 8'bz;  // Controlled_Buffer controlled_buffer_8
  assign dout = decoder_2_out3 ? D_q : 8'bz;  // Controlled_Buffer controlled_buffer_9
  assign dout = decoder_2_out4 ? lout : 8'bz;  // Controlled_Buffer controlled_buffer_10
  assign dout = decoder_2_out5 ? hout : 8'bz;  // Controlled_Buffer controlled_buffer_11
  assign dout = decoder_2_out6 ? Z_q : 8'bz;  // Controlled_Buffer controlled_buffer_12
  assign dout = decoder_2_out7 ? fout : 8'bz;  // Controlled_Buffer controlled_buffer_13
endmodule

module control (
  input  ex,
  input  [2:0] exc,
  input  [7:0] op0,
  output eram,
  output ldx,
  output asp,
  output ldy,
  output aimm,
  output ldf,
  output lram,
  output ealu,
  output spinc,
  output ldh,
  output spdec,
  output ldl,
  output jnz,
  output lprt,
  output ereg,
  output lreg,
  output sel,
  output eop1,
  output eop2,
  output edev,
  output ldev,
  output cc
);

  wire and_1_out, and_13_out, not_1_out;
  wire [3:0] rom_1_data, rom_1_data_2, rom_1_data_3, rom_1_data_4;

  Hex_Digit_Display hex_digit_display_1 (.value(rom_1_data_4));  // open: dp
  ROM #(.addrWidth(12), .dataWidth(16)) rom_1 (
    .addr({4'b0000, op0[7:3], exc}), .data({rom_1_data_4, rom_1_data_3, rom_1_data_2, rom_1_data}));
  Hex_Digit_Display hex_digit_display_2 (.value(rom_1_data_3));  // open: dp
  Hex_Digit_Display hex_digit_display_3 (.value(rom_1_data_2));  // open: dp
  Hex_Digit_Display hex_digit_display_4 (.value(rom_1_data));  // open: dp
  and and_1 (and_1_out, not_1_out, ex);
  not not_1 (not_1_out, rom_1_data_4[3]);
  and and_2 (ereg, rom_1_data_2[3], ex);
  and and_3 (eram, rom_1_data[0], and_1_out);
  and and_4 (asp, rom_1_data[1], and_1_out);
  and and_5 (aimm, rom_1_data[2], and_1_out);
  and and_6 (lram, rom_1_data[3], and_1_out);
  and and_7 (spinc, rom_1_data_2[0], and_1_out);
  and and_8 (spdec, rom_1_data_2[1], and_1_out);
  and and_9 (jnz, rom_1_data_2[2], and_1_out);
  and and_10 (lreg, rom_1_data_3[0], ex);
  and and_11 (sel, rom_1_data_3[1], ex);
  and and_12 (eop1, rom_1_data_3[2], ex);
  and and_13 (and_13_out, rom_1_data_4[3], ex);
  and and_14 (eop2, rom_1_data_3[3], ex);
  and and_15 (edev, rom_1_data_4[0], ex);
  and and_16 (ldx, rom_1_data[0], and_13_out);
  and and_17 (ldy, rom_1_data[1], and_13_out);
  and and_18 (ldf, rom_1_data[2], and_13_out);
  and and_19 (ealu, rom_1_data[3], and_13_out);
  and and_20 (ldh, rom_1_data_2[0], and_13_out);
  and and_21 (ldl, rom_1_data_2[1], and_13_out);
  and and_22 (lprt, rom_1_data_2[2], and_13_out);
  and and_23 (ldev, rom_1_data_4[1], ex);
  and and_24 (cc, rom_1_data_4[2], ex);

  // Notes on the sheet:
  //   contents of rom_1 (hex, n*v repeats v):
  //   4500 7*4000 8281 c108 6*4000 4105 7*4000 4101 7*4000 408c 7*4000 4088 7*4000 40a 4020 6*4000 8a 4020
  //   14*4000 10 4103 6*4000 8420 c810 14*4000 4440 7*4000 40c0 7*4000 8440 5100 6*4000 82c0 5100 6*4000
  //   8440 6080 6*4000 82c0 6080 6*4000 8081 8402 8108 c004 4*4000 8081 8282 8108 c004 4*4000 8081 8402
  //   8108 c004 4*4000 8081 8282 8108 c004 4*4000 8081 8402 c108 5*4000 8081 8282 c108 5*4000 8081 8402
  //   c108 5*4000 8081 8282 c108 5*4000 8081 8402 c108 5*4000 8081 8282 c108 5*4000 8081 8402 c004 5*4000
  //   8081 8282 c004 5*4000 8081 8402 8108 c004 4*4000 8081 8282 8108 c004 4*4000
endmodule

module alu (
  input  [2:0] op,
  input  clk,
  input  ldx,
  input  ldy,
  input  ealu,
  input  ldf,
  input  [7:0] din,
  input  [7:0] fin,
  output [7:0] dout
);

  wire adder_1_cout, and_1_out, and_3_out, and_4_out, decoder_1_out0, decoder_1_out1, decoder_1_out2,
       decoder_1_out3, decoder_1_out4, decoder_1_out5, decoder_1_out7, or_1_out, subtractor_1_bout;
  wire [3:0] comparator_1_lt;
  wire [7:0] adder_1_out, and_2_out, controlled_buffer_1_out, nor_1_out, or_2_out, register_1_q,
       register_2_q, subtractor_1_out;

  Register register_1 (.D(din), .en(ldx), .clk(clk), .Q(register_1_q));  // open: clr
  Register register_2 (.D(din), .en(ldy), .clk(clk), .Q(register_2_q));  // open: clr
  Decoder #(.select(3)) decoder_1 (
    .out0(decoder_1_out0), .out1(decoder_1_out1), .out2(decoder_1_out2), .out3(decoder_1_out3),
    .out4(decoder_1_out4), .out5(decoder_1_out5), .out7(decoder_1_out7), .sel(op), .en(1'b1));  // open: out6
  and and_1 (and_1_out, fin[2], op[1]);
  Adder adder_1 (.a(register_1_q), .b(register_2_q), .out(adder_1_out), .cin(and_1_out), .cout(adder_1_cout));
  or or_1 (or_1_out, decoder_1_out1, decoder_1_out2);
  assign and_2_out = register_1_q & register_2_q;  // AND_Gate and_2, 8 bits wide
  assign or_2_out = register_1_q | register_2_q;  // OR_Gate or_2, 8 bits wide
  assign nor_1_out = ~(register_1_q | register_2_q);  // NOR_Gate nor_1, 8 bits wide
  Comparator comparator_1 (
    .a(register_1_q), .b(register_2_q), .eq(comparator_1_lt[1]), .lt(comparator_1_lt[0]));  // open: gt
  Subtractor subtractor_1 (
    .a(register_1_q), .b(register_2_q), .out(subtractor_1_out), .bin(fin[3]), .bout(subtractor_1_bout));
  and and_3 (and_3_out, decoder_1_out7, subtractor_1_bout);
  assign controlled_buffer_1_out = or_1_out ? adder_1_out : 8'bz;  // Controlled_Buffer controlled_buffer_1
  and and_4 (and_4_out, adder_1_cout, or_1_out);
  assign controlled_buffer_1_out = decoder_1_out3 ? and_2_out : 8'bz;  // Controlled_Buffer controlled_buffer_2
  assign controlled_buffer_1_out = decoder_1_out4 ? or_2_out : 8'bz;  // Controlled_Buffer controlled_buffer_3
  assign controlled_buffer_1_out = decoder_1_out5 ? nor_1_out : 8'bz;  // Controlled_Buffer controlled_buffer_4
  assign controlled_buffer_1_out = decoder_1_out7 ? subtractor_1_out : 8'bz;  // Controlled_Buffer controlled_buffer_5
  or or_3 (comparator_1_lt[3], and_3_out, fin[3]);
  assign controlled_buffer_1_out = decoder_1_out0 ? register_1_q : 8'bz;  // Controlled_Buffer controlled_buffer_6
  or or_4 (comparator_1_lt[2], fin[2], and_4_out);
  assign dout = ealu ? controlled_buffer_1_out : 8'bz;  // Controlled_Buffer controlled_buffer_7
  assign dout = ldf ? {4'b0000, comparator_1_lt} : 8'bz;  // Controlled_Buffer controlled_buffer_8

  // Other names for the same wires on the sheet: fl = fin[0]; fe = fin[1]; fc = fin[2]; fb = fin[3]
endmodule

module main2 (
);

  wire addr_1_eaux, addr_1_eramout, addr_1_erom, addr_1_lramout, and_1_out, and_2_out, and_3_out, and_4_out,
       clock_1_out, control_1_aimm, control_1_asp, control_1_cc, control_1_ealu, control_1_edev,
       control_1_eop1, control_1_eop2, control_1_eram, control_1_ereg, control_1_jnz, control_1_ldev,
       control_1_ldf, control_1_ldh, control_1_ldl, control_1_ldx, control_1_ldy, control_1_lprt,
       control_1_lram, control_1_lreg, control_1_sel, control_1_spdec, control_1_spinc, dev_1_hltout,
       not_1_out, not_2_out, not_3_out, not_4_out, opc_1_ex, opc_1_lop;
  wire [2:0] addr_1_selaux, opc_1_excout, opc_1_sel0, opc_1_sel1;
  wire [3:0] opc_1_op;
  wire [7:0] auxregs_1_dbusout, opc_1_op0out, opc_1_op1out, opc_1_op2out, ram_1_dout, regs_1_fout,
       regs_1_hout, regs_1_lout, rom_1_data;
  wire [15:0] addr_1_addrout, auxregs_1_pcout, auxregs_1_spout;

  Clock clock_1 (.out(clock_1_out));
  not not_1 (not_1_out, dev_1_hltout);
  and and_1 (and_1_out, addr_1_eaux, control_1_eram);
  and and_2 (and_2_out, addr_1_eaux, control_1_lram);
  not not_2 (not_2_out, and_3_out);
  not not_3 (not_3_out, and_3_out);
  not not_4 (not_4_out, not_3_out);
  and and_3 (and_3_out, clock_1_out, not_1_out);
  and and_4 (and_4_out, not_2_out, not_4_out);
  control control_1 (
    .ldy(control_1_ldy), .ldf(control_1_ldf), .ealu(control_1_ealu), .ldh(control_1_ldh),
    .ldl(control_1_ldl), .lprt(control_1_lprt), .ldev(control_1_ldev), .ldx(control_1_ldx),
    .cc(control_1_cc), .ereg(control_1_ereg), .lreg(control_1_lreg), .sel(control_1_sel),
    .asp(control_1_asp), .aimm(control_1_aimm), .lram(control_1_lram), .spinc(control_1_spinc),
    .spdec(control_1_spdec), .jnz(control_1_jnz), .eram(control_1_eram), .eop1(control_1_eop1),
    .eop2(control_1_eop2), .edev(control_1_edev), .op0(opc_1_op0out), .ex(opc_1_ex), .exc(opc_1_excout));
  auxregs auxregs_1 (
    .pcout(auxregs_1_pcout), .spout(auxregs_1_spout), .dbusout(auxregs_1_dbusout), .clk(and_3_out),
    .sel(addr_1_selaux), .h(regs_1_hout), .l(regs_1_lout), .dbus(auxregs_1_dbusout), .lop(opc_1_lop),
    .jnz(control_1_jnz), .en(and_1_out), .ld(and_2_out), .spinc(control_1_spinc), .spdec(control_1_spdec));
  LED led_1 (.in(auxregs_1_dbusout[7]));
  LED led_2 (.in(auxregs_1_dbusout[6]));
  LED led_3 (.in(auxregs_1_dbusout[5]));
  LED led_4 (.in(auxregs_1_dbusout[4]));
  LED led_5 (.in(auxregs_1_dbusout[3]));
  LED led_6 (.in(auxregs_1_dbusout[0]));
  LED led_7 (.in(auxregs_1_dbusout[2]));
  LED led_8 (.in(auxregs_1_dbusout[1]));
  addr addr_1 (
    .eramout(addr_1_eramout), .lramout(addr_1_lramout), .eaux(addr_1_eaux), .selaux(addr_1_selaux),
    .addrout(addr_1_addrout), .erom(addr_1_erom), .eram(control_1_eram), .apc(opc_1_lop),
    .asp(control_1_asp), .aimm(control_1_aimm), .hl({regs_1_hout, regs_1_lout}), .pc(auxregs_1_pcout),
    .sp(auxregs_1_spout), .imm({opc_1_op2out, opc_1_op1out}), .lram(control_1_lram));
  regs regs_1 (
    .lout(regs_1_lout), .fout(regs_1_fout), .dout(auxregs_1_dbusout), .hout(regs_1_hout),
    .ereg(control_1_ereg), .sel(control_1_sel), .ldh(control_1_ldh), .ldl(control_1_ldl),
    .ldf(control_1_ldf), .sel0(opc_1_sel0), .sel1(opc_1_sel1), .din(auxregs_1_dbusout), .clk(and_3_out),
    .lreg(control_1_lreg));
  opc opc_1 (
    .sel0(opc_1_sel0), .sel1(opc_1_sel1), .lop(opc_1_lop), .ex(opc_1_ex), .excout(opc_1_excout),
    .op1out(opc_1_op1out), .op2out(opc_1_op2out), .dbusout(auxregs_1_dbusout), .op0out(opc_1_op0out),
    .op(opc_1_op), .dbus(auxregs_1_dbusout), .fall(and_4_out), .cc(control_1_cc), .eop1(control_1_eop1),
    .eop2(control_1_eop2), .clk(and_3_out));
  ROM #(.addrWidth(15)) rom_1 (.addr(addr_1_addrout[14:0]), .data(rom_1_data));
  RAM #(.addrWidth(15), .clearpin("true"), .enables("line")) ram_1 (
    .addr(addr_1_addrout[14:0]), .we(addr_1_lramout), .clk(and_3_out), .din(auxregs_1_dbusout),
    .dout(ram_1_dout), .clr(1'b0));
  alu alu_1 (
    .dout(auxregs_1_dbusout), .op(opc_1_op[2:0]), .clk(and_3_out), .ldx(control_1_ldx), .ldy(control_1_ldy),
    .ealu(control_1_ealu), .ldf(control_1_ldf), .fin(regs_1_fout), .din(auxregs_1_dbusout));
  dev dev_1 (
    .dbusout(auxregs_1_dbusout), .hltout(dev_1_hltout), .clk(and_3_out), .edev(control_1_edev),
    .ldev(control_1_ldev), .lprt(control_1_lprt), .dbusin(auxregs_1_dbusout));  // open: powout, errout
  assign auxregs_1_dbusout = addr_1_erom ? rom_1_data : 8'bz;  // Controlled_Buffer controlled_buffer_1
  assign auxregs_1_dbusout = addr_1_eramout ? ram_1_dout : 8'bz;  // Controlled_Buffer controlled_buffer_2

  // Notes on the sheet:
  //   contents of rom_1 (hex, n*v repeats v):
  //   0 0 1 1 2 7 b 0 9b 1 8 1 9 3 f2 1 50 6 0 6a 77 0 c7 8 87
endmodule

module screendev (
  input  clk,
  input  edev,
  input  ldev,
  input  [7:0] prt,
  input  [7:0] din,
  output [7:0] dout,
  output [5:0] sx,
  output [5:0] sy,
  output sv,
  output se
);

  wire and_1_out, and_2_out, and_3_out, and_4_out, and_5_out, and_6_out, and_7_out, and_8_out, and_9_out,
       and_10_out, and_11_out, and_12_out, and_13_out, clock_1_out, comparator_1_eq, comparator_2_eq,
       comparator_3_eq, comparator_4_eq, comparator_5_eq, counter_1_carry, counter_2_carry, counter_3_carry,
       d_ff_1_q, d_ff_2_q, d_ff_2_qn, not_1_out, not_2_out, not_3_out, not_4_out, or_1_out, or_2_out;
  wire [0:0] d_ff_3_q;
  wire [8:0] counter_2_q;

  Clock clock_1 (.out(clock_1_out));
  Comparator comparator_1 (.a(prt), .b(8'h2), .eq(comparator_1_eq));  // open: gt, lt
  Comparator comparator_2 (.a(din), .b(8'h1), .eq(comparator_2_eq));  // open: gt, lt
  Comparator comparator_3 (.a(din), .b(8'h2), .eq(comparator_3_eq));  // open: gt, lt
  Comparator comparator_4 (.a(din), .b(8'h3), .eq(comparator_4_eq));  // open: gt, lt
  Comparator comparator_5 (.a(din), .b(8'h4), .eq(comparator_5_eq));  // open: gt, lt
  not not_1 (not_1_out, d_ff_1_q);
  and and_1 (and_1_out, ldev, comparator_1_eq);
  and and_2 (and_2_out, and_1_out, not_1_out, comparator_2_eq);
  and and_3 (and_3_out, and_2_out, and_8_out);
  and and_4 (and_4_out, and_1_out, not_1_out, comparator_3_eq);
  and and_5 (and_5_out, and_4_out, and_8_out);
  and and_6 (and_6_out, and_1_out, not_1_out, comparator_4_eq);
  and and_7 (and_7_out, and_1_out, not_1_out, comparator_5_eq);
  not not_2 (not_2_out, clock_1_out);
  not not_3 (not_3_out, clock_1_out);
  not not_4 (not_4_out, not_2_out);
  and and_8 (and_8_out, not_3_out, not_4_out);
  D_Flip_Flop d_ff_1 (.D(and_2_out), .clk(and_3_out), .Q(d_ff_1_q), .reset(counter_2_carry));  // open: Qn, preset
  D_Flip_Flop d_ff_2 (
    .D(and_4_out), .clk(and_5_out), .Q(d_ff_2_q), .Qn(d_ff_2_qn), .reset(counter_2_carry));  // open: preset
  and and_9 (and_9_out, d_ff_1_q, and_1_out);
  // RGB_Video #(.cursor("No Cursor"), .height(64), .scale(6), .width(64)) rgb_video_1: pin names not known
  or or_1 (or_1_out, and_9_out, counter_1_carry);
  Counter #(.max('h7), .width(3)) counter_1 (
    .count(d_ff_2_q), .carry(counter_1_carry), .up(1'b1), .clk(clock_1_out), .clr(and_10_out));  // open: load, D, Q
  and and_10 (and_10_out, counter_1_carry, and_8_out);
  Counter #(.max('h1ff), .width(9)) counter_2 (
    .count(or_1_out), .Q(counter_2_q), .carry(counter_2_carry), .up(1'b1), .clk(and_8_out),
    .clr(counter_2_carry));  // open: load, D
  D_Flip_Flop d_ff_3 (.D(and_11_out), .clk(and_12_out), .Q(d_ff_3_q[0]));  // open: Qn, preset, reset
  and and_11 (and_11_out, d_ff_2_qn, and_7_out);
  and and_12 (and_12_out, and_7_out, clock_1_out);
  RAM #(.addrWidth(9), .clearpin("true"), .enables("line")) ram_1 (
    .addr(counter_2_q), .we(and_9_out), .clk(clock_1_out), .din(din), .clr(and_6_out));  // open: dout
  Counter #(.max('h3f), .width(6)) counter_3 (
    .count(d_ff_2_q), .Q(sx), .carry(counter_3_carry), .up(1'b1), .clk(and_8_out), .clr(or_2_out));  // open: load, D
  or or_2 (or_2_out, and_13_out, counter_2_carry);
  Counter #(.max('h3f), .width(6)) counter_4 (
    .count(counter_3_carry), .Q(sy), .up(1'b1), .clk(and_8_out), .clr(counter_2_carry));  // open: load, D, carry
  assign dout = edev ? {{7{1'b0}}, d_ff_3_q[0]} : 8'bz;  // Controlled_Buffer controlled_buffer_1
  and and_13 (and_13_out, counter_3_carry, and_8_out);
endmodule

module video (
  input  clk,
  output [13:0] vram_addr,
  output v_10,
  output v_03
);

  wire and_1_out, and_2_out, and_3_out, and_4_out, and_5_out, and_6_out, and_7_out, and_8_out, and_9_out,
       and_10_out, and_11_out, and_12_out, and_13_out, and_14_out, bitselector_1_out, comparator_1_eq,
       comparator_2_eq, comparator_3_eq, comparator_4_eq, comparator_5_eq, comparator_6_eq, comparator_7_eq,
       comparator_8_eq, comparator_9_eq, comparator_10_eq, comparator_11_lt, comparator_12_lt, nor_1_out,
       not_1_out, not_2_out, not_3_out, or_1_out, or_2_out, s_r_ff_1_q, s_r_ff_1_qn, s_r_ff_2_q, s_r_ff_2_qn,
       s_r_ff_3_q, s_r_ff_3_qn, s_r_ff_4_q, s_r_ff_4_qn, s_r_ff_5_q, s_r_ff_5_qn, s_r_ff_6_qn, s_r_ff_7_q,
       s_r_ff_7_qn, s_r_ff_8_qn, tkc_carry;
  wire [0:0] subtractor_2_out;
  wire [2:0] subtractor_1_out;
  wire [7:0] tkc_q;
  wire [9:0] hsc_q;

  not not_1 (not_1_out, clk);
  not not_2 (not_2_out, clk);
  not not_3 (not_3_out, not_2_out);
  and and_1 (and_1_out, not_1_out, not_3_out);
  Counter #(.max('h3ff), .width(10)) hsc (
    .count(comparator_10_eq), .Q(hsc_q), .up(1'b1), .clk(and_1_out), .clr(and_8_out));  // open: load, D, carry
  Counter tkc (.count(1'b1), .Q(tkc_q), .carry(tkc_carry), .up(1'b1), .clk(clk), .clr(and_2_out));  // open: load, D
  and and_2 (and_2_out, and_1_out, tkc_carry);
  nor nor_1 (nor_1_out, hsc_q[8], hsc_q[9]);
  Comparator #(.mode("unsigned")) comparator_1 (.a(hsc_q[7:0]), .b(8'h5), .eq(comparator_1_eq));  // open: gt, lt
  Comparator #(.mode("unsigned")) comparator_2 (.a(hsc_q[7:0]), .b(8'h9), .eq(comparator_2_eq));  // open: gt, lt
  Comparator #(.mode("unsigned")) comparator_3 (.a(hsc_q[7:0]), .b(8'h54), .eq(comparator_3_eq));  // open: gt, lt
  Comparator #(.mode("unsigned")) comparator_4 (.a(hsc_q[7:0]), .b(8'h33), .eq(comparator_4_eq));  // open: gt, lt
  Comparator #(.mode("unsigned")) comparator_5 (.a(hsc_q[7:0]), .b(8'h69), .eq(comparator_5_eq));  // open: gt, lt
  Comparator #(.mode("unsigned")) comparator_6 (.a(hsc_q[7:0]), .b(8'h6f), .eq(comparator_6_eq));  // open: gt, lt
  Comparator #(.mode("unsigned")) comparator_7 (.a(tkc_q), .b(8'hf), .eq(comparator_7_eq));  // open: gt, lt
  Comparator #(.mode("unsigned")) comparator_8 (.a(tkc_q), .b(8'h2f), .eq(comparator_8_eq));  // open: gt, lt
  Comparator #(.mode("unsigned")) comparator_9 (.a(tkc_q), .b(8'hf7), .eq(comparator_9_eq));  // open: gt, lt
  Comparator #(.mode("unsigned"), .width(7)) comparator_10 (
    .a(tkc_q[6:0]), .b(7'b1000000), .eq(comparator_10_eq));  // open: gt, lt
  Comparator #(.mode("unsigned"), .width(7)) comparator_11 (
    .a(tkc_q[6:0]), .b(7'b0000111), .lt(comparator_11_lt));  // open: gt, eq
  Comparator #(.mode("unsigned"), .width(7)) comparator_12 (
    .a(tkc_q[6:0]), .b(7'b1101111), .lt(comparator_12_lt));  // open: gt, eq
  Subtractor subtractor_1 (.a(tkc_q), .b(8'h30), .out({vram_addr[4:0], subtractor_1_out}));  // open: bin, bout
  and and_3 (and_3_out, comparator_1_eq, nor_1_out);
  and and_4 (and_4_out, comparator_2_eq, nor_1_out);
  and and_5 (and_5_out, comparator_3_eq, nor_1_out);
  and and_6 (and_6_out, comparator_4_eq, hsc_q[9]);
  and and_7 (and_7_out, comparator_5_eq, hsc_q[9]);
  and and_8 (and_8_out, comparator_6_eq, hsc_q[9]);
  S_R_Flip_Flop s_r_ff_1 (
    .S(and_3_out), .R(and_4_out), .clk(and_1_out), .Q(s_r_ff_1_q), .Qn(s_r_ff_1_qn));  // open: reset, preset
  S_R_Flip_Flop s_r_ff_2 (
    .S(and_4_out), .R(and_5_out), .clk(and_1_out), .Q(s_r_ff_2_q), .Qn(s_r_ff_2_qn));  // open: reset, preset
  S_R_Flip_Flop s_r_ff_3 (
    .S(and_5_out), .R(and_6_out), .clk(and_1_out), .Q(s_r_ff_3_q), .Qn(s_r_ff_3_qn));  // open: reset, preset
  S_R_Flip_Flop s_r_ff_4 (
    .S(and_6_out), .R(and_7_out), .clk(and_1_out), .Q(s_r_ff_4_q), .Qn(s_r_ff_4_qn));  // open: reset, preset
  S_R_Flip_Flop s_r_ff_5 (
    .S(and_7_out), .R(and_8_out), .clk(and_1_out), .Q(s_r_ff_5_q), .reset(and_8_out), .Qn(s_r_ff_5_qn));  // open: preset
  S_R_Flip_Flop s_r_ff_6 (
    .S(comparator_7_eq), .R(comparator_8_eq), .clk(and_1_out), .Qn(s_r_ff_6_qn));  // open: Q, reset, preset
  S_R_Flip_Flop s_r_ff_7 (
    .S(comparator_8_eq), .R(comparator_9_eq), .clk(and_1_out), .Q(s_r_ff_7_q), .Qn(s_r_ff_7_qn));  // open: reset, preset
  S_R_Flip_Flop s_r_ff_8 (
    .S(comparator_9_eq), .R(tkc_carry), .clk(and_1_out), .Qn(s_r_ff_8_qn));  // open: Q, reset, preset
  and and_9 (and_9_out, s_r_ff_1_qn, s_r_ff_2_qn, s_r_ff_3_qn, s_r_ff_4_qn, s_r_ff_5_qn);
  and and_10 (and_10_out, s_r_ff_6_qn, s_r_ff_7_qn, s_r_ff_8_qn);
  or or_1 (or_1_out, s_r_ff_3_q, s_r_ff_4_q, s_r_ff_2_q);
  and and_11 (and_11_out, and_10_out, or_1_out);
  or or_2 (or_2_out, s_r_ff_1_q, s_r_ff_5_q);
  and and_12 (and_12_out, s_r_ff_7_q, s_r_ff_3_q);
  and and_13 (and_13_out, or_2_out, comparator_11_lt);
  and and_14 (and_14_out, and_9_out, comparator_12_lt);
  BitSelector bitselector_1 (.in({8{1'b1}}), .out(bitselector_1_out), .sel(subtractor_1_out));
  Subtractor #(.width(10)) subtractor_2 (
    .a(hsc_q), .b(10'h4a), .out({vram_addr[13:5], subtractor_2_out[0]}));  // open: bin, bout
  and and_15 (v_10, bitselector_1_out, and_12_out);
  nor nor_2 (v_03, and_11_out, and_13_out, and_14_out);

  // Notes on the sheet:
  //   vram_data
  //   n_p_broad
  //   n_p_short
  //   t_back
  //   t_front
  //   t_data
  //   t_sync
  //   s_post
  //   s_empty0
  //   s_data
  //   s_empty1
  //   s_pre
  //   s_eq
endmodule

module video74 (
  input  rise,
  input  clk,
  input  [7:0] vd,
  output v_10,
  output v_03,
  output [12:0] vma
);

  wire EQ_5_pin1, EQ_5_pin3, EQ_5_pin5, EQ_5_pin7, EQ_5_pin9, EQ_5_pin12, EQ_5_pin14, EQ_5_pin16, EQ_5_pin18,
       EQ_6F_pin1, EQ_6F_pin3, EQ_6F_pin5, EQ_6F_pin7, EQ_6F_pin9, EQ_6F_pin12, EQ_6F_pin14, EQ_6F_pin16,
       EQ_6F_pin18, EQ_09_pin1, EQ_09_pin3, EQ_09_pin5, EQ_09_pin7, EQ_09_pin9, EQ_09_pin12, EQ_09_pin14,
       EQ_09_pin16, EQ_09_pin18, EQ_33_pin1, EQ_33_pin3, EQ_33_pin5, EQ_33_pin7, EQ_33_pin9, EQ_33_pin12,
       EQ_33_pin14, EQ_33_pin16, EQ_33_pin18, EQ_54_pin1, EQ_54_pin3, EQ_54_pin5, EQ_54_pin7, EQ_54_pin9,
       EQ_54_pin12, EQ_54_pin14, EQ_54_pin16, EQ_54_pin18, EQ_69_pin1, EQ_69_pin3, EQ_69_pin5, EQ_69_pin7,
       EQ_69_pin9, EQ_69_pin12, EQ_69_pin14, EQ_69_pin16, EQ_69_pin18, hsc0, hsc0Q, hsc1, hsc1Q, hsc2, hsc2Q,
       hsc3, hsc3Q, hsc4, hsc4Q, hsc5, hsc5Q, hsc6, hsc7, hsc8, hsc9, HSC_0_pin3, HSC_0_pin4, HSC_0_pin5,
       HSC_0_pin6, HSC_0_pin7, HSC_0_pin9, HSC_0_pin15, HSC_1_pin1, HSC_1_pin3, HSC_1_pin4, HSC_1_pin5,
       HSC_1_pin6, HSC_1_pin7, HSC_1_pin9, HSC_1_pin15, HSC_2_pin3, HSC_2_pin4, HSC_2_pin5, HSC_2_pin6,
       HSC_2_pin7, HSC_2_pin9, hsc_eORd, hsc_inc, hsc_n1S, hsc_n2S, hsc_n3S, hsc_n4S, hsc_n5S, hsc_n9,
       hsc_nEQ_05, hsc_nEQ_6A, hsc_nEQ_6E, hsc_nEQ_34, hsc_nEQ_54, hsc_nEQ_A, hsc_nR, hsc_or_89, hsc_pp,
       latch_vram, n7402_1_pin1, n7402_1_pin2, n7404_1_pin2, n7404_1_pin6, n7404_2_pin3, n7408_1_pin8,
       n7411_1_pin2, n7411_1_pin13, n7432_2_pin11, n7432_3_pin3, n7432_3_pin6, n7432_3_pin8, n7432_3_pin11,
       n7432_4_pin3, n7432_4_pin6, n74151_1_pin7, n74283_1_pin2, n74283_1_pin6, n74283_1_pin7, n74283_1_pin9,
       n74283_1_pin11, n74283_1_pin15, n74283_2_pin2, n74283_2_pin6, n74283_2_pin9, n74283_2_pin11,
       n74283_2_pin15, n74283_3_pin2, n74283_3_pin6, n74283_3_pin11, n74283_3_pin15, n74573_1_pin1,
       n74682_1_pin3, n74682_1_pin5, n74682_1_pin7, n74682_1_pin9, n74682_1_pin12, n74682_1_pin14,
       n74682_1_pin16, n74682_1_pin17, n74682_1_pin18, n74682_2_pin3, n74682_2_pin5, n74682_2_pin7,
       n74682_2_pin9, n74682_2_pin12, n74682_2_pin14, n74682_2_pin16, n74682_2_pin17, n74682_2_pin18,
       n74688_1_pin1, n74688_1_pin3, n74688_1_pin5, n74688_1_pin7, n74688_1_pin9, n74688_1_pin12,
       n74688_1_pin14, n74688_1_pin16, n74688_1_pin18, n74688_2_pin1, n74688_2_pin3, n74688_2_pin5,
       n74688_2_pin7, n74688_2_pin9, n74688_2_pin12, n74688_2_pin14, n74688_2_pin16, n74688_2_pin18,
       n74688_3_pin1, n74688_3_pin3, n74688_3_pin5, n74688_3_pin7, n74688_3_pin9, n74688_3_pin12,
       n74688_3_pin14, n74688_3_pin16, n74688_3_pin18, n74688_4_pin1, n74688_4_pin3, n74688_4_pin5,
       n74688_4_pin7, n74688_4_pin9, n74688_4_pin12, n74688_4_pin14, n74688_4_pin16, n74688_4_pin18,
       nV03_broad, nV03_short, nV03_sync, tkc0, tkc0Q, tkc1, tkc1Q, tkc2, tkc2Q, tkc3Q, tkc7_LE_6F,
       tkc7_LE_07, TKC_0_pin3, TKC_0_pin4, TKC_0_pin5, TKC_0_pin6, TKC_0_pin7, TKC_0_pin9, TKC_0_pin10,
       TKC_0_pin15, TKC_1_pin3, TKC_1_pin4, TKC_1_pin5, TKC_1_pin6, TKC_1_pin7, TKC_1_pin9, tkc_nEQ_0F,
       tkc_nEQ_0F_2, tkc_nEQ_28, tkc_nEQ_80, tkc_nEQ_F8, tkc_nRC0, tkc_RC0, vbit, vd0_x, vd1_x, vd2_x, vd3_x,
       vd4_x, vd5_x, vd6_x, vd7_x, vma5, vma14;

  _74161 HSC_0 (
    .pin1(hsc_nR), .pin2(clk), .pin3(HSC_0_pin3), .pin4(HSC_0_pin4), .pin5(HSC_0_pin5), .pin6(HSC_0_pin6),
    .pin7(HSC_0_pin7), .pin15(HSC_0_pin15), .pin14(hsc0), .pin13(hsc1), .pin12(hsc2), .pin11(hsc3),
    .pin10(hsc_inc), .pin9(HSC_0_pin9));
  _74161 HSC_1 (
    .pin1(HSC_1_pin1), .pin2(clk), .pin3(HSC_1_pin3), .pin4(HSC_1_pin4), .pin5(HSC_1_pin5),
    .pin6(HSC_1_pin6), .pin7(HSC_1_pin7), .pin15(HSC_1_pin15), .pin14(hsc4), .pin13(hsc5), .pin12(hsc6),
    .pin11(hsc7), .pin10(HSC_0_pin15), .pin9(HSC_1_pin9));
  _74161 HSC_2 (
    .pin1(HSC_1_pin1), .pin2(clk), .pin3(HSC_2_pin3), .pin4(HSC_2_pin4), .pin5(HSC_2_pin5),
    .pin6(HSC_2_pin6), .pin7(HSC_2_pin7), .pin14(hsc8), .pin13(hsc9), .pin10(HSC_1_pin15), .pin9(HSC_2_pin9));  // open: pin15, pin12, pin11
  _74161 TKC_0 (
    .pin1(tkc_nRC0), .pin2(clk), .pin3(TKC_0_pin3), .pin4(TKC_0_pin4), .pin5(TKC_0_pin5), .pin6(TKC_0_pin6),
    .pin7(TKC_0_pin7), .pin15(TKC_0_pin15), .pin14(tkc0), .pin13(tkc1), .pin12(tkc2), .pin11(vma[0]),
    .pin10(TKC_0_pin10), .pin9(TKC_0_pin9));
  _74161 TKC_1 (
    .pin1(tkc_nRC0), .pin2(clk), .pin3(TKC_1_pin3), .pin4(TKC_1_pin4), .pin5(TKC_1_pin5), .pin6(TKC_1_pin6),
    .pin7(TKC_1_pin7), .pin15(tkc_RC0), .pin14(vma[1]), .pin13(vma[2]), .pin12(vma[3]), .pin11(vma[4]),
    .pin10(TKC_0_pin15), .pin9(TKC_1_pin9));
  _7404 #(.ShowInternalStructure("true")) u_7404_1 (
    .pin1(hsc_nR), .pin2(n7404_1_pin2), .pin3(n7404_1_pin2), .pin4(HSC_1_pin1), .pin5(tkc_nEQ_0F),
    .pin6(n7404_1_pin6), .pin13(tkc_RC0), .pin12(tkc_nRC0), .pin11(hsc9), .pin10(hsc_n9),
    .pin9(n7404_1_pin6), .pin8(tkc_nEQ_0F_2));
  _74688 u_74688_1 (
    .pin1(n74688_1_pin1), .pin2(tkc0), .pin3(n74688_1_pin3), .pin4(tkc1), .pin5(n74688_1_pin5), .pin6(tkc2),
    .pin7(n74688_1_pin7), .pin8(vma[0]), .pin9(n74688_1_pin9), .pin19(tkc_nEQ_80), .pin18(n74688_1_pin18),
    .pin17(vma[4]), .pin16(n74688_1_pin16), .pin15(vma[3]), .pin14(n74688_1_pin14), .pin13(vma[2]),
    .pin12(n74688_1_pin12), .pin11(vma[1]));
  _74682 u_74682_1 (
    .pin1(tkc7_LE_07), .pin2(tkc0), .pin3(n74682_1_pin3), .pin4(tkc1), .pin5(n74682_1_pin5), .pin6(tkc2),
    .pin7(n74682_1_pin7), .pin8(vma[0]), .pin9(n74682_1_pin9), .pin18(n74682_1_pin18),
    .pin17(n74682_1_pin17), .pin16(n74682_1_pin16), .pin15(vma[3]), .pin14(n74682_1_pin14), .pin13(vma[2]),
    .pin12(n74682_1_pin12), .pin11(vma[1]));  // open: pin19
  _74682 u_74682_2 (
    .pin1(tkc7_LE_6F), .pin2(tkc0), .pin3(n74682_2_pin3), .pin4(tkc1), .pin5(n74682_2_pin5), .pin6(tkc2),
    .pin7(n74682_2_pin7), .pin8(vma[0]), .pin9(n74682_2_pin9), .pin18(n74682_2_pin18),
    .pin17(n74682_2_pin17), .pin16(n74682_2_pin16), .pin15(vma[3]), .pin14(n74682_2_pin14), .pin13(vma[2]),
    .pin12(n74682_2_pin12), .pin11(vma[1]));  // open: pin19
  _74688 u_74688_2 (
    .pin1(n74688_2_pin1), .pin2(tkc0), .pin3(n74688_2_pin3), .pin4(tkc1), .pin5(n74688_2_pin5), .pin6(tkc2),
    .pin7(n74688_2_pin7), .pin8(vma[0]), .pin9(n74688_2_pin9), .pin19(tkc_nEQ_0F), .pin18(n74688_2_pin18),
    .pin17(vma[4]), .pin16(n74688_2_pin16), .pin15(vma[3]), .pin14(n74688_2_pin14), .pin13(vma[2]),
    .pin12(n74688_2_pin12), .pin11(vma[1]));
  _74688 u_74688_3 (
    .pin1(n74688_3_pin1), .pin2(tkc0), .pin3(n74688_3_pin3), .pin4(tkc1), .pin5(n74688_3_pin5), .pin6(tkc2),
    .pin7(n74688_3_pin7), .pin8(vma[0]), .pin9(n74688_3_pin9), .pin19(tkc_nEQ_28), .pin18(n74688_3_pin18),
    .pin17(vma[4]), .pin16(n74688_3_pin16), .pin15(vma[3]), .pin14(n74688_3_pin14), .pin13(vma[2]),
    .pin12(n74688_3_pin12), .pin11(vma[1]));
  _74688 u_74688_4 (
    .pin1(n74688_4_pin1), .pin2(tkc0), .pin3(n74688_4_pin3), .pin4(tkc1), .pin5(n74688_4_pin5), .pin6(tkc2),
    .pin7(n74688_4_pin7), .pin8(vma[0]), .pin9(n74688_4_pin9), .pin19(tkc_nEQ_F8), .pin18(n74688_4_pin18),
    .pin17(vma[4]), .pin16(n74688_4_pin16), .pin15(vma[3]), .pin14(n74688_4_pin14), .pin13(vma[2]),
    .pin12(n74688_4_pin12), .pin11(vma[1]));
  _74688 EQ_5 (
    .pin1(EQ_5_pin1), .pin2(hsc0), .pin3(EQ_5_pin3), .pin4(hsc1), .pin5(EQ_5_pin5), .pin6(hsc2),
    .pin7(EQ_5_pin7), .pin8(hsc3), .pin9(EQ_5_pin9), .pin19(hsc_nEQ_05), .pin18(EQ_5_pin18), .pin17(hsc7),
    .pin16(EQ_5_pin16), .pin15(hsc6), .pin14(EQ_5_pin14), .pin13(hsc5), .pin12(EQ_5_pin12), .pin11(hsc4));
  _74688 EQ_09 (
    .pin1(EQ_09_pin1), .pin2(hsc0), .pin3(EQ_09_pin3), .pin4(hsc1), .pin5(EQ_09_pin5), .pin6(hsc2),
    .pin7(EQ_09_pin7), .pin8(hsc3), .pin9(EQ_09_pin9), .pin19(hsc_nEQ_A), .pin18(EQ_09_pin18), .pin17(hsc7),
    .pin16(EQ_09_pin16), .pin15(hsc6), .pin14(EQ_09_pin14), .pin13(hsc5), .pin12(EQ_09_pin12), .pin11(hsc4));
  _74688 EQ_54 (
    .pin1(EQ_54_pin1), .pin2(hsc0), .pin3(EQ_54_pin3), .pin4(hsc1), .pin5(EQ_54_pin5), .pin6(hsc2),
    .pin7(EQ_54_pin7), .pin8(hsc3), .pin9(EQ_54_pin9), .pin19(hsc_nEQ_54), .pin18(EQ_54_pin18), .pin17(hsc7),
    .pin16(EQ_54_pin16), .pin15(hsc6), .pin14(EQ_54_pin14), .pin13(hsc5), .pin12(EQ_54_pin12), .pin11(hsc4));
  _74688 EQ_33 (
    .pin1(EQ_33_pin1), .pin2(hsc0), .pin3(EQ_33_pin3), .pin4(hsc1), .pin5(EQ_33_pin5), .pin6(hsc2),
    .pin7(EQ_33_pin7), .pin8(hsc3), .pin9(EQ_33_pin9), .pin19(hsc_nEQ_34), .pin18(EQ_33_pin18), .pin17(hsc7),
    .pin16(EQ_33_pin16), .pin15(hsc6), .pin14(EQ_33_pin14), .pin13(hsc5), .pin12(EQ_33_pin12), .pin11(hsc4));
  _74688 EQ_69 (
    .pin1(EQ_69_pin1), .pin2(hsc0), .pin3(EQ_69_pin3), .pin4(hsc1), .pin5(EQ_69_pin5), .pin6(hsc2),
    .pin7(EQ_69_pin7), .pin8(hsc3), .pin9(EQ_69_pin9), .pin19(hsc_nEQ_6A), .pin18(EQ_69_pin18), .pin17(hsc7),
    .pin16(EQ_69_pin16), .pin15(hsc6), .pin14(EQ_69_pin14), .pin13(hsc5), .pin12(EQ_69_pin12), .pin11(hsc4));
  _74688 EQ_6F (
    .pin1(EQ_6F_pin1), .pin2(hsc0), .pin3(EQ_6F_pin3), .pin4(hsc1), .pin5(EQ_6F_pin5), .pin6(hsc2),
    .pin7(EQ_6F_pin7), .pin8(hsc3), .pin9(EQ_6F_pin9), .pin19(hsc_nEQ_6E), .pin18(EQ_6F_pin18), .pin17(hsc7),
    .pin16(EQ_6F_pin16), .pin15(hsc6), .pin14(EQ_6F_pin14), .pin13(hsc5), .pin12(EQ_6F_pin12), .pin11(hsc4));
  _74283 #(.ShowInternalStructure("true")) u_74283_1 (
    .pin1(vma[5]), .pin2(n74283_1_pin2), .pin3(hsc1), .pin4(vma5), .pin5(hsc0), .pin6(n74283_1_pin6),
    .pin7(n74283_1_pin7), .pin15(n74283_1_pin15), .pin14(hsc2), .pin13(vma[6]), .pin12(hsc3),
    .pin11(n74283_1_pin11), .pin10(vma[7]), .pin9(n74283_1_pin9));
  _74283 #(.ShowInternalStructure("true")) u_74283_2 (
    .pin1(vma[9]), .pin2(n74283_2_pin2), .pin3(hsc5), .pin4(vma[8]), .pin5(hsc4), .pin6(n74283_2_pin6),
    .pin7(n74283_1_pin9), .pin15(n74283_2_pin15), .pin14(hsc6), .pin13(vma[10]), .pin12(hsc7),
    .pin11(n74283_2_pin11), .pin10(vma[11]), .pin9(n74283_2_pin9));
  _74283 #(.ShowInternalStructure("true")) u_74283_3 (
    .pin1(vma14), .pin2(n74283_3_pin2), .pin3(hsc9), .pin4(vma[12]), .pin5(hsc8), .pin6(n74283_3_pin6),
    .pin7(n74283_2_pin9), .pin15(n74283_3_pin15), .pin11(n74283_3_pin11));  // open: pin14, pin13, pin12, pin10, pin9
  _7432 #(.ShowInternalStructure("true")) u_7432_1 (
    .pin1(hsc_or_89), .pin2(hsc_nEQ_05), .pin3(hsc_n1S), .pin4(hsc_or_89), .pin5(hsc_nEQ_A), .pin6(hsc_n2S),
    .pin13(hsc_nEQ_34), .pin12(hsc_n9), .pin11(hsc_n4S), .pin10(hsc_nEQ_54), .pin9(hsc_or_89), .pin8(hsc_n3S));
  _7432 #(.ShowInternalStructure("true")) u_7432_2 (
    .pin1(hsc_n9), .pin2(hsc_nEQ_6A), .pin3(hsc_n5S), .pin4(hsc_n9), .pin5(hsc_nEQ_6E), .pin6(hsc_nR),
    .pin13(hsc2Q), .pin12(hsc3Q), .pin11(n7432_2_pin11), .pin10(n7432_2_pin11), .pin9(hsc4Q), .pin8(hsc_eORd));
  _74279 #(.ShowInternalStructure("true")) u_74279_1 (
    .pin1(hsc_n2S), .pin2(hsc_n1S), .pin3(hsc_n1S), .pin4(hsc1Q), .pin5(hsc_n3S), .pin6(hsc_n2S),
    .pin7(hsc2Q), .pin15(hsc_n4S), .pin14(hsc_n5S), .pin13(hsc4Q), .pin12(hsc_n3S), .pin11(hsc_n3S),
    .pin10(hsc_n4S), .pin9(hsc3Q));
  _74279 #(.ShowInternalStructure("true")) u_74279_2 (
    .pin1(hsc_nR), .pin2(hsc_n5S), .pin3(hsc_n5S), .pin4(hsc5Q), .pin5(tkc_nEQ_28), .pin6(tkc_nEQ_0F),
    .pin7(tkc1Q), .pin15(tkc_nEQ_F8), .pin14(tkc_nRC0), .pin13(tkc3Q), .pin12(tkc_nEQ_28),
    .pin11(tkc_nEQ_28), .pin10(tkc_nEQ_F8), .pin9(tkc2Q));
  _74151 u_74151_1 (
    .pin1(vd3_x), .pin2(vd2_x), .pin3(vd1_x), .pin4(vd0_x), .pin5(vbit), .pin7(n74151_1_pin7), .pin15(vd4_x),
    .pin14(vd5_x), .pin13(vd6_x), .pin12(vd7_x), .pin11(tkc0), .pin10(tkc1), .pin9(tkc2));  // open: pin6
  _74573 u_74573_1 (
    .pin1(n74573_1_pin1), .pin2(vd[0]), .pin3(vd[1]), .pin4(vd[2]), .pin5(vd[3]), .pin6(vd[4]), .pin7(vd[5]),
    .pin8(vd[6]), .pin9(vd[7]), .pin19(vd0_x), .pin18(vd1_x), .pin17(vd2_x), .pin16(vd3_x), .pin15(vd4_x),
    .pin14(vd5_x), .pin13(vd6_x), .pin12(vd7_x), .pin11(latch_vram));
  _7432 #(.ShowInternalStructure("true")) u_7432_3 (
    .pin1(hsc1Q), .pin2(hsc2Q), .pin3(n7432_3_pin3), .pin4(n7432_3_pin3), .pin5(hsc3Q), .pin6(n7432_3_pin6),
    .pin13(tkc1Q), .pin12(tkc2Q), .pin11(n7432_3_pin11), .pin10(n7432_3_pin11), .pin9(tkc3Q),
    .pin8(n7432_3_pin8));
  _7432 #(.ShowInternalStructure("true")) u_7432_4 (
    .pin1(n7432_3_pin6), .pin2(hsc4Q), .pin3(n7432_4_pin3), .pin4(n7432_4_pin3), .pin5(hsc5Q),
    .pin6(n7432_4_pin6), .pin13(hsc8), .pin12(hsc9), .pin11(hsc_or_89), .pin10(hsc1Q), .pin9(hsc5Q),
    .pin8(hsc_pp));
  _7404 #(.ShowInternalStructure("true")) u_7404_2 (
    .pin1(n7432_4_pin6), .pin2(hsc0Q), .pin3(n7404_2_pin3), .pin4(hsc_inc), .pin13(n7432_3_pin8),
    .pin12(tkc0Q));  // open: pin5, pin6, pin11, pin10, pin9, pin8
  _7408 #(.ShowInternalStructure("true")) u_7408_1 (
    .pin1(tkc0Q), .pin2(hsc_eORd), .pin3(nV03_sync), .pin4(hsc_pp), .pin5(tkc7_LE_07), .pin6(nV03_broad),
    .pin13(hsc0Q), .pin12(tkc7_LE_6F), .pin11(nV03_short), .pin10(hsc3Q), .pin9(tkc2Q), .pin8(n7408_1_pin8));
  _7408 #(.ShowInternalStructure("true")) u_7408_2 (
    .pin1(n7408_1_pin8), .pin2(vbit), .pin3(v_10), .pin4(tkc_nEQ_80), .pin5(tkc_nRC0), .pin6(n7404_2_pin3));  // open: pin13, pin12, pin11, pin10, pin9, pin8
  _7402 #(.ShowInternalStructure("true")) u_7402_1 (
    .pin1(n7402_1_pin1), .pin2(n7402_1_pin2), .pin3(n7402_1_pin2), .pin4(n7402_1_pin2), .pin5(nV03_broad),
    .pin6(nV03_short), .pin13(v_03), .pin12(n7402_1_pin1), .pin11(nV03_sync));  // open: pin10, pin9, pin8
  _7411 #(.ShowInternalStructure("true")) u_7411_1 (
    .pin1(rise), .pin2(n7411_1_pin2), .pin3(tkc0), .pin4(tkc1), .pin5(tkc2), .pin6(n7411_1_pin2),
    .pin13(n7411_1_pin13), .pin12(latch_vram));  // open: pin11, pin10, pin9, pin8
  // also tied to GND on the sheet: {HSC_0_pin3, HSC_0_pin4, HSC_0_pin5, HSC_0_pin6, HSC_1_pin3, HSC_1_pin4, HSC_1_pin5, HSC_1_pin6, HSC_2_pin3, HSC_2_pin4, HSC_2_pin5, HSC_2_pin6, TKC_0_pin3, TKC_0_pin4, TKC_0_pin5, TKC_0_pin6, TKC_1_pin3, TKC_1_pin4, TKC_1_pin5, TKC_1_pin6, n74688_1_pin1, n74688_1_pin3, n74688_1_pin5, n74688_1_pin7, n74688_1_pin9, n74682_1_pin9, n74688_2_pin1, n74688_3_pin1, n74688_4_pin1, n74688_4_pin3, n74688_4_pin5, n74688_4_pin7, n74688_1_pin16, n74688_1_pin14, n74688_1_pin12, n74682_1_pin18, n74682_1_pin17, n74682_1_pin16, n74682_1_pin14, n74682_1_pin12, n74682_2_pin18, n74682_2_pin17, n74682_2_pin12, n74688_2_pin18, n74688_2_pin16, n74688_2_pin14, n74688_2_pin12, n74688_3_pin18, n74688_3_pin16, n74688_3_pin12, EQ_5_pin1, EQ_5_pin3, EQ_5_pin5, EQ_5_pin9, EQ_09_pin1, EQ_09_pin3, EQ_09_pin7, EQ_54_pin1, EQ_54_pin3, EQ_54_pin5, EQ_54_pin9, EQ_33_pin1, EQ_33_pin7, EQ_33_pin9, EQ_69_pin1, EQ_69_pin3, EQ_69_pin7, EQ_6F_pin1, n74283_1_pin2, n74283_1_pin6, n74283_1_pin7, n74283_2_pin6, EQ_5_pin18, EQ_5_pin16, EQ_5_pin14, EQ_5_pin12, EQ_09_pin18, EQ_09_pin16, EQ_09_pin14, EQ_09_pin12, EQ_54_pin18, EQ_54_pin14, EQ_33_pin18, EQ_33_pin16, EQ_69_pin18, EQ_69_pin12, EQ_6F_pin18, EQ_6F_pin12, n74283_2_pin15, n74283_3_pin15, n74283_3_pin11, n74151_1_pin7, n74573_1_pin1}
  // also tied to VCC on the sheet: {HSC_0_pin7, HSC_1_pin7, HSC_2_pin7, TKC_0_pin7, TKC_1_pin7, n74682_1_pin3, n74682_1_pin5, n74682_1_pin7, n74682_2_pin3, n74682_2_pin5, n74682_2_pin7, n74682_2_pin9, n74688_2_pin3, n74688_2_pin5, n74688_2_pin7, n74688_2_pin9, n74688_3_pin3, n74688_3_pin5, n74688_3_pin7, n74688_3_pin9, n74688_4_pin9, HSC_0_pin9, HSC_1_pin9, HSC_2_pin9, TKC_0_pin10, TKC_0_pin9, TKC_1_pin9, n74688_1_pin18, n74682_2_pin16, n74682_2_pin14, n74688_3_pin14, n74688_4_pin18, n74688_4_pin16, n74688_4_pin14, n74688_4_pin12, EQ_5_pin7, EQ_09_pin5, EQ_09_pin9, EQ_54_pin7, EQ_33_pin3, EQ_33_pin5, EQ_69_pin5, EQ_69_pin9, EQ_6F_pin3, EQ_6F_pin5, EQ_6F_pin7, EQ_6F_pin9, n74283_2_pin2, n74283_3_pin2, n74283_3_pin6, EQ_54_pin16, EQ_54_pin12, EQ_33_pin14, EQ_33_pin12, EQ_69_pin16, EQ_69_pin14, EQ_6F_pin16, EQ_6F_pin14, n74283_1_pin15, n74283_1_pin11, n74283_2_pin11, n7411_1_pin13}

  // Other names for the same wires on the sheet: tkc3 = vma[0]; tkc4 = vma[1]; tkc5 = vma[2]; tkc6 = vma[3];
  //   tkc7 = vma[4]; vma6 = vma[5]; vma7 = vma[6]; vma8 = vma[7]; vma9 = vma[8]; vma10 = vma[9]; vma11 = vma[10];
  //   vma12 = vma[11]; vma13 = vma[12]
endmodule

module alu74 (
  input  [2:0] op,
  input  seq_load,
  input  seq_unused,
  input  ldx,
  input  ldy,
  input  ealu,
  input  ldf,
  input  [7:0] din,
  input  [7:0] fin,
  output [7:0] dout
);

  wire a0, a1, a2, a3, a4, a5, a6, a7, b0, b1, b2, b3, b4, b5, b6, b7, b_in, b_out, c_in, c_out, n0, n1, n2,
       n3, n4, n5, n6, n7, n7485_1_pin2, n7485_1_pin3, n7485_1_pin4, n7485_1_pin5, n7485_1_pin6,
       n7485_1_pin7, n74138_1_pin4, n74138_1_pin5, n74244_5_pin11, n74244_5_pin13, n74244_5_pin15,
       n74244_5_pin17, n74283_1_pin9, n74283_3_pin9, n74374_1_pin1, n74374_2_pin1, nb_out, nE_adc, nE_add,
       nE_add_adc, nE_and, nE_cmp, nE_nor, nE_or, nE_pass, nE_sub, nLDF, ny0, ny1, ny2, ny3, ny4, ny5, ny6,
       ny7, o0, o1, o2, o3, o4, o5, o6, o7, s0, s1, s2, s3, s4, s5, s6, s7, x0, x1, x2, x3, x4, x5, x6, x7,
       xc, XeqY, XltY, y0, y1, y2, y3, y4, y5, y6, y7, yc;

  _74374 u_74374_1 (
    .pin1(n74374_1_pin1), .pin2(x0), .pin3(din[0]), .pin4(din[1]), .pin5(x1), .pin6(x2), .pin7(din[2]),
    .pin8(din[3]), .pin9(x3), .pin19(x7), .pin18(din[7]), .pin17(din[6]), .pin16(x6), .pin15(x5),
    .pin14(din[5]), .pin13(din[4]), .pin12(x4), .pin11(xc));
  _74374 u_74374_2 (
    .pin1(n74374_2_pin1), .pin2(y0), .pin3(din[0]), .pin4(din[1]), .pin5(y1), .pin6(y2), .pin7(din[2]),
    .pin8(din[3]), .pin9(y3), .pin19(y7), .pin18(din[7]), .pin17(din[6]), .pin16(y6), .pin15(y5),
    .pin14(din[5]), .pin13(din[4]), .pin12(y4), .pin11(yc));
  _7408 #(.ShowInternalStructure("true")) u_7408_1 (
    .pin1(op[1]), .pin2(fin[2]), .pin3(c_in), .pin4(nE_adc), .pin5(nE_add), .pin6(nE_add_adc), .pin13(ldx),
    .pin12(seq_load), .pin11(xc), .pin10(ldy), .pin9(seq_load), .pin8(yc));
  _7404 #(.ShowInternalStructure("true")) u_7404_1 (
    .pin1(y0), .pin2(ny0), .pin3(y1), .pin4(ny1), .pin5(y2), .pin6(ny2), .pin13(y5), .pin12(ny5), .pin11(y4),
    .pin10(ny4), .pin9(y3), .pin8(ny3));
  _7404 #(.ShowInternalStructure("true")) u_7404_2 (
    .pin1(y6), .pin2(ny6), .pin3(y7), .pin4(ny7), .pin5(ldf), .pin6(nLDF), .pin13(fin[3]), .pin12(b_in),
    .pin11(nb_out), .pin10(b_out));  // open: pin9, pin8
  _74244 u_74244_1 (
    .pin1(nE_pass), .pin2(x0), .pin3(dout[4]), .pin4(x1), .pin5(dout[5]), .pin6(x2), .pin7(dout[6]),
    .pin8(x3), .pin9(dout[7]), .pin19(nE_pass), .pin18(dout[0]), .pin17(x4), .pin16(dout[1]), .pin15(x5),
    .pin14(dout[2]), .pin13(x6), .pin12(dout[3]), .pin11(x7));
  _74283 #(.ShowInternalStructure("true")) u_74283_1 (
    .pin1(s1), .pin2(y1), .pin3(x1), .pin4(s0), .pin5(x0), .pin6(y0), .pin7(c_in), .pin15(y2), .pin14(x2),
    .pin13(s2), .pin12(x3), .pin11(y3), .pin10(s3), .pin9(n74283_1_pin9));
  _74283 #(.ShowInternalStructure("true")) u_74283_2 (
    .pin1(s5), .pin2(y5), .pin3(x5), .pin4(s4), .pin5(x4), .pin6(y4), .pin7(n74283_1_pin9), .pin15(y6),
    .pin14(x6), .pin13(s6), .pin12(x7), .pin11(y7), .pin10(s7), .pin9(c_out));
  _74283 #(.ShowInternalStructure("true")) u_74283_3 (
    .pin1(b1), .pin2(ny1), .pin3(x1), .pin4(b0), .pin5(x0), .pin6(ny0), .pin7(b_in), .pin15(ny2), .pin14(x2),
    .pin13(b2), .pin12(x3), .pin11(ny3), .pin10(b3), .pin9(n74283_3_pin9));
  _74283 #(.ShowInternalStructure("true")) u_74283_4 (
    .pin1(b5), .pin2(ny5), .pin3(x5), .pin4(b4), .pin5(x4), .pin6(ny4), .pin7(n74283_3_pin9), .pin15(ny6),
    .pin14(x6), .pin13(b6), .pin12(x7), .pin11(ny7), .pin10(b7), .pin9(nb_out));
  _74138 u_74138_1 (
    .pin1(op[0]), .pin2(op[1]), .pin3(op[2]), .pin4(n74138_1_pin4), .pin5(n74138_1_pin5), .pin6(ealu),
    .pin7(nE_sub), .pin15(nE_pass), .pin14(nE_add), .pin13(nE_adc), .pin12(nE_and), .pin11(nE_or),
    .pin10(nE_nor), .pin9(nE_cmp));
  _74244 u_74244_2 (
    .pin1(nE_add_adc), .pin2(s0), .pin3(dout[4]), .pin4(s1), .pin5(dout[5]), .pin6(s2), .pin7(dout[6]),
    .pin8(s3), .pin9(dout[7]), .pin19(nE_add_adc), .pin18(dout[0]), .pin17(s4), .pin16(dout[1]), .pin15(s5),
    .pin14(dout[2]), .pin13(s6), .pin12(dout[3]), .pin11(s7));
  _74244 u_74244_3 (
    .pin1(nE_sub), .pin2(b0), .pin3(dout[4]), .pin4(b1), .pin5(dout[5]), .pin6(b2), .pin7(dout[6]),
    .pin8(b3), .pin9(dout[7]), .pin19(nE_sub), .pin18(dout[0]), .pin17(b4), .pin16(dout[1]), .pin15(b5),
    .pin14(dout[2]), .pin13(b6), .pin12(dout[3]), .pin11(b7));
  _7485 #(.ShowInternalStructure("true")) u_7485_1 (
    .pin1(y3), .pin2(n7485_1_pin2), .pin3(n7485_1_pin3), .pin4(n7485_1_pin4), .pin5(n7485_1_pin5),
    .pin6(n7485_1_pin6), .pin7(n7485_1_pin7), .pin15(x3), .pin14(y2), .pin13(x2), .pin12(x1), .pin11(y1),
    .pin10(x0), .pin9(y0));
  _7408 #(.ShowInternalStructure("true")) u_7408_2 (
    .pin1(x0), .pin2(y0), .pin3(a0), .pin4(x1), .pin5(y1), .pin6(a1), .pin13(x3), .pin12(y3), .pin11(a3),
    .pin10(x2), .pin9(y2), .pin8(a2));
  _74244 u_74244_4 (
    .pin1(nE_and), .pin2(a0), .pin3(dout[4]), .pin4(a1), .pin5(dout[5]), .pin6(a2), .pin7(dout[6]),
    .pin8(a3), .pin9(dout[7]), .pin19(nE_and), .pin18(dout[0]), .pin17(a4), .pin16(dout[1]), .pin15(a5),
    .pin14(dout[2]), .pin13(a6), .pin12(dout[3]), .pin11(a7));
  _74244 u_74244_5 (
    .pin1(nLDF), .pin2(XltY), .pin3(dout[4]), .pin4(XeqY), .pin5(dout[5]), .pin6(c_out), .pin7(dout[6]),
    .pin8(b_out), .pin9(dout[7]), .pin19(nLDF), .pin18(dout[0]), .pin17(n74244_5_pin17), .pin16(dout[1]),
    .pin15(n74244_5_pin15), .pin14(dout[2]), .pin13(n74244_5_pin13), .pin12(dout[3]), .pin11(n74244_5_pin11));
  _7485 #(.ShowInternalStructure("true")) u_7485_2 (
    .pin1(y7), .pin2(n7485_1_pin7), .pin3(n7485_1_pin6), .pin4(n7485_1_pin5), .pin6(XeqY), .pin7(XltY),
    .pin15(x7), .pin14(y6), .pin13(x6), .pin12(x5), .pin11(y5), .pin10(x4), .pin9(y4));  // open: pin5
  _7408 #(.ShowInternalStructure("true")) u_7408_3 (
    .pin1(x4), .pin2(y4), .pin3(a4), .pin4(x5), .pin5(y5), .pin6(a5), .pin13(x7), .pin12(y7), .pin11(a7),
    .pin10(x6), .pin9(y6), .pin8(a6));
  _7432 #(.ShowInternalStructure("true")) u_7432_1 (
    .pin1(x0), .pin2(y0), .pin3(o0), .pin4(x1), .pin5(y1), .pin6(o1), .pin13(x3), .pin12(y3), .pin11(o3),
    .pin10(x2), .pin9(y2), .pin8(o2));
  _7432 #(.ShowInternalStructure("true")) u_7432_2 (
    .pin1(x4), .pin2(y4), .pin3(o4), .pin4(x5), .pin5(y5), .pin6(o5), .pin13(x7), .pin12(y7), .pin11(o7),
    .pin10(x6), .pin9(y6), .pin8(o6));
  _74244 u_74244_6 (
    .pin1(nE_or), .pin2(a0), .pin3(dout[4]), .pin4(o1), .pin5(dout[5]), .pin6(o2), .pin7(dout[6]), .pin8(o3),
    .pin9(dout[7]), .pin19(nE_or), .pin18(dout[0]), .pin17(o4), .pin16(dout[1]), .pin15(o5), .pin14(dout[2]),
    .pin13(o6), .pin12(dout[3]), .pin11(o7));
  _7404 #(.ShowInternalStructure("true")) u_7404_3 (
    .pin1(o0), .pin2(n0), .pin3(o1), .pin4(n1), .pin5(o2), .pin6(n2), .pin13(o5), .pin12(n5), .pin11(o4),
    .pin10(n4), .pin9(o3), .pin8(n3));
  _7404 #(.ShowInternalStructure("true")) u_7404_4 (
    .pin1(o6), .pin2(n6), .pin3(o7), .pin4(n7));  // open: pin5, pin6, pin13, pin12, pin11, pin10, pin9, pin8
  _74244 u_74244_7 (
    .pin1(nE_nor), .pin2(a0), .pin3(dout[4]), .pin4(n1), .pin5(dout[5]), .pin6(n2), .pin7(dout[6]),
    .pin8(n3), .pin9(dout[7]), .pin19(nE_nor), .pin18(dout[0]), .pin17(n4), .pin16(dout[1]), .pin15(n5),
    .pin14(dout[2]), .pin13(n6), .pin12(dout[3]), .pin11(n7));
  // also tied to GND on the sheet: {n74374_1_pin1, n74374_2_pin1, n74138_1_pin4, n74138_1_pin5, n7485_1_pin2, n7485_1_pin4, n74244_5_pin17, n74244_5_pin15, n74244_5_pin13, n74244_5_pin11}
  // also tied to VCC on the sheet: n7485_1_pin3

  // Other names for the same wires on the sheet: d0 = din[0]; d1 = din[1]; d2 = din[2]; d3 = din[3]; d4 = din[4];
  //   d5 = din[5]; d6 = din[6]; d7 = din[7]; z0 = dout[0]; z1 = dout[1]; z2 = dout[2]; z3 = dout[3]; z4 = dout[4];
  //   z5 = dout[5]; z6 = dout[6]; z7 = dout[7]; fl = fin[0]; fe = fin[1]; fc = fin[2]; fb = fin[3]; f4 = fin[4];
  //   f5 = fin[5]; f6 = fin[6]; f7 = fin[7]
endmodule

module regs74 (
  input  lreg,
  input  ereg,
  input  sel,
  input  ldh,
  input  ldl,
  input  ldf,
  input  [2:0] sel0,
  input  [2:0] sel1,
  input  [7:0] din,
  input  seq_unuse,
  input  n_seq_load,
  output [7:0] dout,
  output [7:0] lout,
  output [7:0] hout,
  output [7:0] fout
);

  wire a, a_en, a_we, b, b_en, b_we, c, c_en, c_we, d_en, d_we, f_en, f_pin1, f_we, h_en, h_pin1, h_we, l_en,
       l_pin1, l_we, lpreset, n7432_1_pin3, n7432_1_pin6, n7432_1_pin11, n7432_2_pin3, n7432_2_pin11,
       n74138_1_pin4, n74138_1_pin5, n74238_1_pin4, n74573_1_pin11, n74573_2_pin11, n74573_3_pin11, nlpreset,
       nsel, sel0_t, sel00x, sel1_t, sel01x, sel02x, sel10x, sel11x, sel12x, we, z_en, z_we;

  _7408 #(.ShowInternalStructure("true")) u_7408_1 (
    .pin1(sel0_t), .pin2(sel0[1]), .pin3(sel01x), .pin4(sel0_t), .pin5(sel0[0]), .pin6(sel00x),
    .pin13(sel0_t), .pin12(sel0[2]), .pin11(sel02x), .pin10(sel1_t), .pin9(sel1[0]), .pin8(sel10x));
  _7408 #(.ShowInternalStructure("true")) u_7408_2 (
    .pin1(sel1_t), .pin2(sel1[1]), .pin3(sel11x), .pin4(sel1_t), .pin5(sel1[2]), .pin6(sel12x), .pin13(nsel),
    .pin12(nlpreset), .pin11(sel0_t), .pin10(sel), .pin9(nlpreset), .pin8(sel1_t));
  _7432 #(.ShowInternalStructure("true")) u_7432_1 (
    .pin1(sel00x), .pin2(sel10x), .pin3(n7432_1_pin3), .pin4(sel02x), .pin5(sel12x), .pin6(n7432_1_pin6),
    .pin13(sel01x), .pin12(sel11x), .pin11(n7432_1_pin11), .pin10(n7432_1_pin11), .pin9(ldf), .pin8(b));
  _7432 #(.ShowInternalStructure("true")) u_7432_2 (
    .pin1(n7432_1_pin3), .pin2(ldh), .pin3(n7432_2_pin3), .pin4(n7432_2_pin3), .pin5(ldf), .pin6(a),
    .pin13(ldh), .pin12(ldl), .pin11(n7432_2_pin11), .pin10(n7432_2_pin11), .pin9(ldf), .pin8(lpreset));
  _7432 #(.ShowInternalStructure("true")) u_7432_3 (
    .pin1(n7432_1_pin6), .pin2(lpreset), .pin3(c), .pin13(lpreset), .pin12(lreg), .pin11(we));  // open: pin4, pin5, pin6, pin10, pin9, pin8
  _7404 #(.ShowInternalStructure("true")) u_7404_1 (
    .pin11(sel), .pin10(nsel), .pin9(lpreset), .pin8(nlpreset));  // open: pin1, pin2, pin3, pin4, pin5, pin6, pin13, pin12
  _74573 #(.ShowInternalStructure("true")) u_a (
    .pin1(a_en), .pin2(din[0]), .pin3(din[1]), .pin4(din[2]), .pin5(din[3]), .pin6(din[4]), .pin7(din[5]),
    .pin8(din[6]), .pin9(din[7]), .pin19(dout[0]), .pin18(dout[1]), .pin17(dout[2]), .pin16(dout[3]),
    .pin15(dout[4]), .pin14(dout[5]), .pin13(dout[6]), .pin12(dout[7]), .pin11(a_we));
  _74573 u_b (
    .pin1(b_en), .pin2(din[0]), .pin3(din[1]), .pin4(din[2]), .pin5(din[3]), .pin6(din[4]), .pin7(din[5]),
    .pin8(din[6]), .pin9(din[7]), .pin19(dout[0]), .pin18(dout[1]), .pin17(dout[2]), .pin16(dout[3]),
    .pin15(dout[4]), .pin14(dout[5]), .pin13(dout[6]), .pin12(dout[7]), .pin11(b_we));
  _74573 u_c (
    .pin1(c_en), .pin2(din[0]), .pin3(din[1]), .pin4(din[2]), .pin5(din[3]), .pin6(din[4]), .pin7(din[5]),
    .pin8(din[6]), .pin9(din[7]), .pin19(dout[0]), .pin18(dout[1]), .pin17(dout[2]), .pin16(dout[3]),
    .pin15(dout[4]), .pin14(dout[5]), .pin13(dout[6]), .pin12(dout[7]), .pin11(c_we));
  _74573 d (
    .pin1(d_en), .pin2(din[0]), .pin3(din[1]), .pin4(din[2]), .pin5(din[3]), .pin6(din[4]), .pin7(din[5]),
    .pin8(din[6]), .pin9(din[7]), .pin19(dout[0]), .pin18(dout[1]), .pin17(dout[2]), .pin16(dout[3]),
    .pin15(dout[4]), .pin14(dout[5]), .pin13(dout[6]), .pin12(dout[7]), .pin11(d_we));
  _74238 #(.ShowInternalStructure("true")) u_74238_1 (
    .pin1(a), .pin2(b), .pin3(c), .pin4(n74238_1_pin4), .pin5(n_seq_load), .pin6(we), .pin7(f_we),
    .pin15(a_we), .pin14(b_we), .pin13(c_we), .pin12(d_we), .pin11(l_we), .pin10(h_we), .pin9(z_we));
  _74573 l (
    .pin1(l_pin1), .pin2(din[0]), .pin3(din[1]), .pin4(din[2]), .pin5(din[3]), .pin6(din[4]), .pin7(din[5]),
    .pin8(din[6]), .pin9(din[7]), .pin19(lout[0]), .pin18(lout[1]), .pin17(lout[2]), .pin16(lout[3]),
    .pin15(lout[4]), .pin14(lout[5]), .pin13(lout[6]), .pin12(lout[7]), .pin11(l_we));
  _74573 h (
    .pin1(h_pin1), .pin2(din[0]), .pin3(din[1]), .pin4(din[2]), .pin5(din[3]), .pin6(din[4]), .pin7(din[5]),
    .pin8(din[6]), .pin9(din[7]), .pin19(hout[0]), .pin18(hout[1]), .pin17(hout[2]), .pin16(hout[3]),
    .pin15(hout[4]), .pin14(hout[5]), .pin13(hout[6]), .pin12(hout[7]), .pin11(h_we));
  _74573 f (
    .pin1(f_pin1), .pin2(din[0]), .pin3(din[1]), .pin4(din[2]), .pin5(din[3]), .pin6(din[4]), .pin7(din[5]),
    .pin8(din[6]), .pin9(din[7]), .pin19(fout[0]), .pin18(fout[1]), .pin17(fout[2]), .pin16(fout[3]),
    .pin15(fout[4]), .pin14(fout[5]), .pin13(fout[6]), .pin12(fout[7]), .pin11(f_we));
  _74573 z (
    .pin1(z_en), .pin2(din[0]), .pin3(din[1]), .pin4(din[2]), .pin5(din[3]), .pin6(din[4]), .pin7(din[5]),
    .pin8(din[6]), .pin9(din[7]), .pin19(dout[0]), .pin18(dout[1]), .pin17(dout[2]), .pin16(dout[3]),
    .pin15(dout[4]), .pin14(dout[5]), .pin13(dout[6]), .pin12(dout[7]), .pin11(z_we));
  _74138 u_74138_1 (
    .pin1(a), .pin2(b), .pin3(c), .pin4(n74138_1_pin4), .pin5(n74138_1_pin5), .pin6(ereg), .pin7(f_en),
    .pin15(a_en), .pin14(b_en), .pin13(c_en), .pin12(d_en), .pin11(l_en), .pin10(h_en), .pin9(z_en));
  _74573 u_74573_1 (
    .pin1(l_en), .pin2(lout[0]), .pin3(lout[1]), .pin4(lout[2]), .pin5(lout[3]), .pin6(lout[4]),
    .pin7(lout[5]), .pin8(lout[6]), .pin9(lout[7]), .pin19(dout[0]), .pin18(dout[1]), .pin17(dout[2]),
    .pin16(dout[3]), .pin15(dout[4]), .pin14(dout[5]), .pin13(dout[6]), .pin12(dout[7]),
    .pin11(n74573_1_pin11));
  _74573 u_74573_2 (
    .pin1(h_en), .pin2(hout[0]), .pin3(hout[1]), .pin4(hout[2]), .pin5(hout[3]), .pin6(hout[4]),
    .pin7(hout[5]), .pin8(hout[6]), .pin9(hout[7]), .pin19(dout[0]), .pin18(dout[1]), .pin17(dout[2]),
    .pin16(dout[3]), .pin15(dout[4]), .pin14(dout[5]), .pin13(dout[6]), .pin12(dout[7]),
    .pin11(n74573_2_pin11));
  _74573 u_74573_3 (
    .pin1(f_en), .pin2(fout[0]), .pin3(fout[1]), .pin4(fout[2]), .pin5(fout[3]), .pin6(fout[4]),
    .pin7(fout[5]), .pin8(fout[6]), .pin9(fout[7]), .pin19(dout[0]), .pin18(dout[1]), .pin17(dout[2]),
    .pin16(dout[3]), .pin15(dout[4]), .pin14(dout[5]), .pin13(dout[6]), .pin12(dout[7]),
    .pin11(n74573_3_pin11));
  // also tied to GND on the sheet: {n74238_1_pin4, l_pin1, h_pin1, f_pin1, n74138_1_pin4, n74138_1_pin5}
  // also tied to VCC on the sheet: {n74573_1_pin11, n74573_2_pin11, n74573_3_pin11}

  // Other names for the same wires on the sheet: d0 = din[0]; d1 = din[1]; d2 = din[2]; d3 = din[3]; d4 = din[4];
  //   d5 = din[5]; d6 = din[6]; d7 = din[7]; q0 = dout[0]; q1 = dout[1]; q2 = dout[2]; q3 = dout[3]; q4 = dout[4];
  //   q5 = dout[5]; q6 = dout[6]; q7 = dout[7]; f0 = fout[0]; f1 = fout[1]; f2 = fout[2]; f3 = fout[3]; f4 = fout[4];
  //   f5 = fout[5]; f6 = fout[6]; f7 = fout[7]; h0 = hout[0]; h1 = hout[1]; h2 = hout[2]; h3 = hout[3]; h4 = hout[4];
  //   h5 = hout[5]; h6 = hout[6]; h7 = hout[7]; l0 = lout[0]; l1 = lout[1]; l2 = lout[2]; l3 = lout[3]; l4 = lout[4];
  //   l5 = lout[5]; l6 = lout[6]; l7 = lout[7]
endmodule

module opc74 (
  input  seq_cnt,
  input  seq_lop,
  input  clk,
  input  [7:0] dbus,
  input  cc,
  input  eop1,
  input  eop2,
  output [7:0] op0out,
  output [3:0] op,
  output [2:0] sel0,
  output [2:0] sel1,
  output lop,
  output ex,
  output [2:0] excout,
  output [7:0] op1out,
  output [7:0] op2out,
  output [7:0] dbusout,
  output [1:0] opc_out
);

  wire a001, a010, a101, ld1, ld1_x, ld2, ld2_x, ld3, ld3_x, lop0, lop1, lop2, lopN, mw_lda, n7411_2_pin6,
       n7427_1_pin6, n7427_1_pin13, n7427_2_pin9, n7485_1_pin1, n7485_1_pin2, n7485_1_pin3, n7485_1_pin4,
       n7485_1_pin9, n7485_1_pin11, n7485_1_pin14, n74163_1_pin3, n74163_1_pin4, n74163_1_pin5,
       n74163_1_pin6, n74163_1_pin9, n74163_1_pin10, n74163_2_pin3, n74163_2_pin4, n74163_2_pin5,
       n74163_2_pin6, n74163_2_pin9, n74163_2_pin10, n74238_1_pin3, n74238_1_pin4, n74238_1_pin5,
       n74238_1_pin6, n74573_1_pin11, n74573_2_pin11, n_cc, n_eop1, n_eop2, n_mw_lda, nop0, nop1, nop2, ny,
       op0_pin1, op1_pin1, op2_pin1, op_gt_6, opc_eq_0, opc_eq_1, opc_eq_2, opc_eq_3;

  _74573 op0 (
    .pin1(op0_pin1), .pin2(dbus[0]), .pin3(dbus[1]), .pin4(dbus[2]), .pin5(dbus[3]), .pin6(dbus[4]),
    .pin7(dbus[5]), .pin8(dbus[6]), .pin9(dbus[7]), .pin19(op0out[0]), .pin18(op0out[1]), .pin17(op0out[2]),
    .pin16(op0out[3]), .pin15(op[0]), .pin14(op[1]), .pin13(op[2]), .pin12(op[3]), .pin11(lop0));
  _74573 op1 (
    .pin1(op1_pin1), .pin2(dbus[0]), .pin3(dbus[1]), .pin4(dbus[2]), .pin5(dbus[3]), .pin6(dbus[4]),
    .pin7(dbus[5]), .pin8(dbus[6]), .pin9(dbus[7]), .pin19(op1out[0]), .pin18(op1out[1]), .pin17(op1out[2]),
    .pin16(op1out[3]), .pin15(op1out[4]), .pin14(op1out[5]), .pin13(op1out[6]), .pin12(op1out[7]),
    .pin11(lop1));
  _74573 u_74573_1 (
    .pin1(n_eop1), .pin2(op1out[0]), .pin3(op1out[1]), .pin4(op1out[2]), .pin5(op1out[3]), .pin6(op1out[4]),
    .pin7(op1out[5]), .pin8(op1out[6]), .pin9(op1out[7]), .pin19(dbusout[0]), .pin18(dbusout[1]),
    .pin17(dbusout[2]), .pin16(dbusout[3]), .pin15(dbusout[4]), .pin14(dbusout[5]), .pin13(dbusout[6]),
    .pin12(dbusout[7]), .pin11(n74573_1_pin11));
  _74573 op2 (
    .pin1(op2_pin1), .pin2(dbus[0]), .pin3(dbus[1]), .pin4(dbus[2]), .pin5(dbus[3]), .pin6(dbus[4]),
    .pin7(dbus[5]), .pin8(dbus[6]), .pin9(dbus[7]), .pin19(op2out[0]), .pin18(op2out[1]), .pin17(op2out[2]),
    .pin16(op2out[3]), .pin15(op2out[4]), .pin14(op2out[5]), .pin13(op2out[6]), .pin12(op2out[7]),
    .pin11(lop2));
  _74573 u_74573_2 (
    .pin1(n_eop2), .pin2(op2out[0]), .pin3(op2out[1]), .pin4(op2out[2]), .pin5(op2out[3]), .pin6(op2out[4]),
    .pin7(op2out[5]), .pin8(op2out[6]), .pin9(op2out[7]), .pin19(dbusout[0]), .pin18(dbusout[1]),
    .pin17(dbusout[2]), .pin16(dbusout[3]), .pin15(dbusout[4]), .pin14(dbusout[5]), .pin13(dbusout[6]),
    .pin12(dbusout[7]), .pin11(n74573_2_pin11));
  _7404 #(.ShowInternalStructure("true")) u_7404_1 (
    .pin1(op0out[3]), .pin2(ny), .pin3(lop), .pin4(ex), .pin5(cc), .pin6(n_cc), .pin13(op[0]), .pin12(nop0),
    .pin11(op[1]), .pin10(nop1), .pin9(op[2]), .pin8(nop2));
  _7485 #(.ShowInternalStructure("true")) u_7485_1 (
    .pin1(n7485_1_pin1), .pin2(n7485_1_pin2), .pin3(n7485_1_pin3), .pin4(n7485_1_pin4), .pin5(op_gt_6),
    .pin15(op[3]), .pin14(n7485_1_pin14), .pin13(op[2]), .pin12(op[1]), .pin11(n7485_1_pin11), .pin10(op[0]),
    .pin9(n7485_1_pin9));  // open: pin6, pin7
  _7408 #(.ShowInternalStructure("true")) u_7408_1 (
    .pin1(lopN), .pin2(opc_eq_0), .pin3(lop0), .pin4(lopN), .pin5(opc_eq_1), .pin6(lop1), .pin13(lopN),
    .pin12(opc_eq_2), .pin11(lop2), .pin10(seq_lop), .pin9(lop), .pin8(lopN));
  _74238 u_74238_1 (
    .pin1(opc_out[0]), .pin2(opc_out[1]), .pin3(n74238_1_pin3), .pin4(n74238_1_pin4), .pin5(n74238_1_pin5),
    .pin6(n74238_1_pin6), .pin15(opc_eq_0), .pin14(opc_eq_1), .pin13(opc_eq_2), .pin12(opc_eq_3));  // open: pin7, pin11, pin10, pin9
  _74163 #(.ShowInternalStructure("true")) u_74163_1 (
    .pin1(n_cc), .pin2(seq_cnt), .pin3(n74163_1_pin3), .pin4(n74163_1_pin4), .pin5(n74163_1_pin5),
    .pin6(n74163_1_pin6), .pin7(lop), .pin14(opc_out[0]), .pin13(opc_out[1]), .pin10(n74163_1_pin10),
    .pin9(n74163_1_pin9));  // open: pin15, pin12, pin11
  _74163 #(.ShowInternalStructure("true")) u_74163_2 (
    .pin1(n_cc), .pin2(seq_cnt), .pin3(n74163_2_pin3), .pin4(n74163_2_pin4), .pin5(n74163_2_pin5),
    .pin6(n74163_2_pin6), .pin7(ex), .pin14(excout[0]), .pin13(excout[1]), .pin12(excout[2]),
    .pin10(n74163_2_pin10), .pin9(n74163_2_pin9));  // open: pin15, pin11
  _7404 #(.ShowInternalStructure("true")) u_7404_2 (
    .pin1(eop1), .pin2(n_eop1), .pin3(eop2), .pin4(n_eop2), .pin13(n_mw_lda), .pin12(mw_lda));  // open: pin5, pin6, pin11, pin10, pin9, pin8
  _7411 #(.ShowInternalStructure("true")) u_7411_1 (
    .pin1(op[1]), .pin2(nop0), .pin3(op[0]), .pin4(nop1), .pin5(nop2), .pin6(a001), .pin13(nop2),
    .pin12(a010), .pin11(op[0]), .pin10(nop1), .pin9(op[2]), .pin8(a101));
  _7411 #(.ShowInternalStructure("true")) u_7411_2 (
    .pin3(nop0), .pin4(nop1), .pin5(nop2), .pin6(n7411_2_pin6));  // open: pin1, pin2, pin13, pin12, pin11, pin10, pin9, pin8
  _7427 #(.ShowInternalStructure("true")) u_7427_1 (
    .pin1(n7411_2_pin6), .pin2(a101), .pin3(a101), .pin4(a010), .pin5(a001), .pin6(n7427_1_pin6),
    .pin13(n7427_1_pin13), .pin12(n_mw_lda), .pin11(ld1_x), .pin10(ld2_x), .pin9(ld3_x), .pin8(lop));
  _7427 #(.ShowInternalStructure("true")) u_7427_2 (
    .pin1(mw_lda), .pin2(op_gt_6), .pin3(n7427_1_pin6), .pin4(op_gt_6), .pin5(op0out[3]), .pin6(ld3),
    .pin13(ny), .pin12(ld1), .pin11(ld1), .pin10(ld3), .pin9(n7427_2_pin9), .pin8(ld2));
  _7408 #(.ShowInternalStructure("true")) u_7408_2 (
    .pin1(opc_eq_1), .pin2(ld1), .pin3(ld1_x), .pin4(opc_eq_2), .pin5(ld2), .pin6(ld2_x), .pin10(opc_eq_3),
    .pin9(ld3), .pin8(ld3_x));  // open: pin13, pin12, pin11

  assign op0out[7:4] = op;
  assign sel0 = op0out[2:0];
  assign sel1 = op2out[2:0];
  // also tied to GND on the sheet: {op0_pin1, op1_pin1, op2_pin1, n7485_1_pin1, n7485_1_pin2, n7485_1_pin4, n74238_1_pin3, n74238_1_pin4, n74238_1_pin5, n74163_1_pin3, n74163_1_pin4, n74163_1_pin5, n74163_1_pin6, n74163_2_pin3, n74163_2_pin4, n74163_2_pin5, n74163_2_pin6, n7485_1_pin9, n7427_1_pin13, n7427_2_pin9}
  // also tied to VCC on the sheet: {n74573_1_pin11, n74573_2_pin11, n7485_1_pin3, n74238_1_pin6, n7485_1_pin14, n7485_1_pin11, n74163_1_pin10, n74163_1_pin9, n74163_2_pin10, n74163_2_pin9}

  // Other names for the same wires on the sheet: d0 = dbus[0]; d1 = dbus[1]; d2 = dbus[2]; d3 = dbus[3]; d4 = dbus[4];
  //   d5 = dbus[5]; d6 = dbus[6]; d7 = dbus[7]; q0 = dbusout[0]; q1 = dbusout[1]; q2 = dbusout[2]; q3 = dbusout[3];
  //   q4 = dbusout[4]; q5 = dbusout[5]; q6 = dbusout[6]; q7 = dbusout[7]; e_exc = ex; exc0 = excout[0];
  //   exc1 = excout[1]; exc2 = excout[2]; n_e_exc = lop; y = op0out[3]; op10 = op1out[0]; op11 = op1out[1];
  //   op12 = op1out[2]; op13 = op1out[3]; op14 = op1out[4]; op15 = op1out[5]; op16 = op1out[6]; op17 = op1out[7];
  //   op23 = op2out[3]; op24 = op2out[4]; op25 = op2out[5]; op26 = op2out[6]; op27 = op2out[7]; opc0 = opc_out[0];
  //   opc1 = opc_out[1]; sel00 = op0out[0]; sel01 = op0out[1]; sel02 = op0out[2]; op20 = op2out[0]; op21 = op2out[1];
  //   op22 = op2out[2]

  // Notes on the sheet:
  //   NOTs used by auxregs board
  //   ANDs used by auxregs board
  //   AND used by auxregs board
endmodule

module main_test (
);

  wire addr74_1_eaux, addr74_1_eramout, addr74_1_erom, addr74_1_lramout, aimm, asp, cc, clk, ealu, ebank,
       edev, eop1, eop2, eram, ereg, err, ex, hlt, jnz, lbank, ldev, ldf, ldh, ldl, ldx, ldy, lop, lprt,
       lram, lreg, mb_EQ_0, n74163_1_pin3, n74163_1_pin4, n74163_1_pin5, n74163_1_pin6, n74163_1_pin10,
       n74163_1_pin13, n74163_1_pin14, n74238_1_pin3, n74238_1_pin4, n74238_1_pin5, n74238_1_pin6, n_hlt,
       n_seq_3, nclk, nreset, reset, sel, seq_0, seq_1, seq_2, seq_3, spdec, spinc, video74_1_v_03,
       video74_1_v_10;
  wire [1:0] opc;
  wire [2:0] addr74_1_selaux, exc, sel0, sel1;
  wire [3:0] op;
  wire [7:0] dbus, f, mb, op0, op1, op2, regs74_1_hout, regs74_1_lout, vd;
  wire [12:0] vma;
  wire [15:0] addr, auxregs74_1_pcout, auxregs74_1_spout;

  regs74 regs74_1 (
    .hout(regs74_1_hout), .fout(f), .dout(dbus), .lout(regs74_1_lout), .sel(sel), .ldh(ldh), .ldl(ldl),
    .ldf(ldf), .sel0(sel0), .sel1(sel1), .lreg(lreg), .din(dbus), .seq_unuse(seq_1), .n_seq_load(seq_3),
    .ereg(ereg));
  auxregs74 auxregs74_1 (
    .pcout(auxregs74_1_pcout), .spout(auxregs74_1_spout), .dbusout(dbus), .mb_EQ_0(mb_EQ_0), .mb_out(mb),
    .reset(reset), .fall(seq_2), .nclk(seq_3), .clk(seq_1), .sel(addr74_1_selaux), .h(regs74_1_hout),
    .l(regs74_1_lout), .dbus(dbus), .lop(lop), .jnz(jnz), .eaux(addr74_1_eaux), .en(eram), .ld(lram),
    .nreset(nreset), .spinc(spinc), .spdec(spdec));
  alu74 alu74_1 (
    .dout(dbus), .op(op[2:0]), .seq_load(seq_3), .seq_unused(seq_1), .ldx(ldx), .ldy(ldy), .ealu(ealu),
    .ldf(ldf), .din(dbus), .fin(f));
  Clock clock_1 (.out(clk));
  Button button_1 (.out(reset));
  _7404 #(.ShowInternalStructure("true")) u_7404_1 (
    .pin1(reset), .pin2(nreset), .pin3(clk), .pin4(nclk), .pin13(seq_3), .pin12(n_seq_3), .pin11(hlt),
    .pin10(n_hlt));  // open: pin5, pin6, pin9, pin8
  _74163 #(.ShowInternalStructure("true")) u_74163_1 (
    .pin1(n_seq_3), .pin2(clk), .pin3(n74163_1_pin3), .pin4(n74163_1_pin4), .pin5(n74163_1_pin5),
    .pin6(n74163_1_pin6), .pin7(n_hlt), .pin14(n74163_1_pin14), .pin13(n74163_1_pin13), .pin10(n74163_1_pin10));  // open: pin15, pin12, pin11, pin9
  addr74 addr74_1 (
    .lbank(lbank), .ebank(ebank), .erom(addr74_1_erom), .eramout(addr74_1_eramout),
    .lramout(addr74_1_lramout), .eaux(addr74_1_eaux), .selaux(addr74_1_selaux), .addrout(addr), .eram(eram),
    .apc(lop), .asp(asp), .aimm(aimm), .hl({regs74_1_hout, regs74_1_lout}), .pc(auxregs74_1_pcout),
    .sp(auxregs74_1_spout), .mb_EQ_0(mb_EQ_0), .imm({op2, op1}), .lram(lram));
  _74238 #(.ShowInternalStructure("true")) u_74238_1 (
    .pin1(n74163_1_pin14), .pin2(n74163_1_pin13), .pin3(n74238_1_pin3), .pin4(n74238_1_pin4),
    .pin5(n74238_1_pin5), .pin6(n74238_1_pin6), .pin15(seq_0), .pin14(seq_1), .pin13(seq_2), .pin12(seq_3));  // open: pin7, pin11, pin10, pin9
  dev74 dev74_1 (
    .dbus_out(dbus), .err_out(err), .hlt_out(hlt), .clk(seq_1), .edev(edev), .ldev(ldev), .lprt(lprt),
    .dbus(dbus), .nclk(seq_3));
  mem74 mem74_1 (
    .clk(seq_2), .erom(addr74_1_erom), .eram(addr74_1_eramout), .lram(addr74_1_lramout), .addr(addr),
    .dbus(dbus), .dbus_out(dbus));
  opc74 opc74_1 (
    .opc_out(opc), .op0out(op0), .op(op), .sel0(sel0), .sel1(sel1), .lop(lop), .ex(ex), .excout(exc),
    .op1out(op1), .op2out(op2), .dbusout(dbus), .seq_cnt(seq_2), .seq_lop(seq_3), .clk(seq_1), .dbus(dbus),
    .cc(cc), .eop1(eop1), .eop2(eop2));
  control74 control74_1 (
    .eram(eram), .asp(asp), .aimm(aimm), .lram(lram), .spinc(spinc), .spdec(spdec), .jnz(jnz), .ldx(ldx),
    .ldy(ldy), .ldf(ldf), .ealu(ealu), .ldh(ldh), .ldl(ldl), .lprt(lprt), .ereg(ereg), .lreg(lreg),
    .sel(sel), .eop1(eop1), .eop2(eop2), .edev(edev), .ldev(ldev), .cc(cc), .op0(op0), .nclk(nclk), .ex(ex),
    .opc(opc), .exc(exc));
  LED led_1 (.in(video74_1_v_10));
  video74 video74_1 (.rise(seq_0), .clk(seq_1), .vd(vd), .v_10(video74_1_v_10), .v_03(video74_1_v_03), .vma(vma));
  LED led_2 (.in(video74_1_v_03));
  vram74 vram74_1 (
    .rise(seq_0), .fall(seq_2), .nclk(seq_3), .clk(seq_1), .ebank(ebank), .lbank(lbank), .dbus(dbus),
    .mb(mb), .vma(vma), .addr(addr), .vd(vd), .dbus_out(dbus));
  // also tied to GND on the sheet: {n74163_1_pin3, n74163_1_pin4, n74163_1_pin5, n74163_1_pin6, n74238_1_pin3, n74238_1_pin4, n74238_1_pin5}
  // also tied to VCC on the sheet: {n74163_1_pin10, n74238_1_pin6}
endmodule

module auxregs74 (
  input  nreset,
  input  reset,
  input  fall,
  input  nclk,
  input  clk,
  input  [2:0] sel,
  input  [7:0] h,
  input  [7:0] l,
  input  [7:0] dbus,
  input  lop,
  input  jnz,
  input  eaux,
  input  en,
  input  ld,
  input  spinc,
  input  spdec,
  output [15:0] pcout,
  output [15:0] spout,
  output [7:0] dbusout,
  output mb_EQ_0,
  output [7:0] mb_out
);

  wire d_EQ_0, d_nEQ_0, jmp, lmb, mb_pin1, n74138_2_pin4, n74573_1_pin11, n74688_1_pin1, n74688_1_pin3,
       n74688_1_pin5, n74688_1_pin7, n74688_1_pin9, n74688_1_pin11, n74688_1_pin13, n74688_1_pin15,
       n74688_1_pin17, n_eaux, n_emb, n_epch, n_epcl, n_esph, n_espl, n_jmp, n_jmp_x, n_lmb, n_lpch,
       n_lpch_x, n_lpcl, n_lpcl_x, n_lsph, n_lspl, n_pcinc_x, n_spdec_x, n_spinc_x, pc0_pin4, pc0_pin12,
       pc0_pin13, pc0x, pc1_pin12, pc1_pin13, pc1x, pc2_pin12, pc2_pin13, pc2x, pc3x, pc4x, pc5x, pc6x, pc7x,
       pc8x, pc9x, pcAx, pcBx, pcCx, pcDx, pcEx, pcFx, sp0_pin12, sp0_pin13, sp0_pin14, sp1_pin12, sp1_pin13,
       sp1_pin14, sp2_pin12, sp2_pin13, sp2_pin14, sp3_pin14;

  _74138 #(.ShowInternalStructure("true")) u_74138_1 (
    .pin1(sel[0]), .pin2(sel[1]), .pin3(sel[2]), .pin4(nclk), .pin5(n_eaux), .pin6(ld), .pin7(n_lpch),
    .pin13(n_lmb), .pin11(n_lspl), .pin10(n_lsph), .pin9(n_lpcl));  // open: pin15, pin14, pin12
  _7400 #(.ShowInternalStructure("true")) u_7400_1 (
    .pin1(lop), .pin2(fall), .pin3(n_pcinc_x), .pin4(spinc), .pin5(fall), .pin6(n_spinc_x), .pin13(spdec),
    .pin12(fall), .pin11(n_spdec_x), .pin10(jmp), .pin9(fall), .pin8(n_jmp_x));
  _74244 u_74244_1 (
    .pin1(n_jmp), .pin2(l[0]), .pin3(pc4x), .pin4(l[1]), .pin5(pc5x), .pin6(l[2]), .pin7(pc6x), .pin8(l[3]),
    .pin9(pc7x), .pin19(n_jmp), .pin18(pc0x), .pin17(l[4]), .pin16(pc1x), .pin15(l[5]), .pin14(pc2x),
    .pin13(l[6]), .pin12(pc3x), .pin11(l[7]));
  _74193 #(.ShowInternalStructure("true")) pc0 (
    .pin1(pc1x), .pin2(pcout[1]), .pin3(pcout[0]), .pin4(pc0_pin4), .pin5(n_pcinc_x), .pin6(pcout[2]),
    .pin7(pcout[3]), .pin15(pc0x), .pin14(reset), .pin13(pc0_pin13), .pin12(pc0_pin12), .pin11(n_lpcl_x),
    .pin10(pc2x), .pin9(pc3x));
  _74193 pc1 (
    .pin1(pc5x), .pin2(pcout[5]), .pin3(pcout[4]), .pin4(pc0_pin13), .pin5(pc0_pin12), .pin6(pcout[6]),
    .pin7(pcout[7]), .pin15(pc4x), .pin14(reset), .pin13(pc1_pin13), .pin12(pc1_pin12), .pin11(n_lpcl_x),
    .pin10(pc6x), .pin9(pc7x));
  _74244 u_74244_2 (
    .pin1(n_epcl), .pin2(pcout[0]), .pin3(dbusout[4]), .pin4(pcout[1]), .pin5(dbusout[5]), .pin6(pcout[2]),
    .pin7(dbusout[6]), .pin8(pcout[3]), .pin9(dbusout[7]), .pin19(n_epcl), .pin18(dbusout[0]),
    .pin17(pcout[4]), .pin16(dbusout[1]), .pin15(pcout[5]), .pin14(dbusout[2]), .pin13(pcout[6]),
    .pin12(dbusout[3]), .pin11(pcout[7]));
  _74244 u_74244_3 (
    .pin1(jmp), .pin2(dbus[0]), .pin3(pc4x), .pin4(dbus[1]), .pin5(pc5x), .pin6(dbus[2]), .pin7(pc6x),
    .pin8(dbus[3]), .pin9(pc7x), .pin19(jmp), .pin18(pc0x), .pin17(dbus[4]), .pin16(pc1x), .pin15(dbus[5]),
    .pin14(pc2x), .pin13(dbus[6]), .pin12(pc3x), .pin11(dbus[7]));
  _74193 pc2 (
    .pin1(pc9x), .pin2(pcout[9]), .pin3(pcout[8]), .pin4(pc1_pin13), .pin5(pc1_pin12), .pin6(pcout[10]),
    .pin7(pcout[11]), .pin15(pc8x), .pin14(reset), .pin13(pc2_pin13), .pin12(pc2_pin12), .pin11(n_lpch_x),
    .pin10(pcAx), .pin9(pcBx));
  _74193 pc3 (
    .pin1(pcDx), .pin2(pcout[13]), .pin3(pcout[12]), .pin4(pc2_pin13), .pin5(pc2_pin12), .pin6(pcout[14]),
    .pin7(pcout[15]), .pin15(pcCx), .pin14(reset), .pin11(n_lpch_x), .pin10(pcEx), .pin9(pcFx));  // open: pin13, pin12
  _74244 u_74244_4 (
    .pin1(n_epch), .pin2(pcout[8]), .pin3(dbusout[4]), .pin4(pcout[9]), .pin5(dbusout[5]), .pin6(pcout[10]),
    .pin7(dbusout[6]), .pin8(pcout[11]), .pin9(dbusout[7]), .pin19(n_epch), .pin18(dbusout[0]),
    .pin17(pcout[12]), .pin16(dbusout[1]), .pin15(pcout[13]), .pin14(dbusout[2]), .pin13(pcout[14]),
    .pin12(dbusout[3]), .pin11(pcout[15]));
  _74138 #(.ShowInternalStructure("true")) u_74138_2 (
    .pin1(sel[0]), .pin2(sel[1]), .pin3(sel[2]), .pin4(n74138_2_pin4), .pin5(n_eaux), .pin6(en),
    .pin7(n_epch), .pin13(n_emb), .pin11(n_espl), .pin10(n_esph), .pin9(n_epcl));  // open: pin15, pin14, pin12
  _7404 #(.ShowInternalStructure("true")) u_7404_1 (
    .pin1(n_lmb), .pin2(lmb), .pin3(d_nEQ_0), .pin4(d_EQ_0), .pin13(eaux), .pin12(n_eaux), .pin11(jmp),
    .pin10(n_jmp));  // open: pin5, pin6, pin9, pin8
  Register #(.trigger("high"), .width(16)) pcX (.D(pcout), .en(1'b1), .clk(1'b1));  // open: Q, clr
  Register #(.trigger("high"), .width(16)) spX (.D(spout), .en(1'b1), .clk(1'b1));  // open: Q, clr
  _74244 u_74244_5 (
    .pin1(n_jmp), .pin2(h[0]), .pin3(pcCx), .pin4(h[1]), .pin5(pcDx), .pin6(h[2]), .pin7(pcEx), .pin8(h[3]),
    .pin9(pcFx), .pin19(n_jmp), .pin18(pc8x), .pin17(h[4]), .pin16(pc9x), .pin15(h[5]), .pin14(pcAx),
    .pin13(h[6]), .pin12(pcBx), .pin11(h[7]));
  _74688 u_74688_1 (
    .pin1(n74688_1_pin1), .pin2(dbus[0]), .pin3(n74688_1_pin3), .pin4(dbus[1]), .pin5(n74688_1_pin5),
    .pin6(dbus[2]), .pin7(n74688_1_pin7), .pin8(dbus[3]), .pin9(n74688_1_pin9), .pin19(d_nEQ_0),
    .pin18(dbus[7]), .pin17(n74688_1_pin17), .pin16(dbus[6]), .pin15(n74688_1_pin15), .pin14(dbus[5]),
    .pin13(n74688_1_pin13), .pin12(dbus[4]), .pin11(n74688_1_pin11));
  _74193 sp0 (
    .pin1(dbus[1]), .pin2(spout[1]), .pin3(spout[0]), .pin4(n_spdec_x), .pin5(n_spinc_x), .pin6(spout[2]),
    .pin7(spout[3]), .pin15(dbus[0]), .pin14(sp0_pin14), .pin13(sp0_pin13), .pin12(sp0_pin12),
    .pin11(n_lspl), .pin10(dbus[2]), .pin9(dbus[3]));
  _74193 sp1 (
    .pin1(dbus[5]), .pin2(spout[5]), .pin3(spout[4]), .pin4(sp0_pin13), .pin5(sp0_pin12), .pin6(spout[6]),
    .pin7(spout[7]), .pin15(dbus[4]), .pin14(sp1_pin14), .pin13(sp1_pin13), .pin12(sp1_pin12),
    .pin11(n_lspl), .pin10(dbus[6]), .pin9(dbus[7]));
  _74244 u_74244_6 (
    .pin1(n_espl), .pin2(spout[0]), .pin3(dbusout[4]), .pin4(spout[1]), .pin5(dbusout[5]), .pin6(spout[2]),
    .pin7(dbusout[6]), .pin8(spout[3]), .pin9(dbusout[7]), .pin19(n_espl), .pin18(dbusout[0]),
    .pin17(spout[4]), .pin16(dbusout[1]), .pin15(spout[5]), .pin14(dbusout[2]), .pin13(spout[6]),
    .pin12(dbusout[3]), .pin11(spout[7]));
  _7408 #(.ShowInternalStructure("true")) u_7408_1 (
    .pin1(jnz), .pin2(d_nEQ_0), .pin3(jmp), .pin13(n_lpcl), .pin12(n_jmp_x), .pin11(n_lpcl_x),
    .pin10(n_lpch), .pin9(n_jmp_x), .pin8(n_lpch_x));  // open: pin4, pin5, pin6
  _74244 u_74244_7 (
    .pin1(jmp), .pin2(dbus[0]), .pin3(pcCx), .pin4(dbus[1]), .pin5(pcDx), .pin6(dbus[2]), .pin7(pcEx),
    .pin8(dbus[3]), .pin9(pcFx), .pin19(jmp), .pin18(pc8x), .pin17(dbus[4]), .pin16(pc9x), .pin15(dbus[5]),
    .pin14(pcAx), .pin13(dbus[6]), .pin12(pcBx), .pin11(dbus[7]));
  _74573 mb (
    .pin1(mb_pin1), .pin2(dbus[0]), .pin3(dbus[1]), .pin4(dbus[2]), .pin5(dbus[3]), .pin6(dbus[4]),
    .pin7(dbus[5]), .pin8(dbus[6]), .pin9(dbus[7]), .pin19(mb_out[0]), .pin18(mb_out[1]), .pin17(mb_out[2]),
    .pin16(mb_out[3]), .pin15(mb_out[4]), .pin14(mb_out[5]), .pin13(mb_out[6]), .pin12(mb_out[7]), .pin11(lmb));
  _74193 #(.ShowInternalStructure("true")) sp2 (
    .pin1(dbus[1]), .pin2(spout[9]), .pin3(spout[8]), .pin4(sp1_pin13), .pin5(sp1_pin12), .pin6(spout[10]),
    .pin7(spout[11]), .pin15(dbus[0]), .pin14(sp2_pin14), .pin13(sp2_pin13), .pin12(sp2_pin12),
    .pin11(n_lsph), .pin10(dbus[2]), .pin9(dbus[3]));
  _74193 sp3 (
    .pin1(dbus[5]), .pin2(spout[13]), .pin3(spout[12]), .pin4(sp2_pin13), .pin5(sp2_pin12), .pin6(spout[14]),
    .pin7(spout[15]), .pin15(dbus[4]), .pin14(sp3_pin14), .pin11(n_lsph), .pin10(dbus[6]), .pin9(dbus[7]));  // open: pin13, pin12
  _74244 u_74244_8 (
    .pin1(n_esph), .pin2(spout[8]), .pin3(dbusout[4]), .pin4(spout[9]), .pin5(dbusout[5]), .pin6(spout[10]),
    .pin7(dbusout[6]), .pin8(spout[11]), .pin9(dbusout[7]), .pin19(n_esph), .pin18(dbusout[0]),
    .pin17(spout[12]), .pin16(dbusout[1]), .pin15(spout[13]), .pin14(dbusout[2]), .pin13(spout[14]),
    .pin12(dbusout[3]), .pin11(spout[15]));
  _7430 u_7430_1 (
    .pin1(mb_out[5]), .pin2(mb_out[4]), .pin3(mb_out[3]), .pin4(mb_out[2]), .pin5(mb_out[1]),
    .pin6(mb_out[0]), .pin12(mb_out[6]), .pin11(mb_out[7]), .pin8(mb_EQ_0));  // open: pin13, pin10, pin9
  _74573 u_74573_1 (
    .pin1(n_emb), .pin2(mb_out[0]), .pin3(mb_out[1]), .pin4(mb_out[2]), .pin5(mb_out[3]), .pin6(mb_out[4]),
    .pin7(mb_out[5]), .pin8(mb_out[6]), .pin9(mb_out[7]), .pin19(dbusout[0]), .pin18(dbusout[1]),
    .pin17(dbusout[2]), .pin16(dbusout[3]), .pin15(dbusout[4]), .pin14(dbusout[5]), .pin13(dbusout[6]),
    .pin12(dbusout[7]), .pin11(n74573_1_pin11));
  // also tied to GND on the sheet: {n74138_2_pin4, n74688_1_pin1, n74688_1_pin3, n74688_1_pin5, n74688_1_pin7, n74688_1_pin9, n74688_1_pin17, n74688_1_pin15, n74688_1_pin13, n74688_1_pin11, sp0_pin14, sp1_pin14, mb_pin1, sp2_pin14, sp3_pin14}
  // also tied to VCC on the sheet: {pc0_pin4, n74573_1_pin11}

  // Other names for the same wires on the sheet: d0 = dbus[0]; d1 = dbus[1]; d2 = dbus[2]; d3 = dbus[3]; d4 = dbus[4];
  //   d5 = dbus[5]; d6 = dbus[6]; d7 = dbus[7]; q0 = dbusout[0]; q1 = dbusout[1]; q2 = dbusout[2]; q3 = dbusout[3];
  //   q4 = dbusout[4]; q5 = dbusout[5]; q6 = dbusout[6]; q7 = dbusout[7]; mb0 = mb_out[0]; mb1 = mb_out[1];
  //   mb2 = mb_out[2]; mb3 = mb_out[3]; mb4 = mb_out[4]; mb5 = mb_out[5]; mb6 = mb_out[6]; mb7 = mb_out[7];
  //   pc0 = pcout[0]; pc1 = pcout[1]; pc2 = pcout[2]; pc3 = pcout[3]; pc4 = pcout[4]; pc5 = pcout[5]; pc6 = pcout[6];
  //   pc7 = pcout[7]; pc8 = pcout[8]; pc9 = pcout[9]; pcA = pcout[10]; pcB = pcout[11]; pcC = pcout[12];
  //   pcD = pcout[13]; pcE = pcout[14]; pcF = pcout[15]; sp0 = spout[0]; sp1 = spout[1]; sp2 = spout[2];
  //   sp3 = spout[3]; sp4 = spout[4]; sp5 = spout[5]; sp6 = spout[6]; sp7 = spout[7]; sp8 = spout[8]; sp9 = spout[9];
  //   spA = spout[10]; spB = spout[11]; spC = spout[12]; spD = spout[13]; spE = spout[14]; spF = spout[15]

  // Notes on the sheet:
  //   NOTE: these NOTs should be from another board
  //   for display purposes only
  //   NOTE: these ANDs are on the opc board
endmodule

module addr74 (
  input  mb_EQ_0,
  input  lram,
  input  eram,
  input  apc,
  input  asp,
  input  aimm,
  input  [15:0] hl,
  input  [15:0] pc,
  input  [15:0] sp,
  input  [15:0] imm,
  output lbank,
  output ebank,
  output erom,
  output eramout,
  output lramout,
  output eaux,
  output [2:0] selaux,
  output [15:0] addrout
);

  wire a_ram, a_upper, bank, n7421_1_pin6, n7421_1_pin8, n7421_2_pin6, n7432_1_pin6, n7432_1_pin11,
       n74573_1_pin11, n74573_2_pin11, n74573_3_pin11, n74573_4_pin11, n74573_5_pin11, n74573_6_pin11,
       n74573_7_pin11, n74573_8_pin11, n_adE, n_adF, n_ahl, n_aimm, n_apc, n_asp, n_eaux, pc_load;

  Hex_Digit_Display hex_digit_display_1 (.value(addrout[15:12]));  // open: dp
  _74573 u_74573_1 (
    .pin1(n_ahl), .pin2(hl[0]), .pin3(hl[1]), .pin4(hl[2]), .pin5(hl[3]), .pin6(hl[4]), .pin7(hl[5]),
    .pin8(hl[6]), .pin9(hl[7]), .pin19(addrout[0]), .pin18(addrout[1]), .pin17(addrout[2]),
    .pin16(addrout[3]), .pin15(addrout[4]), .pin14(addrout[5]), .pin13(addrout[6]), .pin12(addrout[7]),
    .pin11(n74573_1_pin11));
  _74573 u_74573_2 (
    .pin1(n_ahl), .pin2(hl[8]), .pin3(hl[9]), .pin4(hl[10]), .pin5(hl[11]), .pin6(hl[12]), .pin7(hl[13]),
    .pin8(hl[14]), .pin9(hl[15]), .pin19(addrout[8]), .pin18(addrout[9]), .pin17(addrout[10]),
    .pin16(addrout[11]), .pin15(addrout[12]), .pin14(addrout[13]), .pin13(addrout[14]), .pin12(addrout[15]),
    .pin11(n74573_2_pin11));
  _74573 u_74573_3 (
    .pin1(n_asp), .pin2(sp[0]), .pin3(sp[1]), .pin4(sp[2]), .pin5(sp[3]), .pin6(sp[4]), .pin7(sp[5]),
    .pin8(sp[6]), .pin9(sp[7]), .pin19(addrout[0]), .pin18(addrout[1]), .pin17(addrout[2]),
    .pin16(addrout[3]), .pin15(addrout[4]), .pin14(addrout[5]), .pin13(addrout[6]), .pin12(addrout[7]),
    .pin11(n74573_3_pin11));
  _74573 u_74573_4 (
    .pin1(n_asp), .pin2(sp[8]), .pin3(sp[9]), .pin4(sp[10]), .pin5(sp[11]), .pin6(sp[12]), .pin7(sp[13]),
    .pin8(sp[14]), .pin9(sp[15]), .pin19(addrout[8]), .pin18(addrout[9]), .pin17(addrout[10]),
    .pin16(addrout[11]), .pin15(addrout[12]), .pin14(addrout[13]), .pin13(addrout[14]), .pin12(addrout[15]),
    .pin11(n74573_4_pin11));
  Hex_Digit_Display hex_digit_display_2 (.value(addrout[11:8]));  // open: dp
  Hex_Digit_Display hex_digit_display_3 (.value(addrout[7:4]));  // open: dp
  Hex_Digit_Display hex_digit_display_4 (.value(addrout[3:0]));  // open: dp
  _74573 u_74573_5 (
    .pin1(n_apc), .pin2(pc[0]), .pin3(pc[1]), .pin4(pc[2]), .pin5(pc[3]), .pin6(pc[4]), .pin7(pc[5]),
    .pin8(pc[6]), .pin9(pc[7]), .pin19(addrout[0]), .pin18(addrout[1]), .pin17(addrout[2]),
    .pin16(addrout[3]), .pin15(addrout[4]), .pin14(addrout[5]), .pin13(addrout[6]), .pin12(addrout[7]),
    .pin11(n74573_5_pin11));
  _74573 u_74573_6 (
    .pin1(n_apc), .pin2(pc[8]), .pin3(pc[9]), .pin4(pc[10]), .pin5(pc[11]), .pin6(pc[12]), .pin7(pc[13]),
    .pin8(pc[14]), .pin9(pc[15]), .pin19(addrout[8]), .pin18(addrout[9]), .pin17(addrout[10]),
    .pin16(addrout[11]), .pin15(addrout[12]), .pin14(addrout[13]), .pin13(addrout[14]), .pin12(addrout[15]),
    .pin11(n74573_6_pin11));
  _74573 u_74573_7 (
    .pin1(n_aimm), .pin2(imm[0]), .pin3(imm[1]), .pin4(imm[2]), .pin5(imm[3]), .pin6(imm[4]), .pin7(imm[5]),
    .pin8(imm[6]), .pin9(imm[7]), .pin19(addrout[0]), .pin18(addrout[1]), .pin17(addrout[2]),
    .pin16(addrout[3]), .pin15(addrout[4]), .pin14(addrout[5]), .pin13(addrout[6]), .pin12(addrout[7]),
    .pin11(n74573_7_pin11));
  _74573 u_74573_8 (
    .pin1(n_aimm), .pin2(imm[8]), .pin3(imm[9]), .pin4(imm[10]), .pin5(imm[11]), .pin6(imm[12]),
    .pin7(imm[13]), .pin8(imm[14]), .pin9(imm[15]), .pin19(addrout[8]), .pin18(addrout[9]),
    .pin17(addrout[10]), .pin16(addrout[11]), .pin15(addrout[12]), .pin14(addrout[13]), .pin13(addrout[14]),
    .pin12(addrout[15]), .pin11(n74573_8_pin11));
  _7421 #(.ShowInternalStructure("true")) u_7421_1 (
    .pin1(addrout[3]), .pin2(addrout[4]), .pin4(addrout[5]), .pin5(addrout[6]), .pin6(n7421_1_pin6),
    .pin13(addrout[7]), .pin12(addrout[8]), .pin10(addrout[9]), .pin9(addrout[10]), .pin8(n7421_1_pin8));  // open: pin3, pin11
  _7421 #(.ShowInternalStructure("true")) u_7421_2 (
    .pin1(n7421_1_pin6), .pin2(addrout[11]), .pin4(addrout[12]), .pin5(addrout[13]), .pin6(n7421_2_pin6),
    .pin13(n7421_1_pin8), .pin12(addrout[14]), .pin10(addrout[15]), .pin9(n7421_2_pin6), .pin8(a_upper));  // open: pin3, pin11
  _7432 #(.ShowInternalStructure("true")) u_7432_1 (
    .pin1(eram), .pin2(apc), .pin3(pc_load), .pin4(addrout[1]), .pin5(addrout[2]), .pin6(n7432_1_pin6),
    .pin13(apc), .pin12(asp), .pin11(n7432_1_pin11), .pin10(n7432_1_pin11), .pin9(aimm), .pin8(n_ahl));
  _7408 #(.ShowInternalStructure("true")) u_7408_1 (
    .pin1(n7432_1_pin6), .pin2(a_upper), .pin3(eaux), .pin4(n_eaux), .pin5(addrout[15]), .pin6(a_ram),
    .pin13(a_ram), .pin12(eram), .pin11(eramout), .pin10(a_ram), .pin9(lram), .pin8(lramout));
  _7404 #(.ShowInternalStructure("true")) u_7404_1 (
    .pin1(aimm), .pin2(n_aimm), .pin3(apc), .pin4(n_apc), .pin5(asp), .pin6(n_asp), .pin13(eaux),
    .pin12(n_eaux), .pin11(addrout[14]), .pin10(n_adE), .pin9(addrout[15]), .pin8(n_adF));
  _7408 #(.ShowInternalStructure("true")) u_7408_2 (
    .pin1(pc_load), .pin2(n_adF), .pin3(erom), .pin13(addrout[15]), .pin12(n_adE), .pin11(bank));  // open: pin4, pin5, pin6, pin10, pin9, pin8
  _7411 #(.ShowInternalStructure("true")) u_7411_1 (
    .pin3(mb_EQ_0), .pin4(lram), .pin5(bank), .pin6(lbank), .pin11(mb_EQ_0), .pin10(eram), .pin9(bank),
    .pin8(ebank));  // open: pin1, pin2, pin13, pin12

  assign selaux = addrout[2:0];
  // also tied to VCC on the sheet: {n74573_1_pin11, n74573_2_pin11, n74573_3_pin11, n74573_4_pin11, n74573_5_pin11, n74573_6_pin11, n74573_7_pin11, n74573_8_pin11}

  // Other names for the same wires on the sheet: ad0 = addrout[0]; ad1 = addrout[1]; ad2 = addrout[2];
  //   ad3 = addrout[3]; ad4 = addrout[4]; ad5 = addrout[5]; ad6 = addrout[6]; ad7 = addrout[7]; ad8 = addrout[8];
  //   ad9 = addrout[9]; adA = addrout[10]; adB = addrout[11]; adC = addrout[12]; adD = addrout[13]; adE = addrout[14];
  //   adF = addrout[15]; eram_out = eramout; l0 = hl[0]; l1 = hl[1]; l2 = hl[2]; l3 = hl[3]; l4 = hl[4]; l5 = hl[5];
  //   l6 = hl[6]; l7 = hl[7]; h0 = hl[8]; h1 = hl[9]; h2 = hl[10]; h3 = hl[11]; h4 = hl[12]; h5 = hl[13]; h6 = hl[14];
  //   h7 = hl[15]; op00 = imm[0]; op01 = imm[1]; op02 = imm[2]; op03 = imm[3]; op04 = imm[4]; op05 = imm[5];
  //   op06 = imm[6]; op07 = imm[7]; op10 = imm[8]; op11 = imm[9]; op12 = imm[10]; op13 = imm[11]; op14 = imm[12];
  //   op15 = imm[13]; op16 = imm[14]; op17 = imm[15]; lram_out = lramout; pcA = pc[10]; pcB = pc[11]; pcC = pc[12];
  //   pcD = pc[13]; pcE = pc[14]; pcF = pc[15]; spA = sp[10]; spB = sp[11]; spC = sp[12]; spD = sp[13]; spE = sp[14];
  //   spF = sp[15]
endmodule

module AT28C64B_MAIN (
  input  VCC,
  input  NC0,
  input  nWE,
  input  A12,
  input  NC1,
  input  A7,
  input  A8,
  input  A6,
  input  A9,
  input  A5,
  input  A11,
  input  A4,
  input  nOE,
  input  A3,
  input  A10,
  input  A2,
  input  nCE,
  input  A1,
  input  A0,
  input  GND,
  output IO7,
  output IO6,
  output IO0,
  output IO5,
  output IO1,
  output IO4,
  output IO2,
  output IO3
);

  wire and_1_out, nor_1_out;
  wire [7:0] rom_1_data;

  ROM #(.addrWidth(13)) rom_1 (.addr({A12, A11, A10, A9, A8, A7, A6, A5, A4, A3, A2, A1, A0}), .data(rom_1_data));
  assign {IO7, IO6, IO5, IO4, IO3, IO2, IO1, IO0} = and_1_out ? rom_1_data : 8'bz;  // Controlled_Buffer controlled_buffer_1
  and and_1 (and_1_out, nor_1_out, nWE);
  nor nor_1 (nor_1_out, nCE, nOE);

  // Notes on the sheet:
  //   contents of rom_1 (hex, n*v repeats v):
  //   0 1 20 c0 80 0 66 20 c1 80 50 17 0 60 1 0 ee 77 0 c7 8 87 0 0 55 0 ab 6 1 e0 ab df 7 b7 2 50 f 0 6f
  //   8 0 6 2 e0 ab df 7 b7 2 50 f 0 6f 0 12 8 0 6 3 e0 12 df 7 b7 2 50 f 0 6f 0 55 1 ab 6 1 e1 ab df 7 b7
  //   2 50 f 0 6f 8 1 6 2 e0 ab df 7 b7 2 50 f 0 6f 0 12 9 0 6 3 e1 12 df 7 b7 2 50 f 0 6f 0 55 2 ab 6 1
  //   e2 ab df 7 b7 2 50 f 0 6f 8 2 6 2 e0 ab df 7 b7 2 50 f 0 6f 0 12 a 0 6 3 e2 12 df 7 b7 2 50 f 0 6f 0
  //   55 3 ab 6 1 e3 ab df 7 b7 2 50 f 0 6f 8 3 6 2 e0 ab df 7 b7 2 50 f 0 6f 0 12 b 0 6 3 e3 12 df 7 b7 2
  //   50 f 0 6f 6 ab e6 ab df 7 b7 2 50 f 0 6f 8 6 e0 ab df 7 b7 2 50 f 0 6f 0 12 e 0 e6 12 df 7 b7 2 50 f
  //   0 6f 50 fe fe 50 c1 80 1b 6 4 e3 66 df 7 b7 2 50 f 0 6f 12 c1 80 6 5 e2 66 df 7 b7 2 50 f 0 6f 50 fe
  //   fe 50 c1 80 0 77 28 19 6 6 e1 77 df 7 b7 2 50 f 0 6f 12 c1 80 6 7 e2 77 df 7 b7 2 50 f 0 6f 50 ff fe
  //   24 fc ff 25 fd ff 0 1 1 2 38 39 38 39 48 49 4a 4b 6 8 e0 2 df 7 b7 2 50 f 0 6f 6 9 e1 1 df 7 b7 2 50
  //   f 0 6f 6 a e2 2 df 7 b7 2 50 f 0 6f 6 b e3 1 df 7 b7 2 50 f 0 6f 30 66 48 6 d e0 66 df 7 b7 2 50 f 0
  //   6f 38 4e e6 66 df 7 b7 2 50 f 0 6f 50 ee ee 6 e e5 ee df 7 b7 2 50 f 0 6f 50 ee ee 6 f e4 ee df 7 b7
  //   2 50 f 0 6f 50 ce 1 60 1 6 10 e1 0 b7 2 50 f 0 6f 0 2 20 c0 80 50 c0 80 1a e2 1 df 7 b7 2 50 e5 1 6f
  //   1 0 50 bf 1 69 1 1 69 0 1 1 2 98 1 6 11 e0 3 df 7 b7 2 50 f 0 6f 6 12 e1 2 df 7 b7 2 50 f 0 6f 0 1 1
  //   2 98 1 6 12 e7 9 df 7 b7 2 50 f 0 6f c7 4 0 1 1 2 a8 1 a 7 6 13 e0 4 df 7 b7 2 50 f 0 6f 6 14 e1 2
  //   df 7 b7 2 50 f 0 6f 6 15 e2 9 df 7 b7 2 50 f 0 6f 7 55 2 75 3 11 ba 3 6 16 e7 55 df 7 b7 2 50 f 0 6f
  //   6 17 e2 11 df 7 b7 2 50 f 0 6f 7 66 2 75 3 1f ca 3 6 18 e7 66 df 7 b7 2 50 f 0 6f 6 19 e2 7f df 7 b7
  //   2 50 f 0 6f 7 77 2 75 3 1f da 3 6 1a e7 77 df 7 b7 2 50 f 0 6f 6 1b e2 80 df 7 b7 2 50 f 0 6f b7 f7
  //   2 f 3 4 fa 3 6 1c e7 0 df 7 b7 2 50 f 0 6f 6 1d e2 b df 7 b7 2 50 f 0 6f c7 8 2 f 3 4 fa 3 6 1e e7 0
  //   df 7 b7 2 50 f 0 6f 6 1f e2 a df 7 b7 2 50 f 0 6f b7 fb 0 1 90 ff 3f 6 20 e0 0 df 7 b7 2 50 f 0 6f
  //   4f 6 21 e7 d df 7 b7 2 50 f 0 6f 0 ee 20 0 0 11 0 0 6 22 e1 ee b7 2 50 f 0 6f 20 1 c0 11 1 c0 6 23
  //   e1 ee df 7 b7 2 50 f 0 6f 0 dd 50 1 c0 28 19 6 24 e1 dd df 7 b7 2 50 f 0 6f 0 66 20 80 80 11 80 80 6
  //   25 e1 66 df 7 b7 2 50 f 0 6f 3 1 23 fa ff 11 80 80 6 26 e1 66 b7 2 50 f 0 6f 0 77 20 80 80 11 80 80
  //   6 27 e1 77 df 7 b7 2 50 f 0 6f 11 1 c0 6 28 e1 dd df 7 b7 2 50 f 0 6f 0 55 50 1 c0 28 19 6 29 e1 55
  //   df 7 b7 2 50 f 0 6f 50 ff 8f 24 fc ff 25 fd ff 0 1 1 2 38 39 38 39 48 49 4a 4b 6 8 e0 2 df 7 b7 2 50
  //   f 0 6f 6 9 e1 1 df 7 b7 2 50 f 0 6f 6 a e2 2 df 7 b7 2 50 f 0 6f 6 b e3 1 df 7 b7 2 50 f 0 6f 30 66
  //   48 6 d e0 66 df 7 b7 2 50 f 0 6f 38 4e e6 66 df 7 b7 2 50 f 0 6f 50 41 4 8 5 9 4 30 4 30 6 50 19 4
  //   60 1 8 6 6 30 e0 4 df 7 b7 2 50 f 0 6f 50 37 4 60 1 6 0 d 0 c 1 1b e3 0 b7 2 50 33 4 6f 91 1 a0 0 96
  //   1 50 1b 4 60 1 4c 4d 60 1 6 0 0 ff 77 0 c7 8 87 0 61 20 62 74
endmodule
module AT28C64B_MC0 (
  input  VCC,
  input  NC0,
  input  nWE,
  input  A12,
  input  NC1,
  input  A7,
  input  A8,
  input  A6,
  input  A9,
  input  A5,
  input  A11,
  input  A4,
  input  nOE,
  input  A3,
  input  A10,
  input  A2,
  input  nCE,
  input  A1,
  input  A0,
  input  GND,
  output IO7,
  output IO6,
  output IO0,
  output IO5,
  output IO1,
  output IO4,
  output IO2,
  output IO3
);

  wire and_1_out, nor_1_out;
  wire [7:0] rom_1_data;

  ROM #(.addrWidth(13)) rom_1 (.addr({A12, A11, A10, A9, A8, A7, A6, A5, A4, A3, A2, A1, A0}), .data(rom_1_data));
  assign {IO7, IO6, IO5, IO4, IO3, IO2, IO1, IO0} = and_1_out ? rom_1_data : 8'bz;  // Controlled_Buffer controlled_buffer_1
  and and_1 (and_1_out, nor_1_out, nWE);
  nor nor_1 (nor_1_out, nCE, nOE);

  // Notes on the sheet:
  //   contents of rom_1 (hex, n*v repeats v):
  //   8*0 82 8 6*0 5 7*0 1 7*0 8c 7*0 88 7*0 a 20 6*0 8a 20 14*0 10 3 6*0 20 10 14*0 40 7*0 c0 7*0 40 7*0
  //   c0 7*0 40 80 6*0 c0 80 6*0 81 2 8 4 4*0 81 82 8 4 4*0 81 2 8 4 4*0 81 82 8 4 4*0 81 2 8 5*0 81 82 8
  //   5*0 81 2 8 5*0 81 82 8 5*0 81 2 8 5*0 81 82 8 5*0 81 2 4 5*0 81 82 4 5*0 81 2 8 4 4*0 81 82 8 4
endmodule

module AT28C64B_MC1 (
  input  VCC,
  input  NC0,
  input  nWE,
  input  A12,
  input  NC1,
  input  A7,
  input  A8,
  input  A6,
  input  A9,
  input  A5,
  input  A11,
  input  A4,
  input  nOE,
  input  A3,
  input  A10,
  input  A2,
  input  nCE,
  input  A1,
  input  A0,
  input  GND,
  output IO7,
  output IO6,
  output IO0,
  output IO5,
  output IO1,
  output IO4,
  output IO2,
  output IO3
);

  wire and_1_out, nor_1_out;
  wire [7:0] rom_1_data;

  ROM #(.addrWidth(13)) rom_1 (.addr({A12, A11, A10, A9, A8, A7, A6, A5, A4, A3, A2, A1, A0}), .data(rom_1_data));
  assign {IO7, IO6, IO5, IO4, IO3, IO2, IO1, IO0} = and_1_out ? rom_1_data : 8'bz;  // Controlled_Buffer controlled_buffer_1
  and and_1 (and_1_out, nor_1_out, nWE);
  nor nor_1 (nor_1_out, nCE, nOE);

  // Notes on the sheet:
  //   contents of rom_1 (hex, n*v repeats v):
  //   45 7*40 82 c1 6*40 41 7*40 41 23*40 4 7*40 0 15*40 0 41 6*40 84 c8 14*40 44 15*40 84 51 6*40 82 51
  //   6*40 84 60 6*40 82 60 6*40 80 84 81 c0 4*40 80 82 81 c0 4*40 80 84 81 c0 4*40 80 82 81 c0 4*40 80 84
  //   c1 5*40 80 82 c1 5*40 80 84 c1 5*40 80 82 c1 5*40 80 84 c1 5*40 80 82 c1 5*40 80 84 c0 5*40 80 82 c0
  //   5*40 80 84 81 c0 4*40 80 82 81 c0 4*40
endmodule

module AS6C6264 (
  input  CLK,
  input  VCC,
  input  NC0,
  input  nWE,
  input  A12,
  input  CE2,
  input  A7,
  input  A8,
  input  A6,
  input  A9,
  input  A5,
  input  A11,
  input  A4,
  input  nOE,
  input  A3,
  input  A10,
  input  A2,
  input  nCE,
  input  A1,
  input  A0,
  input  GND,
  input  I0,
  input  I1,
  input  I2,
  input  I3,
  input  I4,
  input  I5,
  input  I6,
  input  I7,
  output IO7,
  output IO6,
  output IO0,
  output IO5,
  output IO1,
  output IO4,
  output IO2,
  output IO3
);

  wire and_1_out, and_2_out, not_1_out, not_2_out, not_3_out, not_4_out;
  wire [7:0] ram_1_dout;

  and and_1 (and_1_out, not_1_out, CE2, not_2_out);
  not not_1 (not_1_out, nCE);
  not not_2 (not_2_out, nWE);
  and and_2 (and_2_out, not_3_out, CE2, not_4_out, nWE);
  not not_3 (not_3_out, nCE);
  not not_4 (not_4_out, nOE);
  RAM #(.addrWidth(13), .asyncread("true")) ram_1 (
    .addr({A12, A11, A10, A9, A8, A7, A6, A5, A4, A3, A2, A1, A0}), .we(and_1_out), .oe(and_2_out),
    .clk(CLK), .din({I7, I6, I5, I4, I3, I2, I1, I0}), .dout(ram_1_dout));
  assign {IO7, IO6, IO5, IO4, IO3, IO2, IO1, IO0} = and_2_out ? ram_1_dout : 8'bz;  // Controlled_Buffer controlled_buffer_1
endmodule

module mem74 (
  input  clk,
  input  erom,
  input  eram,
  input  lram,
  input  [15:0] addr,
  input  [7:0] dbus,
  output [7:0] dbus_out
);

  wire n_eram, n_erom, n_lram;

  _7404 #(.ShowInternalStructure("true")) u_7404_1 (
    .pin1(erom), .pin2(n_erom), .pin3(eram), .pin4(n_eram), .pin5(lram), .pin6(n_lram));  // open: pin13, pin12, pin11, pin10, pin9, pin8
  AT28C64B_MAIN ROM (
    .IO0(dbus_out[0]), .IO1(dbus_out[1]), .IO2(dbus_out[2]), .IO7(dbus_out[7]), .IO6(dbus_out[6]),
    .IO5(dbus_out[5]), .IO4(dbus_out[4]), .IO3(dbus_out[3]), .A12(addr[12]), .A7(addr[7]), .A6(addr[6]),
    .A5(addr[5]), .A4(addr[4]), .A3(addr[3]), .A2(addr[2]), .A1(addr[1]), .A0(addr[0]), .nWE(1'b1),
    .A8(addr[8]), .A9(addr[9]), .A11(addr[11]), .nOE(n_erom), .A10(addr[10]), .nCE(1'b0));  // open: NC0, GND, NC1, VCC
  AS6C6264 RAM (
    .IO0(dbus_out[0]), .IO1(dbus_out[1]), .IO2(dbus_out[2]), .IO7(dbus_out[7]), .IO6(dbus_out[6]),
    .IO5(dbus_out[5]), .IO4(dbus_out[4]), .IO3(dbus_out[3]), .I0(dbus[0]), .I1(dbus[1]), .I2(dbus[2]),
    .I3(dbus[3]), .I4(dbus[4]), .I5(dbus[5]), .I6(dbus[6]), .I7(dbus[7]), .A12(addr[12]), .A7(addr[7]),
    .A6(addr[6]), .A5(addr[5]), .A4(addr[4]), .A3(addr[3]), .A2(addr[2]), .A1(addr[1]), .A0(addr[0]),
    .CLK(clk), .nWE(n_lram), .CE2(1'b1), .A8(addr[8]), .A9(addr[9]), .A11(addr[11]), .nOE(n_eram),
    .A10(addr[10]), .nCE(1'b0));  // open: NC0, GND, VCC

  // Other names for the same wires on the sheet: ad0 = addr[0]; ad1 = addr[1]; ad2 = addr[2]; ad3 = addr[3];
  //   ad4 = addr[4]; ad5 = addr[5]; ad6 = addr[6]; ad7 = addr[7]; ad8 = addr[8]; ad9 = addr[9]; adA = addr[10];
  //   adB = addr[11]; adC = addr[12]; adD = addr[13]; adE = addr[14]; adF = addr[15]; d0 = dbus[0]; d1 = dbus[1];
  //   d2 = dbus[2]; d3 = dbus[3]; d4 = dbus[4]; d5 = dbus[5]; d6 = dbus[6]; d7 = dbus[7]; q0 = dbus_out[0];
  //   q1 = dbus_out[1]; q2 = dbus_out[2]; q3 = dbus_out[3]; q4 = dbus_out[4]; q5 = dbus_out[5]; q6 = dbus_out[6];
  //   q7 = dbus_out[7]
endmodule

module control74 (
  input  nclk,
  input  ex,
  input  [1:0] opc,
  input  [2:0] exc,
  input  [7:0] op0,
  output eram,
  output asp,
  output aimm,
  output lram,
  output spinc,
  output spdec,
  output jnz,
  output ldx,
  output ldy,
  output ldf,
  output ealu,
  output ldh,
  output ldl,
  output lprt,
  output ereg,
  output lreg,
  output sel,
  output eop1,
  output eop2,
  output edev,
  output ldev,
  output cc
);

  wire eta, etb, mc0, mc0_x, mc1, mc1_x, mc2, mc2_x, mc3, mc3_x, mc4, mc4_x, mc5, mc5_x, mc6, mc6_x, mc7,
       mc7_x, mc8, mc8_x, mc9, mc9_x, mcA, mcA_x, mcB, mcB_x, mcC, mcC_x, mcD, mcD_x, mcE, mcE_x, mcF, mcF_x,
       n74573_1_pin1, n74573_2_pin1, n_ex, n_mcE_x, n_mcF_x, n_opc0;

  _7408 #(.ShowInternalStructure("true")) u_7408_1 (
    .pin1(mc1_x), .pin2(eta), .pin3(asp), .pin4(mc0_x), .pin5(eta), .pin6(eram), .pin13(mc2_x), .pin12(eta),
    .pin11(aimm), .pin10(mc3_x), .pin9(eta), .pin8(lram));
  _7408 #(.ShowInternalStructure("true")) u_7408_2 (
    .pin1(mc5_x), .pin2(eta), .pin3(spdec), .pin4(mc4_x), .pin5(eta), .pin6(spinc), .pin13(mc6_x),
    .pin12(eta), .pin11(jnz), .pin10(mc0_x), .pin9(etb), .pin8(ldx));
  _7408 #(.ShowInternalStructure("true")) u_7408_3 (
    .pin1(mc2_x), .pin2(etb), .pin3(ldf), .pin4(mc1_x), .pin5(etb), .pin6(ldy), .pin13(mc3_x), .pin12(etb),
    .pin11(ealu), .pin10(mc4_x), .pin9(etb), .pin8(ldh));
  _7408 #(.ShowInternalStructure("true")) u_7408_4 (
    .pin1(mc6_x), .pin2(etb), .pin3(lprt), .pin4(mc5_x), .pin5(etb), .pin6(ldl), .pin13(mc7_x), .pin12(ex),
    .pin11(ereg), .pin10(mc8_x), .pin9(ex), .pin8(lreg));
  _7408 #(.ShowInternalStructure("true")) u_7408_5 (
    .pin1(mcA_x), .pin2(ex), .pin3(eop1), .pin4(mc9_x), .pin5(ex), .pin6(sel), .pin13(mcB_x), .pin12(ex),
    .pin11(eop2), .pin10(mcC_x), .pin9(ex), .pin8(edev));
  _74573 u_74573_1 (
    .pin1(n74573_1_pin1), .pin2(mc0), .pin3(mc1), .pin4(mc2), .pin5(mc3), .pin6(mc4), .pin7(mc5), .pin8(mc6),
    .pin9(mc7), .pin19(mc0_x), .pin18(mc1_x), .pin17(mc2_x), .pin16(mc3_x), .pin15(mc4_x), .pin14(mc5_x),
    .pin13(mc6_x), .pin12(mc7_x), .pin11(nclk));
  _74573 u_74573_2 (
    .pin1(n74573_2_pin1), .pin2(mc8), .pin3(mc9), .pin4(mcA), .pin5(mcB), .pin6(mcC), .pin7(mcD), .pin8(mcE),
    .pin9(mcF), .pin19(mc8_x), .pin18(mc9_x), .pin17(mcA_x), .pin16(mcB_x), .pin15(mcC_x), .pin14(mcD_x),
    .pin13(mcE_x), .pin12(mcF_x), .pin11(nclk));
  _7404 #(.ShowInternalStructure("true")) u_7404_1 (
    .pin1(mcE_x), .pin2(n_mcE_x), .pin3(mcF_x), .pin4(n_mcF_x), .pin5(ex), .pin6(n_ex), .pin13(opc[0]),
    .pin12(n_opc0));  // open: pin11, pin10, pin9, pin8
  _7408 #(.ShowInternalStructure("true")) u_7408_6 (
    .pin1(mcD_x), .pin2(ex), .pin3(ldev), .pin4(mcE_x), .pin5(ex), .pin6(cc), .pin13(n_mcF_x), .pin12(ex),
    .pin11(eta), .pin10(mcF_x), .pin9(ex), .pin8(etb));
  AT28C64B_MC0 at28c64b_mc0_1 (
    .IO0(mc0), .IO1(mc1), .IO2(mc2), .IO7(mc7), .IO6(mc6), .IO5(mc5), .IO4(mc4), .IO3(mc3), .A12(1'b0),
    .A7(op0[7]), .A6(op0[6]), .A5(op0[5]), .A4(op0[4]), .A3(op0[3]), .A2(exc[2]), .A1(exc[1]), .A0(exc[0]),
    .nWE(1'b1), .A8(1'b0), .A9(1'b0), .A11(1'b0), .nOE(1'b0), .A10(1'b0), .nCE(1'b0));  // open: NC0, GND, NC1, VCC
  AT28C64B_MC1 at28c64b_mc1_1 (
    .IO0(mc8), .IO1(mc9), .IO2(mcA), .IO7(mcF), .IO6(mcE), .IO5(mcD), .IO4(mcC), .IO3(mcB), .A12(1'b0),
    .A7(op0[7]), .A6(op0[6]), .A5(op0[5]), .A4(op0[4]), .A3(op0[3]), .A2(exc[2]), .A1(exc[1]), .A0(exc[0]),
    .nWE(1'b1), .A8(1'b0), .A9(1'b0), .A11(1'b0), .nOE(1'b0), .A10(1'b0), .nCE(1'b0));  // open: NC0, GND, NC1, VCC
  // also tied to GND on the sheet: {n74573_1_pin1, n74573_2_pin1}
endmodule

module dev74 (
  input  nclk,
  input  clk,
  input  edev,
  input  ldev,
  input  lprt,
  input  [7:0] dbus,
  output err_out,
  output hlt_out,
  output [7:0] dbus_out
);

  wire esta, lprt_x, lsta, n7408_1_pin3, n74573_1_pin1, n74573_1_pin12, n74573_1_pin13, n74573_1_pin14,
       n74573_1_pin15, n74573_1_pin17, n74573_1_pin19, n74573_2_pin1, n74573_3_pin11, n_esta, prt0, prt1,
       prt2, prt3, prt4, prt5, prt6, prt7, prt_EQ_0;

  _74573 u_74573_1 (
    .pin1(n74573_1_pin1), .pin2(dbus[0]), .pin3(dbus[1]), .pin4(dbus[2]), .pin5(dbus[3]), .pin6(dbus[4]),
    .pin7(dbus[5]), .pin8(dbus[6]), .pin9(dbus[7]), .pin19(n74573_1_pin19), .pin18(err_out),
    .pin17(n74573_1_pin17), .pin16(hlt_out), .pin15(n74573_1_pin15), .pin14(n74573_1_pin14),
    .pin13(n74573_1_pin13), .pin12(n74573_1_pin12), .pin11(lsta));
  _74573 u_74573_2 (
    .pin1(n74573_2_pin1), .pin2(dbus[0]), .pin3(dbus[1]), .pin4(dbus[2]), .pin5(dbus[3]), .pin6(dbus[4]),
    .pin7(dbus[5]), .pin8(dbus[6]), .pin9(dbus[7]), .pin19(prt0), .pin18(prt1), .pin17(prt2), .pin16(prt3),
    .pin15(prt4), .pin14(prt5), .pin13(prt6), .pin12(prt7), .pin11(lprt_x));
  _7430 #(.ShowInternalStructure("true")) u_7430_1 (
    .pin1(prt5), .pin2(prt4), .pin3(prt3), .pin4(prt2), .pin5(prt1), .pin6(prt0), .pin12(prt6), .pin11(prt7),
    .pin8(prt_EQ_0));  // open: pin13, pin10, pin9
  _7408 #(.ShowInternalStructure("true")) u_7408_1 (
    .pin1(nclk), .pin2(ldev), .pin3(n7408_1_pin3), .pin4(n7408_1_pin3), .pin5(prt_EQ_0), .pin6(lsta),
    .pin13(lprt), .pin12(nclk), .pin11(lprt_x), .pin10(edev), .pin9(prt_EQ_0), .pin8(esta));
  _7404 #(.ShowInternalStructure("true")) u_7404_1 (
    .pin13(esta), .pin12(n_esta));  // open: pin1, pin2, pin3, pin4, pin5, pin6, pin11, pin10, pin9, pin8
  _74573 u_74573_3 (
    .pin1(n_esta), .pin2(n74573_1_pin19), .pin3(err_out), .pin4(n74573_1_pin17), .pin5(hlt_out),
    .pin6(n74573_1_pin15), .pin7(n74573_1_pin14), .pin8(n74573_1_pin13), .pin9(n74573_1_pin12),
    .pin19(dbus_out[0]), .pin18(dbus_out[1]), .pin17(dbus_out[2]), .pin16(dbus_out[3]), .pin15(dbus_out[4]),
    .pin14(dbus_out[5]), .pin13(dbus_out[6]), .pin12(dbus_out[7]), .pin11(n74573_3_pin11));
  LED err (.in(err_out));
  LED hlt (.in(hlt_out));
  // also tied to GND on the sheet: {n74573_1_pin1, n74573_2_pin1}
  // also tied to VCC on the sheet: n74573_3_pin11

  // Other names for the same wires on the sheet: d0 = dbus[0]; d1 = dbus[1]; d2 = dbus[2]; d3 = dbus[3]; d4 = dbus[4];
  //   d5 = dbus[5]; d6 = dbus[6]; d7 = dbus[7]; q0 = dbus_out[0]; q1 = dbus_out[1]; q2 = dbus_out[2];
  //   q3 = dbus_out[3]; q4 = dbus_out[4]; q5 = dbus_out[5]; q6 = dbus_out[6]; q7 = dbus_out[7]; err = err_out;
  //   hlt = hlt_out
endmodule

module vram74 (
  input  rise,
  input  fall,
  input  nclk,
  input  clk,
  input  ebank,
  input  lbank,
  input  [7:0] dbus,
  input  [7:0] mb,
  input  [12:0] vma,
  input  [15:0] addr,
  output [7:0] vd,
  output [7:0] dbus_out
);

  wire bank, evram, lvram, n74573_1_pin11, n74573_2_pin7, n74573_2_pin8, n74573_2_pin9, n74573_2_pin11,
       n74573_3_pin11, n74573_4_pin11, n74573_5_pin11, n_bank, n_evram, n_lvram, n_mb0, vma0_x, vma1_x,
       vma2_x, vma3_x, vma4_x, vma5_x, vma6_x, vma7_x, vma8_x, vma9_x, vmaA_x, vmaB_x, vmaC_x, vram;

  _74573 u_74573_1 (
    .pin1(bank), .pin2(vma[0]), .pin3(vma[1]), .pin4(vma[2]), .pin5(vma[3]), .pin6(vma[4]), .pin7(vma[5]),
    .pin8(vma[6]), .pin9(vma[7]), .pin19(vma0_x), .pin18(vma1_x), .pin17(vma2_x), .pin16(vma3_x),
    .pin15(vma4_x), .pin14(vma5_x), .pin13(vma6_x), .pin12(vma7_x), .pin11(n74573_1_pin11));
  _74573 u_74573_2 (
    .pin1(bank), .pin2(vma[8]), .pin3(vma[9]), .pin4(vma[10]), .pin5(vma[11]), .pin6(vma[12]),
    .pin7(n74573_2_pin7), .pin8(n74573_2_pin8), .pin9(n74573_2_pin9), .pin19(vma8_x), .pin18(vma9_x),
    .pin17(vmaA_x), .pin16(vmaB_x), .pin15(vmaC_x), .pin11(n74573_2_pin11));  // open: pin14, pin13, pin12
  _74573 u_74573_3 (
    .pin1(n_bank), .pin2(addr[0]), .pin3(addr[1]), .pin4(addr[2]), .pin5(addr[3]), .pin6(addr[4]),
    .pin7(addr[5]), .pin8(addr[6]), .pin9(addr[7]), .pin19(vma0_x), .pin18(vma1_x), .pin17(vma2_x),
    .pin16(vma3_x), .pin15(vma4_x), .pin14(vma5_x), .pin13(vma6_x), .pin12(vma7_x), .pin11(n74573_3_pin11));
  _74573 u_74573_4 (
    .pin1(n_bank), .pin2(addr[8]), .pin3(addr[9]), .pin4(addr[10]), .pin5(addr[11]), .pin6(addr[12]),
    .pin7(addr[13]), .pin8(addr[14]), .pin9(addr[15]), .pin19(vma8_x), .pin18(vma9_x), .pin17(vmaA_x),
    .pin16(vmaB_x), .pin15(vmaC_x), .pin11(n74573_4_pin11));  // open: pin14, pin13, pin12
  AS6C6264 as6c6264_1 (
    .IO0(vd[0]), .IO1(vd[1]), .IO2(vd[2]), .IO7(vd[7]), .IO6(vd[6]), .IO5(vd[5]), .IO4(vd[4]), .IO3(vd[3]),
    .I0(dbus[0]), .I1(dbus[1]), .I2(dbus[2]), .I3(dbus[3]), .I4(dbus[4]), .I5(dbus[5]), .I6(dbus[6]),
    .I7(dbus[7]), .A12(vmaC_x), .A7(vma7_x), .A6(vma6_x), .A5(vma5_x), .A4(vma4_x), .A3(vma3_x), .A2(vma2_x),
    .A1(vma1_x), .A0(vma0_x), .CLK(clk), .nWE(n_lvram), .CE2(1'b1), .A8(vma8_x), .A9(vma9_x), .A11(vmaB_x),
    .nOE(1'b0), .A10(vmaA_x), .nCE(1'b0));  // open: NC0, GND, VCC
  _7404 u_7404_1 (
    .pin1(mb[0]), .pin2(n_mb0), .pin3(evram), .pin4(n_evram), .pin5(lvram), .pin6(n_lvram), .pin13(bank),
    .pin12(n_bank));  // open: pin11, pin10, pin9, pin8
  _7430 u_7430_1 (
    .pin1(mb[5]), .pin2(mb[4]), .pin3(mb[3]), .pin4(mb[2]), .pin5(mb[1]), .pin6(n_mb0), .pin12(mb[6]),
    .pin11(mb[7]), .pin8(vram));  // open: pin13, pin10, pin9
  _7408 #(.ShowInternalStructure("true")) u_7408_1 (
    .pin1(vram), .pin2(ebank), .pin3(evram), .pin4(vram), .pin5(lbank), .pin6(lvram));  // open: pin13, pin12, pin11, pin10, pin9, pin8
  _7432 u_7432_1 (
    .pin1(ebank), .pin2(lbank), .pin3(bank));  // open: pin4, pin5, pin6, pin13, pin12, pin11, pin10, pin9, pin8
  _74573 u_74573_5 (
    .pin1(n_evram), .pin2(vd[0]), .pin3(vd[1]), .pin4(vd[2]), .pin5(vd[3]), .pin6(vd[4]), .pin7(vd[5]),
    .pin8(vd[6]), .pin9(vd[7]), .pin19(dbus_out[0]), .pin18(dbus_out[1]), .pin17(dbus_out[2]),
    .pin16(dbus_out[3]), .pin15(dbus_out[4]), .pin14(dbus_out[5]), .pin13(dbus_out[6]), .pin12(dbus_out[7]),
    .pin11(n74573_5_pin11));
  // also tied to GND on the sheet: {n74573_2_pin7, n74573_2_pin8, n74573_2_pin9}
  // also tied to VCC on the sheet: {n74573_1_pin11, n74573_2_pin11, n74573_3_pin11, n74573_4_pin11, n74573_5_pin11}

  // Other names for the same wires on the sheet: ad0 = addr[0]; ad1 = addr[1]; ad2 = addr[2]; ad3 = addr[3];
  //   ad4 = addr[4]; ad5 = addr[5]; ad6 = addr[6]; ad7 = addr[7]; ad8 = addr[8]; ad9 = addr[9]; adA = addr[10];
  //   adB = addr[11]; adC = addr[12]; adD = addr[13]; adE = addr[14]; adF = addr[15]; d0 = dbus[0]; d1 = dbus[1];
  //   d2 = dbus[2]; d3 = dbus[3]; d4 = dbus[4]; d5 = dbus[5]; d6 = dbus[6]; d7 = dbus[7]; q0 = dbus_out[0];
  //   q1 = dbus_out[1]; q2 = dbus_out[2]; q3 = dbus_out[3]; q4 = dbus_out[4]; q5 = dbus_out[5]; q6 = dbus_out[6];
  //   q7 = dbus_out[7]; vmaA = vma[10]; vmaB = vma[11]; vmaC = vma[12]

  // Notes on the sheet:
  //   ANDs should be on another board
  //   bank signal already exists on addr
endmodule

module main74 (
);

  wire a0, a001, a1, a2, a3, a4, a5, a6, a7, a010, a101, a_aux, a_bank, a_en, a_upper, a_we, ad0, ad1, ad2,
       ad3, ad4, ad5, ad6, ad7, ad8, ad9, adA, adB, adC, adD, adE, adF, aimm, asp, axd0, axd1, axd2, axd3,
       axd4, axd5, axd6, axd7, axq0, axq1, axq2, axq3, axq4, axq5, axq6, axq7, b0, b1, b2, b3, b4, b5, b6,
       b7, b_en, b_in, b_out, b_we, bank, bank_vram, c_en, c_in, c_out, c_we, cc, clk, d0, d1, d2, d3, d4,
       d5, d6, d7, d_en, d_EQ_0, d_nEQ_0, d_we, dx0, dx1, dx2, dx3, dx4, dx5, dx6, dx7, ealu, eaux, ebank,
       edev, el_vram, emem, emem_x, eop1, eop2, EQ_5_pin1, EQ_5_pin3, EQ_5_pin5, EQ_5_pin7, EQ_5_pin9,
       EQ_5_pin12, EQ_5_pin14, EQ_5_pin16, EQ_5_pin18, EQ_6F_pin1, EQ_6F_pin3, EQ_6F_pin5, EQ_6F_pin7,
       EQ_6F_pin9, EQ_6F_pin12, EQ_6F_pin14, EQ_6F_pin16, EQ_6F_pin18, EQ_09_pin1, EQ_09_pin3, EQ_09_pin5,
       EQ_09_pin7, EQ_09_pin9, EQ_09_pin12, EQ_09_pin14, EQ_09_pin16, EQ_09_pin18, EQ_33_pin1, EQ_33_pin3,
       EQ_33_pin5, EQ_33_pin7, EQ_33_pin9, EQ_33_pin12, EQ_33_pin14, EQ_33_pin16, EQ_33_pin18, EQ_54_pin1,
       EQ_54_pin3, EQ_54_pin5, EQ_54_pin7, EQ_54_pin9, EQ_54_pin12, EQ_54_pin14, EQ_54_pin16, EQ_54_pin18,
       EQ_69_pin1, EQ_69_pin3, EQ_69_pin5, EQ_69_pin7, EQ_69_pin9, EQ_69_pin12, EQ_69_pin14, EQ_69_pin16,
       EQ_69_pin18, eram, ereg, erom, esta, eta, etb, evram, ex, exc0, exc1, exc2, f4, f5, f6, f7, f_en,
       f_pin1, f_we, flag_b, flag_c, flag_e, flag_l, h0, h1, h2, h3, h4, h5, h6, h7, h_en, h_pin1, h_we,
       hsc0, hsc0Q, hsc1, hsc1Q, hsc2, hsc2Q, hsc3, hsc3Q, hsc4, hsc4Q, hsc5, hsc5Q, hsc6, hsc7, hsc8, hsc9,
       HSC_0_pin3, HSC_0_pin4, HSC_0_pin5, HSC_0_pin6, HSC_0_pin7, HSC_0_pin9, HSC_0_pin15, HSC_1_pin1,
       HSC_1_pin3, HSC_1_pin4, HSC_1_pin5, HSC_1_pin6, HSC_1_pin7, HSC_1_pin9, HSC_1_pin15, HSC_2_pin3,
       HSC_2_pin4, HSC_2_pin5, HSC_2_pin6, HSC_2_pin7, HSC_2_pin9, hsc_eORd, hsc_inc, hsc_n1S, hsc_n2S,
       hsc_n3S, hsc_n4S, hsc_n5S, hsc_n9, hsc_nEQ_05, hsc_nEQ_6A, hsc_nEQ_6E, hsc_nEQ_34, hsc_nEQ_54,
       hsc_nEQ_A, hsc_nR, hsc_or_89, hsc_pp, jmp, jnz, l0, l1, l2, l3, l4, l5, l6, l7, l_en, l_pin1, l_we,
       latch_vram, lbank, ld1, ld1_x, ld2, ld2_x, ld3, ld3_x, ldev, ldf, ldh, ldl, ldx, ldy, lmb, lmem, lop0,
       lop1, lop2, lopN, lpreset, lprt, lprt_x, lram, lreg, lsta, lvram, mb0, mb1, mb2, mb3, mb4, mb5, mb6,
       mb7, mb_EQ_0, mb_nEQ_0, mb_nEQ_1, mb_nGT_1, mb_pin1, mc0, mc0_x, mc1, mc1_x, mc2, mc2_x, mc3, mc3_x,
       mc4, mc4_x, mc5, mc5_x, mc6, mc6_x, mc7, mc7_x, mc8, mc8_x, mc9, mc9_x, mcA, mcA_x, mcB, mcB_x, mcC,
       mcC_x, mcD, mcD_x, mcE, mcE_x, mcF, mcF_x, mw_lda, n0, n1, n2, n3, n4, n5, n6, n7, n7402_1_pin1,
       n7402_1_pin2, n7404_1_pin2, n7404_1_pin6, n7404_4_pin3, n7404_13_pin6, n7404_13_pin8, n7408_3_pin8,
       n7411_2_pin6, n7411_2_pin11, n7411_3_pin2, n7411_3_pin9, n7411_3_pin13, n7411_4_pin13, n7411_5_pin13,
       n7421_1_pin6, n7421_1_pin8, n7421_2_pin6, n7427_1_pin6, n7427_1_pin13, n7427_2_pin9, n7432_2_pin11,
       n7432_3_pin3, n7432_3_pin6, n7432_3_pin8, n7432_3_pin11, n7432_4_pin3, n7432_4_pin6, n7432_5_pin3,
       n7432_5_pin6, n7432_5_pin11, n7432_6_pin3, n7432_6_pin11, n7432_10_pin6, n7432_10_pin11, n7485_1_pin1,
       n7485_1_pin2, n7485_1_pin3, n7485_1_pin4, n7485_1_pin9, n7485_1_pin11, n7485_1_pin14, n7485_2_pin2,
       n7485_2_pin3, n7485_2_pin4, n7485_2_pin5, n7485_2_pin6, n7485_2_pin7, n74125_1_pin1, n74125_1_pin3,
       n74125_1_pin4, n74125_1_pin6, n74125_1_pin8, n74125_1_pin10, n74125_1_pin13, n74125_2_pin1,
       n74125_2_pin3, n74125_2_pin4, n74125_2_pin6, n74125_2_pin8, n74125_2_pin10, n74125_2_pin11,
       n74125_2_pin13, n74125_3_pin1, n74125_3_pin3, n74125_3_pin4, n74125_3_pin6, n74125_3_pin8,
       n74125_3_pin10, n74125_3_pin11, n74125_3_pin13, n74125_4_pin1, n74125_4_pin3, n74125_4_pin4,
       n74125_4_pin6, n74125_4_pin8, n74125_4_pin10, n74125_4_pin11, n74125_4_pin13, n74125_5_pin1,
       n74125_5_pin3, n74125_5_pin4, n74125_5_pin6, n74125_5_pin8, n74125_5_pin10, n74125_5_pin11,
       n74125_5_pin13, n74125_6_pin1, n74125_6_pin3, n74125_6_pin4, n74125_6_pin6, n74125_6_pin8,
       n74125_6_pin10, n74125_6_pin11, n74125_6_pin13, n74138_1_pin4, n74138_3_pin4, n74138_3_pin5,
       n74138_4_pin4, n74138_4_pin5, n74151_1_pin7, n74163_1_pin3, n74163_1_pin4, n74163_1_pin5,
       n74163_1_pin6, n74163_1_pin9, n74163_1_pin10, n74163_2_pin3, n74163_2_pin4, n74163_2_pin5,
       n74163_2_pin6, n74163_2_pin9, n74163_2_pin10, n74163_3_pin3, n74163_3_pin4, n74163_3_pin5,
       n74163_3_pin6, n74163_3_pin9, n74163_3_pin10, n74163_3_pin13, n74163_3_pin14, n74238_1_pin3,
       n74238_1_pin4, n74238_1_pin5, n74238_1_pin6, n74238_2_pin4, n74238_3_pin3, n74238_3_pin4,
       n74238_3_pin5, n74238_3_pin6, n74244_1_pin1, n74244_1_pin19, n74244_2_pin1, n74244_2_pin19,
       n74244_3_pin1, n74244_3_pin19, n74244_10_pin1, n74244_10_pin19, n74244_17_pin11, n74244_17_pin13,
       n74244_17_pin15, n74244_17_pin17, n74283_1_pin2, n74283_1_pin6, n74283_1_pin7, n74283_1_pin9,
       n74283_1_pin11, n74283_1_pin15, n74283_2_pin2, n74283_2_pin6, n74283_2_pin9, n74283_2_pin11,
       n74283_2_pin15, n74283_3_pin2, n74283_3_pin6, n74283_3_pin11, n74283_3_pin15, n74283_4_pin9,
       n74283_6_pin9, n74374_1_pin1, n74374_2_pin1, n74573_1_pin1, n74573_2_pin11, n74573_3_pin7,
       n74573_3_pin8, n74573_3_pin9, n74573_3_pin11, n74573_4_pin11, n74573_5_pin11, n74573_6_pin11,
       n74573_7_pin11, n74573_8_pin11, n74573_9_pin11, n74573_10_pin1, n74573_11_pin1, n74573_12_pin11,
       n74573_13_pin11, n74573_14_pin11, n74573_15_pin11, n74573_16_pin1, n74573_16_pin11, n74573_16_pin12,
       n74573_16_pin13, n74573_16_pin14, n74573_16_pin15, n74573_16_pin16, n74573_16_pin17, n74573_16_pin18,
       n74573_16_pin19, n74573_17_pin1, n74573_18_pin11, n74573_19_pin11, n74573_20_pin11, n74573_21_pin11,
       n74573_22_pin11, n74573_23_pin1, n74573_24_pin11, n74573_25_pin11, n74573_26_pin11, n74682_1_pin3,
       n74682_1_pin5, n74682_1_pin7, n74682_1_pin9, n74682_1_pin12, n74682_1_pin14, n74682_1_pin16,
       n74682_1_pin17, n74682_1_pin18, n74682_2_pin3, n74682_2_pin5, n74682_2_pin7, n74682_2_pin9,
       n74682_2_pin12, n74682_2_pin14, n74682_2_pin16, n74682_2_pin17, n74682_2_pin18, n74682_3_pin3,
       n74682_3_pin5, n74682_3_pin7, n74682_3_pin9, n74682_3_pin12, n74682_3_pin14, n74682_3_pin16,
       n74682_3_pin18, n74688_1_pin1, n74688_1_pin3, n74688_1_pin5, n74688_1_pin7, n74688_1_pin9,
       n74688_1_pin12, n74688_1_pin14, n74688_1_pin16, n74688_1_pin18, n74688_2_pin1, n74688_2_pin3,
       n74688_2_pin5, n74688_2_pin7, n74688_2_pin9, n74688_2_pin12, n74688_2_pin14, n74688_2_pin16,
       n74688_2_pin18, n74688_3_pin1, n74688_3_pin3, n74688_3_pin5, n74688_3_pin7, n74688_3_pin9,
       n74688_3_pin12, n74688_3_pin14, n74688_3_pin16, n74688_3_pin18, n74688_4_pin1, n74688_4_pin3,
       n74688_4_pin5, n74688_4_pin7, n74688_4_pin9, n74688_4_pin12, n74688_4_pin14, n74688_4_pin16,
       n74688_4_pin18, n74688_5_pin1, n74688_5_pin3, n74688_5_pin5, n74688_5_pin7, n74688_5_pin9,
       n74688_5_pin11, n74688_5_pin13, n74688_5_pin15, n74688_5_pin17, n_adE, n_adF, n_ahl, n_aimm, n_apc,
       n_asp, n_bank, n_cc, n_eaux, n_el_vram, n_emb, n_eop1, n_eop2, n_epch, n_epcl, n_eram, n_ereg, n_erom,
       n_esph, n_espl, n_esta, n_evram, n_ex, n_hlt, n_jmp, n_jmp_x, n_lmb, n_lmem, n_lpch, n_lpch_x, n_lpcl,
       n_lpcl_x, n_lram, n_lsph, n_lspl, n_lvram, n_mcF_x, n_mw_lda, n_pcinc_x, n_r_we, n_seq_3, n_spdec_x,
       n_spinc_x, nb_out, nclk, nE_adc, nE_add, nE_add_adc, nE_and, nE_cmp, nE_nor, nE_or, nE_pass, nE_sub,
       nLDF, nlpreset, nop0, nop1, nop2, nreset, nsel, nV03_broad, nV03_short, nV03_sync, ny, ny0, ny1, ny2,
       ny3, ny4, ny5, ny6, ny7, o0, o1, o2, o3, o4, o5, o6, o7, op0, op00, op0_pin1, op01, op1, op1_pin1,
       op02, op2, op2_pin1, op03, op3, op10, op11, op12, op13, op14, op15, op16, op17, op20, op21, op22,
       op23, op24, op25, op26, op27, op_gt_6, opc0, opc1, opc_eq_0, opc_eq_1, opc_eq_2, opc_eq_3, pc0,
       pc0_pin4, pc0_pin12, pc0_pin13, pc0x, pc1, pc1_pin12, pc1_pin13, pc1x, pc2, pc2_pin12, pc2_pin13,
       pc2x, pc3, pc3x, pc4, pc4x, pc5, pc5x, pc6, pc6x, pc7, pc7x, pc8, pc8x, pc9, pc9x, pcA, pcAx, pcB,
       pcBx, pcC, pcCx, pcD, pcDx, pcE, pcEx, pcF, pcFx, prt0, prt1, prt2, prt3, prt4, prt5, prt6, prt7,
       prt_EQ_0, r_we, rd0, rd1, rd2, rd3, rd4, rd5, rd6, rd7, reset, rise, rq0, rq1, rq2, rq3, rq4, rq5,
       rq6, rq7, rs_a, rs_b, rs_c, s0, s1, s2, s3, s4, s5, s6, s7, sel, sel0, sel00x, sel1, sel01x, sel02x,
       sel10x, sel11x, sel12x, seq_0, seq_1, seq_2, seq_3, sp0, sp0_pin12, sp0_pin13, sp0_pin14, sp1,
       sp1_pin12, sp1_pin13, sp1_pin14, sp2, sp2_pin12, sp2_pin13, sp2_pin14, sp3, sp3_pin14, sp4, sp5, sp6,
       sp7, sp8, sp9, spA, spB, spC, spD, spdec, spE, spF, spinc, st0, st1, st2, st3, st4, st5, st6, st7,
       tkc0, tkc0Q, tkc1, tkc1Q, tkc2, tkc2Q, tkc3, tkc3Q, tkc4, tkc5, tkc6, tkc7, tkc7_LE_6F, tkc7_LE_07,
       TKC_0_pin3, TKC_0_pin4, TKC_0_pin5, TKC_0_pin6, TKC_0_pin7, TKC_0_pin9, TKC_0_pin10, TKC_0_pin15,
       TKC_1_pin3, TKC_1_pin4, TKC_1_pin5, TKC_1_pin6, TKC_1_pin7, TKC_1_pin9, tkc_nEQ_0F, tkc_nEQ_0F_2,
       tkc_nEQ_28, tkc_nEQ_80, tkc_nEQ_F8, tkc_nRC0, tkc_RC0, v_03, v_10, vbit, vd0, vd0_x, vd1, vd1_x, vd2,
       vd2_x, vd3, vd3_x, vd4, vd4_x, vd5, vd5_x, vd6, vd6_x, vd7, vd7_x, vma0_x, vma1_x, vma2_x, vma3_x,
       vma4_x, vma5, vma5_x, vma6, vma6_x, vma7, vma7_x, vma8, vma8_x, vma9, vma9_x, vmaA, vmaA_x, vmaB,
       vmaB_x, vmaC, vmaC_x, vmaD, vmaE, vram_d0, vram_d1, vram_d2, vram_d3, vram_d4, vram_d5, vram_d6,
       vram_d7, x0, x1, x2, x3, x4, x5, x6, x7, xc, XeqY, XltY, y0, y1, y2, y3, y4, y5, y6, y7, yc, z_en,
       z_we;

  Hex_Digit_Display hex_digit_display_1 (.value({op3, op2, op1, op0}));  // open: dp
  Hex_Digit_Display hex_digit_display_2 (.value({op03, op02, op01, op00}));  // open: dp
  _74161 #(.ShowInternalStructure("true")) HSC_0 (
    .pin1(hsc_nR), .pin2(clk), .pin3(HSC_0_pin3), .pin4(HSC_0_pin4), .pin5(HSC_0_pin5), .pin6(HSC_0_pin6),
    .pin7(HSC_0_pin7), .pin15(HSC_0_pin15), .pin14(hsc0), .pin13(hsc1), .pin12(hsc2), .pin11(hsc3),
    .pin10(hsc_inc), .pin9(HSC_0_pin9));
  _74161 #(.ShowInternalStructure("true")) HSC_1 (
    .pin1(HSC_1_pin1), .pin2(clk), .pin3(HSC_1_pin3), .pin4(HSC_1_pin4), .pin5(HSC_1_pin5),
    .pin6(HSC_1_pin6), .pin7(HSC_1_pin7), .pin15(HSC_1_pin15), .pin14(hsc4), .pin13(hsc5), .pin12(hsc6),
    .pin11(hsc7), .pin10(HSC_0_pin15), .pin9(HSC_1_pin9));
  _74161 #(.ShowInternalStructure("true")) HSC_2 (
    .pin1(HSC_1_pin1), .pin2(clk), .pin3(HSC_2_pin3), .pin4(HSC_2_pin4), .pin5(HSC_2_pin5),
    .pin6(HSC_2_pin6), .pin7(HSC_2_pin7), .pin14(hsc8), .pin13(hsc9), .pin10(HSC_1_pin15), .pin9(HSC_2_pin9));  // open: pin15, pin12, pin11
  _74161 #(.ShowInternalStructure("true")) TKC_0 (
    .pin1(tkc_nRC0), .pin2(clk), .pin3(TKC_0_pin3), .pin4(TKC_0_pin4), .pin5(TKC_0_pin5), .pin6(TKC_0_pin6),
    .pin7(TKC_0_pin7), .pin15(TKC_0_pin15), .pin14(tkc0), .pin13(tkc1), .pin12(tkc2), .pin11(tkc3),
    .pin10(TKC_0_pin10), .pin9(TKC_0_pin9));
  _74161 #(.ShowInternalStructure("true")) TKC_1 (
    .pin1(tkc_nRC0), .pin2(clk), .pin3(TKC_1_pin3), .pin4(TKC_1_pin4), .pin5(TKC_1_pin5), .pin6(TKC_1_pin6),
    .pin7(TKC_1_pin7), .pin15(tkc_RC0), .pin14(tkc4), .pin13(tkc5), .pin12(tkc6), .pin11(tkc7),
    .pin10(TKC_0_pin15), .pin9(TKC_1_pin9));
  _7404 #(.ShowInternalStructure("true")) u_7404_1 (
    .pin1(hsc_nR), .pin2(n7404_1_pin2), .pin3(n7404_1_pin2), .pin4(HSC_1_pin1), .pin5(tkc_nEQ_0F),
    .pin6(n7404_1_pin6), .pin13(tkc_RC0), .pin12(tkc_nRC0), .pin11(hsc9), .pin10(hsc_n9),
    .pin9(n7404_1_pin6), .pin8(tkc_nEQ_0F_2));
  _74688 #(.ShowInternalStructure("true")) u_74688_1 (
    .pin1(n74688_1_pin1), .pin2(tkc0), .pin3(n74688_1_pin3), .pin4(tkc1), .pin5(n74688_1_pin5), .pin6(tkc2),
    .pin7(n74688_1_pin7), .pin8(tkc3), .pin9(n74688_1_pin9), .pin19(tkc_nEQ_80), .pin18(n74688_1_pin18),
    .pin17(tkc7), .pin16(n74688_1_pin16), .pin15(tkc6), .pin14(n74688_1_pin14), .pin13(tkc5),
    .pin12(n74688_1_pin12), .pin11(tkc4));
  _74682 #(.ShowInternalStructure("true")) u_74682_1 (
    .pin1(tkc7_LE_07), .pin2(tkc0), .pin3(n74682_1_pin3), .pin4(tkc1), .pin5(n74682_1_pin5), .pin6(tkc2),
    .pin7(n74682_1_pin7), .pin8(tkc3), .pin9(n74682_1_pin9), .pin18(n74682_1_pin18), .pin17(n74682_1_pin17),
    .pin16(n74682_1_pin16), .pin15(tkc6), .pin14(n74682_1_pin14), .pin13(tkc5), .pin12(n74682_1_pin12),
    .pin11(tkc4));  // open: pin19
  _74682 #(.ShowInternalStructure("true")) u_74682_2 (
    .pin1(tkc7_LE_6F), .pin2(tkc0), .pin3(n74682_2_pin3), .pin4(tkc1), .pin5(n74682_2_pin5), .pin6(tkc2),
    .pin7(n74682_2_pin7), .pin8(tkc3), .pin9(n74682_2_pin9), .pin18(n74682_2_pin18), .pin17(n74682_2_pin17),
    .pin16(n74682_2_pin16), .pin15(tkc6), .pin14(n74682_2_pin14), .pin13(tkc5), .pin12(n74682_2_pin12),
    .pin11(tkc4));  // open: pin19
  _74688 #(.ShowInternalStructure("true")) u_74688_2 (
    .pin1(n74688_2_pin1), .pin2(tkc0), .pin3(n74688_2_pin3), .pin4(tkc1), .pin5(n74688_2_pin5), .pin6(tkc2),
    .pin7(n74688_2_pin7), .pin8(tkc3), .pin9(n74688_2_pin9), .pin19(tkc_nEQ_0F), .pin18(n74688_2_pin18),
    .pin17(tkc7), .pin16(n74688_2_pin16), .pin15(tkc6), .pin14(n74688_2_pin14), .pin13(tkc5),
    .pin12(n74688_2_pin12), .pin11(tkc4));
  _74688 #(.ShowInternalStructure("true")) u_74688_3 (
    .pin1(n74688_3_pin1), .pin2(tkc0), .pin3(n74688_3_pin3), .pin4(tkc1), .pin5(n74688_3_pin5), .pin6(tkc2),
    .pin7(n74688_3_pin7), .pin8(tkc3), .pin9(n74688_3_pin9), .pin19(tkc_nEQ_28), .pin18(n74688_3_pin18),
    .pin17(tkc7), .pin16(n74688_3_pin16), .pin15(tkc6), .pin14(n74688_3_pin14), .pin13(tkc5),
    .pin12(n74688_3_pin12), .pin11(tkc4));
  _74688 #(.ShowInternalStructure("true")) u_74688_4 (
    .pin1(n74688_4_pin1), .pin2(tkc0), .pin3(n74688_4_pin3), .pin4(tkc1), .pin5(n74688_4_pin5), .pin6(tkc2),
    .pin7(n74688_4_pin7), .pin8(tkc3), .pin9(n74688_4_pin9), .pin19(tkc_nEQ_F8), .pin18(n74688_4_pin18),
    .pin17(tkc7), .pin16(n74688_4_pin16), .pin15(tkc6), .pin14(n74688_4_pin14), .pin13(tkc5),
    .pin12(n74688_4_pin12), .pin11(tkc4));
  _7404 #(.ShowInternalStructure("true")) u_7404_2 (
    .pin1(op03), .pin2(ny), .pin3(n_ex), .pin4(ex), .pin5(cc), .pin6(n_cc), .pin13(op0), .pin12(nop0),
    .pin11(op1), .pin10(nop1), .pin9(op2), .pin8(nop2));
  _7485 #(.ShowInternalStructure("true")) u_7485_1 (
    .pin1(n7485_1_pin1), .pin2(n7485_1_pin2), .pin3(n7485_1_pin3), .pin4(n7485_1_pin4), .pin5(op_gt_6),
    .pin15(op3), .pin14(n7485_1_pin14), .pin13(op2), .pin12(op1), .pin11(n7485_1_pin11), .pin10(op0),
    .pin9(n7485_1_pin9));  // open: pin6, pin7
  _7408 #(.ShowInternalStructure("true")) u_7408_1 (
    .pin1(lopN), .pin2(opc_eq_0), .pin3(lop0), .pin4(lopN), .pin5(opc_eq_1), .pin6(lop1), .pin13(lopN),
    .pin12(opc_eq_2), .pin11(lop2), .pin10(seq_1), .pin9(n_ex), .pin8(lopN));
  _74238 #(.ShowInternalStructure("true")) u_74238_1 (
    .pin1(opc0), .pin2(opc1), .pin3(n74238_1_pin3), .pin4(n74238_1_pin4), .pin5(n74238_1_pin5),
    .pin6(n74238_1_pin6), .pin15(opc_eq_0), .pin14(opc_eq_1), .pin13(opc_eq_2), .pin12(opc_eq_3));  // open: pin7, pin11, pin10, pin9
  _74163 #(.ShowInternalStructure("true")) u_74163_1 (
    .pin1(n_cc), .pin2(seq_0), .pin3(n74163_1_pin3), .pin4(n74163_1_pin4), .pin5(n74163_1_pin5),
    .pin6(n74163_1_pin6), .pin7(n_ex), .pin14(opc0), .pin13(opc1), .pin10(n74163_1_pin10),
    .pin9(n74163_1_pin9));  // open: pin15, pin12, pin11
  _74163 #(.ShowInternalStructure("true")) u_74163_2 (
    .pin1(n_cc), .pin2(seq_0), .pin3(n74163_2_pin3), .pin4(n74163_2_pin4), .pin5(n74163_2_pin5),
    .pin6(n74163_2_pin6), .pin7(ex), .pin14(exc0), .pin13(exc1), .pin12(exc2), .pin10(n74163_2_pin10),
    .pin9(n74163_2_pin9));  // open: pin15, pin11
  Hex_Digit_Display hex_digit_display_3 (.value({op17, op16, op15, op14}));  // open: dp
  Hex_Digit_Display hex_digit_display_4 (.value({op13, op12, op11, op10}));  // open: dp
  Hex_Digit_Display hex_digit_display_5 (.value({op27, op26, op25, op24}));  // open: dp
  Hex_Digit_Display hex_digit_display_6 (.value({op23, op22, op21, op20}));  // open: dp
  _74688 #(.ShowInternalStructure("true")) EQ_5 (
    .pin1(EQ_5_pin1), .pin2(hsc0), .pin3(EQ_5_pin3), .pin4(hsc1), .pin5(EQ_5_pin5), .pin6(hsc2),
    .pin7(EQ_5_pin7), .pin8(hsc3), .pin9(EQ_5_pin9), .pin19(hsc_nEQ_05), .pin18(EQ_5_pin18), .pin17(hsc7),
    .pin16(EQ_5_pin16), .pin15(hsc6), .pin14(EQ_5_pin14), .pin13(hsc5), .pin12(EQ_5_pin12), .pin11(hsc4));
  _74688 #(.ShowInternalStructure("true")) EQ_09 (
    .pin1(EQ_09_pin1), .pin2(hsc0), .pin3(EQ_09_pin3), .pin4(hsc1), .pin5(EQ_09_pin5), .pin6(hsc2),
    .pin7(EQ_09_pin7), .pin8(hsc3), .pin9(EQ_09_pin9), .pin19(hsc_nEQ_A), .pin18(EQ_09_pin18), .pin17(hsc7),
    .pin16(EQ_09_pin16), .pin15(hsc6), .pin14(EQ_09_pin14), .pin13(hsc5), .pin12(EQ_09_pin12), .pin11(hsc4));
  _74688 #(.ShowInternalStructure("true")) EQ_54 (
    .pin1(EQ_54_pin1), .pin2(hsc0), .pin3(EQ_54_pin3), .pin4(hsc1), .pin5(EQ_54_pin5), .pin6(hsc2),
    .pin7(EQ_54_pin7), .pin8(hsc3), .pin9(EQ_54_pin9), .pin19(hsc_nEQ_54), .pin18(EQ_54_pin18), .pin17(hsc7),
    .pin16(EQ_54_pin16), .pin15(hsc6), .pin14(EQ_54_pin14), .pin13(hsc5), .pin12(EQ_54_pin12), .pin11(hsc4));
  _74688 #(.ShowInternalStructure("true")) EQ_33 (
    .pin1(EQ_33_pin1), .pin2(hsc0), .pin3(EQ_33_pin3), .pin4(hsc1), .pin5(EQ_33_pin5), .pin6(hsc2),
    .pin7(EQ_33_pin7), .pin8(hsc3), .pin9(EQ_33_pin9), .pin19(hsc_nEQ_34), .pin18(EQ_33_pin18), .pin17(hsc7),
    .pin16(EQ_33_pin16), .pin15(hsc6), .pin14(EQ_33_pin14), .pin13(hsc5), .pin12(EQ_33_pin12), .pin11(hsc4));
  _74688 #(.ShowInternalStructure("true")) EQ_69 (
    .pin1(EQ_69_pin1), .pin2(hsc0), .pin3(EQ_69_pin3), .pin4(hsc1), .pin5(EQ_69_pin5), .pin6(hsc2),
    .pin7(EQ_69_pin7), .pin8(hsc3), .pin9(EQ_69_pin9), .pin19(hsc_nEQ_6A), .pin18(EQ_69_pin18), .pin17(hsc7),
    .pin16(EQ_69_pin16), .pin15(hsc6), .pin14(EQ_69_pin14), .pin13(hsc5), .pin12(EQ_69_pin12), .pin11(hsc4));
  _74688 #(.ShowInternalStructure("true")) EQ_6F (
    .pin1(EQ_6F_pin1), .pin2(hsc0), .pin3(EQ_6F_pin3), .pin4(hsc1), .pin5(EQ_6F_pin5), .pin6(hsc2),
    .pin7(EQ_6F_pin7), .pin8(hsc3), .pin9(EQ_6F_pin9), .pin19(hsc_nEQ_6E), .pin18(EQ_6F_pin18), .pin17(hsc7),
    .pin16(EQ_6F_pin16), .pin15(hsc6), .pin14(EQ_6F_pin14), .pin13(hsc5), .pin12(EQ_6F_pin12), .pin11(hsc4));
  _74283 #(.ShowInternalStructure("true")) u_74283_1 (
    .pin1(vma6), .pin2(n74283_1_pin2), .pin3(hsc1), .pin4(vma5), .pin5(hsc0), .pin6(n74283_1_pin6),
    .pin7(n74283_1_pin7), .pin15(n74283_1_pin15), .pin14(hsc2), .pin13(vma7), .pin12(hsc3),
    .pin11(n74283_1_pin11), .pin10(vma8), .pin9(n74283_1_pin9));
  _74283 #(.ShowInternalStructure("true")) u_74283_2 (
    .pin1(vmaA), .pin2(n74283_2_pin2), .pin3(hsc5), .pin4(vma9), .pin5(hsc4), .pin6(n74283_2_pin6),
    .pin7(n74283_1_pin9), .pin15(n74283_2_pin15), .pin14(hsc6), .pin13(vmaB), .pin12(hsc7),
    .pin11(n74283_2_pin11), .pin10(vmaC), .pin9(n74283_2_pin9));
  _74283 #(.ShowInternalStructure("true")) u_74283_3 (
    .pin1(vmaE), .pin2(n74283_3_pin2), .pin3(hsc9), .pin4(vmaD), .pin5(hsc8), .pin6(n74283_3_pin6),
    .pin7(n74283_2_pin9), .pin15(n74283_3_pin15), .pin11(n74283_3_pin11));  // open: pin14, pin13, pin12, pin10, pin9
  _7404 #(.ShowInternalStructure("true")) u_7404_3 (
    .pin1(eop1), .pin2(n_eop1), .pin3(eop2), .pin4(n_eop2), .pin5(n_mw_lda), .pin6(mw_lda), .pin13(erom),
    .pin12(n_erom), .pin11(eram), .pin10(n_eram), .pin9(lram), .pin8(n_lram));
  _7411 #(.ShowInternalStructure("true")) u_7411_1 (
    .pin1(op1), .pin2(nop0), .pin3(op0), .pin4(nop1), .pin5(nop2), .pin6(a001), .pin13(nop2), .pin12(a010),
    .pin11(op0), .pin10(nop1), .pin9(op2), .pin8(a101));
  _7411 #(.ShowInternalStructure("true")) u_7411_2 (
    .pin1(seq_2), .pin2(ldev), .pin3(nop0), .pin4(nop1), .pin5(nop2), .pin6(n7411_2_pin6), .pin13(prt_EQ_0),
    .pin12(lsta), .pin11(n7411_2_pin11), .pin10(edev), .pin9(prt_EQ_0), .pin8(esta));
  _7427 #(.ShowInternalStructure("true")) u_7427_1 (
    .pin1(n7411_2_pin6), .pin2(a101), .pin3(a101), .pin4(a010), .pin5(a001), .pin6(n7427_1_pin6),
    .pin13(n7427_1_pin13), .pin12(n_mw_lda), .pin11(ld1_x), .pin10(ld2_x), .pin9(ld3_x), .pin8(n_ex));
  _7427 #(.ShowInternalStructure("true")) u_7427_2 (
    .pin1(mw_lda), .pin2(op_gt_6), .pin3(n7427_1_pin6), .pin4(op_gt_6), .pin5(op03), .pin6(ld3), .pin13(ny),
    .pin12(ld1), .pin11(ld1), .pin10(ld3), .pin9(n7427_2_pin9), .pin8(ld2));
  _7408 #(.ShowInternalStructure("true")) u_7408_2 (
    .pin1(opc_eq_1), .pin2(ld1), .pin3(ld1_x), .pin4(opc_eq_2), .pin5(ld2), .pin6(ld2_x), .pin13(lprt),
    .pin12(seq_2), .pin11(lprt_x), .pin10(opc_eq_3), .pin9(ld3), .pin8(ld3_x));
  Hex_Digit_Display hex_digit_display_7 (.value({pcF, pcE, pcD, pcC}));  // open: dp
  Hex_Digit_Display hex_digit_display_8 (.value({pcB, pcA, pc9, pc8}));  // open: dp
  Hex_Digit_Display hex_digit_display_9 (.value({pc7, pc6, pc5, pc4}));  // open: dp
  Hex_Digit_Display hex_digit_display_10 (.value({pc3, pc2, pc1, pc0}));  // open: dp
  AS6C6264 as6c6264_1 (
    .IO0(vd0), .IO1(vd1), .IO2(vd2), .IO7(vd7), .IO6(vd6), .IO5(vd5), .IO4(vd4), .IO3(vd3), .I0(vram_d0),
    .I1(vram_d1), .I2(vram_d2), .I3(vram_d3), .I4(vram_d4), .I5(vram_d5), .I6(vram_d6), .I7(vram_d7),
    .A12(vmaC_x), .A7(vma7_x), .A6(vma6_x), .A5(vma5_x), .A4(vma4_x), .A3(vma3_x), .A2(vma2_x), .A1(vma1_x),
    .A0(vma0_x), .CLK(clk), .nWE(n_lvram), .CE2(1'b1), .A8(vma8_x), .A9(vma9_x), .A11(vmaB_x), .nOE(1'b0),
    .A10(vmaA_x), .nCE(1'b0));  // open: NC0, GND, VCC
  Hex_Digit_Display hex_digit_display_11 (.value({spF, spE, spD, spC}));  // open: dp
  Hex_Digit_Display hex_digit_display_12 (.value({spB, spA, sp9, sp8}));  // open: dp
  _7432 #(.ShowInternalStructure("true")) u_7432_1 (
    .pin1(hsc_or_89), .pin2(hsc_nEQ_05), .pin3(hsc_n1S), .pin4(hsc_or_89), .pin5(hsc_nEQ_A), .pin6(hsc_n2S),
    .pin13(hsc_nEQ_34), .pin12(hsc_n9), .pin11(hsc_n4S), .pin10(hsc_nEQ_54), .pin9(hsc_or_89), .pin8(hsc_n3S));
  _7432 #(.ShowInternalStructure("true")) u_7432_2 (
    .pin1(hsc_n9), .pin2(hsc_nEQ_6A), .pin3(hsc_n5S), .pin4(hsc_n9), .pin5(hsc_nEQ_6E), .pin6(hsc_nR),
    .pin13(hsc2Q), .pin12(hsc3Q), .pin11(n7432_2_pin11), .pin10(n7432_2_pin11), .pin9(hsc4Q), .pin8(hsc_eORd));
  _74279 #(.ShowInternalStructure("true")) u_74279_1 (
    .pin1(hsc_n2S), .pin2(hsc_n1S), .pin3(hsc_n1S), .pin4(hsc1Q), .pin5(hsc_n3S), .pin6(hsc_n2S),
    .pin7(hsc2Q), .pin15(hsc_n4S), .pin14(hsc_n5S), .pin13(hsc4Q), .pin12(hsc_n3S), .pin11(hsc_n3S),
    .pin10(hsc_n4S), .pin9(hsc3Q));
  _74279 #(.ShowInternalStructure("true")) u_74279_2 (
    .pin1(hsc_nR), .pin2(hsc_n5S), .pin3(hsc_n5S), .pin4(hsc5Q), .pin5(tkc_nEQ_28), .pin6(tkc_nEQ_0F),
    .pin7(tkc1Q), .pin15(tkc_nEQ_F8), .pin14(tkc_nRC0), .pin13(tkc3Q), .pin12(tkc_nEQ_28),
    .pin11(tkc_nEQ_28), .pin10(tkc_nEQ_F8), .pin9(tkc2Q));
  _74151 #(.ShowInternalStructure("true")) u_74151_1 (
    .pin1(vd3_x), .pin2(vd2_x), .pin3(vd1_x), .pin4(vd0_x), .pin5(vbit), .pin7(n74151_1_pin7), .pin15(vd4_x),
    .pin14(vd5_x), .pin13(vd6_x), .pin12(vd7_x), .pin11(tkc0), .pin10(tkc1), .pin9(tkc2));  // open: pin6
  _74573 #(.ShowInternalStructure("true")) u_74573_1 (
    .pin1(n74573_1_pin1), .pin2(vd0), .pin3(vd1), .pin4(vd2), .pin5(vd3), .pin6(vd4), .pin7(vd5), .pin8(vd6),
    .pin9(vd7), .pin19(vd0_x), .pin18(vd1_x), .pin17(vd2_x), .pin16(vd3_x), .pin15(vd4_x), .pin14(vd5_x),
    .pin13(vd6_x), .pin12(vd7_x), .pin11(latch_vram));
  _74573 #(.ShowInternalStructure("true")) u_74573_2 (
    .pin1(el_vram), .pin2(tkc3), .pin3(tkc4), .pin4(tkc5), .pin5(tkc6), .pin6(tkc7), .pin7(vma5),
    .pin8(vma6), .pin9(vma7), .pin19(vma0_x), .pin18(vma1_x), .pin17(vma2_x), .pin16(vma3_x), .pin15(vma4_x),
    .pin14(vma5_x), .pin13(vma6_x), .pin12(vma7_x), .pin11(n74573_2_pin11));
  _74573 #(.ShowInternalStructure("true")) u_74573_3 (
    .pin1(el_vram), .pin2(vma8), .pin3(vma9), .pin4(vmaA), .pin5(vmaB), .pin6(vmaC), .pin7(n74573_3_pin7),
    .pin8(n74573_3_pin8), .pin9(n74573_3_pin9), .pin19(vma8_x), .pin18(vma9_x), .pin17(vmaA_x),
    .pin16(vmaB_x), .pin15(vmaC_x), .pin11(n74573_3_pin11));  // open: pin14, pin13, pin12
  _74573 #(.ShowInternalStructure("true")) u_74573_4 (
    .pin1(n_el_vram), .pin2(ad0), .pin3(ad1), .pin4(ad2), .pin5(ad3), .pin6(ad4), .pin7(ad5), .pin8(ad6),
    .pin9(ad7), .pin19(vma0_x), .pin18(vma1_x), .pin17(vma2_x), .pin16(vma3_x), .pin15(vma4_x),
    .pin14(vma5_x), .pin13(vma6_x), .pin12(vma7_x), .pin11(n74573_4_pin11));
  _74573 #(.ShowInternalStructure("true")) u_74573_5 (
    .pin1(n_el_vram), .pin2(ad8), .pin3(ad9), .pin4(adA), .pin5(adB), .pin6(adC), .pin7(adD), .pin8(adE),
    .pin9(adF), .pin19(vma8_x), .pin18(vma9_x), .pin17(vmaA_x), .pin16(vmaB_x), .pin15(vmaC_x),
    .pin11(n74573_5_pin11));  // open: pin14, pin13, pin12
  _74573 #(.ShowInternalStructure("true")) u_op0 (
    .pin1(op0_pin1), .pin2(dx0), .pin3(dx1), .pin4(dx2), .pin5(dx3), .pin6(dx4), .pin7(dx5), .pin8(dx6),
    .pin9(dx7), .pin19(op00), .pin18(op01), .pin17(op02), .pin16(op03), .pin15(op0), .pin14(op1),
    .pin13(op2), .pin12(op3), .pin11(lop0));
  _74573 #(.ShowInternalStructure("true")) u_op1 (
    .pin1(op1_pin1), .pin2(dx0), .pin3(dx1), .pin4(dx2), .pin5(dx3), .pin6(dx4), .pin7(dx5), .pin8(dx6),
    .pin9(dx7), .pin19(op10), .pin18(op11), .pin17(op12), .pin16(op13), .pin15(op14), .pin14(op15),
    .pin13(op16), .pin12(op17), .pin11(lop1));
  _74573 #(.ShowInternalStructure("true")) u_74573_6 (
    .pin1(n_eop1), .pin2(op10), .pin3(op11), .pin4(op12), .pin5(op13), .pin6(op14), .pin7(op15), .pin8(op16),
    .pin9(op17), .pin19(d0), .pin18(d1), .pin17(d2), .pin16(d3), .pin15(d4), .pin14(d5), .pin13(d6),
    .pin12(d7), .pin11(n74573_6_pin11));
  _74573 #(.ShowInternalStructure("true")) u_op2 (
    .pin1(op2_pin1), .pin2(dx0), .pin3(dx1), .pin4(dx2), .pin5(dx3), .pin6(dx4), .pin7(dx5), .pin8(dx6),
    .pin9(dx7), .pin19(op20), .pin18(op21), .pin17(op22), .pin16(op23), .pin15(op24), .pin14(op25),
    .pin13(op26), .pin12(op27), .pin11(lop2));
  _74573 #(.ShowInternalStructure("true")) u_74573_7 (
    .pin1(n_eop2), .pin2(op20), .pin3(op21), .pin4(op22), .pin5(op23), .pin6(op24), .pin7(op25), .pin8(op26),
    .pin9(op27), .pin19(d0), .pin18(d1), .pin17(d2), .pin16(d3), .pin15(d4), .pin14(d5), .pin13(d6),
    .pin12(d7), .pin11(n74573_7_pin11));
  Hex_Digit_Display hex_digit_display_13 (.value({sp7, sp6, sp5, sp4}));  // open: dp
  Hex_Digit_Display hex_digit_display_14 (.value({sp3, sp2, sp1, sp0}));  // open: dp
  AT28C64B_MAIN ROM (
    .IO0(d0), .IO1(d1), .IO2(d2), .IO7(d7), .IO6(d6), .IO5(d5), .IO4(d4), .IO3(d3), .A12(adC), .A7(ad7),
    .A6(ad6), .A5(ad5), .A4(ad4), .A3(ad3), .A2(ad2), .A1(ad1), .A0(ad0), .nWE(1'b1), .A8(ad8), .A9(ad9),
    .A11(adB), .nOE(n_erom), .A10(adA), .nCE(1'b0));  // open: NC0, GND, NC1, VCC
  _7432 #(.ShowInternalStructure("true")) u_7432_3 (
    .pin1(hsc1Q), .pin2(hsc2Q), .pin3(n7432_3_pin3), .pin4(n7432_3_pin3), .pin5(hsc3Q), .pin6(n7432_3_pin6),
    .pin13(tkc1Q), .pin12(tkc2Q), .pin11(n7432_3_pin11), .pin10(n7432_3_pin11), .pin9(tkc3Q),
    .pin8(n7432_3_pin8));
  _7432 #(.ShowInternalStructure("true")) u_7432_4 (
    .pin1(n7432_3_pin6), .pin2(hsc4Q), .pin3(n7432_4_pin3), .pin4(n7432_4_pin3), .pin5(hsc5Q),
    .pin6(n7432_4_pin6), .pin13(hsc8), .pin12(hsc9), .pin11(hsc_or_89), .pin10(hsc1Q), .pin9(hsc5Q),
    .pin8(hsc_pp));
  _7404 #(.ShowInternalStructure("true")) u_7404_4 (
    .pin1(n7432_4_pin6), .pin2(hsc0Q), .pin3(n7404_4_pin3), .pin4(hsc_inc), .pin13(n7432_3_pin8),
    .pin12(tkc0Q));  // open: pin5, pin6, pin11, pin10, pin9, pin8
  _7408 #(.ShowInternalStructure("true")) u_7408_3 (
    .pin1(tkc0Q), .pin2(hsc_eORd), .pin3(nV03_sync), .pin4(hsc_pp), .pin5(tkc7_LE_07), .pin6(nV03_broad),
    .pin13(hsc0Q), .pin12(tkc7_LE_6F), .pin11(nV03_short), .pin10(hsc3Q), .pin9(tkc2Q), .pin8(n7408_3_pin8));
  _7408 #(.ShowInternalStructure("true")) u_7408_4 (
    .pin1(n7408_3_pin8), .pin2(vbit), .pin3(v_10), .pin4(tkc_nEQ_80), .pin5(tkc_nRC0), .pin6(n7404_4_pin3),
    .pin13(bank_vram), .pin12(ebank), .pin11(evram), .pin10(bank_vram), .pin9(lbank), .pin8(lvram));
  _7402 #(.ShowInternalStructure("true")) u_7402_1 (
    .pin1(n7402_1_pin1), .pin2(n7402_1_pin2), .pin3(n7402_1_pin2), .pin4(n7402_1_pin2), .pin5(nV03_broad),
    .pin6(nV03_short), .pin13(v_03), .pin12(n7402_1_pin1), .pin11(nV03_sync), .pin10(n_el_vram),
    .pin9(evram), .pin8(lvram));
  _7411 #(.ShowInternalStructure("true")) u_7411_3 (
    .pin1(rise), .pin2(n7411_3_pin2), .pin3(tkc0), .pin4(tkc1), .pin5(tkc2), .pin6(n7411_3_pin2),
    .pin13(n7411_3_pin13), .pin12(latch_vram), .pin11(mb_nGT_1), .pin10(mb_nEQ_1), .pin9(n7411_3_pin9),
    .pin8(mb_EQ_0));
  _7404 #(.ShowInternalStructure("true")) u_7404_5 (
    .pin1(evram), .pin2(n_evram), .pin3(lvram), .pin4(n_lvram), .pin5(n_el_vram), .pin6(el_vram),
    .pin13(mb_nEQ_1), .pin12(bank_vram), .pin11(n_lmb), .pin10(lmb));  // open: pin9, pin8
  _74682 #(.ShowInternalStructure("true")) u_74682_3 (
    .pin1(mb_nGT_1), .pin2(mb0), .pin3(n74682_3_pin3), .pin4(mb1), .pin5(n74682_3_pin5), .pin6(mb2),
    .pin7(n74682_3_pin7), .pin8(mb3), .pin9(n74682_3_pin9), .pin19(mb_nEQ_1), .pin18(n74682_3_pin18),
    .pin17(mb7), .pin16(n74682_3_pin16), .pin15(mb6), .pin14(n74682_3_pin14), .pin13(mb5),
    .pin12(n74682_3_pin12), .pin11(mb4));
  _74573 #(.ShowInternalStructure("true")) u_74573_8 (
    .pin1(n_evram), .pin2(vd0), .pin3(vd1), .pin4(vd2), .pin5(vd3), .pin6(vd4), .pin7(vd5), .pin8(vd6),
    .pin9(vd7), .pin19(d0), .pin18(d1), .pin17(d2), .pin16(d3), .pin15(d4), .pin14(d5), .pin13(d6),
    .pin12(d7), .pin11(n74573_8_pin11));
  _74244 #(.ShowInternalStructure("true")) u_74244_1 (
    .pin1(n74244_1_pin1), .pin2(d0), .pin3(vram_d4), .pin4(d1), .pin5(vram_d5), .pin6(d2), .pin7(vram_d6),
    .pin8(d3), .pin9(vram_d7), .pin19(n74244_1_pin19), .pin18(vram_d0), .pin17(d4), .pin16(vram_d1),
    .pin15(d5), .pin14(vram_d2), .pin13(d6), .pin12(vram_d3), .pin11(d7));
  _74244 #(.ShowInternalStructure("true")) u_74244_2 (
    .pin1(n74244_2_pin1), .pin2(d0), .pin3(dx4), .pin4(d1), .pin5(dx5), .pin6(d2), .pin7(dx6), .pin8(d3),
    .pin9(dx7), .pin19(n74244_2_pin19), .pin18(dx0), .pin17(d4), .pin16(dx1), .pin15(d5), .pin14(dx2),
    .pin13(d6), .pin12(dx3), .pin11(d7));
  _74573 #(.ShowInternalStructure("true")) u_74573_9 (
    .pin1(n_esta), .pin2(st0), .pin3(st1), .pin4(st2), .pin5(st3), .pin6(st4), .pin7(st5), .pin8(st6),
    .pin9(st7), .pin19(d0), .pin18(d1), .pin17(d2), .pin16(d3), .pin15(d4), .pin14(d5), .pin13(d6),
    .pin12(d7), .pin11(n74573_9_pin11));
  _74573 #(.ShowInternalStructure("true")) u_74573_10 (
    .pin1(n74573_10_pin1), .pin2(dx0), .pin3(dx1), .pin4(dx2), .pin5(dx3), .pin6(dx4), .pin7(dx5),
    .pin8(dx6), .pin9(dx7), .pin19(st0), .pin18(st1), .pin17(st2), .pin16(st3), .pin15(st4), .pin14(st5),
    .pin13(st6), .pin12(st7), .pin11(lsta));
  _74573 #(.ShowInternalStructure("true")) u_74573_11 (
    .pin1(n74573_11_pin1), .pin2(dx0), .pin3(dx1), .pin4(dx2), .pin5(dx3), .pin6(dx4), .pin7(dx5),
    .pin8(dx6), .pin9(dx7), .pin19(prt0), .pin18(prt1), .pin17(prt2), .pin16(prt3), .pin15(prt4),
    .pin14(prt5), .pin13(prt6), .pin12(prt7), .pin11(lprt_x));
  _7430 #(.ShowInternalStructure("true")) u_7430_1 (
    .pin1(prt5), .pin2(prt4), .pin3(prt3), .pin4(prt2), .pin5(prt1), .pin6(prt0), .pin12(prt6), .pin11(prt7),
    .pin8(prt_EQ_0));  // open: pin13, pin10, pin9
  AS6C6264 RAM (
    .IO0(d0), .IO1(d1), .IO2(d2), .IO7(d7), .IO6(d6), .IO5(d5), .IO4(d4), .IO3(d3), .I0(d0), .I1(d1),
    .I2(d2), .I3(d3), .I4(d4), .I5(d5), .I6(d6), .I7(d7), .A12(adC), .A7(ad7), .A6(ad6), .A5(ad5), .A4(ad4),
    .A3(ad3), .A2(ad2), .A1(ad1), .A0(ad0), .CLK(clk), .nWE(n_lram), .CE2(1'b1), .A8(ad8), .A9(ad9),
    .A11(adB), .nOE(n_eram), .A10(adA), .nCE(1'b0));  // open: NC0, GND, VCC
  LED led_1 (.in(n74125_1_pin3));
  LED led_2 (.in(n74125_1_pin6));
  LED led_3 (.in(n74125_2_pin3));
  LED led_4 (.in(n74125_2_pin6));
  LED led_5 (.in(n74125_3_pin3));
  LED led_6 (.in(n74125_3_pin6));
  LED led_7 (.in(n74125_4_pin3));
  LED led_8 (.in(n74125_4_pin6));
  LED led_9 (.in(n74125_5_pin3));
  LED led_10 (.in(n74125_5_pin6));
  LED led_11 (.in(n74125_6_pin3));
  LED led_12 (.in(n74125_6_pin6));
  _7408 #(.ShowInternalStructure("true")) u_7408_5 (
    .pin1(mc1_x), .pin2(eta), .pin3(asp), .pin4(mc0_x), .pin5(eta), .pin6(emem_x), .pin13(mc2_x),
    .pin12(eta), .pin11(aimm), .pin10(mc3_x), .pin9(eta), .pin8(lmem));
  _7408 #(.ShowInternalStructure("true")) u_7408_6 (
    .pin1(mc5_x), .pin2(eta), .pin3(spdec), .pin4(mc4_x), .pin5(eta), .pin6(spinc), .pin13(mc6_x),
    .pin12(eta), .pin11(jnz), .pin10(mc0_x), .pin9(etb), .pin8(ldx));
  _7408 #(.ShowInternalStructure("true")) u_7408_7 (
    .pin1(mc2_x), .pin2(etb), .pin3(ldf), .pin4(mc1_x), .pin5(etb), .pin6(ldy), .pin13(mc3_x), .pin12(etb),
    .pin11(ealu), .pin10(mc4_x), .pin9(etb), .pin8(ldh));
  _7408 #(.ShowInternalStructure("true")) u_7408_8 (
    .pin1(mc6_x), .pin2(etb), .pin3(lprt), .pin4(mc5_x), .pin5(etb), .pin6(ldl), .pin13(mc7_x), .pin12(ex),
    .pin11(ereg), .pin10(mc8_x), .pin9(ex), .pin8(lreg));
  _7408 #(.ShowInternalStructure("true")) u_7408_9 (
    .pin1(mcA_x), .pin2(ex), .pin3(eop1), .pin4(mc9_x), .pin5(ex), .pin6(sel), .pin13(mcB_x), .pin12(ex),
    .pin11(eop2), .pin10(mcC_x), .pin9(ex), .pin8(edev));
  _74573 #(.ShowInternalStructure("true")) u_74573_12 (
    .pin1(n_ahl), .pin2(l0), .pin3(l1), .pin4(l2), .pin5(l3), .pin6(l4), .pin7(l5), .pin8(l6), .pin9(l7),
    .pin19(ad0), .pin18(ad1), .pin17(ad2), .pin16(ad3), .pin15(ad4), .pin14(ad5), .pin13(ad6), .pin12(ad7),
    .pin11(n74573_12_pin11));
  _74573 #(.ShowInternalStructure("true")) u_74573_13 (
    .pin1(n_ahl), .pin2(h0), .pin3(h1), .pin4(h2), .pin5(h3), .pin6(h4), .pin7(h5), .pin8(h6), .pin9(h7),
    .pin19(ad8), .pin18(ad9), .pin17(adA), .pin16(adB), .pin15(adC), .pin14(adD), .pin13(adE), .pin12(adF),
    .pin11(n74573_13_pin11));
  _74573 #(.ShowInternalStructure("true")) u_74573_14 (
    .pin1(n_asp), .pin2(sp0), .pin3(sp1), .pin4(sp2), .pin5(sp3), .pin6(sp4), .pin7(sp5), .pin8(sp6),
    .pin9(sp7), .pin19(ad0), .pin18(ad1), .pin17(ad2), .pin16(ad3), .pin15(ad4), .pin14(ad5), .pin13(ad6),
    .pin12(ad7), .pin11(n74573_14_pin11));
  _74573 #(.ShowInternalStructure("true")) u_74573_15 (
    .pin1(n_asp), .pin2(sp8), .pin3(sp9), .pin4(spA), .pin5(spB), .pin6(spC), .pin7(spD), .pin8(spE),
    .pin9(spF), .pin19(ad8), .pin18(ad9), .pin17(adA), .pin16(adB), .pin15(adC), .pin14(adD), .pin13(adE),
    .pin12(adF), .pin11(n74573_15_pin11));
  _74573 #(.ShowInternalStructure("true")) mb (
    .pin1(mb_pin1), .pin2(axd0), .pin3(axd1), .pin4(axd2), .pin5(axd3), .pin6(axd4), .pin7(axd5),
    .pin8(axd6), .pin9(axd7), .pin19(mb0), .pin18(mb1), .pin17(mb2), .pin16(mb3), .pin15(mb4), .pin14(mb5),
    .pin13(mb6), .pin12(mb7), .pin11(lmb));
  _74138 #(.ShowInternalStructure("true")) u_74138_1 (
    .pin1(ad0), .pin2(ad1), .pin3(ad2), .pin4(n74138_1_pin4), .pin5(n_eaux), .pin6(emem), .pin7(n_epch),
    .pin13(n_emb), .pin11(n_espl), .pin10(n_esph), .pin9(n_epcl));  // open: pin15, pin14, pin12
  _74573 #(.ShowInternalStructure("true")) u_74573_16 (
    .pin1(n74573_16_pin1), .pin2(d0), .pin3(d1), .pin4(d2), .pin5(d3), .pin6(d4), .pin7(d5), .pin8(d6),
    .pin9(d7), .pin19(n74573_16_pin19), .pin18(n74573_16_pin18), .pin17(n74573_16_pin17),
    .pin16(n74573_16_pin16), .pin15(n74573_16_pin15), .pin14(n74573_16_pin14), .pin13(n74573_16_pin13),
    .pin12(n74573_16_pin12), .pin11(n74573_16_pin11));
  _74125 #(.ShowInternalStructure("true")) u_74125_1 (
    .pin1(n74125_1_pin1), .pin2(ex), .pin3(n74125_1_pin3), .pin4(n74125_1_pin4), .pin5(ldh),
    .pin6(n74125_1_pin6), .pin13(n74125_1_pin13), .pin10(n74125_1_pin10), .pin9(emem), .pin8(n74125_1_pin8));  // open: pin12, pin11
  _74125 #(.ShowInternalStructure("true")) u_74125_2 (
    .pin1(n74125_2_pin1), .pin2(ldl), .pin3(n74125_2_pin3), .pin4(n74125_2_pin4), .pin5(lprt),
    .pin6(n74125_2_pin6), .pin13(n74125_2_pin13), .pin12(asp), .pin11(n74125_2_pin11),
    .pin10(n74125_2_pin10), .pin9(aimm), .pin8(n74125_2_pin8));
  _74125 #(.ShowInternalStructure("true")) u_74125_3 (
    .pin1(n74125_3_pin1), .pin2(ereg), .pin3(n74125_3_pin3), .pin4(n74125_3_pin4), .pin5(lreg),
    .pin6(n74125_3_pin6), .pin13(n74125_3_pin13), .pin12(lmem), .pin11(n74125_3_pin11),
    .pin10(n74125_3_pin10), .pin9(spinc), .pin8(n74125_3_pin8));
  _74125 #(.ShowInternalStructure("true")) u_74125_4 (
    .pin1(n74125_4_pin1), .pin2(sel), .pin3(n74125_4_pin3), .pin4(n74125_4_pin4), .pin5(eop1),
    .pin6(n74125_4_pin6), .pin13(n74125_4_pin13), .pin12(spdec), .pin11(n74125_4_pin11),
    .pin10(n74125_4_pin10), .pin9(jnz), .pin8(n74125_4_pin8));
  _74125 #(.ShowInternalStructure("true")) u_74125_5 (
    .pin1(n74125_5_pin1), .pin2(eop2), .pin3(n74125_5_pin3), .pin4(n74125_5_pin4), .pin5(edev),
    .pin6(n74125_5_pin6), .pin13(n74125_5_pin13), .pin12(ldx), .pin11(n74125_5_pin11),
    .pin10(n74125_5_pin10), .pin9(ldy), .pin8(n74125_5_pin8));
  _74125 #(.ShowInternalStructure("true")) u_74125_6 (
    .pin1(n74125_6_pin1), .pin2(ldev), .pin3(n74125_6_pin3), .pin4(n74125_6_pin4), .pin5(cc),
    .pin6(n74125_6_pin6), .pin13(n74125_6_pin13), .pin12(ldf), .pin11(n74125_6_pin11),
    .pin10(n74125_6_pin10), .pin9(ealu), .pin8(n74125_6_pin8));
  LED led_13 (.in(n74573_16_pin19));
  LED led_14 (.in(n74573_16_pin18));
  LED led_15 (.in(n74573_16_pin17));
  LED led_16 (.in(n74573_16_pin16));
  LED led_17 (.in(n74573_16_pin15));
  LED led_18 (.in(n74573_16_pin14));
  LED led_19 (.in(n74573_16_pin13));
  LED led_20 (.in(n74573_16_pin12));
  LED led_21 (.in(n74125_1_pin8));
  LED led_22 (.in(n74125_2_pin11));
  LED led_23 (.in(n74125_2_pin8));
  LED led_24 (.in(n74125_3_pin11));
  LED led_25 (.in(n74125_3_pin8));
  LED led_26 (.in(n74125_4_pin11));
  LED led_27 (.in(n74125_4_pin8));
  LED led_28 (.in(n74125_5_pin11));
  LED led_29 (.in(n74125_5_pin8));
  LED led_30 (.in(n74125_6_pin11));
  LED led_31 (.in(n74125_6_pin8));
  _74573 #(.ShowInternalStructure("true")) u_74573_17 (
    .pin1(n74573_17_pin1), .pin2(mc0), .pin3(mc1), .pin4(mc2), .pin5(mc3), .pin6(mc4), .pin7(mc5),
    .pin8(mc6), .pin9(mc7), .pin19(mc0_x), .pin18(mc1_x), .pin17(mc2_x), .pin16(mc3_x), .pin15(mc4_x),
    .pin14(mc5_x), .pin13(mc6_x), .pin12(mc7_x), .pin11(seq_0));
  _7404 #(.ShowInternalStructure("true")) u_7404_6 (
    .pin3(mcF_x), .pin4(n_mcF_x), .pin5(ereg), .pin6(n_ereg), .pin13(r_we), .pin12(n_r_we), .pin11(sel),
    .pin10(nsel), .pin9(lpreset), .pin8(nlpreset));  // open: pin1, pin2
  _7408 #(.ShowInternalStructure("true")) u_7408_10 (
    .pin1(mcD_x), .pin2(ex), .pin3(ldev), .pin4(mcE_x), .pin5(ex), .pin6(cc), .pin13(n_mcF_x), .pin12(ex),
    .pin11(eta), .pin10(mcF_x), .pin9(ex), .pin8(etb));
  _74244 #(.ShowInternalStructure("true")) u_74244_3 (
    .pin1(n74244_3_pin1), .pin2(d0), .pin3(rd4), .pin4(d1), .pin5(rd5), .pin6(d2), .pin7(rd6), .pin8(d3),
    .pin9(rd7), .pin19(n74244_3_pin19), .pin18(rd0), .pin17(d4), .pin16(rd1), .pin15(d5), .pin14(rd2),
    .pin13(d6), .pin12(rd3), .pin11(d7));
  _74244 #(.ShowInternalStructure("true")) u_74244_4 (
    .pin1(n_ereg), .pin2(rq0), .pin3(d4), .pin4(rq1), .pin5(d5), .pin6(rq2), .pin7(d6), .pin8(rq3),
    .pin9(d7), .pin19(n_ereg), .pin18(d0), .pin17(rq4), .pin16(d1), .pin15(rq5), .pin14(d2), .pin13(rq6),
    .pin12(d3), .pin11(rq7));
  _74573 #(.ShowInternalStructure("true")) u_74573_18 (
    .pin1(n_apc), .pin2(pc0), .pin3(pc1), .pin4(pc2), .pin5(pc3), .pin6(pc4), .pin7(pc5), .pin8(pc6),
    .pin9(pc7), .pin19(ad0), .pin18(ad1), .pin17(ad2), .pin16(ad3), .pin15(ad4), .pin14(ad5), .pin13(ad6),
    .pin12(ad7), .pin11(n74573_18_pin11));
  _74573 #(.ShowInternalStructure("true")) u_74573_19 (
    .pin1(n_apc), .pin2(pc8), .pin3(pc9), .pin4(pcA), .pin5(pcB), .pin6(pcC), .pin7(pcD), .pin8(pcE),
    .pin9(pcF), .pin19(ad8), .pin18(ad9), .pin17(adA), .pin16(adB), .pin15(adC), .pin14(adD), .pin13(adE),
    .pin12(adF), .pin11(n74573_19_pin11));
  _74573 #(.ShowInternalStructure("true")) u_74573_20 (
    .pin1(n_aimm), .pin2(op10), .pin3(op11), .pin4(op12), .pin5(op13), .pin6(op14), .pin7(op15), .pin8(op16),
    .pin9(op17), .pin19(ad0), .pin18(ad1), .pin17(ad2), .pin16(ad3), .pin15(ad4), .pin14(ad5), .pin13(ad6),
    .pin12(ad7), .pin11(n74573_20_pin11));
  _74573 #(.ShowInternalStructure("true")) u_74573_21 (
    .pin1(n_aimm), .pin2(op20), .pin3(op21), .pin4(op22), .pin5(op23), .pin6(op24), .pin7(op25), .pin8(op26),
    .pin9(op27), .pin19(ad8), .pin18(ad9), .pin17(adA), .pin16(adB), .pin15(adC), .pin14(adD), .pin13(adE),
    .pin12(adF), .pin11(n74573_21_pin11));
  _74573 #(.ShowInternalStructure("true")) u_74573_22 (
    .pin1(n_emb), .pin2(mb0), .pin3(mb1), .pin4(mb2), .pin5(mb3), .pin6(mb4), .pin7(mb5), .pin8(mb6),
    .pin9(mb7), .pin19(axq0), .pin18(axq1), .pin17(axq2), .pin16(axq3), .pin15(axq4), .pin14(axq5),
    .pin13(axq6), .pin12(axq7), .pin11(n74573_22_pin11));
  _74138 #(.ShowInternalStructure("true")) u_74138_2 (
    .pin1(ad0), .pin2(ad1), .pin3(ad2), .pin4(n_lmem), .pin5(n_eaux), .pin6(seq_2), .pin7(n_lpch),
    .pin13(n_lmb), .pin11(n_lspl), .pin10(n_lsph), .pin9(n_lpcl));  // open: pin15, pin14, pin12
  _74374 #(.ShowInternalStructure("true")) u_74374_1 (
    .pin1(n74374_1_pin1), .pin2(x0), .pin3(d0), .pin4(d1), .pin5(x1), .pin6(x2), .pin7(d2), .pin8(d3),
    .pin9(x3), .pin19(x7), .pin18(d7), .pin17(d6), .pin16(x6), .pin15(x5), .pin14(d5), .pin13(d4),
    .pin12(x4), .pin11(xc));
  _74374 #(.ShowInternalStructure("true")) u_74374_2 (
    .pin1(n74374_2_pin1), .pin2(y0), .pin3(d0), .pin4(d1), .pin5(y1), .pin6(y2), .pin7(d2), .pin8(d3),
    .pin9(y3), .pin19(y7), .pin18(d7), .pin17(d6), .pin16(y6), .pin15(y5), .pin14(d5), .pin13(d4),
    .pin12(y4), .pin11(yc));
  _7408 #(.ShowInternalStructure("true")) u_7408_11 (
    .pin1(op1), .pin2(flag_c), .pin3(c_in), .pin4(nE_adc), .pin5(nE_add), .pin6(nE_add_adc), .pin13(ldx),
    .pin12(seq_2), .pin11(xc), .pin10(ldy), .pin9(seq_2), .pin8(yc));
  _7404 #(.ShowInternalStructure("true")) u_7404_7 (
    .pin1(y0), .pin2(ny0), .pin3(y1), .pin4(ny1), .pin5(y2), .pin6(ny2), .pin13(y5), .pin12(ny5), .pin11(y4),
    .pin10(ny4), .pin9(y3), .pin8(ny3));
  _7404 #(.ShowInternalStructure("true")) u_7404_8 (
    .pin1(y6), .pin2(ny6), .pin3(y7), .pin4(ny7), .pin5(ldf), .pin6(nLDF), .pin13(flag_b), .pin12(b_in),
    .pin11(nb_out), .pin10(b_out), .pin9(esta), .pin8(n_esta));
  _74244 #(.ShowInternalStructure("true")) u_74244_5 (
    .pin1(nE_pass), .pin2(y0), .pin3(d4), .pin4(y1), .pin5(d5), .pin6(y2), .pin7(d6), .pin8(y3), .pin9(d7),
    .pin19(nE_pass), .pin18(d0), .pin17(y4), .pin16(d1), .pin15(y5), .pin14(d2), .pin13(y6), .pin12(d3),
    .pin11(y7));
  AT28C64B_MC0 at28c64b_mc0_1 (
    .IO0(mc0), .IO1(mc1), .IO2(mc2), .IO7(mc7), .IO6(mc6), .IO5(mc5), .IO4(mc4), .IO3(mc3), .A12(1'b0),
    .A7(op3), .A6(op2), .A5(op1), .A4(op0), .A3(op03), .A2(exc2), .A1(exc1), .A0(exc0), .nWE(1'b1),
    .A8(1'b0), .A9(1'b0), .A11(1'b0), .nOE(1'b0), .A10(1'b0), .nCE(1'b0));  // open: NC0, GND, NC1, VCC
  _74573 #(.ShowInternalStructure("true")) u_74573_23 (
    .pin1(n74573_23_pin1), .pin2(mc8), .pin3(mc9), .pin4(mcA), .pin5(mcB), .pin6(mcC), .pin7(mcD),
    .pin8(mcE), .pin9(mcF), .pin19(mc8_x), .pin18(mc9_x), .pin17(mcA_x), .pin16(mcB_x), .pin15(mcC_x),
    .pin14(mcD_x), .pin13(mcE_x), .pin12(mcF_x), .pin11(seq_0));
  _74573 #(.ShowInternalStructure("true")) l (
    .pin1(l_pin1), .pin2(rd0), .pin3(rd1), .pin4(rd2), .pin5(rd3), .pin6(rd4), .pin7(rd5), .pin8(rd6),
    .pin9(rd7), .pin19(l0), .pin18(l1), .pin17(l2), .pin16(l3), .pin15(l4), .pin14(l5), .pin13(l6),
    .pin12(l7), .pin11(l_we));
  _74573 #(.ShowInternalStructure("true")) h (
    .pin1(h_pin1), .pin2(rd0), .pin3(rd1), .pin4(rd2), .pin5(rd3), .pin6(rd4), .pin7(rd5), .pin8(rd6),
    .pin9(rd7), .pin19(h0), .pin18(h1), .pin17(h2), .pin16(h3), .pin15(h4), .pin14(h5), .pin13(h6),
    .pin12(h7), .pin11(h_we));
  _74573 #(.ShowInternalStructure("true")) f (
    .pin1(f_pin1), .pin2(rd0), .pin3(rd1), .pin4(rd2), .pin5(rd3), .pin6(rd4), .pin7(rd5), .pin8(rd6),
    .pin9(rd7), .pin19(flag_l), .pin18(flag_e), .pin17(flag_c), .pin16(flag_b), .pin15(f4), .pin14(f5),
    .pin13(f6), .pin12(f7), .pin11(f_we));
  _74244 #(.ShowInternalStructure("true")) u_74244_6 (
    .pin1(n_eaux), .pin2(axq0), .pin3(d4), .pin4(axq1), .pin5(d5), .pin6(axq2), .pin7(d6), .pin8(axq3),
    .pin9(d7), .pin19(n_eaux), .pin18(d0), .pin17(axq4), .pin16(d1), .pin15(axq5), .pin14(d2), .pin13(axq6),
    .pin12(d3), .pin11(axq7));
  _74244 #(.ShowInternalStructure("true")) u_74244_7 (
    .pin1(d_EQ_0), .pin2(l0), .pin3(pc4x), .pin4(l1), .pin5(pc5x), .pin6(l2), .pin7(pc6x), .pin8(l3),
    .pin9(pc7x), .pin19(d_EQ_0), .pin18(pc0x), .pin17(l4), .pin16(pc1x), .pin15(l5), .pin14(pc2x),
    .pin13(l6), .pin12(pc3x), .pin11(l7));
  _74244 #(.ShowInternalStructure("true")) u_74244_8 (
    .pin1(d_nEQ_0), .pin2(axd0), .pin3(pc4x), .pin4(axd1), .pin5(pc5x), .pin6(axd2), .pin7(pc6x),
    .pin8(axd3), .pin9(pc7x), .pin19(d_nEQ_0), .pin18(pc0x), .pin17(axd4), .pin16(pc1x), .pin15(axd5),
    .pin14(pc2x), .pin13(axd6), .pin12(pc3x), .pin11(axd7));
  _74193 #(.ShowInternalStructure("true")) u_pc0 (
    .pin1(pc1x), .pin2(pc1), .pin3(pc0), .pin4(pc0_pin4), .pin5(n_pcinc_x), .pin6(pc2), .pin7(pc3),
    .pin15(pc0x), .pin14(reset), .pin13(pc0_pin13), .pin12(pc0_pin12), .pin11(n_lpcl_x), .pin10(pc2x),
    .pin9(pc3x));
  _74193 #(.ShowInternalStructure("true")) u_pc1 (
    .pin1(pc5x), .pin2(pc5), .pin3(pc4), .pin4(pc0_pin13), .pin5(pc0_pin12), .pin6(pc6), .pin7(pc7),
    .pin15(pc4x), .pin14(reset), .pin13(pc1_pin13), .pin12(pc1_pin12), .pin11(n_lpcl_x), .pin10(pc6x),
    .pin9(pc7x));
  _74244 #(.ShowInternalStructure("true")) u_74244_9 (
    .pin1(n_epcl), .pin2(pc0), .pin3(axq4), .pin4(pc1), .pin5(axq5), .pin6(pc2), .pin7(axq6), .pin8(pc3),
    .pin9(axq7), .pin19(n_epcl), .pin18(axq0), .pin17(pc4), .pin16(axq1), .pin15(pc5), .pin14(axq2),
    .pin13(pc6), .pin12(axq3), .pin11(pc7));
  _74283 #(.ShowInternalStructure("true")) u_74283_4 (
    .pin1(s1), .pin2(y1), .pin3(x1), .pin4(s0), .pin5(x0), .pin6(y0), .pin7(c_in), .pin15(y2), .pin14(x2),
    .pin13(s2), .pin12(x3), .pin11(y3), .pin10(s3), .pin9(n74283_4_pin9));
  _74283 #(.ShowInternalStructure("true")) u_74283_5 (
    .pin1(s5), .pin2(y5), .pin3(x5), .pin4(s4), .pin5(x4), .pin6(y4), .pin7(n74283_4_pin9), .pin15(y6),
    .pin14(x6), .pin13(s6), .pin12(x7), .pin11(y7), .pin10(s7), .pin9(c_out));
  _74283 #(.ShowInternalStructure("true")) u_74283_6 (
    .pin1(b1), .pin2(ny1), .pin3(x1), .pin4(b0), .pin5(x0), .pin6(ny0), .pin7(b_in), .pin15(ny2), .pin14(x2),
    .pin13(b2), .pin12(x3), .pin11(ny3), .pin10(b3), .pin9(n74283_6_pin9));
  _74283 #(.ShowInternalStructure("true")) u_74283_7 (
    .pin1(b5), .pin2(ny5), .pin3(x5), .pin4(b4), .pin5(x4), .pin6(ny4), .pin7(n74283_6_pin9), .pin15(ny6),
    .pin14(x6), .pin13(b6), .pin12(x7), .pin11(ny7), .pin10(b7), .pin9(nb_out));
  _74138 #(.ShowInternalStructure("true")) u_74138_3 (
    .pin1(op0), .pin2(op1), .pin3(op2), .pin4(n74138_3_pin4), .pin5(n74138_3_pin5), .pin6(ealu),
    .pin7(nE_sub), .pin15(nE_pass), .pin14(nE_add), .pin13(nE_adc), .pin12(nE_and), .pin11(nE_or),
    .pin10(nE_nor), .pin9(nE_cmp));
  AT28C64B_MC1 at28c64b_mc1_1 (
    .IO0(mc8), .IO1(mc9), .IO2(mcA), .IO7(mcF), .IO6(mcE), .IO5(mcD), .IO4(mcC), .IO3(mcB), .A12(1'b0),
    .A7(op3), .A6(op2), .A5(op1), .A4(op0), .A3(op03), .A2(exc2), .A1(exc1), .A0(exc0), .nWE(1'b1),
    .A8(1'b0), .A9(1'b0), .A11(1'b0), .nOE(1'b0), .A10(1'b0), .nCE(1'b0));  // open: NC0, GND, NC1, VCC
  _7432 #(.ShowInternalStructure("true")) u_7432_5 (
    .pin1(sel00x), .pin2(sel10x), .pin3(n7432_5_pin3), .pin4(sel02x), .pin5(sel12x), .pin6(n7432_5_pin6),
    .pin13(sel01x), .pin12(sel11x), .pin11(n7432_5_pin11), .pin10(n7432_5_pin11), .pin9(ldf), .pin8(rs_b));
  _7432 #(.ShowInternalStructure("true")) u_7432_6 (
    .pin1(n7432_5_pin3), .pin2(ldh), .pin3(n7432_6_pin3), .pin4(n7432_6_pin3), .pin5(ldf), .pin6(rs_a),
    .pin13(ldh), .pin12(ldl), .pin11(n7432_6_pin11), .pin10(n7432_6_pin11), .pin9(ldf), .pin8(lpreset));
  _7432 #(.ShowInternalStructure("true")) u_7432_7 (
    .pin1(n7432_5_pin6), .pin2(lpreset), .pin3(rs_c), .pin13(lpreset), .pin12(lreg), .pin11(r_we));  // open: pin4, pin5, pin6, pin10, pin9, pin8
  _74573 #(.ShowInternalStructure("true")) u_74573_24 (
    .pin1(l_en), .pin2(l0), .pin3(l1), .pin4(l2), .pin5(l3), .pin6(l4), .pin7(l5), .pin8(l6), .pin9(l7),
    .pin19(rq0), .pin18(rq1), .pin17(rq2), .pin16(rq3), .pin15(rq4), .pin14(rq5), .pin13(rq6), .pin12(rq7),
    .pin11(n74573_24_pin11));
  _74573 #(.ShowInternalStructure("true")) u_74573_25 (
    .pin1(h_en), .pin2(h0), .pin3(h1), .pin4(h2), .pin5(h3), .pin6(h4), .pin7(h5), .pin8(h6), .pin9(h7),
    .pin19(rq0), .pin18(rq1), .pin17(rq2), .pin16(rq3), .pin15(rq4), .pin14(rq5), .pin13(rq6), .pin12(rq7),
    .pin11(n74573_25_pin11));
  _74573 #(.ShowInternalStructure("true")) u_74573_26 (
    .pin1(f_en), .pin2(flag_l), .pin3(flag_e), .pin4(flag_c), .pin5(flag_b), .pin6(f4), .pin7(f5), .pin8(f6),
    .pin9(f7), .pin19(rq0), .pin18(rq1), .pin17(rq2), .pin16(rq3), .pin15(rq4), .pin14(rq5), .pin13(rq6),
    .pin12(rq7), .pin11(n74573_26_pin11));
  _74244 #(.ShowInternalStructure("true")) u_74244_10 (
    .pin1(n74244_10_pin1), .pin2(d0), .pin3(axd4), .pin4(d1), .pin5(axd5), .pin6(d2), .pin7(axd6), .pin8(d3),
    .pin9(axd7), .pin19(n74244_10_pin19), .pin18(axd0), .pin17(d4), .pin16(axd1), .pin15(d5), .pin14(axd2),
    .pin13(d6), .pin12(axd3), .pin11(d7));
  _74244 #(.ShowInternalStructure("true")) u_74244_11 (
    .pin1(d_EQ_0), .pin2(h0), .pin3(pcCx), .pin4(h1), .pin5(pcDx), .pin6(h2), .pin7(pcEx), .pin8(h3),
    .pin9(pcFx), .pin19(d_EQ_0), .pin18(pc8x), .pin17(h4), .pin16(pc9x), .pin15(h5), .pin14(pcAx),
    .pin13(h6), .pin12(pcBx), .pin11(h7));
  _74244 #(.ShowInternalStructure("true")) u_74244_12 (
    .pin1(d_nEQ_0), .pin2(axd0), .pin3(pcCx), .pin4(axd1), .pin5(pcDx), .pin6(axd2), .pin7(pcEx),
    .pin8(axd3), .pin9(pcFx), .pin19(d_nEQ_0), .pin18(pc8x), .pin17(axd4), .pin16(pc9x), .pin15(axd5),
    .pin14(pcAx), .pin13(axd6), .pin12(pcBx), .pin11(axd7));
  _74193 #(.ShowInternalStructure("true")) u_pc2 (
    .pin1(pc9x), .pin2(pc9), .pin3(pc8), .pin4(pc1_pin13), .pin5(pc1_pin12), .pin6(pcA), .pin7(pcB),
    .pin15(pc8x), .pin14(reset), .pin13(pc2_pin13), .pin12(pc2_pin12), .pin11(n_lpch_x), .pin10(pcAx),
    .pin9(pcBx));
  _74193 #(.ShowInternalStructure("true")) u_pc3 (
    .pin1(pcDx), .pin2(pcD), .pin3(pcC), .pin4(pc2_pin13), .pin5(pc2_pin12), .pin6(pcE), .pin7(pcF),
    .pin15(pcCx), .pin14(reset), .pin11(n_lpch_x), .pin10(pcEx), .pin9(pcFx));  // open: pin13, pin12
  _74244 #(.ShowInternalStructure("true")) u_74244_13 (
    .pin1(n_epch), .pin2(pc8), .pin3(axq4), .pin4(pc9), .pin5(axq5), .pin6(pcA), .pin7(axq6), .pin8(pcB),
    .pin9(axq7), .pin19(n_epch), .pin18(axq0), .pin17(pcC), .pin16(axq1), .pin15(pcD), .pin14(axq2),
    .pin13(pcE), .pin12(axq3), .pin11(pcF));
  _74244 #(.ShowInternalStructure("true")) u_74244_14 (
    .pin1(nE_add_adc), .pin2(s0), .pin3(d4), .pin4(s1), .pin5(d5), .pin6(s2), .pin7(d6), .pin8(s3),
    .pin9(d7), .pin19(nE_add_adc), .pin18(d0), .pin17(s4), .pin16(d1), .pin15(s5), .pin14(d2), .pin13(s6),
    .pin12(d3), .pin11(s7));
  _74244 #(.ShowInternalStructure("true")) u_74244_15 (
    .pin1(nE_sub), .pin2(b0), .pin3(d4), .pin4(b1), .pin5(d5), .pin6(b2), .pin7(d6), .pin8(b3), .pin9(d7),
    .pin19(nE_sub), .pin18(d0), .pin17(b4), .pin16(d1), .pin15(b5), .pin14(d2), .pin13(b6), .pin12(d3),
    .pin11(b7));
  _7485 #(.ShowInternalStructure("true")) u_7485_2 (
    .pin1(y3), .pin2(n7485_2_pin2), .pin3(n7485_2_pin3), .pin4(n7485_2_pin4), .pin5(n7485_2_pin5),
    .pin6(n7485_2_pin6), .pin7(n7485_2_pin7), .pin15(x3), .pin14(y2), .pin13(x2), .pin12(x1), .pin11(y1),
    .pin10(x0), .pin9(y0));
  _7408 #(.ShowInternalStructure("true")) u_7408_12 (
    .pin1(x0), .pin2(y0), .pin3(a0), .pin4(x1), .pin5(y1), .pin6(a1), .pin13(x3), .pin12(y3), .pin11(a3),
    .pin10(x2), .pin9(y2), .pin8(a2));
  _74244 #(.ShowInternalStructure("true")) u_74244_16 (
    .pin1(nE_and), .pin2(a0), .pin3(d4), .pin4(a1), .pin5(d5), .pin6(a2), .pin7(d6), .pin8(a3), .pin9(d7),
    .pin19(nE_and), .pin18(d0), .pin17(a4), .pin16(d1), .pin15(a5), .pin14(d2), .pin13(a6), .pin12(d3),
    .pin11(a7));
  _74244 #(.ShowInternalStructure("true")) u_74244_17 (
    .pin1(nLDF), .pin2(XltY), .pin3(d4), .pin4(XeqY), .pin5(d5), .pin6(c_out), .pin7(d6), .pin8(b_out),
    .pin9(d7), .pin19(nLDF), .pin18(d0), .pin17(n74244_17_pin17), .pin16(d1), .pin15(n74244_17_pin15),
    .pin14(d2), .pin13(n74244_17_pin13), .pin12(d3), .pin11(n74244_17_pin11));
  _7408 #(.ShowInternalStructure("true")) u_7408_13 (
    .pin1(sel0), .pin2(op01), .pin3(sel01x), .pin4(sel0), .pin5(op00), .pin6(sel00x), .pin13(sel0),
    .pin12(op02), .pin11(sel02x), .pin10(sel1), .pin9(op10), .pin8(sel10x));
  _7408 #(.ShowInternalStructure("true")) u_7408_14 (
    .pin1(sel1), .pin2(op11), .pin3(sel11x), .pin4(sel1), .pin5(op12), .pin6(sel12x), .pin13(nsel),
    .pin12(nlpreset), .pin11(sel0), .pin10(sel), .pin9(nlpreset), .pin8(sel1));
  _74573 #(.ShowInternalStructure("true")) a (
    .pin1(a_en), .pin2(rd0), .pin3(rd1), .pin4(rd2), .pin5(rd3), .pin6(rd4), .pin7(rd5), .pin8(rd6),
    .pin9(rd7), .pin19(rq0), .pin18(rq1), .pin17(rq2), .pin16(rq3), .pin15(rq4), .pin14(rq5), .pin13(rq6),
    .pin12(rq7), .pin11(a_we));
  _74573 #(.ShowInternalStructure("true")) b (
    .pin1(b_en), .pin2(rd0), .pin3(rd1), .pin4(rd2), .pin5(rd3), .pin6(rd4), .pin7(rd5), .pin8(rd6),
    .pin9(rd7), .pin19(rq0), .pin18(rq1), .pin17(rq2), .pin16(rq3), .pin15(rq4), .pin14(rq5), .pin13(rq6),
    .pin12(rq7), .pin11(b_we));
  _74573 #(.ShowInternalStructure("true")) c (
    .pin1(c_en), .pin2(rd0), .pin3(rd1), .pin4(rd2), .pin5(rd3), .pin6(rd4), .pin7(rd5), .pin8(rd6),
    .pin9(rd7), .pin19(rq0), .pin18(rq1), .pin17(rq2), .pin16(rq3), .pin15(rq4), .pin14(rq5), .pin13(rq6),
    .pin12(rq7), .pin11(c_we));
  _74573 #(.ShowInternalStructure("true")) d (
    .pin1(d_en), .pin2(rd0), .pin3(rd1), .pin4(rd2), .pin5(rd3), .pin6(rd4), .pin7(rd5), .pin8(rd6),
    .pin9(rd7), .pin19(rq0), .pin18(rq1), .pin17(rq2), .pin16(rq3), .pin15(rq4), .pin14(rq5), .pin13(rq6),
    .pin12(rq7), .pin11(d_we));
  _7404 #(.ShowInternalStructure("true")) u_7404_9 (
    .pin1(jmp), .pin2(n_jmp), .pin3(d_nEQ_0), .pin4(d_EQ_0), .pin5(mb_EQ_0), .pin6(mb_nEQ_0), .pin13(eaux),
    .pin12(n_eaux), .pin11(bank), .pin10(n_bank), .pin9(lmem), .pin8(n_lmem));
  _7408 #(.ShowInternalStructure("true")) u_7408_15 (
    .pin1(emem), .pin2(n_adF), .pin3(erom), .pin4(n_lpcl), .pin5(n_jmp_x), .pin6(n_lpcl_x), .pin13(adF),
    .pin12(n_adE), .pin11(a_bank), .pin10(n_lpch), .pin9(n_jmp_x), .pin8(n_lpch_x));
  _7400 #(.ShowInternalStructure("true")) u_7400_1 (
    .pin1(n_ex), .pin2(seq_3), .pin3(n_pcinc_x), .pin4(spinc), .pin5(seq_3), .pin6(n_spinc_x), .pin13(spdec),
    .pin12(seq_3), .pin11(n_spdec_x), .pin10(jmp), .pin9(seq_3), .pin8(n_jmp_x));
  _7411 #(.ShowInternalStructure("true")) u_7411_4 (
    .pin1(jnz), .pin2(d_nEQ_0), .pin3(mb_nEQ_0), .pin4(lmem), .pin5(bank), .pin6(lbank),
    .pin13(n7411_4_pin13), .pin12(jmp), .pin11(mb_nEQ_0), .pin10(emem), .pin9(bank), .pin8(ebank));
  _74193 #(.ShowInternalStructure("true")) u_sp0 (
    .pin1(axd1), .pin2(sp1), .pin3(sp0), .pin4(n_spdec_x), .pin5(n_spinc_x), .pin6(sp2), .pin7(sp3),
    .pin15(axd0), .pin14(sp0_pin14), .pin13(sp0_pin13), .pin12(sp0_pin12), .pin11(n_lspl), .pin10(axd2),
    .pin9(axd3));
  _74193 #(.ShowInternalStructure("true")) u_sp1 (
    .pin1(axd5), .pin2(sp5), .pin3(sp4), .pin4(sp0_pin13), .pin5(sp0_pin12), .pin6(sp6), .pin7(sp7),
    .pin15(axd4), .pin14(sp1_pin14), .pin13(sp1_pin13), .pin12(sp1_pin12), .pin11(n_lspl), .pin10(axd6),
    .pin9(axd7));
  _74244 #(.ShowInternalStructure("true")) u_74244_18 (
    .pin1(n_espl), .pin2(sp0), .pin3(axq4), .pin4(sp1), .pin5(axq5), .pin6(sp2), .pin7(axq6), .pin8(sp3),
    .pin9(axq7), .pin19(n_espl), .pin18(axq0), .pin17(sp4), .pin16(axq1), .pin15(sp5), .pin14(axq2),
    .pin13(sp6), .pin12(axq3), .pin11(sp7));
  _7485 #(.ShowInternalStructure("true")) u_7485_3 (
    .pin1(y7), .pin2(n7485_2_pin7), .pin3(n7485_2_pin6), .pin4(n7485_2_pin5), .pin6(XeqY), .pin7(XltY),
    .pin15(x7), .pin14(y6), .pin13(x6), .pin12(x5), .pin11(y5), .pin10(x4), .pin9(y4));  // open: pin5
  _7408 #(.ShowInternalStructure("true")) u_7408_16 (
    .pin1(x4), .pin2(y4), .pin3(a4), .pin4(x5), .pin5(y5), .pin6(a5), .pin13(x7), .pin12(y7), .pin11(a7),
    .pin10(x6), .pin9(y6), .pin8(a6));
  _7432 #(.ShowInternalStructure("true")) u_7432_8 (
    .pin1(x0), .pin2(y0), .pin3(o0), .pin4(x1), .pin5(y1), .pin6(o1), .pin13(x3), .pin12(y3), .pin11(o3),
    .pin10(x2), .pin9(y2), .pin8(o2));
  _7432 #(.ShowInternalStructure("true")) u_7432_9 (
    .pin1(x4), .pin2(y4), .pin3(o4), .pin4(x5), .pin5(y5), .pin6(o5), .pin13(x7), .pin12(y7), .pin11(o7),
    .pin10(x6), .pin9(y6), .pin8(o6));
  _74244 #(.ShowInternalStructure("true")) u_74244_19 (
    .pin1(nE_or), .pin2(a0), .pin3(d4), .pin4(o1), .pin5(d5), .pin6(o2), .pin7(d6), .pin8(o3), .pin9(d7),
    .pin19(nE_or), .pin18(d0), .pin17(o4), .pin16(d1), .pin15(o5), .pin14(d2), .pin13(o6), .pin12(d3),
    .pin11(o7));
  _74138 #(.ShowInternalStructure("true")) u_74138_4 (
    .pin1(rs_a), .pin2(rs_b), .pin3(rs_c), .pin4(n74138_4_pin4), .pin5(n74138_4_pin5), .pin6(ereg),
    .pin7(f_en), .pin15(a_en), .pin14(b_en), .pin13(c_en), .pin12(d_en), .pin11(l_en), .pin10(h_en),
    .pin9(z_en));
  _74238 #(.ShowInternalStructure("true")) u_74238_2 (
    .pin1(rs_a), .pin2(rs_b), .pin3(rs_c), .pin4(n74238_2_pin4), .pin5(n_r_we), .pin6(seq_2), .pin7(f_we),
    .pin15(a_we), .pin14(b_we), .pin13(c_we), .pin12(d_we), .pin11(l_we), .pin10(h_we), .pin9(z_we));
  _74573 #(.ShowInternalStructure("true")) z (
    .pin1(z_en), .pin2(rd0), .pin3(rd1), .pin4(rd2), .pin5(rd3), .pin6(rd4), .pin7(rd5), .pin8(rd6),
    .pin9(rd7), .pin19(rq0), .pin18(rq1), .pin17(rq2), .pin16(rq3), .pin15(rq4), .pin14(rq5), .pin13(rq6),
    .pin12(rq7), .pin11(z_we));
  _7421 #(.ShowInternalStructure("true")) u_7421_1 (
    .pin1(ad3), .pin2(ad4), .pin4(ad5), .pin5(ad6), .pin6(n7421_1_pin6), .pin13(ad7), .pin12(ad8),
    .pin10(ad9), .pin9(adA), .pin8(n7421_1_pin8));  // open: pin3, pin11
  _7421 #(.ShowInternalStructure("true")) u_7421_2 (
    .pin1(n7421_1_pin6), .pin2(adB), .pin4(adC), .pin5(adD), .pin6(n7421_2_pin6), .pin13(n7421_1_pin8),
    .pin12(adE), .pin10(adF), .pin9(n7421_2_pin6), .pin8(a_aux));  // open: pin3, pin11
  _7432 #(.ShowInternalStructure("true")) u_7432_10 (
    .pin1(emem_x), .pin2(n_ex), .pin3(emem), .pin4(ad1), .pin5(ad2), .pin6(n7432_10_pin6), .pin13(n_ex),
    .pin12(asp), .pin11(n7432_10_pin11), .pin10(n7432_10_pin11), .pin9(aimm), .pin8(n_ahl));
  _7408 #(.ShowInternalStructure("true")) u_7408_17 (
    .pin1(n7432_10_pin6), .pin2(a_aux), .pin3(eaux), .pin4(n_eaux), .pin5(adF), .pin6(a_upper));  // open: pin13, pin12, pin11, pin10, pin9, pin8
  _7411 #(.ShowInternalStructure("true")) u_7411_5 (
    .pin1(a_bank), .pin2(mb_nEQ_0), .pin3(a_upper), .pin4(emem), .pin5(n_bank), .pin6(eram),
    .pin13(n7411_5_pin13), .pin12(bank), .pin11(a_upper), .pin10(lmem), .pin9(n_bank), .pin8(lram));
  _7404 #(.ShowInternalStructure("true")) u_7404_10 (
    .pin1(aimm), .pin2(n_aimm), .pin3(n_ex), .pin4(n_apc), .pin5(asp), .pin6(n_asp), .pin13(eaux),
    .pin12(n_eaux), .pin11(adE), .pin10(n_adE), .pin9(adF), .pin8(n_adF));
  _74688 #(.ShowInternalStructure("true")) u_74688_5 (
    .pin1(n74688_5_pin1), .pin2(axd0), .pin3(n74688_5_pin3), .pin4(axd1), .pin5(n74688_5_pin5), .pin6(axd2),
    .pin7(n74688_5_pin7), .pin8(axd3), .pin9(n74688_5_pin9), .pin19(d_nEQ_0), .pin18(axd7),
    .pin17(n74688_5_pin17), .pin16(axd6), .pin15(n74688_5_pin15), .pin14(axd5), .pin13(n74688_5_pin13),
    .pin12(axd4), .pin11(n74688_5_pin11));
  _74193 #(.ShowInternalStructure("true")) u_sp2 (
    .pin1(axd1), .pin2(sp9), .pin3(sp8), .pin4(sp1_pin13), .pin5(sp1_pin12), .pin6(spA), .pin7(spB),
    .pin15(axd0), .pin14(sp2_pin14), .pin13(sp2_pin13), .pin12(sp2_pin12), .pin11(n_lsph), .pin10(axd2),
    .pin9(axd3));
  _74193 #(.ShowInternalStructure("true")) u_sp3 (
    .pin1(axd5), .pin2(spD), .pin3(spC), .pin4(sp2_pin13), .pin5(sp2_pin12), .pin6(spE), .pin7(spF),
    .pin15(axd4), .pin14(sp3_pin14), .pin11(n_lsph), .pin10(axd6), .pin9(axd7));  // open: pin13, pin12
  _74244 #(.ShowInternalStructure("true")) u_74244_20 (
    .pin1(n_esph), .pin2(sp8), .pin3(axq4), .pin4(sp9), .pin5(axq5), .pin6(spA), .pin7(axq6), .pin8(spB),
    .pin9(axq7), .pin19(n_esph), .pin18(axq0), .pin17(spC), .pin16(axq1), .pin15(spD), .pin14(axq2),
    .pin13(spE), .pin12(axq3), .pin11(spF));
  _7404 #(.ShowInternalStructure("true")) u_7404_11 (
    .pin1(o0), .pin2(n0), .pin3(o1), .pin4(n1), .pin5(o2), .pin6(n2), .pin13(o5), .pin12(n5), .pin11(o4),
    .pin10(n4), .pin9(o3), .pin8(n3));
  _7404 #(.ShowInternalStructure("true")) u_7404_12 (
    .pin1(o6), .pin2(n6), .pin3(o7), .pin4(n7));  // open: pin5, pin6, pin13, pin12, pin11, pin10, pin9, pin8
  _74244 #(.ShowInternalStructure("true")) u_74244_21 (
    .pin1(nE_nor), .pin2(n0), .pin3(d4), .pin4(n1), .pin5(d5), .pin6(n2), .pin7(d6), .pin8(n3), .pin9(d7),
    .pin19(nE_nor), .pin18(d0), .pin17(n4), .pin16(d1), .pin15(n5), .pin14(d2), .pin13(n6), .pin12(d3),
    .pin11(n7));
  Clock clock_1 (.out(clk));
  _7404 #(.ShowInternalStructure("true")) u_7404_13 (
    .pin1(reset), .pin2(nreset), .pin3(clk), .pin4(nclk), .pin5(nclk), .pin6(n7404_13_pin6), .pin13(seq_3),
    .pin12(n_seq_3), .pin11(st3), .pin10(n_hlt), .pin9(n7404_13_pin6), .pin8(n7404_13_pin8));
  Button button_1 (.out(reset));
  _74163 #(.ShowInternalStructure("true")) u_74163_3 (
    .pin1(n_seq_3), .pin2(clk), .pin3(n74163_3_pin3), .pin4(n74163_3_pin4), .pin5(n74163_3_pin5),
    .pin6(n74163_3_pin6), .pin7(n_hlt), .pin14(n74163_3_pin14), .pin13(n74163_3_pin13),
    .pin10(n74163_3_pin10), .pin9(n74163_3_pin9));  // open: pin15, pin12, pin11
  _74238 #(.ShowInternalStructure("true")) u_74238_3 (
    .pin1(n74163_3_pin14), .pin2(n74163_3_pin13), .pin3(n74238_3_pin3), .pin4(n74238_3_pin4),
    .pin5(n74238_3_pin5), .pin6(n74238_3_pin6), .pin15(seq_0), .pin14(seq_1), .pin13(seq_2), .pin12(seq_3));  // open: pin7, pin11, pin10, pin9
  _7408 #(.ShowInternalStructure("true")) u_7408_18 (
    .pin1(n7404_13_pin8), .pin2(clk), .pin3(rise));  // open: pin4, pin5, pin6, pin13, pin12, pin11, pin10, pin9, pin8
  // also tied to GND on the sheet: {HSC_0_pin3, HSC_0_pin4, HSC_0_pin5, HSC_0_pin6, HSC_1_pin3, HSC_1_pin4, HSC_1_pin5, HSC_1_pin6, HSC_2_pin3, HSC_2_pin4, HSC_2_pin5, HSC_2_pin6, TKC_0_pin3, TKC_0_pin4, TKC_0_pin5, TKC_0_pin6, TKC_1_pin3, TKC_1_pin4, TKC_1_pin5, TKC_1_pin6, n74688_1_pin1, n74688_1_pin3, n74688_1_pin5, n74688_1_pin7, n74688_1_pin9, n74682_1_pin9, n74688_2_pin1, n74688_3_pin1, n74688_4_pin1, n74688_4_pin3, n74688_4_pin5, n74688_4_pin7, n7485_1_pin1, n7485_1_pin2, n7485_1_pin4, n74238_1_pin3, n74238_1_pin4, n74238_1_pin5, n74163_1_pin3, n74163_1_pin4, n74163_1_pin5, n74163_1_pin6, n74163_2_pin3, n74163_2_pin4, n74163_2_pin5, n74163_2_pin6, n74688_1_pin16, n74688_1_pin14, n74688_1_pin12, n74682_1_pin18, n74682_1_pin17, n74682_1_pin16, n74682_1_pin14, n74682_1_pin12, n74682_2_pin18, n74682_2_pin17, n74682_2_pin12, n74688_2_pin18, n74688_2_pin16, n74688_2_pin14, n74688_2_pin12, n74688_3_pin18, n74688_3_pin16, n74688_3_pin12, n7485_1_pin9, EQ_5_pin1, EQ_5_pin3, EQ_5_pin5, EQ_5_pin9, EQ_09_pin1, EQ_09_pin3, EQ_09_pin7, EQ_54_pin1, EQ_54_pin3, EQ_54_pin5, EQ_54_pin9, EQ_33_pin1, EQ_33_pin7, EQ_33_pin9, EQ_69_pin1, EQ_69_pin3, EQ_69_pin7, EQ_6F_pin1, n74283_1_pin2, n74283_1_pin6, n74283_1_pin7, n74283_2_pin6, EQ_5_pin18, EQ_5_pin16, EQ_5_pin14, EQ_5_pin12, EQ_09_pin18, EQ_09_pin16, EQ_09_pin14, EQ_09_pin12, EQ_54_pin18, EQ_54_pin14, EQ_33_pin18, EQ_33_pin16, EQ_69_pin18, EQ_69_pin12, EQ_6F_pin18, EQ_6F_pin12, n74283_2_pin15, n74283_3_pin15, n74283_3_pin11, n7427_1_pin13, n7427_2_pin9, n74151_1_pin7, n74573_1_pin1, n74573_3_pin7, n74573_3_pin8, n74573_3_pin9, op0_pin1, op1_pin1, op2_pin1, n74682_3_pin5, n74682_3_pin7, n74682_3_pin9, n74244_1_pin1, n74244_2_pin1, n74573_10_pin1, n74573_11_pin1, n74682_3_pin18, n74682_3_pin16, n74682_3_pin14, n74682_3_pin12, n74244_1_pin19, n74244_2_pin19, mb_pin1, n74138_1_pin4, n74573_16_pin1, n74125_1_pin1, n74125_1_pin4, n74125_2_pin1, n74125_2_pin4, n74125_3_pin1, n74125_3_pin4, n74125_4_pin1, n74125_4_pin4, n74125_5_pin1, n74125_5_pin4, n74125_6_pin1, n74125_6_pin4, n74125_1_pin13, n74125_1_pin10, n74125_2_pin13, n74125_2_pin10, n74125_3_pin13, n74125_3_pin10, n74125_4_pin13, n74125_4_pin10, n74125_5_pin13, n74125_5_pin10, n74125_6_pin13, n74125_6_pin10, n74573_17_pin1, n74244_3_pin1, n74374_1_pin1, n74374_2_pin1, n74244_3_pin19, n74573_23_pin1, l_pin1, h_pin1, f_pin1, n74138_3_pin4, n74138_3_pin5, n74244_10_pin1, n7485_2_pin2, n7485_2_pin4, n74244_10_pin19, n74244_17_pin17, n74244_17_pin15, n74244_17_pin13, n74244_17_pin11, sp0_pin14, sp1_pin14, n74138_4_pin4, n74138_4_pin5, n74238_2_pin4, n74688_5_pin1, n74688_5_pin3, n74688_5_pin5, n74688_5_pin7, n74688_5_pin9, n74688_5_pin17, n74688_5_pin15, n74688_5_pin13, n74688_5_pin11, sp2_pin14, sp3_pin14, n74163_3_pin3, n74163_3_pin4, n74163_3_pin5, n74163_3_pin6, n74238_3_pin3, n74238_3_pin4, n74238_3_pin5}
  // also tied to VCC on the sheet: {HSC_0_pin7, HSC_1_pin7, HSC_2_pin7, TKC_0_pin7, TKC_1_pin7, n74682_1_pin3, n74682_1_pin5, n74682_1_pin7, n74682_2_pin3, n74682_2_pin5, n74682_2_pin7, n74682_2_pin9, n74688_2_pin3, n74688_2_pin5, n74688_2_pin7, n74688_2_pin9, n74688_3_pin3, n74688_3_pin5, n74688_3_pin7, n74688_3_pin9, n74688_4_pin9, n7485_1_pin3, n74238_1_pin6, HSC_0_pin9, HSC_1_pin9, HSC_2_pin9, TKC_0_pin10, TKC_0_pin9, TKC_1_pin9, n74688_1_pin18, n74682_2_pin16, n74682_2_pin14, n74688_3_pin14, n74688_4_pin18, n74688_4_pin16, n74688_4_pin14, n74688_4_pin12, n7485_1_pin14, n7485_1_pin11, n74163_1_pin10, n74163_1_pin9, n74163_2_pin10, n74163_2_pin9, EQ_5_pin7, EQ_09_pin5, EQ_09_pin9, EQ_54_pin7, EQ_33_pin3, EQ_33_pin5, EQ_69_pin5, EQ_69_pin9, EQ_6F_pin3, EQ_6F_pin5, EQ_6F_pin7, EQ_6F_pin9, n74283_2_pin2, n74283_3_pin2, n74283_3_pin6, EQ_54_pin16, EQ_54_pin12, EQ_33_pin14, EQ_33_pin12, EQ_69_pin16, EQ_69_pin14, EQ_6F_pin16, EQ_6F_pin14, n74283_1_pin15, n74283_1_pin11, n74283_2_pin11, n7411_2_pin11, n74573_2_pin11, n74573_3_pin11, n74573_4_pin11, n74573_5_pin11, n74573_6_pin11, n74573_7_pin11, n74682_3_pin3, n7411_3_pin13, n7411_3_pin9, n74573_8_pin11, n74573_9_pin11, n74573_12_pin11, n74573_13_pin11, n74573_14_pin11, n74573_15_pin11, n74573_16_pin11, n74573_18_pin11, n74573_19_pin11, n74573_20_pin11, n74573_21_pin11, n74573_22_pin11, pc0_pin4, n7485_2_pin3, n74573_24_pin11, n74573_25_pin11, n74573_26_pin11, n7411_4_pin13, n7411_5_pin13, n74163_3_pin10, n74163_3_pin9, n74238_3_pin6}

  // Other names for the same wires on the sheet: sel00 = op00; sel01 = op01; sel02 = op02; y = op03; op04 = op0;
  //   op05 = op1; op06 = op2; op07 = op3; sel10 = op10; sel11 = op11; sel12 = op12; seq_aux_up = seq_3;
  //   seq_mc_load = seq_0; seq_opc_count = seq_0; seq_opc_load = seq_1; seq_alu_load = seq_2; seq_aux_load = seq_2;
  //   seq_dev_load = seq_2; seq_reg_load = seq_2; q0 = d0; z0 = d0; q1 = d1; z1 = d1; q2 = d2; z2 = d2; q3 = d3;
  //   z3 = d3; q4 = d4; z4 = d4; q5 = d5; z5 = d5; q6 = d6; z6 = d6; q7 = d7; z7 = d7

  // Notes on the sheet:
  //   OP0
  //   OP1
  //   OP2
  //   PC
  //   SP
endmodule
module pretty74 (
);

  wire a0, a001, a1, a2, a3, a4, a5, a6, a7, a010, a101, a_aux, a_bank, a_en, a_upper, a_we, ad0, ad1, ad2,
       ad3, ad4, ad5, ad6, ad7, ad8, ad9, adA, adB, adC, adD, adE, adF, aimm, asp, axd0, axd1, axd2, axd3,
       axd4, axd5, axd6, axd7, axq0, axq1, axq2, axq3, axq4, axq5, axq6, axq7, b0, b1, b2, b3, b4, b5, b6,
       b7, b_en, b_in, b_out, b_we, bank, bank_vram, c_en, c_in, c_out, c_we, cc, clk, clock_1_out, d0, d1,
       d2, d3, d4, d5, d6, d7, d_en, d_EQ_0, d_nEQ_0, d_we, dbg_x, dbg_y, dx0, dx1, dx2, dx3, dx4, dx5, dx6,
       dx7, ealu, eaux, ebank, edev, el_vram, emem, eop1, eop2, EQ_5_pin1, EQ_5_pin3, EQ_5_pin5, EQ_5_pin7,
       EQ_5_pin9, EQ_5_pin12, EQ_5_pin14, EQ_5_pin16, EQ_5_pin18, EQ_6F_pin1, EQ_6F_pin3, EQ_6F_pin5,
       EQ_6F_pin7, EQ_6F_pin9, EQ_6F_pin12, EQ_6F_pin14, EQ_6F_pin16, EQ_6F_pin18, EQ_09_pin1, EQ_09_pin3,
       EQ_09_pin5, EQ_09_pin7, EQ_09_pin9, EQ_09_pin12, EQ_09_pin14, EQ_09_pin16, EQ_09_pin18, EQ_33_pin1,
       EQ_33_pin3, EQ_33_pin5, EQ_33_pin7, EQ_33_pin9, EQ_33_pin12, EQ_33_pin14, EQ_33_pin16, EQ_33_pin18,
       EQ_54_pin1, EQ_54_pin3, EQ_54_pin5, EQ_54_pin7, EQ_54_pin9, EQ_54_pin12, EQ_54_pin14, EQ_54_pin16,
       EQ_54_pin18, EQ_69_pin1, EQ_69_pin3, EQ_69_pin5, EQ_69_pin7, EQ_69_pin9, EQ_69_pin12, EQ_69_pin14,
       EQ_69_pin16, EQ_69_pin18, eram, ereg, erom, esta, eta, etb, evram, ex, exc0, exc1, exc2, f4, f5, f6,
       f7, f_en, f_pin1, f_we, fall, flag_b, flag_c, flag_e, flag_l, h0, h1, h2, h3, h4, h5, h6, h7, h_en,
       h_pin1, h_we, hsc0, hsc0Q, hsc1, hsc1Q, hsc2, hsc2Q, hsc3, hsc3Q, hsc4, hsc4Q, hsc5, hsc5Q, hsc6,
       hsc7, hsc8, hsc9, HSC_0_pin3, HSC_0_pin4, HSC_0_pin5, HSC_0_pin6, HSC_0_pin7, HSC_0_pin9, HSC_0_pin15,
       HSC_1_pin1, HSC_1_pin3, HSC_1_pin4, HSC_1_pin5, HSC_1_pin6, HSC_1_pin7, HSC_1_pin9, HSC_1_pin15,
       HSC_2_pin3, HSC_2_pin4, HSC_2_pin5, HSC_2_pin6, HSC_2_pin7, HSC_2_pin9, hsc_eORd, hsc_inc, hsc_n1S,
       hsc_n2S, hsc_n3S, hsc_n4S, hsc_n5S, hsc_n9, hsc_nEQ_05, hsc_nEQ_6A, hsc_nEQ_6E, hsc_nEQ_34,
       hsc_nEQ_54, hsc_nEQ_A, hsc_nR, hsc_or_89, hsc_pp, jmp, jnz, l0, l1, l2, l3, l4, l5, l6, l7, l_en,
       l_pin1, l_we, latch_vram, lbank, ld1, ld1_x, ld2, ld2_x, ld3, ld3_x, ldev, ldf, ldh, ldl, ldx, ldy,
       lmb, lmem, lop0, lop1, lop2, lopN, lpreset, lprt, lprt_x, lram, lreg, lsta, lvram, mb0, mb1, mb2, mb3,
       mb4, mb5, mb6, mb7, mb_EQ_0, mb_nEQ_0, mb_pin1, mc0, mc0_x, mc1, mc1_x, mc2, mc2_x, mc3, mc3_x, mc4,
       mc4_x, mc5, mc5_x, mc6, mc6_x, mc7, mc7_x, mc8, mc8_x, mc9, mc9_x, mcA, mcA_x, mcB, mcB_x, mcC, mcC_x,
       mcD, mcD_x, mcE, mcE_x, mcF, mcF_x, mw_lda, n0, n1, n2, n3, n4, n5, n6, n7, n7402_1_pin1,
       n7402_1_pin2, n7404_1_pin2, n7404_1_pin6, n7404_4_pin3, n7404_6_pin6, n7404_6_pin8, n7404_6_pin10,
       n7404_6_pin12, n7408_3_pin8, n7411_2_pin6, n7411_2_pin11, n7411_3_pin2, n7411_3_pin13, n7411_4_pin13,
       n7411_5_pin13, n7421_1_pin6, n7421_1_pin8, n7421_2_pin6, n7427_1_pin6, n7427_1_pin13, n7427_2_pin9,
       n7432_2_pin11, n7432_3_pin3, n7432_3_pin6, n7432_3_pin8, n7432_3_pin11, n7432_4_pin3, n7432_4_pin6,
       n7432_5_pin3, n7432_5_pin6, n7432_5_pin11, n7432_6_pin3, n7432_6_pin11, n7432_10_pin6, n7432_10_pin11,
       n7485_1_pin1, n7485_1_pin2, n7485_1_pin3, n7485_1_pin4, n7485_1_pin9, n7485_1_pin11, n7485_1_pin14,
       n7485_2_pin1, n7485_2_pin2, n7485_2_pin3, n7485_2_pin4, n7485_2_pin9, n7485_2_pin11, n7485_2_pin14,
       n7485_3_pin1, n7485_3_pin2, n7485_3_pin3, n7485_3_pin4, n7485_3_pin9, n7485_3_pin11, n7485_3_pin14,
       n7485_4_pin2, n7485_4_pin3, n7485_4_pin4, n7485_4_pin5, n7485_4_pin6, n7485_4_pin7, n74138_1_pin4,
       n74138_3_pin4, n74138_3_pin5, n74138_4_pin4, n74138_4_pin5, n74151_1_pin7, n74163_1_pin3,
       n74163_1_pin4, n74163_1_pin5, n74163_1_pin6, n74163_1_pin9, n74163_1_pin10, n74163_2_pin3,
       n74163_2_pin4, n74163_2_pin5, n74163_2_pin6, n74163_2_pin9, n74163_2_pin10, n74238_1_pin3,
       n74238_1_pin4, n74238_1_pin5, n74238_1_pin6, n74238_2_pin4, n74244_1_pin1, n74244_1_pin19,
       n74244_2_pin1, n74244_2_pin19, n74244_3_pin1, n74244_3_pin19, n74244_11_pin1, n74244_11_pin19,
       n74244_18_pin11, n74244_18_pin13, n74244_18_pin15, n74244_18_pin17, n74283_1_pin2, n74283_1_pin6,
       n74283_1_pin7, n74283_1_pin9, n74283_1_pin11, n74283_1_pin15, n74283_2_pin2, n74283_2_pin6,
       n74283_2_pin9, n74283_2_pin11, n74283_2_pin15, n74283_3_pin2, n74283_3_pin6, n74283_3_pin11,
       n74283_3_pin15, n74283_4_pin9, n74283_6_pin9, n74374_1_pin1, n74374_2_pin1, n74573_1_pin1,
       n74573_2_pin11, n74573_3_pin7, n74573_3_pin8, n74573_3_pin9, n74573_3_pin11, n74573_4_pin11,
       n74573_5_pin11, n74573_6_pin11, n74573_7_pin11, n74573_8_pin11, n74573_9_pin11, n74573_10_pin1,
       n74573_11_pin1, n74573_12_pin11, n74573_13_pin11, n74573_14_pin11, n74573_15_pin11, n74573_16_pin1,
       n74573_17_pin11, n74573_18_pin11, n74573_19_pin11, n74573_20_pin11, n74573_21_pin11, n74573_22_pin1,
       n74573_23_pin11, n74573_24_pin11, n74573_25_pin11, n74682_1_pin3, n74682_1_pin5, n74682_1_pin7,
       n74682_1_pin9, n74682_1_pin12, n74682_1_pin14, n74682_1_pin16, n74682_1_pin17, n74682_1_pin18,
       n74682_2_pin3, n74682_2_pin5, n74682_2_pin7, n74682_2_pin9, n74682_2_pin12, n74682_2_pin14,
       n74682_2_pin16, n74682_2_pin17, n74682_2_pin18, n74688_1_pin1, n74688_1_pin3, n74688_1_pin5,
       n74688_1_pin7, n74688_1_pin9, n74688_1_pin12, n74688_1_pin14, n74688_1_pin16, n74688_1_pin18,
       n74688_2_pin1, n74688_2_pin3, n74688_2_pin5, n74688_2_pin7, n74688_2_pin9, n74688_2_pin12,
       n74688_2_pin14, n74688_2_pin16, n74688_2_pin18, n74688_3_pin1, n74688_3_pin3, n74688_3_pin5,
       n74688_3_pin7, n74688_3_pin9, n74688_3_pin12, n74688_3_pin14, n74688_3_pin16, n74688_3_pin18,
       n74688_4_pin1, n74688_4_pin3, n74688_4_pin5, n74688_4_pin7, n74688_4_pin9, n74688_4_pin12,
       n74688_4_pin14, n74688_4_pin16, n74688_4_pin18, n74688_5_pin1, n74688_5_pin3, n74688_5_pin5,
       n74688_5_pin7, n74688_5_pin9, n74688_5_pin12, n74688_5_pin14, n74688_5_pin16, n74688_5_pin18,
       n74688_6_pin1, n74688_6_pin3, n74688_6_pin5, n74688_6_pin7, n74688_6_pin9, n74688_6_pin11,
       n74688_6_pin13, n74688_6_pin15, n74688_6_pin17, n_adE, n_adF, n_ahl, n_aimm, n_apc, n_asp, n_bank,
       n_cc, n_ealu_ldf, n_eaux, n_el_vram, n_emb, n_eop1, n_eop2, n_epch, n_epcl, n_eram, n_ereg, n_erom,
       n_esph, n_espl, n_esta, n_evram, n_ex, n_jmp, n_jmp_x, n_lmb, n_lpch, n_lpch_x, n_lpcl, n_lpcl_x,
       n_lram, n_lsph, n_lspl, n_lvram, n_mcE_x, n_mcF_x, n_mw_lda, n_pcinc_x, n_spdec_x, n_spinc_x, nb_out,
       nclk, nE_adc, nE_add, nE_add_adc, nE_and, nE_cmp, nE_nor, nE_or, nE_pass, nE_sub, nLDF, nlpreset,
       nop0, nop1, nop2, nreset, nsel, nV03_broad, nV03_short, nV03_sync, ny, ny0, ny1, ny2, ny3, ny4, ny5,
       ny6, ny7, o0, o1, o2, o3, o4, o5, o6, o7, op0, op00, op0_pin1, op01, op1, op1_pin1, op02, op2,
       op2_pin1, op03, op3, op10, op11, op12, op13, op14, op15, op16, op17, op20, op21, op22, op23, op24,
       op25, op26, op27, op_gt_6, opc0, opc1, opc_eq_0, opc_eq_1, opc_eq_2, opc_eq_3, pc0, pc0_pin4,
       pc0_pin12, pc0_pin13, pc0x, pc1, pc1_pin12, pc1_pin13, pc1x, pc2, pc2_pin12, pc2_pin13, pc2x, pc3,
       pc3x, pc4, pc4x, pc5, pc5x, pc6, pc6x, pc7, pc7x, pc8, pc8x, pc9, pc9x, pcA, pcAx, pcB, pcBx, pcC,
       pcCx, pcD, pcDx, pcE, pcEx, pcF, pcFx, prt0, prt1, prt2, prt3, prt4, prt5, prt6, prt7, prt_EQ_0,
       prt_nEQ_0, r_we, rd0, rd1, rd2, rd3, rd4, rd5, rd6, rd7, reset, rise, rq0, rq1, rq2, rq3, rq4, rq5,
       rq6, rq7, rs_a, rs_b, rs_c, s0, s1, s2, s3, s4, s5, s6, s7, sel, sel0, sel00x, sel1, sel01x, sel02x,
       sel10x, sel11x, sel12x, sp0, sp0_pin12, sp0_pin13, sp0_pin14, sp1, sp1_pin12, sp1_pin13, sp1_pin14,
       sp2, sp2_pin12, sp2_pin13, sp2_pin14, sp3, sp3_pin14, sp4, sp5, sp6, sp7, sp8, sp9, spA, spB, spC,
       spD, spdec, spE, spF, spinc, st0, st1, st2, st3, st4, st5, st6, st7, tkc0, tkc0Q, tkc1, tkc1Q, tkc2,
       tkc2Q, tkc3, tkc3Q, tkc4, tkc5, tkc6, tkc7, tkc7_LE_6F, tkc7_LE_07, TKC_0_pin3, TKC_0_pin4,
       TKC_0_pin5, TKC_0_pin6, TKC_0_pin7, TKC_0_pin9, TKC_0_pin10, TKC_0_pin15, TKC_1_pin3, TKC_1_pin4,
       TKC_1_pin5, TKC_1_pin6, TKC_1_pin7, TKC_1_pin9, tkc_nEQ_0F, tkc_nEQ_0F_2, tkc_nEQ_28, tkc_nEQ_80,
       tkc_nEQ_F8, tkc_nRC0, tkc_RC0, v_03, v_10, vbit, vd0, vd0_x, vd1, vd1_x, vd2, vd2_x, vd3, vd3_x, vd4,
       vd4_x, vd5, vd5_x, vd6, vd6_x, vd7, vd7_x, vma0_x, vma1_x, vma2_x, vma3_x, vma4_x, vma5, vma5_x, vma6,
       vma6_x, vma7, vma7_x, vma8, vma8_x, vma9, vma9_x, vmaA, vmaA_x, vmaB, vmaB_x, vmaC, vmaC_x, vmaD,
       vmaE, vram_d0, vram_d1, vram_d2, vram_d3, vram_d4, vram_d5, vram_d6, vram_d7, x0, x1, x2, x3, x4, x5,
       x6, x7, xc, XeqY, XltY, y0, y1, y2, y3, y4, y5, y6, y7, yc, z0, z1, z2, z3, z4, z5, z6, z7, z_en, z_we;

  _74161 #(.ShowInternalStructure("true")) HSC_0 (
    .pin1(hsc_nR), .pin2(clk), .pin3(HSC_0_pin3), .pin4(HSC_0_pin4), .pin5(HSC_0_pin5), .pin6(HSC_0_pin6),
    .pin7(HSC_0_pin7), .pin15(HSC_0_pin15), .pin14(hsc0), .pin13(hsc1), .pin12(hsc2), .pin11(hsc3),
    .pin10(hsc_inc), .pin9(HSC_0_pin9));
  _74161 #(.ShowInternalStructure("true")) HSC_1 (
    .pin1(HSC_1_pin1), .pin2(clk), .pin3(HSC_1_pin3), .pin4(HSC_1_pin4), .pin5(HSC_1_pin5),
    .pin6(HSC_1_pin6), .pin7(HSC_1_pin7), .pin15(HSC_1_pin15), .pin14(hsc4), .pin13(hsc5), .pin12(hsc6),
    .pin11(hsc7), .pin10(HSC_0_pin15), .pin9(HSC_1_pin9));
  _74161 #(.ShowInternalStructure("true")) HSC_2 (
    .pin1(HSC_1_pin1), .pin2(clk), .pin3(HSC_2_pin3), .pin4(HSC_2_pin4), .pin5(HSC_2_pin5),
    .pin6(HSC_2_pin6), .pin7(HSC_2_pin7), .pin14(hsc8), .pin13(hsc9), .pin10(HSC_1_pin15), .pin9(HSC_2_pin9));  // open: pin15, pin12, pin11
  _74161 #(.ShowInternalStructure("true")) TKC_0 (
    .pin1(tkc_nRC0), .pin2(clk), .pin3(TKC_0_pin3), .pin4(TKC_0_pin4), .pin5(TKC_0_pin5), .pin6(TKC_0_pin6),
    .pin7(TKC_0_pin7), .pin15(TKC_0_pin15), .pin14(tkc0), .pin13(tkc1), .pin12(tkc2), .pin11(tkc3),
    .pin10(TKC_0_pin10), .pin9(TKC_0_pin9));
  _74161 #(.ShowInternalStructure("true")) TKC_1 (
    .pin1(tkc_nRC0), .pin2(clk), .pin3(TKC_1_pin3), .pin4(TKC_1_pin4), .pin5(TKC_1_pin5), .pin6(TKC_1_pin6),
    .pin7(TKC_1_pin7), .pin15(tkc_RC0), .pin14(tkc4), .pin13(tkc5), .pin12(tkc6), .pin11(tkc7),
    .pin10(TKC_0_pin15), .pin9(TKC_1_pin9));
  _7404 #(.ShowInternalStructure("true")) u_7404_1 (
    .pin1(hsc_nR), .pin2(n7404_1_pin2), .pin3(n7404_1_pin2), .pin4(HSC_1_pin1), .pin5(tkc_nEQ_0F),
    .pin6(n7404_1_pin6), .pin13(tkc_RC0), .pin12(tkc_nRC0), .pin11(hsc9), .pin10(hsc_n9),
    .pin9(n7404_1_pin6), .pin8(tkc_nEQ_0F_2));
  _74688 #(.ShowInternalStructure("true")) u_74688_1 (
    .pin1(n74688_1_pin1), .pin2(tkc0), .pin3(n74688_1_pin3), .pin4(tkc1), .pin5(n74688_1_pin5), .pin6(tkc2),
    .pin7(n74688_1_pin7), .pin8(tkc3), .pin9(n74688_1_pin9), .pin19(tkc_nEQ_80), .pin18(n74688_1_pin18),
    .pin17(tkc7), .pin16(n74688_1_pin16), .pin15(tkc6), .pin14(n74688_1_pin14), .pin13(tkc5),
    .pin12(n74688_1_pin12), .pin11(tkc4));
  _74682 #(.ShowInternalStructure("true")) u_74682_1 (
    .pin1(tkc7_LE_07), .pin2(tkc0), .pin3(n74682_1_pin3), .pin4(tkc1), .pin5(n74682_1_pin5), .pin6(tkc2),
    .pin7(n74682_1_pin7), .pin8(tkc3), .pin9(n74682_1_pin9), .pin18(n74682_1_pin18), .pin17(n74682_1_pin17),
    .pin16(n74682_1_pin16), .pin15(tkc6), .pin14(n74682_1_pin14), .pin13(tkc5), .pin12(n74682_1_pin12),
    .pin11(tkc4));  // open: pin19
  _74682 #(.ShowInternalStructure("true")) u_74682_2 (
    .pin1(tkc7_LE_6F), .pin2(tkc0), .pin3(n74682_2_pin3), .pin4(tkc1), .pin5(n74682_2_pin5), .pin6(tkc2),
    .pin7(n74682_2_pin7), .pin8(tkc3), .pin9(n74682_2_pin9), .pin18(n74682_2_pin18), .pin17(n74682_2_pin17),
    .pin16(n74682_2_pin16), .pin15(tkc6), .pin14(n74682_2_pin14), .pin13(tkc5), .pin12(n74682_2_pin12),
    .pin11(tkc4));  // open: pin19
  _74688 #(.ShowInternalStructure("true")) u_74688_2 (
    .pin1(n74688_2_pin1), .pin2(tkc0), .pin3(n74688_2_pin3), .pin4(tkc1), .pin5(n74688_2_pin5), .pin6(tkc2),
    .pin7(n74688_2_pin7), .pin8(tkc3), .pin9(n74688_2_pin9), .pin19(tkc_nEQ_0F), .pin18(n74688_2_pin18),
    .pin17(tkc7), .pin16(n74688_2_pin16), .pin15(tkc6), .pin14(n74688_2_pin14), .pin13(tkc5),
    .pin12(n74688_2_pin12), .pin11(tkc4));
  _74688 #(.ShowInternalStructure("true")) u_74688_3 (
    .pin1(n74688_3_pin1), .pin2(tkc0), .pin3(n74688_3_pin3), .pin4(tkc1), .pin5(n74688_3_pin5), .pin6(tkc2),
    .pin7(n74688_3_pin7), .pin8(tkc3), .pin9(n74688_3_pin9), .pin19(tkc_nEQ_28), .pin18(n74688_3_pin18),
    .pin17(tkc7), .pin16(n74688_3_pin16), .pin15(tkc6), .pin14(n74688_3_pin14), .pin13(tkc5),
    .pin12(n74688_3_pin12), .pin11(tkc4));
  _74688 #(.ShowInternalStructure("true")) u_74688_4 (
    .pin1(n74688_4_pin1), .pin2(tkc0), .pin3(n74688_4_pin3), .pin4(tkc1), .pin5(n74688_4_pin5), .pin6(tkc2),
    .pin7(n74688_4_pin7), .pin8(tkc3), .pin9(n74688_4_pin9), .pin19(tkc_nEQ_F8), .pin18(n74688_4_pin18),
    .pin17(tkc7), .pin16(n74688_4_pin16), .pin15(tkc6), .pin14(n74688_4_pin14), .pin13(tkc5),
    .pin12(n74688_4_pin12), .pin11(tkc4));
  _7404 #(.ShowInternalStructure("true")) u_7404_2 (
    .pin1(op03), .pin2(ny), .pin3(n_ex), .pin4(ex), .pin5(cc), .pin6(n_cc), .pin13(op0), .pin12(nop0),
    .pin11(op1), .pin10(nop1), .pin9(op2), .pin8(nop2));
  _7485 #(.ShowInternalStructure("true")) u_7485_1 (
    .pin1(n7485_1_pin1), .pin2(n7485_1_pin2), .pin3(n7485_1_pin3), .pin4(n7485_1_pin4), .pin5(op_gt_6),
    .pin15(op3), .pin14(n7485_1_pin14), .pin13(op2), .pin12(op1), .pin11(n7485_1_pin11), .pin10(op0),
    .pin9(n7485_1_pin9));  // open: pin6, pin7
  _7408 #(.ShowInternalStructure("true")) u_7408_1 (
    .pin1(lopN), .pin2(opc_eq_0), .pin3(lop0), .pin4(lopN), .pin5(opc_eq_1), .pin6(lop1), .pin13(lopN),
    .pin12(opc_eq_2), .pin11(lop2), .pin10(nclk), .pin9(n_ex), .pin8(lopN));
  _74238 #(.ShowInternalStructure("true")) u_74238_1 (
    .pin1(opc0), .pin2(opc1), .pin3(n74238_1_pin3), .pin4(n74238_1_pin4), .pin5(n74238_1_pin5),
    .pin6(n74238_1_pin6), .pin15(opc_eq_0), .pin14(opc_eq_1), .pin13(opc_eq_2), .pin12(opc_eq_3));  // open: pin7, pin11, pin10, pin9
  _74163 #(.ShowInternalStructure("true")) u_74163_1 (
    .pin1(n_cc), .pin2(nclk), .pin3(n74163_1_pin3), .pin4(n74163_1_pin4), .pin5(n74163_1_pin5),
    .pin6(n74163_1_pin6), .pin7(n_ex), .pin14(opc0), .pin13(opc1), .pin10(n74163_1_pin10),
    .pin9(n74163_1_pin9));  // open: pin15, pin12, pin11
  _74163 #(.ShowInternalStructure("true")) u_74163_2 (
    .pin1(n_cc), .pin2(nclk), .pin3(n74163_2_pin3), .pin4(n74163_2_pin4), .pin5(n74163_2_pin5),
    .pin6(n74163_2_pin6), .pin7(ex), .pin14(exc0), .pin13(exc1), .pin12(exc2), .pin10(n74163_2_pin10),
    .pin9(n74163_2_pin9));  // open: pin15, pin11
  _74688 #(.ShowInternalStructure("true")) EQ_5 (
    .pin1(EQ_5_pin1), .pin2(hsc0), .pin3(EQ_5_pin3), .pin4(hsc1), .pin5(EQ_5_pin5), .pin6(hsc2),
    .pin7(EQ_5_pin7), .pin8(hsc3), .pin9(EQ_5_pin9), .pin19(hsc_nEQ_05), .pin18(EQ_5_pin18), .pin17(hsc7),
    .pin16(EQ_5_pin16), .pin15(hsc6), .pin14(EQ_5_pin14), .pin13(hsc5), .pin12(EQ_5_pin12), .pin11(hsc4));
  _74688 #(.ShowInternalStructure("true")) EQ_09 (
    .pin1(EQ_09_pin1), .pin2(hsc0), .pin3(EQ_09_pin3), .pin4(hsc1), .pin5(EQ_09_pin5), .pin6(hsc2),
    .pin7(EQ_09_pin7), .pin8(hsc3), .pin9(EQ_09_pin9), .pin19(hsc_nEQ_A), .pin18(EQ_09_pin18), .pin17(hsc7),
    .pin16(EQ_09_pin16), .pin15(hsc6), .pin14(EQ_09_pin14), .pin13(hsc5), .pin12(EQ_09_pin12), .pin11(hsc4));
  _74688 #(.ShowInternalStructure("true")) EQ_54 (
    .pin1(EQ_54_pin1), .pin2(hsc0), .pin3(EQ_54_pin3), .pin4(hsc1), .pin5(EQ_54_pin5), .pin6(hsc2),
    .pin7(EQ_54_pin7), .pin8(hsc3), .pin9(EQ_54_pin9), .pin19(hsc_nEQ_54), .pin18(EQ_54_pin18), .pin17(hsc7),
    .pin16(EQ_54_pin16), .pin15(hsc6), .pin14(EQ_54_pin14), .pin13(hsc5), .pin12(EQ_54_pin12), .pin11(hsc4));
  _74688 #(.ShowInternalStructure("true")) EQ_33 (
    .pin1(EQ_33_pin1), .pin2(hsc0), .pin3(EQ_33_pin3), .pin4(hsc1), .pin5(EQ_33_pin5), .pin6(hsc2),
    .pin7(EQ_33_pin7), .pin8(hsc3), .pin9(EQ_33_pin9), .pin19(hsc_nEQ_34), .pin18(EQ_33_pin18), .pin17(hsc7),
    .pin16(EQ_33_pin16), .pin15(hsc6), .pin14(EQ_33_pin14), .pin13(hsc5), .pin12(EQ_33_pin12), .pin11(hsc4));
  _74688 #(.ShowInternalStructure("true")) EQ_69 (
    .pin1(EQ_69_pin1), .pin2(hsc0), .pin3(EQ_69_pin3), .pin4(hsc1), .pin5(EQ_69_pin5), .pin6(hsc2),
    .pin7(EQ_69_pin7), .pin8(hsc3), .pin9(EQ_69_pin9), .pin19(hsc_nEQ_6A), .pin18(EQ_69_pin18), .pin17(hsc7),
    .pin16(EQ_69_pin16), .pin15(hsc6), .pin14(EQ_69_pin14), .pin13(hsc5), .pin12(EQ_69_pin12), .pin11(hsc4));
  _74688 #(.ShowInternalStructure("true")) EQ_6F (
    .pin1(EQ_6F_pin1), .pin2(hsc0), .pin3(EQ_6F_pin3), .pin4(hsc1), .pin5(EQ_6F_pin5), .pin6(hsc2),
    .pin7(EQ_6F_pin7), .pin8(hsc3), .pin9(EQ_6F_pin9), .pin19(hsc_nEQ_6E), .pin18(EQ_6F_pin18), .pin17(hsc7),
    .pin16(EQ_6F_pin16), .pin15(hsc6), .pin14(EQ_6F_pin14), .pin13(hsc5), .pin12(EQ_6F_pin12), .pin11(hsc4));
  _74283 #(.ShowInternalStructure("true")) u_74283_1 (
    .pin1(vma6), .pin2(n74283_1_pin2), .pin3(hsc1), .pin4(vma5), .pin5(hsc0), .pin6(n74283_1_pin6),
    .pin7(n74283_1_pin7), .pin15(n74283_1_pin15), .pin14(hsc2), .pin13(vma7), .pin12(hsc3),
    .pin11(n74283_1_pin11), .pin10(vma8), .pin9(n74283_1_pin9));
  _74283 #(.ShowInternalStructure("true")) u_74283_2 (
    .pin1(vmaA), .pin2(n74283_2_pin2), .pin3(hsc5), .pin4(vma9), .pin5(hsc4), .pin6(n74283_2_pin6),
    .pin7(n74283_1_pin9), .pin15(n74283_2_pin15), .pin14(hsc6), .pin13(vmaB), .pin12(hsc7),
    .pin11(n74283_2_pin11), .pin10(vmaC), .pin9(n74283_2_pin9));
  _74283 #(.ShowInternalStructure("true")) u_74283_3 (
    .pin1(vmaE), .pin2(n74283_3_pin2), .pin3(hsc9), .pin4(vmaD), .pin5(hsc8), .pin6(n74283_3_pin6),
    .pin7(n74283_2_pin9), .pin15(n74283_3_pin15), .pin11(n74283_3_pin11));  // open: pin14, pin13, pin12, pin10, pin9
  _7404 #(.ShowInternalStructure("true")) u_7404_3 (
    .pin1(eop1), .pin2(n_eop1), .pin3(eop2), .pin4(n_eop2), .pin5(n_mw_lda), .pin6(mw_lda), .pin13(erom),
    .pin12(n_erom), .pin11(eram), .pin10(n_eram), .pin9(lram), .pin8(n_lram));
  _7411 #(.ShowInternalStructure("true")) u_7411_1 (
    .pin1(op1), .pin2(nop0), .pin3(op0), .pin4(nop1), .pin5(nop2), .pin6(a001), .pin13(nop2), .pin12(a010),
    .pin11(op0), .pin10(nop1), .pin9(op2), .pin8(a101));
  _7411 #(.ShowInternalStructure("true")) u_7411_2 (
    .pin1(nclk), .pin2(ldev), .pin3(nop0), .pin4(nop1), .pin5(nop2), .pin6(n7411_2_pin6), .pin13(prt_EQ_0),
    .pin12(lsta), .pin11(n7411_2_pin11), .pin10(edev), .pin9(prt_EQ_0), .pin8(esta));
  _7427 #(.ShowInternalStructure("true")) u_7427_1 (
    .pin1(n7411_2_pin6), .pin2(a101), .pin3(a101), .pin4(a010), .pin5(a001), .pin6(n7427_1_pin6),
    .pin13(n7427_1_pin13), .pin12(n_mw_lda), .pin11(ld1_x), .pin10(ld2_x), .pin9(ld3_x), .pin8(n_ex));
  _7427 #(.ShowInternalStructure("true")) u_7427_2 (
    .pin1(mw_lda), .pin2(op_gt_6), .pin3(n7427_1_pin6), .pin4(op_gt_6), .pin5(op03), .pin6(ld3), .pin13(ny),
    .pin12(ld1), .pin11(ld1), .pin10(ld3), .pin9(n7427_2_pin9), .pin8(ld2));
  _7408 #(.ShowInternalStructure("true")) u_7408_2 (
    .pin1(opc_eq_1), .pin2(ld1), .pin3(ld1_x), .pin4(opc_eq_2), .pin5(ld2), .pin6(ld2_x), .pin13(lprt),
    .pin12(nclk), .pin11(lprt_x), .pin10(opc_eq_3), .pin9(ld3), .pin8(ld3_x));
  AS6C6264 as6c6264_1 (
    .IO0(vd0), .IO1(vd1), .IO2(vd2), .IO7(vd7), .IO6(vd6), .IO5(vd5), .IO4(vd4), .IO3(vd3), .I0(vram_d0),
    .I1(vram_d1), .I2(vram_d2), .I3(vram_d3), .I4(vram_d4), .I5(vram_d5), .I6(vram_d6), .I7(vram_d7),
    .A12(vmaC_x), .A7(vma7_x), .A6(vma6_x), .A5(vma5_x), .A4(vma4_x), .A3(vma3_x), .A2(vma2_x), .A1(vma1_x),
    .A0(vma0_x), .CLK(clk), .nWE(n_lvram), .CE2(1'b1), .A8(vma8_x), .A9(vma9_x), .A11(vmaB_x), .nOE(1'b0),
    .A10(vmaA_x), .nCE(1'b0));  // open: NC0, GND, VCC
  _7432 #(.ShowInternalStructure("true")) u_7432_1 (
    .pin1(hsc_or_89), .pin2(hsc_nEQ_05), .pin3(hsc_n1S), .pin4(hsc_or_89), .pin5(hsc_nEQ_A), .pin6(hsc_n2S),
    .pin13(hsc_nEQ_34), .pin12(hsc_n9), .pin11(hsc_n4S), .pin10(hsc_nEQ_54), .pin9(hsc_or_89), .pin8(hsc_n3S));
  _7432 #(.ShowInternalStructure("true")) u_7432_2 (
    .pin1(hsc_n9), .pin2(hsc_nEQ_6A), .pin3(hsc_n5S), .pin4(hsc_n9), .pin5(hsc_nEQ_6E), .pin6(hsc_nR),
    .pin13(hsc2Q), .pin12(hsc3Q), .pin11(n7432_2_pin11), .pin10(n7432_2_pin11), .pin9(hsc4Q), .pin8(hsc_eORd));
  _74279 #(.ShowInternalStructure("true")) u_74279_1 (
    .pin1(hsc_n2S), .pin2(hsc_n1S), .pin3(hsc_n1S), .pin4(hsc1Q), .pin5(hsc_n3S), .pin6(hsc_n2S),
    .pin7(hsc2Q), .pin15(hsc_n4S), .pin14(hsc_n5S), .pin13(hsc4Q), .pin12(hsc_n3S), .pin11(hsc_n3S),
    .pin10(hsc_n4S), .pin9(hsc3Q));
  _74279 #(.ShowInternalStructure("true")) u_74279_2 (
    .pin1(hsc_nR), .pin2(hsc_n5S), .pin3(hsc_n5S), .pin4(hsc5Q), .pin5(tkc_nEQ_28), .pin6(tkc_nEQ_0F),
    .pin7(tkc1Q), .pin15(tkc_nEQ_F8), .pin14(tkc_nRC0), .pin13(tkc3Q), .pin12(tkc_nEQ_28),
    .pin11(tkc_nEQ_28), .pin10(tkc_nEQ_F8), .pin9(tkc2Q));
  _74151 #(.ShowInternalStructure("true")) u_74151_1 (
    .pin1(vd3_x), .pin2(vd2_x), .pin3(vd1_x), .pin4(vd0_x), .pin5(vbit), .pin7(n74151_1_pin7), .pin15(vd4_x),
    .pin14(vd5_x), .pin13(vd6_x), .pin12(vd7_x), .pin11(tkc0), .pin10(tkc1), .pin9(tkc2));  // open: pin6
  _74573 #(.ShowInternalStructure("true")) u_74573_1 (
    .pin1(n74573_1_pin1), .pin2(vd0), .pin3(vd1), .pin4(vd2), .pin5(vd3), .pin6(vd4), .pin7(vd5), .pin8(vd6),
    .pin9(vd7), .pin19(vd0_x), .pin18(vd1_x), .pin17(vd2_x), .pin16(vd3_x), .pin15(vd4_x), .pin14(vd5_x),
    .pin13(vd6_x), .pin12(vd7_x), .pin11(latch_vram));
  _74573 #(.ShowInternalStructure("true")) u_74573_2 (
    .pin1(el_vram), .pin2(tkc3), .pin3(tkc4), .pin4(tkc5), .pin5(tkc6), .pin6(tkc7), .pin7(vma5),
    .pin8(vma6), .pin9(vma7), .pin19(vma0_x), .pin18(vma1_x), .pin17(vma2_x), .pin16(vma3_x), .pin15(vma4_x),
    .pin14(vma5_x), .pin13(vma6_x), .pin12(vma7_x), .pin11(n74573_2_pin11));
  _74573 #(.ShowInternalStructure("true")) u_74573_3 (
    .pin1(el_vram), .pin2(vma8), .pin3(vma9), .pin4(vmaA), .pin5(vmaB), .pin6(vmaC), .pin7(n74573_3_pin7),
    .pin8(n74573_3_pin8), .pin9(n74573_3_pin9), .pin19(vma8_x), .pin18(vma9_x), .pin17(vmaA_x),
    .pin16(vmaB_x), .pin15(vmaC_x), .pin11(n74573_3_pin11));  // open: pin14, pin13, pin12
  _74573 #(.ShowInternalStructure("true")) u_74573_4 (
    .pin1(n_el_vram), .pin2(ad0), .pin3(ad1), .pin4(ad2), .pin5(ad3), .pin6(ad4), .pin7(ad5), .pin8(ad6),
    .pin9(ad7), .pin19(vma0_x), .pin18(vma1_x), .pin17(vma2_x), .pin16(vma3_x), .pin15(vma4_x),
    .pin14(vma5_x), .pin13(vma6_x), .pin12(vma7_x), .pin11(n74573_4_pin11));
  _74573 #(.ShowInternalStructure("true")) u_74573_5 (
    .pin1(n_el_vram), .pin2(ad8), .pin3(ad9), .pin4(adA), .pin5(adB), .pin6(adC), .pin7(adD), .pin8(adE),
    .pin9(adF), .pin19(vma8_x), .pin18(vma9_x), .pin17(vmaA_x), .pin16(vmaB_x), .pin15(vmaC_x),
    .pin11(n74573_5_pin11));  // open: pin14, pin13, pin12
  _74573 #(.ShowInternalStructure("true")) u_op0 (
    .pin1(op0_pin1), .pin2(dx0), .pin3(dx1), .pin4(dx2), .pin5(dx3), .pin6(dx4), .pin7(dx5), .pin8(dx6),
    .pin9(dx7), .pin19(op00), .pin18(op01), .pin17(op02), .pin16(op03), .pin15(op0), .pin14(op1),
    .pin13(op2), .pin12(op3), .pin11(lop0));
  _74573 #(.ShowInternalStructure("true")) u_op1 (
    .pin1(op1_pin1), .pin2(dx0), .pin3(dx1), .pin4(dx2), .pin5(dx3), .pin6(dx4), .pin7(dx5), .pin8(dx6),
    .pin9(dx7), .pin19(op10), .pin18(op11), .pin17(op12), .pin16(op13), .pin15(op14), .pin14(op15),
    .pin13(op16), .pin12(op17), .pin11(lop1));
  _74573 #(.ShowInternalStructure("true")) u_74573_6 (
    .pin1(n_eop1), .pin2(op10), .pin3(op11), .pin4(op12), .pin5(op13), .pin6(op14), .pin7(op15), .pin8(op16),
    .pin9(op17), .pin19(d0), .pin18(d1), .pin17(d2), .pin16(d3), .pin15(d4), .pin14(d5), .pin13(d6),
    .pin12(d7), .pin11(n74573_6_pin11));
  _74573 #(.ShowInternalStructure("true")) u_op2 (
    .pin1(op2_pin1), .pin2(dx0), .pin3(dx1), .pin4(dx2), .pin5(dx3), .pin6(dx4), .pin7(dx5), .pin8(dx6),
    .pin9(dx7), .pin19(op20), .pin18(op21), .pin17(op22), .pin16(op23), .pin15(op24), .pin14(op25),
    .pin13(op26), .pin12(op27), .pin11(lop2));
  _74573 #(.ShowInternalStructure("true")) u_74573_7 (
    .pin1(n_eop2), .pin2(op20), .pin3(op21), .pin4(op22), .pin5(op23), .pin6(op24), .pin7(op25), .pin8(op26),
    .pin9(op27), .pin19(d0), .pin18(d1), .pin17(d2), .pin16(d3), .pin15(d4), .pin14(d5), .pin13(d6),
    .pin12(d7), .pin11(n74573_7_pin11));
  AT28C64B_MAIN ROM (
    .IO0(d0), .IO1(d1), .IO2(d2), .IO7(d7), .IO6(d6), .IO5(d5), .IO4(d4), .IO3(d3), .A12(adC), .A7(ad7),
    .A6(ad6), .A5(ad5), .A4(ad4), .A3(ad3), .A2(ad2), .A1(ad1), .A0(ad0), .nWE(1'b1), .A8(ad8), .A9(ad9),
    .A11(adB), .nOE(n_erom), .A10(adA), .nCE(1'b0));  // open: NC0, GND, NC1, VCC
  _7432 #(.ShowInternalStructure("true")) u_7432_3 (
    .pin1(hsc1Q), .pin2(hsc2Q), .pin3(n7432_3_pin3), .pin4(n7432_3_pin3), .pin5(hsc3Q), .pin6(n7432_3_pin6),
    .pin13(tkc1Q), .pin12(tkc2Q), .pin11(n7432_3_pin11), .pin10(n7432_3_pin11), .pin9(tkc3Q),
    .pin8(n7432_3_pin8));
  _7432 #(.ShowInternalStructure("true")) u_7432_4 (
    .pin1(n7432_3_pin6), .pin2(hsc4Q), .pin3(n7432_4_pin3), .pin4(n7432_4_pin3), .pin5(hsc5Q),
    .pin6(n7432_4_pin6), .pin13(hsc8), .pin12(hsc9), .pin11(hsc_or_89), .pin10(hsc1Q), .pin9(hsc5Q),
    .pin8(hsc_pp));
  _7404 #(.ShowInternalStructure("true")) u_7404_4 (
    .pin1(n7432_4_pin6), .pin2(hsc0Q), .pin3(n7404_4_pin3), .pin4(hsc_inc), .pin13(n7432_3_pin8),
    .pin12(tkc0Q));  // open: pin5, pin6, pin11, pin10, pin9, pin8
  _7408 #(.ShowInternalStructure("true")) u_7408_3 (
    .pin1(tkc0Q), .pin2(hsc_eORd), .pin3(nV03_sync), .pin4(hsc_pp), .pin5(tkc7_LE_07), .pin6(nV03_broad),
    .pin13(hsc0Q), .pin12(tkc7_LE_6F), .pin11(nV03_short), .pin10(hsc3Q), .pin9(tkc2Q), .pin8(n7408_3_pin8));
  _7408 #(.ShowInternalStructure("true")) u_7408_4 (
    .pin1(n7408_3_pin8), .pin2(vbit), .pin3(v_10), .pin4(tkc_nEQ_80), .pin5(tkc_nRC0), .pin6(n7404_4_pin3),
    .pin13(bank_vram), .pin12(ebank), .pin11(evram), .pin10(bank_vram), .pin9(lbank), .pin8(lvram));
  _7402 #(.ShowInternalStructure("true")) u_7402_1 (
    .pin1(n7402_1_pin1), .pin2(n7402_1_pin2), .pin3(n7402_1_pin2), .pin4(n7402_1_pin2), .pin5(nV03_broad),
    .pin6(nV03_short), .pin13(v_03), .pin12(n7402_1_pin1), .pin11(nV03_sync), .pin10(n_el_vram),
    .pin9(evram), .pin8(lvram));
  _7411 #(.ShowInternalStructure("true")) u_7411_3 (
    .pin1(rise), .pin2(n7411_3_pin2), .pin3(tkc0), .pin4(tkc1), .pin5(tkc2), .pin6(n7411_3_pin2),
    .pin13(n7411_3_pin13), .pin12(latch_vram));  // open: pin11, pin10, pin9, pin8
  _7404 #(.ShowInternalStructure("true")) u_7404_5 (
    .pin1(evram), .pin2(n_evram), .pin3(lvram), .pin4(n_lvram), .pin5(n_el_vram), .pin6(el_vram),
    .pin13(n_lmb), .pin12(lmb));  // open: pin11, pin10, pin9, pin8
  _7485 #(.ShowInternalStructure("true")) u_7485_2 (
    .pin1(n7485_2_pin1), .pin2(n7485_2_pin2), .pin3(n7485_2_pin3), .pin4(n7485_2_pin4), .pin6(bank_vram),
    .pin7(mb_EQ_0), .pin15(mb3), .pin14(n7485_2_pin14), .pin13(mb2), .pin12(mb1), .pin11(n7485_2_pin11),
    .pin10(mb0), .pin9(n7485_2_pin9));  // open: pin5
  _7485 #(.ShowInternalStructure("true")) u_7485_3 (
    .pin1(n7485_3_pin1), .pin2(n7485_3_pin2), .pin3(n7485_3_pin3), .pin4(n7485_3_pin4), .pin5(n7485_2_pin4),
    .pin6(n7485_2_pin3), .pin7(n7485_2_pin2), .pin15(mb3), .pin14(n7485_3_pin14), .pin13(mb2), .pin12(mb1),
    .pin11(n7485_3_pin11), .pin10(mb0), .pin9(n7485_3_pin9));
  _74573 #(.ShowInternalStructure("true")) u_74573_8 (
    .pin1(n_evram), .pin2(vd0), .pin3(vd1), .pin4(vd2), .pin5(vd3), .pin6(vd4), .pin7(vd5), .pin8(vd6),
    .pin9(vd7), .pin19(d0), .pin18(d1), .pin17(d2), .pin16(d3), .pin15(d4), .pin14(d5), .pin13(d6),
    .pin12(d7), .pin11(n74573_8_pin11));
  _74244 #(.ShowInternalStructure("true")) u_74244_1 (
    .pin1(n74244_1_pin1), .pin2(d0), .pin3(vram_d4), .pin4(d1), .pin5(vram_d5), .pin6(d2), .pin7(vram_d6),
    .pin8(d3), .pin9(vram_d7), .pin19(n74244_1_pin19), .pin18(vram_d0), .pin17(d4), .pin16(vram_d1),
    .pin15(d5), .pin14(vram_d2), .pin13(d6), .pin12(vram_d3), .pin11(d7));
  _74244 #(.ShowInternalStructure("true")) u_74244_2 (
    .pin1(n74244_2_pin1), .pin2(d0), .pin3(dx4), .pin4(d1), .pin5(dx5), .pin6(d2), .pin7(dx6), .pin8(d3),
    .pin9(dx7), .pin19(n74244_2_pin19), .pin18(dx0), .pin17(d4), .pin16(dx1), .pin15(d5), .pin14(dx2),
    .pin13(d6), .pin12(dx3), .pin11(d7));
  _74573 #(.ShowInternalStructure("true")) u_74573_9 (
    .pin1(n_esta), .pin2(st0), .pin3(st1), .pin4(st2), .pin5(st3), .pin6(st4), .pin7(st5), .pin8(st6),
    .pin9(st7), .pin19(d0), .pin18(d1), .pin17(d2), .pin16(d3), .pin15(d4), .pin14(d5), .pin13(d6),
    .pin12(d7), .pin11(n74573_9_pin11));
  _74573 #(.ShowInternalStructure("true")) u_74573_10 (
    .pin1(n74573_10_pin1), .pin2(dx0), .pin3(dx1), .pin4(dx2), .pin5(dx3), .pin6(dx4), .pin7(dx5),
    .pin8(dx6), .pin9(dx7), .pin19(st0), .pin18(st1), .pin17(st2), .pin16(st3), .pin15(st4), .pin14(st5),
    .pin13(st6), .pin12(st7), .pin11(lsta));
  _74573 #(.ShowInternalStructure("true")) u_74573_11 (
    .pin1(n74573_11_pin1), .pin2(dx0), .pin3(dx1), .pin4(dx2), .pin5(dx3), .pin6(dx4), .pin7(dx5),
    .pin8(dx6), .pin9(dx7), .pin19(prt0), .pin18(prt1), .pin17(prt2), .pin16(prt3), .pin15(prt4),
    .pin14(prt5), .pin13(prt6), .pin12(prt7), .pin11(lprt_x));
  _74688 #(.ShowInternalStructure("true")) u_74688_5 (
    .pin1(n74688_5_pin1), .pin2(prt0), .pin3(n74688_5_pin3), .pin4(prt1), .pin5(n74688_5_pin5), .pin6(prt2),
    .pin7(n74688_5_pin7), .pin8(prt3), .pin9(n74688_5_pin9), .pin19(prt_nEQ_0), .pin18(n74688_5_pin18),
    .pin17(prt7), .pin16(n74688_5_pin16), .pin15(prt6), .pin14(n74688_5_pin14), .pin13(prt5),
    .pin12(n74688_5_pin12), .pin11(prt4));
  _7402 #(.ShowInternalStructure("true")) u_7402_2 (
    .pin1(prt_EQ_0), .pin2(prt_nEQ_0), .pin3(prt_nEQ_0), .pin13(n_ealu_ldf), .pin12(ealu), .pin11(ldf));  // open: pin4, pin5, pin6, pin10, pin9, pin8
  AS6C6264 RAM (
    .IO0(d0), .IO1(d1), .IO2(d2), .IO7(d7), .IO6(d6), .IO5(d5), .IO4(d4), .IO3(d3), .I0(d0), .I1(d1),
    .I2(d2), .I3(d3), .I4(d4), .I5(d5), .I6(d6), .I7(d7), .A12(adC), .A7(ad7), .A6(ad6), .A5(ad5), .A4(ad4),
    .A3(ad3), .A2(ad2), .A1(ad1), .A0(ad0), .CLK(clk), .nWE(n_lram), .CE2(1'b1), .A8(ad8), .A9(ad9),
    .A11(adB), .nOE(n_eram), .A10(adA), .nCE(1'b0));  // open: NC0, GND, VCC
  Button button_1 (.out(reset));
  LED led_1 (.in(d7));
  LED led_2 (.in(d6));
  LED led_3 (.in(ad0));
  LED led_4 (.in(ad1));
  LED led_5 (.in(ad2));
  LED led_6 (.in(ad3));
  LED led_7 (.in(ad4));
  LED led_8 (.in(ad5));
  LED led_9 (.in(ad6));
  LED led_10 (.in(ad7));
  LED led_11 (.in(ad8));
  LED led_12 (.in(ad9));
  LED led_13 (.in(adA));
  LED led_14 (.in(adB));
  LED led_15 (.in(adC));
  LED led_16 (.in(adD));
  LED led_17 (.in(adE));
  LED led_18 (.in(adF));
  LED led_19 (.in(eaux));
  LED led_20 (.in(ebank));
  LED led_21 (.in(lbank));
  LED led_22 (.in(d_EQ_0));
  LED led_23 (.in(n_evram));
  LED led_24 (.in(n_lvram));
  LED led_25 (.in(dbg_x));
  LED led_26 (.in(dbg_y));
  Clock clock_1 (.out(clock_1_out));
  _7404 #(.ShowInternalStructure("true")) u_7404_6 (
    .pin1(reset), .pin2(nreset), .pin3(clk), .pin4(nclk), .pin5(st3), .pin6(n7404_6_pin6), .pin13(clk),
    .pin12(n7404_6_pin12), .pin11(n7404_6_pin12), .pin10(n7404_6_pin10), .pin9(n7404_6_pin10),
    .pin8(n7404_6_pin8));
  _7408 #(.ShowInternalStructure("true")) u_7408_5 (
    .pin1(clock_1_out), .pin2(n7404_6_pin6), .pin3(clk), .pin13(n7404_6_pin8), .pin12(clk), .pin11(rise),
    .pin10(n7404_6_pin10), .pin9(nclk), .pin8(fall));  // open: pin4, pin5, pin6
  _7408 #(.ShowInternalStructure("true")) u_7408_6 (
    .pin1(mc1_x), .pin2(eta), .pin3(asp), .pin4(mc0_x), .pin5(eta), .pin6(emem), .pin13(mc2_x), .pin12(eta),
    .pin11(aimm), .pin10(mc3_x), .pin9(eta), .pin8(lmem));
  _7408 #(.ShowInternalStructure("true")) u_7408_7 (
    .pin1(mc5_x), .pin2(eta), .pin3(spdec), .pin4(mc4_x), .pin5(eta), .pin6(spinc), .pin13(mc6_x),
    .pin12(eta), .pin11(jnz), .pin10(mc0_x), .pin9(etb), .pin8(ldx));
  _7408 #(.ShowInternalStructure("true")) u_7408_8 (
    .pin1(mc2_x), .pin2(etb), .pin3(ldf), .pin4(mc1_x), .pin5(etb), .pin6(ldy), .pin13(mc3_x), .pin12(etb),
    .pin11(ealu), .pin10(mc4_x), .pin9(etb), .pin8(ldh));
  _7408 #(.ShowInternalStructure("true")) u_7408_9 (
    .pin1(mc6_x), .pin2(etb), .pin3(lprt), .pin4(mc5_x), .pin5(etb), .pin6(ldl), .pin13(mc7_x), .pin12(ex),
    .pin11(ereg), .pin10(mc8_x), .pin9(ex), .pin8(lreg));
  _7408 #(.ShowInternalStructure("true")) u_7408_10 (
    .pin1(mcA_x), .pin2(ex), .pin3(eop1), .pin4(mc9_x), .pin5(ex), .pin6(sel), .pin13(mcB_x), .pin12(ex),
    .pin11(eop2), .pin10(mcC_x), .pin9(ex), .pin8(edev));
  _74573 #(.ShowInternalStructure("true")) u_74573_12 (
    .pin1(n_ahl), .pin2(l0), .pin3(l1), .pin4(l2), .pin5(l3), .pin6(l4), .pin7(l5), .pin8(l6), .pin9(l7),
    .pin19(ad0), .pin18(ad1), .pin17(ad2), .pin16(ad3), .pin15(ad4), .pin14(ad5), .pin13(ad6), .pin12(ad7),
    .pin11(n74573_12_pin11));
  _74573 #(.ShowInternalStructure("true")) u_74573_13 (
    .pin1(n_ahl), .pin2(h0), .pin3(h1), .pin4(h2), .pin5(h3), .pin6(h4), .pin7(h5), .pin8(h6), .pin9(h7),
    .pin19(ad8), .pin18(ad9), .pin17(adA), .pin16(adB), .pin15(adC), .pin14(adD), .pin13(adE), .pin12(adF),
    .pin11(n74573_13_pin11));
  _74573 #(.ShowInternalStructure("true")) u_74573_14 (
    .pin1(n_asp), .pin2(sp0), .pin3(sp1), .pin4(sp2), .pin5(sp3), .pin6(sp4), .pin7(sp5), .pin8(sp6),
    .pin9(sp7), .pin19(ad0), .pin18(ad1), .pin17(ad2), .pin16(ad3), .pin15(ad4), .pin14(ad5), .pin13(ad6),
    .pin12(ad7), .pin11(n74573_14_pin11));
  _74573 #(.ShowInternalStructure("true")) u_74573_15 (
    .pin1(n_asp), .pin2(sp8), .pin3(sp9), .pin4(spA), .pin5(spB), .pin6(spC), .pin7(spD), .pin8(spE),
    .pin9(spF), .pin19(ad8), .pin18(ad9), .pin17(adA), .pin16(adB), .pin15(adC), .pin14(adD), .pin13(adE),
    .pin12(adF), .pin11(n74573_15_pin11));
  _74573 #(.ShowInternalStructure("true")) mb (
    .pin1(mb_pin1), .pin2(axd0), .pin3(axd1), .pin4(axd2), .pin5(axd3), .pin6(axd4), .pin7(axd5),
    .pin8(axd6), .pin9(axd7), .pin19(mb0), .pin18(mb1), .pin17(mb2), .pin16(mb3), .pin15(mb4), .pin14(mb5),
    .pin13(mb6), .pin12(mb7), .pin11(lmb));
  _74138 #(.ShowInternalStructure("true")) u_74138_1 (
    .pin1(ad0), .pin2(ad1), .pin3(ad2), .pin4(n74138_1_pin4), .pin5(n_eaux), .pin6(emem), .pin7(n_epch),
    .pin13(n_emb), .pin11(n_espl), .pin10(n_esph), .pin9(n_epcl));  // open: pin15, pin14, pin12
  LED led_27 (.in(d5));
  LED led_28 (.in(d4));
  LED led_29 (.in(d3));
  LED led_30 (.in(d2));
  LED led_31 (.in(d1));
  LED led_32 (.in(d0));
  LED led_33 (.in(emem));
  LED led_34 (.in(asp));
  LED led_35 (.in(aimm));
  LED led_36 (.in(lmem));
  LED led_37 (.in(spinc));
  LED led_38 (.in(spdec));
  LED led_39 (.in(jnz));
  LED led_40 (.in(ldx));
  LED led_41 (.in(ldy));
  LED led_42 (.in(ldf));
  LED led_43 (.in(ealu));
  LED led_44 (.in(ldh));
  LED led_45 (.in(ldl));
  LED led_46 (.in(lprt));
  LED led_47 (.in(ereg));
  LED led_48 (.in(lreg));
  LED led_49 (.in(sel));
  LED led_50 (.in(eop1));
  LED led_51 (.in(eop2));
  LED led_52 (.in(edev));
  LED led_53 (.in(ldev));
  LED led_54 (.in(cc));
  LED led_55 (.in(ex));
  LED led_56 (.in(n_ex));
  _74573 #(.ShowInternalStructure("true")) u_74573_16 (
    .pin1(n74573_16_pin1), .pin2(mc0), .pin3(mc1), .pin4(mc2), .pin5(mc3), .pin6(mc4), .pin7(mc5),
    .pin8(mc6), .pin9(mc7), .pin19(mc0_x), .pin18(mc1_x), .pin17(mc2_x), .pin16(mc3_x), .pin15(mc4_x),
    .pin14(mc5_x), .pin13(mc6_x), .pin12(mc7_x), .pin11(nclk));
  _7404 #(.ShowInternalStructure("true")) u_7404_7 (
    .pin1(mcE_x), .pin2(n_mcE_x), .pin3(mcF_x), .pin4(n_mcF_x), .pin5(ereg), .pin6(n_ereg), .pin11(sel),
    .pin10(nsel), .pin9(lpreset), .pin8(nlpreset));  // open: pin13, pin12
  _7408 #(.ShowInternalStructure("true")) u_7408_11 (
    .pin1(mcD_x), .pin2(ex), .pin3(ldev), .pin4(mcE_x), .pin5(ex), .pin6(cc), .pin13(n_mcF_x), .pin12(ex),
    .pin11(eta), .pin10(mcF_x), .pin9(ex), .pin8(etb));
  _74244 #(.ShowInternalStructure("true")) u_74244_3 (
    .pin1(n74244_3_pin1), .pin2(d0), .pin3(rd4), .pin4(d1), .pin5(rd5), .pin6(d2), .pin7(rd6), .pin8(d3),
    .pin9(rd7), .pin19(n74244_3_pin19), .pin18(rd0), .pin17(d4), .pin16(rd1), .pin15(d5), .pin14(rd2),
    .pin13(d6), .pin12(rd3), .pin11(d7));
  _74244 #(.ShowInternalStructure("true")) u_74244_4 (
    .pin1(n_ereg), .pin2(rq0), .pin3(d4), .pin4(rq1), .pin5(d5), .pin6(rq2), .pin7(d6), .pin8(rq3),
    .pin9(d7), .pin19(n_ereg), .pin18(d0), .pin17(rq4), .pin16(d1), .pin15(rq5), .pin14(d2), .pin13(rq6),
    .pin12(d3), .pin11(rq7));
  _74573 #(.ShowInternalStructure("true")) u_74573_17 (
    .pin1(n_apc), .pin2(pc0), .pin3(pc1), .pin4(pc2), .pin5(pc3), .pin6(pc4), .pin7(pc5), .pin8(pc6),
    .pin9(pc7), .pin19(ad0), .pin18(ad1), .pin17(ad2), .pin16(ad3), .pin15(ad4), .pin14(ad5), .pin13(ad6),
    .pin12(ad7), .pin11(n74573_17_pin11));
  _74573 #(.ShowInternalStructure("true")) u_74573_18 (
    .pin1(n_apc), .pin2(pc8), .pin3(pc9), .pin4(pcA), .pin5(pcB), .pin6(pcC), .pin7(pcD), .pin8(pcE),
    .pin9(pcF), .pin19(ad8), .pin18(ad9), .pin17(adA), .pin16(adB), .pin15(adC), .pin14(adD), .pin13(adE),
    .pin12(adF), .pin11(n74573_18_pin11));
  _74573 #(.ShowInternalStructure("true")) u_74573_19 (
    .pin1(n_aimm), .pin2(op10), .pin3(op11), .pin4(op12), .pin5(op13), .pin6(op14), .pin7(op15), .pin8(op16),
    .pin9(op17), .pin19(ad0), .pin18(ad1), .pin17(ad2), .pin16(ad3), .pin15(ad4), .pin14(ad5), .pin13(ad6),
    .pin12(ad7), .pin11(n74573_19_pin11));
  _74573 #(.ShowInternalStructure("true")) u_74573_20 (
    .pin1(n_aimm), .pin2(op20), .pin3(op21), .pin4(op22), .pin5(op23), .pin6(op24), .pin7(op25), .pin8(op26),
    .pin9(op27), .pin19(ad8), .pin18(ad9), .pin17(adA), .pin16(adB), .pin15(adC), .pin14(adD), .pin13(adE),
    .pin12(adF), .pin11(n74573_20_pin11));
  _74573 #(.ShowInternalStructure("true")) u_74573_21 (
    .pin1(n_emb), .pin2(mb0), .pin3(mb1), .pin4(mb2), .pin5(mb3), .pin6(mb4), .pin7(mb5), .pin8(mb6),
    .pin9(mb7), .pin19(axq0), .pin18(axq1), .pin17(axq2), .pin16(axq3), .pin15(axq4), .pin14(axq5),
    .pin13(axq6), .pin12(axq7), .pin11(n74573_21_pin11));
  _74138 #(.ShowInternalStructure("true")) u_74138_2 (
    .pin1(ad0), .pin2(ad1), .pin3(ad2), .pin4(nclk), .pin5(n_eaux), .pin6(lmem), .pin7(n_lpch),
    .pin13(n_lmb), .pin11(n_lspl), .pin10(n_lsph), .pin9(n_lpcl));  // open: pin15, pin14, pin12
  _74374 #(.ShowInternalStructure("true")) u_74374_1 (
    .pin1(n74374_1_pin1), .pin2(x0), .pin3(d0), .pin4(d1), .pin5(x1), .pin6(x2), .pin7(d2), .pin8(d3),
    .pin9(x3), .pin19(x7), .pin18(d7), .pin17(d6), .pin16(x6), .pin15(x5), .pin14(d5), .pin13(d4),
    .pin12(x4), .pin11(xc));
  _74374 #(.ShowInternalStructure("true")) u_74374_2 (
    .pin1(n74374_2_pin1), .pin2(y0), .pin3(d0), .pin4(d1), .pin5(y1), .pin6(y2), .pin7(d2), .pin8(d3),
    .pin9(y3), .pin19(y7), .pin18(d7), .pin17(d6), .pin16(y6), .pin15(y5), .pin14(d5), .pin13(d4),
    .pin12(y4), .pin11(yc));
  _7408 #(.ShowInternalStructure("true")) u_7408_12 (
    .pin1(op1), .pin2(flag_c), .pin3(c_in), .pin4(nE_adc), .pin5(nE_add), .pin6(nE_add_adc), .pin13(ldx),
    .pin12(nclk), .pin11(xc), .pin10(ldy), .pin9(nclk), .pin8(yc));
  _7404 #(.ShowInternalStructure("true")) u_7404_8 (
    .pin1(y0), .pin2(ny0), .pin3(y1), .pin4(ny1), .pin5(y2), .pin6(ny2), .pin13(y5), .pin12(ny5), .pin11(y4),
    .pin10(ny4), .pin9(y3), .pin8(ny3));
  _7404 #(.ShowInternalStructure("true")) u_7404_9 (
    .pin1(y6), .pin2(ny6), .pin3(y7), .pin4(ny7), .pin5(ldf), .pin6(nLDF), .pin13(flag_b), .pin12(b_in),
    .pin11(nb_out), .pin10(b_out), .pin9(esta), .pin8(n_esta));
  _74244 #(.ShowInternalStructure("true")) u_74244_5 (
    .pin1(n_ealu_ldf), .pin2(z0), .pin3(d4), .pin4(z1), .pin5(d5), .pin6(z2), .pin7(d6), .pin8(z3),
    .pin9(d7), .pin19(n_ealu_ldf), .pin18(d0), .pin17(z4), .pin16(d1), .pin15(z5), .pin14(d2), .pin13(z6),
    .pin12(d3), .pin11(z7));
  AT28C64B_MC0 at28c64b_mc0_1 (
    .IO0(mc0), .IO1(mc1), .IO2(mc2), .IO7(mc7), .IO6(mc6), .IO5(mc5), .IO4(mc4), .IO3(mc3), .A12(1'b0),
    .A7(op3), .A6(op2), .A5(op1), .A4(op0), .A3(op03), .A2(exc2), .A1(exc1), .A0(exc0), .nWE(1'b1),
    .A8(1'b0), .A9(1'b0), .A11(1'b0), .nOE(1'b0), .A10(1'b0), .nCE(1'b0));  // open: NC0, GND, NC1, VCC
  _74573 #(.ShowInternalStructure("true")) u_74573_22 (
    .pin1(n74573_22_pin1), .pin2(mc8), .pin3(mc9), .pin4(mcA), .pin5(mcB), .pin6(mcC), .pin7(mcD),
    .pin8(mcE), .pin9(mcF), .pin19(mc8_x), .pin18(mc9_x), .pin17(mcA_x), .pin16(mcB_x), .pin15(mcC_x),
    .pin14(mcD_x), .pin13(mcE_x), .pin12(mcF_x), .pin11(nclk));
  _74573 #(.ShowInternalStructure("true")) l (
    .pin1(l_pin1), .pin2(rd0), .pin3(rd1), .pin4(rd2), .pin5(rd3), .pin6(rd4), .pin7(rd5), .pin8(rd6),
    .pin9(rd7), .pin19(l0), .pin18(l1), .pin17(l2), .pin16(l3), .pin15(l4), .pin14(l5), .pin13(l6),
    .pin12(l7), .pin11(l_we));
  _74573 #(.ShowInternalStructure("true")) h (
    .pin1(h_pin1), .pin2(rd0), .pin3(rd1), .pin4(rd2), .pin5(rd3), .pin6(rd4), .pin7(rd5), .pin8(rd6),
    .pin9(rd7), .pin19(h0), .pin18(h1), .pin17(h2), .pin16(h3), .pin15(h4), .pin14(h5), .pin13(h6),
    .pin12(h7), .pin11(h_we));
  _74573 #(.ShowInternalStructure("true")) f (
    .pin1(f_pin1), .pin2(rd0), .pin3(rd1), .pin4(rd2), .pin5(rd3), .pin6(rd4), .pin7(rd5), .pin8(rd6),
    .pin9(rd7), .pin19(flag_l), .pin18(flag_e), .pin17(flag_c), .pin16(flag_b), .pin15(f4), .pin14(f5),
    .pin13(f6), .pin12(f7), .pin11(f_we));
  _74244 #(.ShowInternalStructure("true")) u_74244_6 (
    .pin1(n_eaux), .pin2(axq0), .pin3(d4), .pin4(axq1), .pin5(d5), .pin6(axq2), .pin7(d6), .pin8(axq3),
    .pin9(d7), .pin19(n_eaux), .pin18(d0), .pin17(axq4), .pin16(d1), .pin15(axq5), .pin14(d2), .pin13(axq6),
    .pin12(d3), .pin11(axq7));
  _74244 #(.ShowInternalStructure("true")) u_74244_7 (
    .pin1(d_EQ_0), .pin2(l0), .pin3(pc4x), .pin4(l1), .pin5(pc5x), .pin6(l2), .pin7(pc6x), .pin8(l3),
    .pin9(pc7x), .pin19(d_EQ_0), .pin18(pc0x), .pin17(l4), .pin16(pc1x), .pin15(l5), .pin14(pc2x),
    .pin13(l6), .pin12(pc3x), .pin11(l7));
  _74244 #(.ShowInternalStructure("true")) u_74244_8 (
    .pin1(d_nEQ_0), .pin2(axd0), .pin3(pc4x), .pin4(axd1), .pin5(pc5x), .pin6(axd2), .pin7(pc6x),
    .pin8(axd3), .pin9(pc7x), .pin19(d_nEQ_0), .pin18(pc0x), .pin17(axd4), .pin16(pc1x), .pin15(axd5),
    .pin14(pc2x), .pin13(axd6), .pin12(pc3x), .pin11(axd7));
  _74193 #(.ShowInternalStructure("true")) u_pc0 (
    .pin1(pc1x), .pin2(pc1), .pin3(pc0), .pin4(pc0_pin4), .pin5(n_pcinc_x), .pin6(pc2), .pin7(pc3),
    .pin15(pc0x), .pin14(reset), .pin13(pc0_pin13), .pin12(pc0_pin12), .pin11(n_lpcl_x), .pin10(pc2x),
    .pin9(pc3x));
  _74193 #(.ShowInternalStructure("true")) u_pc1 (
    .pin1(pc5x), .pin2(pc5), .pin3(pc4), .pin4(pc0_pin13), .pin5(pc0_pin12), .pin6(pc6), .pin7(pc7),
    .pin15(pc4x), .pin14(reset), .pin13(pc1_pin13), .pin12(pc1_pin12), .pin11(n_lpcl_x), .pin10(pc6x),
    .pin9(pc7x));
  _74244 #(.ShowInternalStructure("true")) u_74244_9 (
    .pin1(n_epcl), .pin2(pc0), .pin3(axq4), .pin4(pc1), .pin5(axq5), .pin6(pc2), .pin7(axq6), .pin8(pc3),
    .pin9(axq7), .pin19(n_epcl), .pin18(axq0), .pin17(pc4), .pin16(axq1), .pin15(pc5), .pin14(axq2),
    .pin13(pc6), .pin12(axq3), .pin11(pc7));
  _74283 #(.ShowInternalStructure("true")) u_74283_4 (
    .pin1(s1), .pin2(y1), .pin3(x1), .pin4(s0), .pin5(x0), .pin6(y0), .pin7(c_in), .pin15(y2), .pin14(x2),
    .pin13(s2), .pin12(x3), .pin11(y3), .pin10(s3), .pin9(n74283_4_pin9));
  _74283 #(.ShowInternalStructure("true")) u_74283_5 (
    .pin1(s5), .pin2(y5), .pin3(x5), .pin4(s4), .pin5(x4), .pin6(y4), .pin7(n74283_4_pin9), .pin15(y6),
    .pin14(x6), .pin13(s6), .pin12(x7), .pin11(y7), .pin10(s7), .pin9(c_out));
  _74283 #(.ShowInternalStructure("true")) u_74283_6 (
    .pin1(b1), .pin2(ny1), .pin3(x1), .pin4(b0), .pin5(x0), .pin6(ny0), .pin7(b_in), .pin15(ny2), .pin14(x2),
    .pin13(b2), .pin12(x3), .pin11(ny3), .pin10(b3), .pin9(n74283_6_pin9));
  _74283 #(.ShowInternalStructure("true")) u_74283_7 (
    .pin1(b5), .pin2(ny5), .pin3(x5), .pin4(b4), .pin5(x4), .pin6(ny4), .pin7(n74283_6_pin9), .pin15(ny6),
    .pin14(x6), .pin13(b6), .pin12(x7), .pin11(ny7), .pin10(b7), .pin9(nb_out));
  _74138 #(.ShowInternalStructure("true")) u_74138_3 (
    .pin1(op0), .pin2(op1), .pin3(op2), .pin4(n74138_3_pin4), .pin5(n74138_3_pin5), .pin6(ealu),
    .pin7(nE_sub), .pin15(nE_pass), .pin14(nE_add), .pin13(nE_adc), .pin12(nE_and), .pin11(nE_or),
    .pin10(nE_nor), .pin9(nE_cmp));
  _74244 #(.ShowInternalStructure("true")) u_74244_10 (
    .pin1(nE_pass), .pin2(y0), .pin3(z4), .pin4(y1), .pin5(z5), .pin6(y2), .pin7(z6), .pin8(y3), .pin9(z7),
    .pin19(nE_pass), .pin18(z0), .pin17(y4), .pin16(z1), .pin15(y5), .pin14(z2), .pin13(y6), .pin12(z3),
    .pin11(y7));
  AT28C64B_MC1 at28c64b_mc1_1 (
    .IO0(mc8), .IO1(mc9), .IO2(mcA), .IO7(mcF), .IO6(mcE), .IO5(mcD), .IO4(mcC), .IO3(mcB), .A12(1'b0),
    .A7(op3), .A6(op2), .A5(op1), .A4(op0), .A3(op03), .A2(exc2), .A1(exc1), .A0(exc0), .nWE(1'b1),
    .A8(1'b0), .A9(1'b0), .A11(1'b0), .nOE(1'b0), .A10(1'b0), .nCE(1'b0));  // open: NC0, GND, NC1, VCC
  _7432 #(.ShowInternalStructure("true")) u_7432_5 (
    .pin1(sel00x), .pin2(sel10x), .pin3(n7432_5_pin3), .pin4(sel02x), .pin5(sel12x), .pin6(n7432_5_pin6),
    .pin13(sel01x), .pin12(sel11x), .pin11(n7432_5_pin11), .pin10(n7432_5_pin11), .pin9(ldf), .pin8(rs_b));
  _7432 #(.ShowInternalStructure("true")) u_7432_6 (
    .pin1(n7432_5_pin3), .pin2(ldh), .pin3(n7432_6_pin3), .pin4(n7432_6_pin3), .pin5(ldf), .pin6(rs_a),
    .pin13(ldh), .pin12(ldl), .pin11(n7432_6_pin11), .pin10(n7432_6_pin11), .pin9(ldf), .pin8(lpreset));
  _7432 #(.ShowInternalStructure("true")) u_7432_7 (
    .pin1(n7432_5_pin6), .pin2(lpreset), .pin3(rs_c), .pin13(lpreset), .pin12(lreg), .pin11(r_we));  // open: pin4, pin5, pin6, pin10, pin9, pin8
  _74573 #(.ShowInternalStructure("true")) u_74573_23 (
    .pin1(l_en), .pin2(l0), .pin3(l1), .pin4(l2), .pin5(l3), .pin6(l4), .pin7(l5), .pin8(l6), .pin9(l7),
    .pin19(rq0), .pin18(rq1), .pin17(rq2), .pin16(rq3), .pin15(rq4), .pin14(rq5), .pin13(rq6), .pin12(rq7),
    .pin11(n74573_23_pin11));
  _74573 #(.ShowInternalStructure("true")) u_74573_24 (
    .pin1(h_en), .pin2(h0), .pin3(h1), .pin4(h2), .pin5(h3), .pin6(h4), .pin7(h5), .pin8(h6), .pin9(h7),
    .pin19(rq0), .pin18(rq1), .pin17(rq2), .pin16(rq3), .pin15(rq4), .pin14(rq5), .pin13(rq6), .pin12(rq7),
    .pin11(n74573_24_pin11));
  _74573 #(.ShowInternalStructure("true")) u_74573_25 (
    .pin1(f_en), .pin2(flag_l), .pin3(flag_e), .pin4(flag_c), .pin5(flag_b), .pin6(f4), .pin7(f5), .pin8(f6),
    .pin9(f7), .pin19(rq0), .pin18(rq1), .pin17(rq2), .pin16(rq3), .pin15(rq4), .pin14(rq5), .pin13(rq6),
    .pin12(rq7), .pin11(n74573_25_pin11));
  _74244 #(.ShowInternalStructure("true")) u_74244_11 (
    .pin1(n74244_11_pin1), .pin2(d0), .pin3(axd4), .pin4(d1), .pin5(axd5), .pin6(d2), .pin7(axd6), .pin8(d3),
    .pin9(axd7), .pin19(n74244_11_pin19), .pin18(axd0), .pin17(d4), .pin16(axd1), .pin15(d5), .pin14(axd2),
    .pin13(d6), .pin12(axd3), .pin11(d7));
  _74244 #(.ShowInternalStructure("true")) u_74244_12 (
    .pin1(d_EQ_0), .pin2(h0), .pin3(pcCx), .pin4(h1), .pin5(pcDx), .pin6(h2), .pin7(pcEx), .pin8(h3),
    .pin9(pcFx), .pin19(d_EQ_0), .pin18(pc8x), .pin17(h4), .pin16(pc9x), .pin15(h5), .pin14(pcAx),
    .pin13(h6), .pin12(pcBx), .pin11(h7));
  _74244 #(.ShowInternalStructure("true")) u_74244_13 (
    .pin1(d_nEQ_0), .pin2(axd0), .pin3(pcCx), .pin4(axd1), .pin5(pcDx), .pin6(axd2), .pin7(pcEx),
    .pin8(axd3), .pin9(pcFx), .pin19(d_nEQ_0), .pin18(pc8x), .pin17(axd4), .pin16(pc9x), .pin15(axd5),
    .pin14(pcAx), .pin13(axd6), .pin12(pcBx), .pin11(axd7));
  _74193 #(.ShowInternalStructure("true")) u_pc2 (
    .pin1(pc9x), .pin2(pc9), .pin3(pc8), .pin4(pc1_pin13), .pin5(pc1_pin12), .pin6(pcA), .pin7(pcB),
    .pin15(pc8x), .pin14(reset), .pin13(pc2_pin13), .pin12(pc2_pin12), .pin11(n_lpch_x), .pin10(pcAx),
    .pin9(pcBx));
  _74193 #(.ShowInternalStructure("true")) u_pc3 (
    .pin1(pcDx), .pin2(pcD), .pin3(pcC), .pin4(pc2_pin13), .pin5(pc2_pin12), .pin6(pcE), .pin7(pcF),
    .pin15(pcCx), .pin14(reset), .pin11(n_lpch_x), .pin10(pcEx), .pin9(pcFx));  // open: pin13, pin12
  _74244 #(.ShowInternalStructure("true")) u_74244_14 (
    .pin1(n_epch), .pin2(pc8), .pin3(axq4), .pin4(pc9), .pin5(axq5), .pin6(pcA), .pin7(axq6), .pin8(pcB),
    .pin9(axq7), .pin19(n_epch), .pin18(axq0), .pin17(pcC), .pin16(axq1), .pin15(pcD), .pin14(axq2),
    .pin13(pcE), .pin12(axq3), .pin11(pcF));
  _74244 #(.ShowInternalStructure("true")) u_74244_15 (
    .pin1(nE_add_adc), .pin2(s0), .pin3(z4), .pin4(s1), .pin5(z5), .pin6(s2), .pin7(z6), .pin8(s3),
    .pin9(z7), .pin19(nE_add_adc), .pin18(z0), .pin17(s4), .pin16(z1), .pin15(s5), .pin14(z2), .pin13(s6),
    .pin12(z3), .pin11(s7));
  _74244 #(.ShowInternalStructure("true")) u_74244_16 (
    .pin1(nE_sub), .pin2(b0), .pin3(z4), .pin4(b1), .pin5(z5), .pin6(b2), .pin7(z6), .pin8(b3), .pin9(z7),
    .pin19(nE_sub), .pin18(z0), .pin17(b4), .pin16(z1), .pin15(b5), .pin14(z2), .pin13(b6), .pin12(z3),
    .pin11(b7));
  _7485 #(.ShowInternalStructure("true")) u_7485_4 (
    .pin1(y3), .pin2(n7485_4_pin2), .pin3(n7485_4_pin3), .pin4(n7485_4_pin4), .pin5(n7485_4_pin5),
    .pin6(n7485_4_pin6), .pin7(n7485_4_pin7), .pin15(x3), .pin14(y2), .pin13(x2), .pin12(x1), .pin11(y1),
    .pin10(x0), .pin9(y0));
  _7408 #(.ShowInternalStructure("true")) u_7408_13 (
    .pin1(x0), .pin2(y0), .pin3(a0), .pin4(x1), .pin5(y1), .pin6(a1), .pin13(x3), .pin12(y3), .pin11(a3),
    .pin10(x2), .pin9(y2), .pin8(a2));
  _74244 #(.ShowInternalStructure("true")) u_74244_17 (
    .pin1(nE_and), .pin2(a0), .pin3(z4), .pin4(a1), .pin5(z5), .pin6(a2), .pin7(z6), .pin8(a3), .pin9(z7),
    .pin19(nE_and), .pin18(z0), .pin17(a4), .pin16(z1), .pin15(a5), .pin14(z2), .pin13(a6), .pin12(z3),
    .pin11(a7));
  _74244 #(.ShowInternalStructure("true")) u_74244_18 (
    .pin1(nLDF), .pin2(XltY), .pin3(z4), .pin4(XeqY), .pin5(z5), .pin6(c_out), .pin7(z6), .pin8(b_out),
    .pin9(z7), .pin19(nLDF), .pin18(z0), .pin17(n74244_18_pin17), .pin16(z1), .pin15(n74244_18_pin15),
    .pin14(z2), .pin13(n74244_18_pin13), .pin12(z3), .pin11(n74244_18_pin11));
  _7408 #(.ShowInternalStructure("true")) u_7408_14 (
    .pin1(sel0), .pin2(op01), .pin3(sel01x), .pin4(sel0), .pin5(op00), .pin6(sel00x), .pin13(sel0),
    .pin12(op02), .pin11(sel02x), .pin10(sel1), .pin9(op10), .pin8(sel10x));
  _7408 #(.ShowInternalStructure("true")) u_7408_15 (
    .pin1(sel1), .pin2(op11), .pin3(sel11x), .pin4(sel1), .pin5(op12), .pin6(sel12x), .pin13(nsel),
    .pin12(nlpreset), .pin11(sel0), .pin10(sel), .pin9(nlpreset), .pin8(sel1));
  _74573 #(.ShowInternalStructure("true")) a (
    .pin1(a_en), .pin2(rd0), .pin3(rd1), .pin4(rd2), .pin5(rd3), .pin6(rd4), .pin7(rd5), .pin8(rd6),
    .pin9(rd7), .pin19(rq0), .pin18(rq1), .pin17(rq2), .pin16(rq3), .pin15(rq4), .pin14(rq5), .pin13(rq6),
    .pin12(rq7), .pin11(a_we));
  _74573 #(.ShowInternalStructure("true")) b (
    .pin1(b_en), .pin2(rd0), .pin3(rd1), .pin4(rd2), .pin5(rd3), .pin6(rd4), .pin7(rd5), .pin8(rd6),
    .pin9(rd7), .pin19(rq0), .pin18(rq1), .pin17(rq2), .pin16(rq3), .pin15(rq4), .pin14(rq5), .pin13(rq6),
    .pin12(rq7), .pin11(b_we));
  _74573 #(.ShowInternalStructure("true")) c (
    .pin1(c_en), .pin2(rd0), .pin3(rd1), .pin4(rd2), .pin5(rd3), .pin6(rd4), .pin7(rd5), .pin8(rd6),
    .pin9(rd7), .pin19(rq0), .pin18(rq1), .pin17(rq2), .pin16(rq3), .pin15(rq4), .pin14(rq5), .pin13(rq6),
    .pin12(rq7), .pin11(c_we));
  _74573 #(.ShowInternalStructure("true")) d (
    .pin1(d_en), .pin2(rd0), .pin3(rd1), .pin4(rd2), .pin5(rd3), .pin6(rd4), .pin7(rd5), .pin8(rd6),
    .pin9(rd7), .pin19(rq0), .pin18(rq1), .pin17(rq2), .pin16(rq3), .pin15(rq4), .pin14(rq5), .pin13(rq6),
    .pin12(rq7), .pin11(d_we));
  _7404 #(.ShowInternalStructure("true")) u_7404_10 (
    .pin1(jmp), .pin2(n_jmp), .pin3(d_nEQ_0), .pin4(d_EQ_0), .pin5(mb_EQ_0), .pin6(mb_nEQ_0), .pin13(eaux),
    .pin12(n_eaux), .pin11(bank), .pin10(n_bank));  // open: pin9, pin8
  _7408 #(.ShowInternalStructure("true")) u_7408_16 (
    .pin1(emem), .pin2(n_adF), .pin3(erom), .pin4(n_lpcl), .pin5(n_jmp_x), .pin6(n_lpcl_x), .pin13(adF),
    .pin12(n_adE), .pin11(a_bank), .pin10(n_lpch), .pin9(n_jmp_x), .pin8(n_lpch_x));
  _7400 #(.ShowInternalStructure("true")) u_7400_1 (
    .pin1(n_ex), .pin2(fall), .pin3(n_pcinc_x), .pin4(spinc), .pin5(fall), .pin6(n_spinc_x), .pin13(spdec),
    .pin12(fall), .pin11(n_spdec_x), .pin10(jmp), .pin9(fall), .pin8(n_jmp_x));
  _7411 #(.ShowInternalStructure("true")) u_7411_4 (
    .pin1(jnz), .pin2(d_nEQ_0), .pin3(mb_nEQ_0), .pin4(lmem), .pin5(bank), .pin6(lbank),
    .pin13(n7411_4_pin13), .pin12(jmp), .pin11(mb_nEQ_0), .pin10(emem), .pin9(bank), .pin8(ebank));
  _74193 #(.ShowInternalStructure("true")) u_sp0 (
    .pin1(axd1), .pin2(sp1), .pin3(sp0), .pin4(n_spdec_x), .pin5(n_spinc_x), .pin6(sp2), .pin7(sp3),
    .pin15(axd0), .pin14(sp0_pin14), .pin13(sp0_pin13), .pin12(sp0_pin12), .pin11(n_lspl), .pin10(axd2),
    .pin9(axd3));
  _74193 #(.ShowInternalStructure("true")) u_sp1 (
    .pin1(axd5), .pin2(sp5), .pin3(sp4), .pin4(sp0_pin13), .pin5(sp0_pin12), .pin6(sp6), .pin7(sp7),
    .pin15(axd4), .pin14(sp1_pin14), .pin13(sp1_pin13), .pin12(sp1_pin12), .pin11(n_lspl), .pin10(axd6),
    .pin9(axd7));
  _74244 #(.ShowInternalStructure("true")) u_74244_19 (
    .pin1(n_espl), .pin2(sp0), .pin3(axq4), .pin4(sp1), .pin5(axq5), .pin6(sp2), .pin7(axq6), .pin8(sp3),
    .pin9(axq7), .pin19(n_espl), .pin18(axq0), .pin17(sp4), .pin16(axq1), .pin15(sp5), .pin14(axq2),
    .pin13(sp6), .pin12(axq3), .pin11(sp7));
  _7485 #(.ShowInternalStructure("true")) u_7485_5 (
    .pin1(y7), .pin2(n7485_4_pin7), .pin3(n7485_4_pin6), .pin4(n7485_4_pin5), .pin6(XeqY), .pin7(XltY),
    .pin15(x7), .pin14(y6), .pin13(x6), .pin12(x5), .pin11(y5), .pin10(x4), .pin9(y4));  // open: pin5
  _7408 #(.ShowInternalStructure("true")) u_7408_17 (
    .pin1(x4), .pin2(y4), .pin3(a4), .pin4(x5), .pin5(y5), .pin6(a5), .pin13(x7), .pin12(y7), .pin11(a7),
    .pin10(x6), .pin9(y6), .pin8(a6));
  _7432 #(.ShowInternalStructure("true")) u_7432_8 (
    .pin1(x0), .pin2(y0), .pin3(o0), .pin4(x1), .pin5(y1), .pin6(o1), .pin13(x3), .pin12(y3), .pin11(o3),
    .pin10(x2), .pin9(y2), .pin8(o2));
  _7432 #(.ShowInternalStructure("true")) u_7432_9 (
    .pin1(x4), .pin2(y4), .pin3(o4), .pin4(x5), .pin5(y5), .pin6(o5), .pin13(x7), .pin12(y7), .pin11(o7),
    .pin10(x6), .pin9(y6), .pin8(o6));
  _74244 #(.ShowInternalStructure("true")) u_74244_20 (
    .pin1(nE_or), .pin2(a0), .pin3(z4), .pin4(o1), .pin5(z5), .pin6(o2), .pin7(z6), .pin8(o3), .pin9(z7),
    .pin19(nE_or), .pin18(z0), .pin17(o4), .pin16(z1), .pin15(o5), .pin14(z2), .pin13(o6), .pin12(z3),
    .pin11(o7));
  _74138 #(.ShowInternalStructure("true")) u_74138_4 (
    .pin1(rs_a), .pin2(rs_b), .pin3(rs_c), .pin4(n74138_4_pin4), .pin5(n74138_4_pin5), .pin6(ereg),
    .pin7(f_en), .pin15(a_en), .pin14(b_en), .pin13(c_en), .pin12(d_en), .pin11(l_en), .pin10(h_en),
    .pin9(z_en));
  _74238 #(.ShowInternalStructure("true")) u_74238_2 (
    .pin1(rs_a), .pin2(rs_b), .pin3(rs_c), .pin4(n74238_2_pin4), .pin5(nclk), .pin6(r_we), .pin7(f_we),
    .pin15(a_we), .pin14(b_we), .pin13(c_we), .pin12(d_we), .pin11(l_we), .pin10(h_we), .pin9(z_we));
  _74573 #(.ShowInternalStructure("true")) z (
    .pin1(z_en), .pin2(rd0), .pin3(rd1), .pin4(rd2), .pin5(rd3), .pin6(rd4), .pin7(rd5), .pin8(rd6),
    .pin9(rd7), .pin19(rq0), .pin18(rq1), .pin17(rq2), .pin16(rq3), .pin15(rq4), .pin14(rq5), .pin13(rq6),
    .pin12(rq7), .pin11(z_we));
  _7421 #(.ShowInternalStructure("true")) u_7421_1 (
    .pin1(ad3), .pin2(ad4), .pin4(ad5), .pin5(ad6), .pin6(n7421_1_pin6), .pin13(ad7), .pin12(ad8),
    .pin10(ad9), .pin9(adA), .pin8(n7421_1_pin8));  // open: pin3, pin11
  _7421 #(.ShowInternalStructure("true")) u_7421_2 (
    .pin1(n7421_1_pin6), .pin2(adB), .pin4(adC), .pin5(adD), .pin6(n7421_2_pin6), .pin13(n7421_1_pin8),
    .pin12(adE), .pin10(adF), .pin9(n7421_2_pin6), .pin8(a_aux));  // open: pin3, pin11
  _7432 #(.ShowInternalStructure("true")) u_7432_10 (
    .pin4(ad1), .pin5(ad2), .pin6(n7432_10_pin6), .pin13(n_ex), .pin12(asp), .pin11(n7432_10_pin11),
    .pin10(n7432_10_pin11), .pin9(aimm), .pin8(n_ahl));  // open: pin1, pin2, pin3
  _7408 #(.ShowInternalStructure("true")) u_7408_18 (
    .pin1(n7432_10_pin6), .pin2(a_aux), .pin3(eaux), .pin4(n_eaux), .pin5(adF), .pin6(a_upper));  // open: pin13, pin12, pin11, pin10, pin9, pin8
  _7411 #(.ShowInternalStructure("true")) u_7411_5 (
    .pin1(a_bank), .pin2(mb_nEQ_0), .pin3(a_upper), .pin4(emem), .pin5(n_bank), .pin6(eram),
    .pin13(n7411_5_pin13), .pin12(bank), .pin11(a_upper), .pin10(lmem), .pin9(n_bank), .pin8(lram));
  _7404 #(.ShowInternalStructure("true")) u_7404_11 (
    .pin1(aimm), .pin2(n_aimm), .pin3(n_ex), .pin4(n_apc), .pin5(asp), .pin6(n_asp), .pin13(eaux),
    .pin12(n_eaux), .pin11(adE), .pin10(n_adE), .pin9(adF), .pin8(n_adF));
  _74688 #(.ShowInternalStructure("true")) u_74688_6 (
    .pin1(n74688_6_pin1), .pin2(axd0), .pin3(n74688_6_pin3), .pin4(axd1), .pin5(n74688_6_pin5), .pin6(axd2),
    .pin7(n74688_6_pin7), .pin8(axd3), .pin9(n74688_6_pin9), .pin19(d_nEQ_0), .pin18(axd7),
    .pin17(n74688_6_pin17), .pin16(axd6), .pin15(n74688_6_pin15), .pin14(axd5), .pin13(n74688_6_pin13),
    .pin12(axd4), .pin11(n74688_6_pin11));
  _74193 #(.ShowInternalStructure("true")) u_sp2 (
    .pin1(axd1), .pin2(sp9), .pin3(sp8), .pin4(sp1_pin13), .pin5(sp1_pin12), .pin6(spA), .pin7(spB),
    .pin15(axd0), .pin14(sp2_pin14), .pin13(sp2_pin13), .pin12(sp2_pin12), .pin11(n_lsph), .pin10(axd2),
    .pin9(axd3));
  _74193 #(.ShowInternalStructure("true")) u_sp3 (
    .pin1(axd5), .pin2(spD), .pin3(spC), .pin4(sp2_pin13), .pin5(sp2_pin12), .pin6(spE), .pin7(spF),
    .pin15(axd4), .pin14(sp3_pin14), .pin11(n_lsph), .pin10(axd6), .pin9(axd7));  // open: pin13, pin12
  _74244 #(.ShowInternalStructure("true")) u_74244_21 (
    .pin1(n_esph), .pin2(sp8), .pin3(axq4), .pin4(sp9), .pin5(axq5), .pin6(spA), .pin7(axq6), .pin8(spB),
    .pin9(axq7), .pin19(n_esph), .pin18(axq0), .pin17(spC), .pin16(axq1), .pin15(spD), .pin14(axq2),
    .pin13(spE), .pin12(axq3), .pin11(spF));
  _7404 #(.ShowInternalStructure("true")) u_7404_12 (
    .pin1(o0), .pin2(n0), .pin3(o1), .pin4(n1), .pin5(o2), .pin6(n2), .pin13(o5), .pin12(n5), .pin11(o4),
    .pin10(n4), .pin9(o3), .pin8(n3));
  _7404 #(.ShowInternalStructure("true")) u_7404_13 (
    .pin1(o6), .pin2(n6), .pin3(o7), .pin4(n7));  // open: pin5, pin6, pin13, pin12, pin11, pin10, pin9, pin8
  _74244 #(.ShowInternalStructure("true")) u_74244_22 (
    .pin1(nE_nor), .pin2(n0), .pin3(z4), .pin4(n1), .pin5(z5), .pin6(n2), .pin7(z6), .pin8(n3), .pin9(z7),
    .pin19(nE_nor), .pin18(z0), .pin17(n4), .pin16(z1), .pin15(n5), .pin14(z2), .pin13(n6), .pin12(z3),
    .pin11(n7));
  // also tied to GND on the sheet: {HSC_0_pin3, HSC_0_pin4, HSC_0_pin5, HSC_0_pin6, HSC_1_pin3, HSC_1_pin4, HSC_1_pin5, HSC_1_pin6, HSC_2_pin3, HSC_2_pin4, HSC_2_pin5, HSC_2_pin6, TKC_0_pin3, TKC_0_pin4, TKC_0_pin5, TKC_0_pin6, TKC_1_pin3, TKC_1_pin4, TKC_1_pin5, TKC_1_pin6, n74688_1_pin1, n74688_1_pin3, n74688_1_pin5, n74688_1_pin7, n74688_1_pin9, n74682_1_pin9, n74688_2_pin1, n74688_3_pin1, n74688_4_pin1, n74688_4_pin3, n74688_4_pin5, n74688_4_pin7, n7485_1_pin1, n7485_1_pin2, n7485_1_pin4, n74238_1_pin3, n74238_1_pin4, n74238_1_pin5, n74163_1_pin3, n74163_1_pin4, n74163_1_pin5, n74163_1_pin6, n74163_2_pin3, n74163_2_pin4, n74163_2_pin5, n74163_2_pin6, n74688_1_pin16, n74688_1_pin14, n74688_1_pin12, n74682_1_pin18, n74682_1_pin17, n74682_1_pin16, n74682_1_pin14, n74682_1_pin12, n74682_2_pin18, n74682_2_pin17, n74682_2_pin12, n74688_2_pin18, n74688_2_pin16, n74688_2_pin14, n74688_2_pin12, n74688_3_pin18, n74688_3_pin16, n74688_3_pin12, n7485_1_pin9, EQ_5_pin1, EQ_5_pin3, EQ_5_pin5, EQ_5_pin9, EQ_09_pin1, EQ_09_pin3, EQ_09_pin7, EQ_54_pin1, EQ_54_pin3, EQ_54_pin5, EQ_54_pin9, EQ_33_pin1, EQ_33_pin7, EQ_33_pin9, EQ_69_pin1, EQ_69_pin3, EQ_69_pin7, EQ_6F_pin1, n74283_1_pin2, n74283_1_pin6, n74283_1_pin7, n74283_2_pin6, EQ_5_pin18, EQ_5_pin16, EQ_5_pin14, EQ_5_pin12, EQ_09_pin18, EQ_09_pin16, EQ_09_pin14, EQ_09_pin12, EQ_54_pin18, EQ_54_pin14, EQ_33_pin18, EQ_33_pin16, EQ_69_pin18, EQ_69_pin12, EQ_6F_pin18, EQ_6F_pin12, n74283_2_pin15, n74283_3_pin15, n74283_3_pin11, n7427_1_pin13, n7427_2_pin9, n74151_1_pin7, n74573_1_pin1, n74573_3_pin7, n74573_3_pin8, n74573_3_pin9, op0_pin1, op1_pin1, op2_pin1, n7485_2_pin1, n7485_3_pin1, n7485_3_pin2, n7485_3_pin3, n7485_3_pin4, n74244_1_pin1, n74244_2_pin1, n74573_10_pin1, n74573_11_pin1, n74688_5_pin1, n74688_5_pin3, n74688_5_pin5, n74688_5_pin7, n74688_5_pin9, n7485_2_pin14, n7485_2_pin11, n7485_2_pin9, n7485_3_pin14, n7485_3_pin11, n74244_1_pin19, n74244_2_pin19, n74688_5_pin18, n74688_5_pin16, n74688_5_pin14, n74688_5_pin12, mb_pin1, n74138_1_pin4, n74573_16_pin1, n74244_3_pin1, n74374_1_pin1, n74374_2_pin1, n74244_3_pin19, n74573_22_pin1, l_pin1, h_pin1, f_pin1, n74138_3_pin4, n74138_3_pin5, n74244_11_pin1, n7485_4_pin2, n7485_4_pin4, n74244_11_pin19, n74244_18_pin17, n74244_18_pin15, n74244_18_pin13, n74244_18_pin11, sp0_pin14, sp1_pin14, n74138_4_pin4, n74138_4_pin5, n74238_2_pin4, n74688_6_pin1, n74688_6_pin3, n74688_6_pin5, n74688_6_pin7, n74688_6_pin9, n74688_6_pin17, n74688_6_pin15, n74688_6_pin13, n74688_6_pin11, sp2_pin14, sp3_pin14}
  // also tied to VCC on the sheet: {HSC_0_pin7, HSC_1_pin7, HSC_2_pin7, TKC_0_pin7, TKC_1_pin7, n74682_1_pin3, n74682_1_pin5, n74682_1_pin7, n74682_2_pin3, n74682_2_pin5, n74682_2_pin7, n74682_2_pin9, n74688_2_pin3, n74688_2_pin5, n74688_2_pin7, n74688_2_pin9, n74688_3_pin3, n74688_3_pin5, n74688_3_pin7, n74688_3_pin9, n74688_4_pin9, n7485_1_pin3, n74238_1_pin6, HSC_0_pin9, HSC_1_pin9, HSC_2_pin9, TKC_0_pin10, TKC_0_pin9, TKC_1_pin9, n74688_1_pin18, n74682_2_pin16, n74682_2_pin14, n74688_3_pin14, n74688_4_pin18, n74688_4_pin16, n74688_4_pin14, n74688_4_pin12, n7485_1_pin14, n7485_1_pin11, n74163_1_pin10, n74163_1_pin9, n74163_2_pin10, n74163_2_pin9, EQ_5_pin7, EQ_09_pin5, EQ_09_pin9, EQ_54_pin7, EQ_33_pin3, EQ_33_pin5, EQ_69_pin5, EQ_69_pin9, EQ_6F_pin3, EQ_6F_pin5, EQ_6F_pin7, EQ_6F_pin9, n74283_2_pin2, n74283_3_pin2, n74283_3_pin6, EQ_54_pin16, EQ_54_pin12, EQ_33_pin14, EQ_33_pin12, EQ_69_pin16, EQ_69_pin14, EQ_6F_pin16, EQ_6F_pin14, n74283_1_pin15, n74283_1_pin11, n74283_2_pin11, n7411_2_pin11, n74573_2_pin11, n74573_3_pin11, n74573_4_pin11, n74573_5_pin11, n74573_6_pin11, n74573_7_pin11, n7411_3_pin13, n7485_3_pin9, n74573_8_pin11, n74573_9_pin11, n74573_12_pin11, n74573_13_pin11, n74573_14_pin11, n74573_15_pin11, n74573_17_pin11, n74573_18_pin11, n74573_19_pin11, n74573_20_pin11, n74573_21_pin11, pc0_pin4, n7485_4_pin3, n74573_23_pin11, n74573_24_pin11, n74573_25_pin11, n7411_4_pin13, n7411_5_pin13}

  // Other names for the same wires on the sheet: mb_EQ_1 = bank_vram; op05 = op1; op06 = op2; op07 = op3; op04 = op0;
  //   q0 = d0; q1 = d1; q2 = d2; q3 = d3; q4 = d4; q5 = d5; q6 = d6; q7 = d7; sel00 = op00; sel01 = op01;
  //   sel02 = op02; sel10 = op10; sel11 = op11; sel12 = op12; y = op03
endmodule

module deleteme (
);

  wire a0, a001, a1, a2, a3, a4, a5, a6, a7, a010, a101, ad0, ad1, ad2, ad3, ad4, ad5, ad6, ad7, ad8, ad9,
       adA, adB, adC, adD, adE, adF, aimm, asp, b0, b1, b2, b3, b4, b5, b6, b7, b_in, b_out, bank_vram, c_in,
       c_out, cc, clk, clock_1_out, d0, d1, d2, d3, d4, d5, d6, d7, d_EQ_0, dbg_x, dbg_y, dx0, dx1, dx2, dx3,
       dx4, dx5, dx6, dx7, ealu, eaux, ebank, edev, el_vram, emem, eop1, eop2, EQ_5_pin1, EQ_5_pin3,
       EQ_5_pin5, EQ_5_pin7, EQ_5_pin9, EQ_5_pin12, EQ_5_pin14, EQ_5_pin16, EQ_5_pin18, EQ_6F_pin1,
       EQ_6F_pin3, EQ_6F_pin5, EQ_6F_pin7, EQ_6F_pin9, EQ_6F_pin12, EQ_6F_pin14, EQ_6F_pin16, EQ_6F_pin18,
       EQ_09_pin1, EQ_09_pin3, EQ_09_pin5, EQ_09_pin7, EQ_09_pin9, EQ_09_pin12, EQ_09_pin14, EQ_09_pin16,
       EQ_09_pin18, EQ_33_pin1, EQ_33_pin3, EQ_33_pin5, EQ_33_pin7, EQ_33_pin9, EQ_33_pin12, EQ_33_pin14,
       EQ_33_pin16, EQ_33_pin18, EQ_54_pin1, EQ_54_pin3, EQ_54_pin5, EQ_54_pin7, EQ_54_pin9, EQ_54_pin12,
       EQ_54_pin14, EQ_54_pin16, EQ_54_pin18, EQ_69_pin1, EQ_69_pin3, EQ_69_pin5, EQ_69_pin7, EQ_69_pin9,
       EQ_69_pin12, EQ_69_pin14, EQ_69_pin16, EQ_69_pin18, eram, ereg, erom, esta, eta, etb, evram, ex, exc0,
       exc1, exc2, fall, flag_b, flag_c, hsc0, hsc0Q, hsc1, hsc1Q, hsc2, hsc2Q, hsc3, hsc3Q, hsc4, hsc4Q,
       hsc5, hsc5Q, hsc6, hsc7, hsc8, hsc9, HSC_0_pin3, HSC_0_pin4, HSC_0_pin5, HSC_0_pin6, HSC_0_pin7,
       HSC_0_pin9, HSC_0_pin15, HSC_1_pin1, HSC_1_pin3, HSC_1_pin4, HSC_1_pin5, HSC_1_pin6, HSC_1_pin7,
       HSC_1_pin9, HSC_1_pin15, HSC_2_pin3, HSC_2_pin4, HSC_2_pin5, HSC_2_pin6, HSC_2_pin7, HSC_2_pin9,
       hsc_eORd, hsc_inc, hsc_n1S, hsc_n2S, hsc_n3S, hsc_n4S, hsc_n5S, hsc_n9, hsc_nEQ_05, hsc_nEQ_6A,
       hsc_nEQ_6E, hsc_nEQ_34, hsc_nEQ_54, hsc_nEQ_A, hsc_nR, hsc_or_89, hsc_pp, jnz, latch_vram, lbank, ld1,
       ld1_x, ld2, ld2_x, ld3, ld3_x, ldev, ldf, ldh, ldl, ldx, ldy, lmem, lop0, lop1, lop2, lopN, lprt,
       lprt_x, lram, lreg, lsta, lvram, mb_EQ_0, mb_nEQ_1, mb_nGT_1, mc0_x, mc1_x, mc2_x, mc3_x, mc4_x,
       mc5_x, mc6_x, mc7_x, mc8_x, mc9_x, mcA_x, mcB_x, mcC_x, mw_lda, n0, n1, n2, n3, n4, n5, n6, n7,
       n7402_1_pin1, n7402_1_pin2, n7404_1_pin2, n7404_1_pin6, n7404_4_pin3, n7404_5_pin6, n7404_5_pin8,
       n7404_5_pin10, n7404_5_pin12, n7408_3_pin8, n7411_2_pin6, n7411_2_pin11, n7411_3_pin2, n7411_3_pin9,
       n7411_3_pin13, n7427_1_pin6, n7427_1_pin13, n7427_2_pin9, n7432_2_pin11, n7432_3_pin3, n7432_3_pin6,
       n7432_3_pin8, n7432_3_pin11, n7432_4_pin3, n7432_4_pin6, n7485_1_pin1, n7485_1_pin2, n7485_1_pin3,
       n7485_1_pin4, n7485_1_pin9, n7485_1_pin11, n7485_1_pin14, n7485_2_pin2, n7485_2_pin3, n7485_2_pin4,
       n7485_2_pin5, n7485_2_pin6, n7485_2_pin7, n74138_1_pin4, n74138_1_pin5, n74151_1_pin7, n74163_1_pin3,
       n74163_1_pin4, n74163_1_pin5, n74163_1_pin6, n74163_1_pin9, n74163_1_pin10, n74163_2_pin3,
       n74163_2_pin4, n74163_2_pin5, n74163_2_pin6, n74163_2_pin9, n74163_2_pin10, n74244_5_pin11,
       n74244_5_pin13, n74244_5_pin15, n74244_5_pin17, n74283_1_pin2, n74283_1_pin6, n74283_1_pin7,
       n74283_1_pin9, n74283_1_pin11, n74283_1_pin15, n74283_2_pin2, n74283_2_pin6, n74283_2_pin9,
       n74283_2_pin11, n74283_2_pin15, n74283_3_pin2, n74283_3_pin6, n74283_3_pin11, n74283_3_pin15,
       n74283_4_pin9, n74283_6_pin9, n74374_1_pin1, n74374_2_pin1, n74573_1_pin1, n74573_2_pin11,
       n74573_3_pin7, n74573_3_pin8, n74573_3_pin9, n74573_3_pin11, n74573_4_pin11, n74573_5_pin11,
       n74573_6_pin11, n74573_7_pin11, n74682_1_pin3, n74682_1_pin5, n74682_1_pin7, n74682_1_pin9,
       n74682_1_pin12, n74682_1_pin14, n74682_1_pin16, n74682_1_pin17, n74682_1_pin18, n74682_2_pin3,
       n74682_2_pin5, n74682_2_pin7, n74682_2_pin9, n74682_2_pin12, n74682_2_pin14, n74682_2_pin16,
       n74682_2_pin17, n74682_2_pin18, n74688_1_pin1, n74688_1_pin3, n74688_1_pin5, n74688_1_pin7,
       n74688_1_pin9, n74688_1_pin12, n74688_1_pin14, n74688_1_pin16, n74688_1_pin18, n74688_2_pin1,
       n74688_2_pin3, n74688_2_pin5, n74688_2_pin7, n74688_2_pin9, n74688_2_pin12, n74688_2_pin14,
       n74688_2_pin16, n74688_2_pin18, n74688_3_pin1, n74688_3_pin3, n74688_3_pin5, n74688_3_pin7,
       n74688_3_pin9, n74688_3_pin12, n74688_3_pin14, n74688_3_pin16, n74688_3_pin18, n74688_4_pin1,
       n74688_4_pin3, n74688_4_pin5, n74688_4_pin7, n74688_4_pin9, n74688_4_pin12, n74688_4_pin14,
       n74688_4_pin16, n74688_4_pin18, n_cc, n_el_vram, n_eop1, n_eop2, n_eram, n_erom, n_esta, n_evram,
       n_ex, n_lram, n_lvram, n_mw_lda, nb_out, nclk, nE_adc, nE_add, nE_add_adc, nE_and, nE_cmp, nE_nor,
       nE_or, nE_pass, nE_sub, nLDF, nop0, nop1, nop2, nreset, nV03_broad, nV03_short, nV03_sync, ny, ny0,
       ny1, ny2, ny3, ny4, ny5, ny6, ny7, o0, o1, o2, o3, o4, o5, o6, o7, op0, op00, op0_pin1, op01, op1,
       op1_pin1, op02, op2, op2_pin1, op03, op3, op10, op11, op12, op13, op14, op15, op16, op17, op20, op21,
       op22, op23, op24, op25, op26, op27, op_gt_6, opc0, opc1, opc_eq_0, opc_eq_1, opc_eq_2, opc_eq_3,
       prt_EQ_0, q0, q1, q2, q3, q4, q5, q6, q7, reset, rise, s0, s1, s2, s3, s4, s5, s6, s7, sel, spdec,
       spinc, st3, tkc0, tkc0Q, tkc1, tkc1Q, tkc2, tkc2Q, tkc3, tkc3Q, tkc4, tkc5, tkc6, tkc7, tkc7_LE_6F,
       tkc7_LE_07, TKC_0_pin3, TKC_0_pin4, TKC_0_pin5, TKC_0_pin6, TKC_0_pin7, TKC_0_pin9, TKC_0_pin10,
       TKC_0_pin15, TKC_1_pin3, TKC_1_pin4, TKC_1_pin5, TKC_1_pin6, TKC_1_pin7, TKC_1_pin9, tkc_nEQ_0F,
       tkc_nEQ_0F_2, tkc_nEQ_28, tkc_nEQ_80, tkc_nEQ_F8, tkc_nRC0, tkc_RC0, v_03, v_10, vbit, vd0, vd0_x,
       vd1, vd1_x, vd2, vd2_x, vd3, vd3_x, vd4, vd4_x, vd5, vd5_x, vd6, vd6_x, vd7, vd7_x, vma0_x, vma1_x,
       vma2_x, vma3_x, vma4_x, vma5, vma5_x, vma6, vma6_x, vma7, vma7_x, vma8, vma8_x, vma9, vma9_x, vmaA,
       vmaA_x, vmaB, vmaB_x, vmaC, vmaC_x, vmaD, vmaE, vram_d0, vram_d1, vram_d2, vram_d3, vram_d4, vram_d5,
       vram_d6, vram_d7, x0, x1, x2, x3, x4, x5, x6, x7, xc, XeqY, XltY, y0, y1, y2, y3, y4, y5, y6, y7, yc,
       z0, z1, z2, z3, z4, z5, z6, z7;

  _74161 #(.ShowInternalStructure("true")) HSC_0 (
    .pin1(hsc_nR), .pin2(clk), .pin3(HSC_0_pin3), .pin4(HSC_0_pin4), .pin5(HSC_0_pin5), .pin6(HSC_0_pin6),
    .pin7(HSC_0_pin7), .pin15(HSC_0_pin15), .pin14(hsc0), .pin13(hsc1), .pin12(hsc2), .pin11(hsc3),
    .pin10(hsc_inc), .pin9(HSC_0_pin9));
  _74161 #(.ShowInternalStructure("true")) HSC_1 (
    .pin1(HSC_1_pin1), .pin2(clk), .pin3(HSC_1_pin3), .pin4(HSC_1_pin4), .pin5(HSC_1_pin5),
    .pin6(HSC_1_pin6), .pin7(HSC_1_pin7), .pin15(HSC_1_pin15), .pin14(hsc4), .pin13(hsc5), .pin12(hsc6),
    .pin11(hsc7), .pin10(HSC_0_pin15), .pin9(HSC_1_pin9));
  _74161 #(.ShowInternalStructure("true")) HSC_2 (
    .pin1(HSC_1_pin1), .pin2(clk), .pin3(HSC_2_pin3), .pin4(HSC_2_pin4), .pin5(HSC_2_pin5),
    .pin6(HSC_2_pin6), .pin7(HSC_2_pin7), .pin14(hsc8), .pin13(hsc9), .pin10(HSC_1_pin15), .pin9(HSC_2_pin9));  // open: pin15, pin12, pin11
  _74161 #(.ShowInternalStructure("true")) TKC_0 (
    .pin1(tkc_nRC0), .pin2(clk), .pin3(TKC_0_pin3), .pin4(TKC_0_pin4), .pin5(TKC_0_pin5), .pin6(TKC_0_pin6),
    .pin7(TKC_0_pin7), .pin15(TKC_0_pin15), .pin14(tkc0), .pin13(tkc1), .pin12(tkc2), .pin11(tkc3),
    .pin10(TKC_0_pin10), .pin9(TKC_0_pin9));
  _74161 #(.ShowInternalStructure("true")) TKC_1 (
    .pin1(tkc_nRC0), .pin2(clk), .pin3(TKC_1_pin3), .pin4(TKC_1_pin4), .pin5(TKC_1_pin5), .pin6(TKC_1_pin6),
    .pin7(TKC_1_pin7), .pin15(tkc_RC0), .pin14(tkc4), .pin13(tkc5), .pin12(tkc6), .pin11(tkc7),
    .pin10(TKC_0_pin15), .pin9(TKC_1_pin9));
  _7404 #(.ShowInternalStructure("true")) u_7404_1 (
    .pin1(hsc_nR), .pin2(n7404_1_pin2), .pin3(n7404_1_pin2), .pin4(HSC_1_pin1), .pin5(tkc_nEQ_0F),
    .pin6(n7404_1_pin6), .pin13(tkc_RC0), .pin12(tkc_nRC0), .pin11(hsc9), .pin10(hsc_n9),
    .pin9(n7404_1_pin6), .pin8(tkc_nEQ_0F_2));
  _74688 #(.ShowInternalStructure("true")) u_74688_1 (
    .pin1(n74688_1_pin1), .pin2(tkc0), .pin3(n74688_1_pin3), .pin4(tkc1), .pin5(n74688_1_pin5), .pin6(tkc2),
    .pin7(n74688_1_pin7), .pin8(tkc3), .pin9(n74688_1_pin9), .pin19(tkc_nEQ_80), .pin18(n74688_1_pin18),
    .pin17(tkc7), .pin16(n74688_1_pin16), .pin15(tkc6), .pin14(n74688_1_pin14), .pin13(tkc5),
    .pin12(n74688_1_pin12), .pin11(tkc4));
  _74682 #(.ShowInternalStructure("true")) u_74682_1 (
    .pin1(tkc7_LE_07), .pin2(tkc0), .pin3(n74682_1_pin3), .pin4(tkc1), .pin5(n74682_1_pin5), .pin6(tkc2),
    .pin7(n74682_1_pin7), .pin8(tkc3), .pin9(n74682_1_pin9), .pin18(n74682_1_pin18), .pin17(n74682_1_pin17),
    .pin16(n74682_1_pin16), .pin15(tkc6), .pin14(n74682_1_pin14), .pin13(tkc5), .pin12(n74682_1_pin12),
    .pin11(tkc4));  // open: pin19
  _74682 #(.ShowInternalStructure("true")) u_74682_2 (
    .pin1(tkc7_LE_6F), .pin2(tkc0), .pin3(n74682_2_pin3), .pin4(tkc1), .pin5(n74682_2_pin5), .pin6(tkc2),
    .pin7(n74682_2_pin7), .pin8(tkc3), .pin9(n74682_2_pin9), .pin18(n74682_2_pin18), .pin17(n74682_2_pin17),
    .pin16(n74682_2_pin16), .pin15(tkc6), .pin14(n74682_2_pin14), .pin13(tkc5), .pin12(n74682_2_pin12),
    .pin11(tkc4));  // open: pin19
  _74688 #(.ShowInternalStructure("true")) u_74688_2 (
    .pin1(n74688_2_pin1), .pin2(tkc0), .pin3(n74688_2_pin3), .pin4(tkc1), .pin5(n74688_2_pin5), .pin6(tkc2),
    .pin7(n74688_2_pin7), .pin8(tkc3), .pin9(n74688_2_pin9), .pin19(tkc_nEQ_0F), .pin18(n74688_2_pin18),
    .pin17(tkc7), .pin16(n74688_2_pin16), .pin15(tkc6), .pin14(n74688_2_pin14), .pin13(tkc5),
    .pin12(n74688_2_pin12), .pin11(tkc4));
  _74688 #(.ShowInternalStructure("true")) u_74688_3 (
    .pin1(n74688_3_pin1), .pin2(tkc0), .pin3(n74688_3_pin3), .pin4(tkc1), .pin5(n74688_3_pin5), .pin6(tkc2),
    .pin7(n74688_3_pin7), .pin8(tkc3), .pin9(n74688_3_pin9), .pin19(tkc_nEQ_28), .pin18(n74688_3_pin18),
    .pin17(tkc7), .pin16(n74688_3_pin16), .pin15(tkc6), .pin14(n74688_3_pin14), .pin13(tkc5),
    .pin12(n74688_3_pin12), .pin11(tkc4));
  _74688 #(.ShowInternalStructure("true")) u_74688_4 (
    .pin1(n74688_4_pin1), .pin2(tkc0), .pin3(n74688_4_pin3), .pin4(tkc1), .pin5(n74688_4_pin5), .pin6(tkc2),
    .pin7(n74688_4_pin7), .pin8(tkc3), .pin9(n74688_4_pin9), .pin19(tkc_nEQ_F8), .pin18(n74688_4_pin18),
    .pin17(tkc7), .pin16(n74688_4_pin16), .pin15(tkc6), .pin14(n74688_4_pin14), .pin13(tkc5),
    .pin12(n74688_4_pin12), .pin11(tkc4));
  _7404 #(.ShowInternalStructure("true")) u_7404_2 (
    .pin1(op03), .pin2(ny), .pin3(n_ex), .pin4(ex), .pin5(cc), .pin6(n_cc), .pin13(op0), .pin12(nop0),
    .pin11(op1), .pin10(nop1), .pin9(op2), .pin8(nop2));
  _7485 #(.ShowInternalStructure("true")) u_7485_1 (
    .pin1(n7485_1_pin1), .pin2(n7485_1_pin2), .pin3(n7485_1_pin3), .pin4(n7485_1_pin4), .pin5(op_gt_6),
    .pin15(op3), .pin14(n7485_1_pin14), .pin13(op2), .pin12(op1), .pin11(n7485_1_pin11), .pin10(op0),
    .pin9(n7485_1_pin9));  // open: pin6, pin7
  _7408 #(.ShowInternalStructure("true")) u_7408_1 (
    .pin1(lopN), .pin2(opc_eq_0), .pin3(lop0), .pin4(lopN), .pin5(opc_eq_1), .pin6(lop1), .pin13(lopN),
    .pin12(opc_eq_2), .pin11(lop2), .pin10(nclk), .pin9(n_ex), .pin8(lopN));
  _74163 #(.ShowInternalStructure("true")) u_74163_1 (
    .pin1(n_cc), .pin2(nclk), .pin3(n74163_1_pin3), .pin4(n74163_1_pin4), .pin5(n74163_1_pin5),
    .pin6(n74163_1_pin6), .pin7(n_ex), .pin14(opc0), .pin13(opc1), .pin10(n74163_1_pin10),
    .pin9(n74163_1_pin9));  // open: pin15, pin12, pin11
  _74163 #(.ShowInternalStructure("true")) u_74163_2 (
    .pin1(n_cc), .pin2(nclk), .pin3(n74163_2_pin3), .pin4(n74163_2_pin4), .pin5(n74163_2_pin5),
    .pin6(n74163_2_pin6), .pin7(ex), .pin14(exc0), .pin13(exc1), .pin12(exc2), .pin10(n74163_2_pin10),
    .pin9(n74163_2_pin9));  // open: pin15, pin11
  _74688 #(.ShowInternalStructure("true")) EQ_5 (
    .pin1(EQ_5_pin1), .pin2(hsc0), .pin3(EQ_5_pin3), .pin4(hsc1), .pin5(EQ_5_pin5), .pin6(hsc2),
    .pin7(EQ_5_pin7), .pin8(hsc3), .pin9(EQ_5_pin9), .pin19(hsc_nEQ_05), .pin18(EQ_5_pin18), .pin17(hsc7),
    .pin16(EQ_5_pin16), .pin15(hsc6), .pin14(EQ_5_pin14), .pin13(hsc5), .pin12(EQ_5_pin12), .pin11(hsc4));
  _74688 #(.ShowInternalStructure("true")) EQ_09 (
    .pin1(EQ_09_pin1), .pin2(hsc0), .pin3(EQ_09_pin3), .pin4(hsc1), .pin5(EQ_09_pin5), .pin6(hsc2),
    .pin7(EQ_09_pin7), .pin8(hsc3), .pin9(EQ_09_pin9), .pin19(hsc_nEQ_A), .pin18(EQ_09_pin18), .pin17(hsc7),
    .pin16(EQ_09_pin16), .pin15(hsc6), .pin14(EQ_09_pin14), .pin13(hsc5), .pin12(EQ_09_pin12), .pin11(hsc4));
  _74688 #(.ShowInternalStructure("true")) EQ_54 (
    .pin1(EQ_54_pin1), .pin2(hsc0), .pin3(EQ_54_pin3), .pin4(hsc1), .pin5(EQ_54_pin5), .pin6(hsc2),
    .pin7(EQ_54_pin7), .pin8(hsc3), .pin9(EQ_54_pin9), .pin19(hsc_nEQ_54), .pin18(EQ_54_pin18), .pin17(hsc7),
    .pin16(EQ_54_pin16), .pin15(hsc6), .pin14(EQ_54_pin14), .pin13(hsc5), .pin12(EQ_54_pin12), .pin11(hsc4));
  _74688 #(.ShowInternalStructure("true")) EQ_33 (
    .pin1(EQ_33_pin1), .pin2(hsc0), .pin3(EQ_33_pin3), .pin4(hsc1), .pin5(EQ_33_pin5), .pin6(hsc2),
    .pin7(EQ_33_pin7), .pin8(hsc3), .pin9(EQ_33_pin9), .pin19(hsc_nEQ_34), .pin18(EQ_33_pin18), .pin17(hsc7),
    .pin16(EQ_33_pin16), .pin15(hsc6), .pin14(EQ_33_pin14), .pin13(hsc5), .pin12(EQ_33_pin12), .pin11(hsc4));
  _74688 #(.ShowInternalStructure("true")) EQ_69 (
    .pin1(EQ_69_pin1), .pin2(hsc0), .pin3(EQ_69_pin3), .pin4(hsc1), .pin5(EQ_69_pin5), .pin6(hsc2),
    .pin7(EQ_69_pin7), .pin8(hsc3), .pin9(EQ_69_pin9), .pin19(hsc_nEQ_6A), .pin18(EQ_69_pin18), .pin17(hsc7),
    .pin16(EQ_69_pin16), .pin15(hsc6), .pin14(EQ_69_pin14), .pin13(hsc5), .pin12(EQ_69_pin12), .pin11(hsc4));
  _74688 #(.ShowInternalStructure("true")) EQ_6F (
    .pin1(EQ_6F_pin1), .pin2(hsc0), .pin3(EQ_6F_pin3), .pin4(hsc1), .pin5(EQ_6F_pin5), .pin6(hsc2),
    .pin7(EQ_6F_pin7), .pin8(hsc3), .pin9(EQ_6F_pin9), .pin19(hsc_nEQ_6E), .pin18(EQ_6F_pin18), .pin17(hsc7),
    .pin16(EQ_6F_pin16), .pin15(hsc6), .pin14(EQ_6F_pin14), .pin13(hsc5), .pin12(EQ_6F_pin12), .pin11(hsc4));
  _74283 #(.ShowInternalStructure("true")) u_74283_1 (
    .pin1(vma6), .pin2(n74283_1_pin2), .pin3(hsc1), .pin4(vma5), .pin5(hsc0), .pin6(n74283_1_pin6),
    .pin7(n74283_1_pin7), .pin15(n74283_1_pin15), .pin14(hsc2), .pin13(vma7), .pin12(hsc3),
    .pin11(n74283_1_pin11), .pin10(vma8), .pin9(n74283_1_pin9));
  _74283 #(.ShowInternalStructure("true")) u_74283_2 (
    .pin1(vmaA), .pin2(n74283_2_pin2), .pin3(hsc5), .pin4(vma9), .pin5(hsc4), .pin6(n74283_2_pin6),
    .pin7(n74283_1_pin9), .pin15(n74283_2_pin15), .pin14(hsc6), .pin13(vmaB), .pin12(hsc7),
    .pin11(n74283_2_pin11), .pin10(vmaC), .pin9(n74283_2_pin9));
  _74283 #(.ShowInternalStructure("true")) u_74283_3 (
    .pin1(vmaE), .pin2(n74283_3_pin2), .pin3(hsc9), .pin4(vmaD), .pin5(hsc8), .pin6(n74283_3_pin6),
    .pin7(n74283_2_pin9), .pin15(n74283_3_pin15), .pin11(n74283_3_pin11));  // open: pin14, pin13, pin12, pin10, pin9
  _7404 #(.ShowInternalStructure("true")) u_7404_3 (
    .pin1(eop1), .pin2(n_eop1), .pin3(eop2), .pin4(n_eop2), .pin5(n_mw_lda), .pin6(mw_lda), .pin13(erom),
    .pin12(n_erom), .pin11(eram), .pin10(n_eram), .pin9(lram), .pin8(n_lram));
  _7411 #(.ShowInternalStructure("true")) u_7411_1 (
    .pin1(op1), .pin2(nop0), .pin3(op0), .pin4(nop1), .pin5(nop2), .pin6(a001), .pin13(nop2), .pin12(a010),
    .pin11(op0), .pin10(nop1), .pin9(op2), .pin8(a101));
  _7411 #(.ShowInternalStructure("true")) u_7411_2 (
    .pin1(nclk), .pin2(ldev), .pin3(nop0), .pin4(nop1), .pin5(nop2), .pin6(n7411_2_pin6), .pin13(prt_EQ_0),
    .pin12(lsta), .pin11(n7411_2_pin11), .pin10(edev), .pin9(prt_EQ_0), .pin8(esta));
  _7427 #(.ShowInternalStructure("true")) u_7427_1 (
    .pin1(n7411_2_pin6), .pin2(a101), .pin3(a101), .pin4(a010), .pin5(a001), .pin6(n7427_1_pin6),
    .pin13(n7427_1_pin13), .pin12(n_mw_lda), .pin11(ld1_x), .pin10(ld2_x), .pin9(ld3_x), .pin8(n_ex));
  _7427 #(.ShowInternalStructure("true")) u_7427_2 (
    .pin1(mw_lda), .pin2(op_gt_6), .pin3(n7427_1_pin6), .pin4(op_gt_6), .pin5(op03), .pin6(ld3), .pin13(ny),
    .pin12(ld1), .pin11(ld1), .pin10(ld3), .pin9(n7427_2_pin9), .pin8(ld2));
  _7408 #(.ShowInternalStructure("true")) u_7408_2 (
    .pin1(opc_eq_1), .pin2(ld1), .pin3(ld1_x), .pin4(opc_eq_2), .pin5(ld2), .pin6(ld2_x), .pin13(lprt),
    .pin12(nclk), .pin11(lprt_x), .pin10(opc_eq_3), .pin9(ld3), .pin8(ld3_x));
  AS6C6264 as6c6264_1 (
    .IO0(vd0), .IO1(vd1), .IO2(vd2), .IO7(vd7), .IO6(vd6), .IO5(vd5), .IO4(vd4), .IO3(vd3), .I0(vram_d0),
    .I1(vram_d1), .I2(vram_d2), .I3(vram_d3), .I4(vram_d4), .I5(vram_d5), .I6(vram_d6), .I7(vram_d7),
    .A12(vmaC_x), .A7(vma7_x), .A6(vma6_x), .A5(vma5_x), .A4(vma4_x), .A3(vma3_x), .A2(vma2_x), .A1(vma1_x),
    .A0(vma0_x), .CLK(clk), .nWE(n_lvram), .CE2(1'b1), .A8(vma8_x), .A9(vma9_x), .A11(vmaB_x), .nOE(1'b0),
    .A10(vmaA_x), .nCE(1'b0));  // open: NC0, GND, VCC
  _7432 #(.ShowInternalStructure("true")) u_7432_1 (
    .pin1(hsc_or_89), .pin2(hsc_nEQ_05), .pin3(hsc_n1S), .pin4(hsc_or_89), .pin5(hsc_nEQ_A), .pin6(hsc_n2S),
    .pin13(hsc_nEQ_34), .pin12(hsc_n9), .pin11(hsc_n4S), .pin10(hsc_nEQ_54), .pin9(hsc_or_89), .pin8(hsc_n3S));
  _7432 #(.ShowInternalStructure("true")) u_7432_2 (
    .pin1(hsc_n9), .pin2(hsc_nEQ_6A), .pin3(hsc_n5S), .pin4(hsc_n9), .pin5(hsc_nEQ_6E), .pin6(hsc_nR),
    .pin13(hsc2Q), .pin12(hsc3Q), .pin11(n7432_2_pin11), .pin10(n7432_2_pin11), .pin9(hsc4Q), .pin8(hsc_eORd));
  _74279 #(.ShowInternalStructure("true")) u_74279_1 (
    .pin1(hsc_n2S), .pin2(hsc_n1S), .pin3(hsc_n1S), .pin4(hsc1Q), .pin5(hsc_n3S), .pin6(hsc_n2S),
    .pin7(hsc2Q), .pin15(hsc_n4S), .pin14(hsc_n5S), .pin13(hsc4Q), .pin12(hsc_n3S), .pin11(hsc_n3S),
    .pin10(hsc_n4S), .pin9(hsc3Q));
  _74279 #(.ShowInternalStructure("true")) u_74279_2 (
    .pin1(hsc_nR), .pin2(hsc_n5S), .pin3(hsc_n5S), .pin4(hsc5Q), .pin5(tkc_nEQ_28), .pin6(tkc_nEQ_0F),
    .pin7(tkc1Q), .pin15(tkc_nEQ_F8), .pin14(tkc_nRC0), .pin13(tkc3Q), .pin12(tkc_nEQ_28),
    .pin11(tkc_nEQ_28), .pin10(tkc_nEQ_F8), .pin9(tkc2Q));
  _74151 #(.ShowInternalStructure("true")) u_74151_1 (
    .pin1(vd3_x), .pin2(vd2_x), .pin3(vd1_x), .pin4(vd0_x), .pin5(vbit), .pin7(n74151_1_pin7), .pin15(vd4_x),
    .pin14(vd5_x), .pin13(vd6_x), .pin12(vd7_x), .pin11(tkc0), .pin10(tkc1), .pin9(tkc2));  // open: pin6
  _74573 #(.ShowInternalStructure("true")) u_74573_1 (
    .pin1(n74573_1_pin1), .pin2(vd0), .pin3(vd1), .pin4(vd2), .pin5(vd3), .pin6(vd4), .pin7(vd5), .pin8(vd6),
    .pin9(vd7), .pin19(vd0_x), .pin18(vd1_x), .pin17(vd2_x), .pin16(vd3_x), .pin15(vd4_x), .pin14(vd5_x),
    .pin13(vd6_x), .pin12(vd7_x), .pin11(latch_vram));
  _74573 #(.ShowInternalStructure("true")) u_74573_2 (
    .pin1(el_vram), .pin2(tkc3), .pin3(tkc4), .pin4(tkc5), .pin5(tkc6), .pin6(tkc7), .pin7(vma5),
    .pin8(vma6), .pin9(vma7), .pin19(vma0_x), .pin18(vma1_x), .pin17(vma2_x), .pin16(vma3_x), .pin15(vma4_x),
    .pin14(vma5_x), .pin13(vma6_x), .pin12(vma7_x), .pin11(n74573_2_pin11));
  _74573 #(.ShowInternalStructure("true")) u_74573_3 (
    .pin1(el_vram), .pin2(vma8), .pin3(vma9), .pin4(vmaA), .pin5(vmaB), .pin6(vmaC), .pin7(n74573_3_pin7),
    .pin8(n74573_3_pin8), .pin9(n74573_3_pin9), .pin19(vma8_x), .pin18(vma9_x), .pin17(vmaA_x),
    .pin16(vmaB_x), .pin15(vmaC_x), .pin11(n74573_3_pin11));  // open: pin14, pin13, pin12
  _74573 #(.ShowInternalStructure("true")) u_74573_4 (
    .pin1(n_el_vram), .pin2(ad0), .pin3(ad1), .pin4(ad2), .pin5(ad3), .pin6(ad4), .pin7(ad5), .pin8(ad6),
    .pin9(ad7), .pin19(vma0_x), .pin18(vma1_x), .pin17(vma2_x), .pin16(vma3_x), .pin15(vma4_x),
    .pin14(vma5_x), .pin13(vma6_x), .pin12(vma7_x), .pin11(n74573_4_pin11));
  _74573 #(.ShowInternalStructure("true")) u_74573_5 (
    .pin1(n_el_vram), .pin2(ad8), .pin3(ad9), .pin4(adA), .pin5(adB), .pin6(adC), .pin7(adD), .pin8(adE),
    .pin9(adF), .pin19(vma8_x), .pin18(vma9_x), .pin17(vmaA_x), .pin16(vmaB_x), .pin15(vmaC_x),
    .pin11(n74573_5_pin11));  // open: pin14, pin13, pin12
  _74573 #(.ShowInternalStructure("true")) u_op0 (
    .pin1(op0_pin1), .pin2(dx0), .pin3(dx1), .pin4(dx2), .pin5(dx3), .pin6(dx4), .pin7(dx5), .pin8(dx6),
    .pin9(dx7), .pin19(op00), .pin18(op01), .pin17(op02), .pin16(op03), .pin15(op0), .pin14(op1),
    .pin13(op2), .pin12(op3), .pin11(lop0));
  _74573 #(.ShowInternalStructure("true")) u_op1 (
    .pin1(op1_pin1), .pin2(dx0), .pin3(dx1), .pin4(dx2), .pin5(dx3), .pin6(dx4), .pin7(dx5), .pin8(dx6),
    .pin9(dx7), .pin19(op10), .pin18(op11), .pin17(op12), .pin16(op13), .pin15(op14), .pin14(op15),
    .pin13(op16), .pin12(op17), .pin11(lop1));
  _74573 #(.ShowInternalStructure("true")) u_74573_6 (
    .pin1(n_eop1), .pin2(op10), .pin3(op11), .pin4(op12), .pin5(op13), .pin6(op14), .pin7(op15), .pin8(op16),
    .pin9(op17), .pin19(q0), .pin18(q1), .pin17(q2), .pin16(q3), .pin15(q4), .pin14(q5), .pin13(q6),
    .pin12(q7), .pin11(n74573_6_pin11));
  _74573 #(.ShowInternalStructure("true")) u_op2 (
    .pin1(op2_pin1), .pin2(dx0), .pin3(dx1), .pin4(dx2), .pin5(dx3), .pin6(dx4), .pin7(dx5), .pin8(dx6),
    .pin9(dx7), .pin19(op20), .pin18(op21), .pin17(op22), .pin16(op23), .pin15(op24), .pin14(op25),
    .pin13(op26), .pin12(op27), .pin11(lop2));
  _74573 #(.ShowInternalStructure("true")) u_74573_7 (
    .pin1(n_eop2), .pin2(op20), .pin3(op21), .pin4(op22), .pin5(op23), .pin6(op24), .pin7(op25), .pin8(op26),
    .pin9(op27), .pin19(q0), .pin18(q1), .pin17(q2), .pin16(q3), .pin15(q4), .pin14(q5), .pin13(q6),
    .pin12(q7), .pin11(n74573_7_pin11));
  _7432 #(.ShowInternalStructure("true")) u_7432_3 (
    .pin1(hsc1Q), .pin2(hsc2Q), .pin3(n7432_3_pin3), .pin4(n7432_3_pin3), .pin5(hsc3Q), .pin6(n7432_3_pin6),
    .pin13(tkc1Q), .pin12(tkc2Q), .pin11(n7432_3_pin11), .pin10(n7432_3_pin11), .pin9(tkc3Q),
    .pin8(n7432_3_pin8));
  _7432 #(.ShowInternalStructure("true")) u_7432_4 (
    .pin1(n7432_3_pin6), .pin2(hsc4Q), .pin3(n7432_4_pin3), .pin4(n7432_4_pin3), .pin5(hsc5Q),
    .pin6(n7432_4_pin6), .pin13(hsc8), .pin12(hsc9), .pin11(hsc_or_89), .pin10(hsc1Q), .pin9(hsc5Q),
    .pin8(hsc_pp));
  _7404 #(.ShowInternalStructure("true")) u_7404_4 (
    .pin1(n7432_4_pin6), .pin2(hsc0Q), .pin3(n7404_4_pin3), .pin4(hsc_inc), .pin13(n7432_3_pin8),
    .pin12(tkc0Q));  // open: pin5, pin6, pin11, pin10, pin9, pin8
  _7408 #(.ShowInternalStructure("true")) u_7408_3 (
    .pin1(tkc0Q), .pin2(hsc_eORd), .pin3(nV03_sync), .pin4(hsc_pp), .pin5(tkc7_LE_07), .pin6(nV03_broad),
    .pin13(hsc0Q), .pin12(tkc7_LE_6F), .pin11(nV03_short), .pin10(hsc3Q), .pin9(tkc2Q), .pin8(n7408_3_pin8));
  _7408 #(.ShowInternalStructure("true")) u_7408_4 (
    .pin1(n7408_3_pin8), .pin2(vbit), .pin3(v_10), .pin4(tkc_nEQ_80), .pin5(tkc_nRC0), .pin6(n7404_4_pin3),
    .pin13(bank_vram), .pin12(ebank), .pin11(evram), .pin10(bank_vram), .pin9(lbank), .pin8(lvram));
  _7402 #(.ShowInternalStructure("true")) u_7402_1 (
    .pin1(n7402_1_pin1), .pin2(n7402_1_pin2), .pin3(n7402_1_pin2), .pin4(n7402_1_pin2), .pin5(nV03_broad),
    .pin6(nV03_short), .pin13(v_03), .pin12(n7402_1_pin1), .pin11(nV03_sync), .pin10(n_el_vram),
    .pin9(evram), .pin8(lvram));
  _7411 #(.ShowInternalStructure("true")) u_7411_3 (
    .pin1(rise), .pin2(n7411_3_pin2), .pin3(tkc0), .pin4(tkc1), .pin5(tkc2), .pin6(n7411_3_pin2),
    .pin13(n7411_3_pin13), .pin12(latch_vram), .pin11(mb_nGT_1), .pin10(mb_nEQ_1), .pin9(n7411_3_pin9),
    .pin8(mb_EQ_0));
  Button button_1 (.out(reset));
  LED led_1 (.in(q7));
  LED led_2 (.in(q6));
  LED led_3 (.in(ad0));
  LED led_4 (.in(ad1));
  LED led_5 (.in(ad2));
  LED led_6 (.in(ad3));
  LED led_7 (.in(ad4));
  LED led_8 (.in(ad5));
  LED led_9 (.in(ad6));
  LED led_10 (.in(ad7));
  LED led_11 (.in(ad8));
  LED led_12 (.in(ad9));
  LED led_13 (.in(adA));
  LED led_14 (.in(adB));
  LED led_15 (.in(adC));
  LED led_16 (.in(adD));
  LED led_17 (.in(adE));
  LED led_18 (.in(adF));
  LED led_19 (.in(eaux));
  LED led_20 (.in(ebank));
  LED led_21 (.in(lbank));
  LED led_22 (.in(d_EQ_0));
  LED led_23 (.in(n_evram));
  LED led_24 (.in(n_lvram));
  LED led_25 (.in(dbg_x));
  LED led_26 (.in(dbg_y));
  Clock clock_1 (.out(clock_1_out));
  _7404 #(.ShowInternalStructure("true")) u_7404_5 (
    .pin1(reset), .pin2(nreset), .pin3(clk), .pin4(nclk), .pin5(st3), .pin6(n7404_5_pin6), .pin13(clk),
    .pin12(n7404_5_pin12), .pin11(n7404_5_pin12), .pin10(n7404_5_pin10), .pin9(n7404_5_pin10),
    .pin8(n7404_5_pin8));
  _7408 #(.ShowInternalStructure("true")) u_7408_5 (
    .pin1(clock_1_out), .pin2(n7404_5_pin6), .pin3(clk), .pin13(n7404_5_pin8), .pin12(clk), .pin11(rise),
    .pin10(n7404_5_pin10), .pin9(nclk), .pin8(fall));  // open: pin4, pin5, pin6
  _7408 #(.ShowInternalStructure("true")) u_7408_6 (
    .pin1(mc1_x), .pin2(eta), .pin3(asp), .pin4(mc0_x), .pin5(eta), .pin6(emem), .pin13(mc2_x), .pin12(eta),
    .pin11(aimm), .pin10(mc3_x), .pin9(eta), .pin8(lmem));
  _7408 #(.ShowInternalStructure("true")) u_7408_7 (
    .pin1(mc5_x), .pin2(eta), .pin3(spdec), .pin4(mc4_x), .pin5(eta), .pin6(spinc), .pin13(mc6_x),
    .pin12(eta), .pin11(jnz), .pin10(mc0_x), .pin9(etb), .pin8(ldx));
  _7408 #(.ShowInternalStructure("true")) u_7408_8 (
    .pin1(mc2_x), .pin2(etb), .pin3(ldf), .pin4(mc1_x), .pin5(etb), .pin6(ldy), .pin13(mc3_x), .pin12(etb),
    .pin11(ealu), .pin10(mc4_x), .pin9(etb), .pin8(ldh));
  _7408 #(.ShowInternalStructure("true")) u_7408_9 (
    .pin1(mc6_x), .pin2(etb), .pin3(lprt), .pin4(mc5_x), .pin5(etb), .pin6(ldl), .pin13(mc7_x), .pin12(ex),
    .pin11(ereg), .pin10(mc8_x), .pin9(ex), .pin8(lreg));
  _7408 #(.ShowInternalStructure("true")) u_7408_10 (
    .pin1(mcA_x), .pin2(ex), .pin3(eop1), .pin4(mc9_x), .pin5(ex), .pin6(sel), .pin13(mcB_x), .pin12(ex),
    .pin11(eop2), .pin10(mcC_x), .pin9(ex), .pin8(edev));
  LED led_27 (.in(q5));
  LED led_28 (.in(q4));
  LED led_29 (.in(q3));
  LED led_30 (.in(q2));
  LED led_31 (.in(q1));
  LED led_32 (.in(q0));
  LED led_33 (.in(emem));
  LED led_34 (.in(asp));
  LED led_35 (.in(aimm));
  LED led_36 (.in(lmem));
  LED led_37 (.in(spinc));
  LED led_38 (.in(spdec));
  LED led_39 (.in(jnz));
  LED led_40 (.in(ldx));
  LED led_41 (.in(ldy));
  LED led_42 (.in(ldf));
  LED led_43 (.in(ealu));
  LED led_44 (.in(ldh));
  LED led_45 (.in(ldl));
  LED led_46 (.in(lprt));
  LED led_47 (.in(ereg));
  LED led_48 (.in(lreg));
  LED led_49 (.in(sel));
  LED led_50 (.in(eop1));
  LED led_51 (.in(eop2));
  LED led_52 (.in(edev));
  LED led_53 (.in(ldev));
  LED led_54 (.in(cc));
  LED led_55 (.in(ex));
  LED led_56 (.in(n_ex));
  _74374 #(.ShowInternalStructure("true")) u_74374_1 (
    .pin1(n74374_1_pin1), .pin2(x0), .pin3(d0), .pin4(d1), .pin5(x1), .pin6(x2), .pin7(d2), .pin8(d3),
    .pin9(x3), .pin19(x7), .pin18(d7), .pin17(d6), .pin16(x6), .pin15(x5), .pin14(d5), .pin13(d4),
    .pin12(x4), .pin11(xc));
  _74374 #(.ShowInternalStructure("true")) u_74374_2 (
    .pin1(n74374_2_pin1), .pin2(y0), .pin3(d0), .pin4(d1), .pin5(y1), .pin6(y2), .pin7(d2), .pin8(d3),
    .pin9(y3), .pin19(y7), .pin18(d7), .pin17(d6), .pin16(y6), .pin15(y5), .pin14(d5), .pin13(d4),
    .pin12(y4), .pin11(yc));
  _7408 #(.ShowInternalStructure("true")) u_7408_11 (
    .pin1(op1), .pin2(flag_c), .pin3(c_in), .pin4(nE_adc), .pin5(nE_add), .pin6(nE_add_adc), .pin13(ldx),
    .pin12(nclk), .pin11(xc), .pin10(ldy), .pin9(nclk), .pin8(yc));
  _7404 #(.ShowInternalStructure("true")) u_7404_6 (
    .pin1(y0), .pin2(ny0), .pin3(y1), .pin4(ny1), .pin5(y2), .pin6(ny2), .pin13(y5), .pin12(ny5), .pin11(y4),
    .pin10(ny4), .pin9(y3), .pin8(ny3));
  _7404 #(.ShowInternalStructure("true")) u_7404_7 (
    .pin1(y6), .pin2(ny6), .pin3(y7), .pin4(ny7), .pin5(ldf), .pin6(nLDF), .pin13(flag_b), .pin12(b_in),
    .pin11(nb_out), .pin10(b_out), .pin9(esta), .pin8(n_esta));
  _74283 #(.ShowInternalStructure("true")) u_74283_4 (
    .pin1(s1), .pin2(y1), .pin3(x1), .pin4(s0), .pin5(x0), .pin6(y0), .pin7(c_in), .pin15(y2), .pin14(x2),
    .pin13(s2), .pin12(x3), .pin11(y3), .pin10(s3), .pin9(n74283_4_pin9));
  _74283 #(.ShowInternalStructure("true")) u_74283_5 (
    .pin1(s5), .pin2(y5), .pin3(x5), .pin4(s4), .pin5(x4), .pin6(y4), .pin7(n74283_4_pin9), .pin15(y6),
    .pin14(x6), .pin13(s6), .pin12(x7), .pin11(y7), .pin10(s7), .pin9(c_out));
  _74283 #(.ShowInternalStructure("true")) u_74283_6 (
    .pin1(b1), .pin2(ny1), .pin3(x1), .pin4(b0), .pin5(x0), .pin6(ny0), .pin7(b_in), .pin15(ny2), .pin14(x2),
    .pin13(b2), .pin12(x3), .pin11(ny3), .pin10(b3), .pin9(n74283_6_pin9));
  _74283 #(.ShowInternalStructure("true")) u_74283_7 (
    .pin1(b5), .pin2(ny5), .pin3(x5), .pin4(b4), .pin5(x4), .pin6(ny4), .pin7(n74283_6_pin9), .pin15(ny6),
    .pin14(x6), .pin13(b6), .pin12(x7), .pin11(ny7), .pin10(b7), .pin9(nb_out));
  _74138 #(.ShowInternalStructure("true")) u_74138_1 (
    .pin1(op0), .pin2(op1), .pin3(op2), .pin4(n74138_1_pin4), .pin5(n74138_1_pin5), .pin6(ealu),
    .pin7(nE_sub), .pin15(nE_pass), .pin14(nE_add), .pin13(nE_adc), .pin12(nE_and), .pin11(nE_or),
    .pin10(nE_nor), .pin9(nE_cmp));
  _74244 #(.ShowInternalStructure("true")) u_74244_1 (
    .pin1(nE_pass), .pin2(y0), .pin3(z4), .pin4(y1), .pin5(z5), .pin6(y2), .pin7(z6), .pin8(y3), .pin9(z7),
    .pin19(nE_pass), .pin18(z0), .pin17(y4), .pin16(z1), .pin15(y5), .pin14(z2), .pin13(y6), .pin12(z3),
    .pin11(y7));
  _74244 #(.ShowInternalStructure("true")) u_74244_2 (
    .pin1(nE_add_adc), .pin2(s0), .pin3(z4), .pin4(s1), .pin5(z5), .pin6(s2), .pin7(z6), .pin8(s3),
    .pin9(z7), .pin19(nE_add_adc), .pin18(z0), .pin17(s4), .pin16(z1), .pin15(s5), .pin14(z2), .pin13(s6),
    .pin12(z3), .pin11(s7));
  _74244 #(.ShowInternalStructure("true")) u_74244_3 (
    .pin1(nE_sub), .pin2(b0), .pin3(z4), .pin4(b1), .pin5(z5), .pin6(b2), .pin7(z6), .pin8(b3), .pin9(z7),
    .pin19(nE_sub), .pin18(z0), .pin17(b4), .pin16(z1), .pin15(b5), .pin14(z2), .pin13(b6), .pin12(z3),
    .pin11(b7));
  _7485 #(.ShowInternalStructure("true")) u_7485_2 (
    .pin1(y3), .pin2(n7485_2_pin2), .pin3(n7485_2_pin3), .pin4(n7485_2_pin4), .pin5(n7485_2_pin5),
    .pin6(n7485_2_pin6), .pin7(n7485_2_pin7), .pin15(x3), .pin14(y2), .pin13(x2), .pin12(x1), .pin11(y1),
    .pin10(x0), .pin9(y0));
  _7408 #(.ShowInternalStructure("true")) u_7408_12 (
    .pin1(x0), .pin2(y0), .pin3(a0), .pin4(x1), .pin5(y1), .pin6(a1), .pin13(x3), .pin12(y3), .pin11(a3),
    .pin10(x2), .pin9(y2), .pin8(a2));
  _74244 #(.ShowInternalStructure("true")) u_74244_4 (
    .pin1(nE_and), .pin2(a0), .pin3(z4), .pin4(a1), .pin5(z5), .pin6(a2), .pin7(z6), .pin8(a3), .pin9(z7),
    .pin19(nE_and), .pin18(z0), .pin17(a4), .pin16(z1), .pin15(a5), .pin14(z2), .pin13(a6), .pin12(z3),
    .pin11(a7));
  _74244 #(.ShowInternalStructure("true")) u_74244_5 (
    .pin1(nLDF), .pin2(XltY), .pin3(z4), .pin4(XeqY), .pin5(z5), .pin6(c_out), .pin7(z6), .pin8(b_out),
    .pin9(z7), .pin19(nLDF), .pin18(z0), .pin17(n74244_5_pin17), .pin16(z1), .pin15(n74244_5_pin15),
    .pin14(z2), .pin13(n74244_5_pin13), .pin12(z3), .pin11(n74244_5_pin11));
  _7485 #(.ShowInternalStructure("true")) u_7485_3 (
    .pin1(y7), .pin2(n7485_2_pin7), .pin3(n7485_2_pin6), .pin4(n7485_2_pin5), .pin6(XeqY), .pin7(XltY),
    .pin15(x7), .pin14(y6), .pin13(x6), .pin12(x5), .pin11(y5), .pin10(x4), .pin9(y4));  // open: pin5
  _7408 #(.ShowInternalStructure("true")) u_7408_13 (
    .pin1(x4), .pin2(y4), .pin3(a4), .pin4(x5), .pin5(y5), .pin6(a5), .pin13(x7), .pin12(y7), .pin11(a7),
    .pin10(x6), .pin9(y6), .pin8(a6));
  _7432 #(.ShowInternalStructure("true")) u_7432_5 (
    .pin1(x0), .pin2(y0), .pin3(o0), .pin4(x1), .pin5(y1), .pin6(o1), .pin13(x3), .pin12(y3), .pin11(o3),
    .pin10(x2), .pin9(y2), .pin8(o2));
  _7432 #(.ShowInternalStructure("true")) u_7432_6 (
    .pin1(x4), .pin2(y4), .pin3(o4), .pin4(x5), .pin5(y5), .pin6(o5), .pin13(x7), .pin12(y7), .pin11(o7),
    .pin10(x6), .pin9(y6), .pin8(o6));
  _74244 #(.ShowInternalStructure("true")) u_74244_6 (
    .pin1(nE_or), .pin2(a0), .pin3(z4), .pin4(o1), .pin5(z5), .pin6(o2), .pin7(z6), .pin8(o3), .pin9(z7),
    .pin19(nE_or), .pin18(z0), .pin17(o4), .pin16(z1), .pin15(o5), .pin14(z2), .pin13(o6), .pin12(z3),
    .pin11(o7));
  _7404 #(.ShowInternalStructure("true")) u_7404_8 (
    .pin1(o0), .pin2(n0), .pin3(o1), .pin4(n1), .pin5(o2), .pin6(n2), .pin13(o5), .pin12(n5), .pin11(o4),
    .pin10(n4), .pin9(o3), .pin8(n3));
  _7404 #(.ShowInternalStructure("true")) u_7404_9 (
    .pin1(o6), .pin2(n6), .pin3(o7), .pin4(n7));  // open: pin5, pin6, pin13, pin12, pin11, pin10, pin9, pin8
  _74244 #(.ShowInternalStructure("true")) u_74244_7 (
    .pin1(nE_nor), .pin2(n0), .pin3(z4), .pin4(n1), .pin5(z5), .pin6(n2), .pin7(z6), .pin8(n3), .pin9(z7),
    .pin19(nE_nor), .pin18(z0), .pin17(n4), .pin16(z1), .pin15(n5), .pin14(z2), .pin13(n6), .pin12(z3),
    .pin11(n7));
  // also tied to GND on the sheet: {HSC_0_pin3, HSC_0_pin4, HSC_0_pin5, HSC_0_pin6, HSC_1_pin3, HSC_1_pin4, HSC_1_pin5, HSC_1_pin6, HSC_2_pin3, HSC_2_pin4, HSC_2_pin5, HSC_2_pin6, TKC_0_pin3, TKC_0_pin4, TKC_0_pin5, TKC_0_pin6, TKC_1_pin3, TKC_1_pin4, TKC_1_pin5, TKC_1_pin6, n74688_1_pin1, n74688_1_pin3, n74688_1_pin5, n74688_1_pin7, n74688_1_pin9, n74682_1_pin9, n74688_2_pin1, n74688_3_pin1, n74688_4_pin1, n74688_4_pin3, n74688_4_pin5, n74688_4_pin7, n7485_1_pin1, n7485_1_pin2, n7485_1_pin4, n74163_1_pin3, n74163_1_pin4, n74163_1_pin5, n74163_1_pin6, n74163_2_pin3, n74163_2_pin4, n74163_2_pin5, n74163_2_pin6, n74688_1_pin16, n74688_1_pin14, n74688_1_pin12, n74682_1_pin18, n74682_1_pin17, n74682_1_pin16, n74682_1_pin14, n74682_1_pin12, n74682_2_pin18, n74682_2_pin17, n74682_2_pin12, n74688_2_pin18, n74688_2_pin16, n74688_2_pin14, n74688_2_pin12, n74688_3_pin18, n74688_3_pin16, n74688_3_pin12, n7485_1_pin9, EQ_5_pin1, EQ_5_pin3, EQ_5_pin5, EQ_5_pin9, EQ_09_pin1, EQ_09_pin3, EQ_09_pin7, EQ_54_pin1, EQ_54_pin3, EQ_54_pin5, EQ_54_pin9, EQ_33_pin1, EQ_33_pin7, EQ_33_pin9, EQ_69_pin1, EQ_69_pin3, EQ_69_pin7, EQ_6F_pin1, n74283_1_pin2, n74283_1_pin6, n74283_1_pin7, n74283_2_pin6, EQ_5_pin18, EQ_5_pin16, EQ_5_pin14, EQ_5_pin12, EQ_09_pin18, EQ_09_pin16, EQ_09_pin14, EQ_09_pin12, EQ_54_pin18, EQ_54_pin14, EQ_33_pin18, EQ_33_pin16, EQ_69_pin18, EQ_69_pin12, EQ_6F_pin18, EQ_6F_pin12, n74283_2_pin15, n74283_3_pin15, n74283_3_pin11, n7427_1_pin13, n7427_2_pin9, n74151_1_pin7, n74573_1_pin1, n74573_3_pin7, n74573_3_pin8, n74573_3_pin9, op0_pin1, op1_pin1, op2_pin1, n74374_1_pin1, n74374_2_pin1, n74138_1_pin4, n74138_1_pin5, n7485_2_pin2, n7485_2_pin4, n74244_5_pin17, n74244_5_pin15, n74244_5_pin13, n74244_5_pin11}
  // also tied to VCC on the sheet: {HSC_0_pin7, HSC_1_pin7, HSC_2_pin7, TKC_0_pin7, TKC_1_pin7, n74682_1_pin3, n74682_1_pin5, n74682_1_pin7, n74682_2_pin3, n74682_2_pin5, n74682_2_pin7, n74682_2_pin9, n74688_2_pin3, n74688_2_pin5, n74688_2_pin7, n74688_2_pin9, n74688_3_pin3, n74688_3_pin5, n74688_3_pin7, n74688_3_pin9, n74688_4_pin9, n7485_1_pin3, HSC_0_pin9, HSC_1_pin9, HSC_2_pin9, TKC_0_pin10, TKC_0_pin9, TKC_1_pin9, n74688_1_pin18, n74682_2_pin16, n74682_2_pin14, n74688_3_pin14, n74688_4_pin18, n74688_4_pin16, n74688_4_pin14, n74688_4_pin12, n7485_1_pin14, n7485_1_pin11, n74163_1_pin10, n74163_1_pin9, n74163_2_pin10, n74163_2_pin9, EQ_5_pin7, EQ_09_pin5, EQ_09_pin9, EQ_54_pin7, EQ_33_pin3, EQ_33_pin5, EQ_69_pin5, EQ_69_pin9, EQ_6F_pin3, EQ_6F_pin5, EQ_6F_pin7, EQ_6F_pin9, n74283_2_pin2, n74283_3_pin2, n74283_3_pin6, EQ_54_pin16, EQ_54_pin12, EQ_33_pin14, EQ_33_pin12, EQ_69_pin16, EQ_69_pin14, EQ_6F_pin16, EQ_6F_pin14, n74283_1_pin15, n74283_1_pin11, n74283_2_pin11, n7411_2_pin11, n74573_2_pin11, n74573_3_pin11, n74573_4_pin11, n74573_5_pin11, n74573_6_pin11, n74573_7_pin11, n7411_3_pin13, n7411_3_pin9, n7485_2_pin3}

  // Other names for the same wires on the sheet: op05 = op1; op06 = op2; op07 = op3; op04 = op0; sel00 = op00;
  //   sel01 = op01; sel02 = op02; sel10 = op10; sel11 = op11; sel12 = op12; y = op03
endmodule
